// Logisim project cpu21-riscv - 副本.circ as structural Verilog: 29 circuits, main circuit ◇单周期RISC-V
module \单周期RISC_V  (
  input  IR1,
  input  IR2,
  input  IR3,
  output RegWrite,
  output MemWrite,
  output [31:0] PC,
  output [31:0] IR,
  output [31:0] RDin,
  output [31:0] MDin,
  output [31:0] LedData
);

  wire and_1_out, and_2_out, and_3_out, and_4_out, and_5_out, AUIPC, Ben, Beq, Blt, CLK, clock_1_out,
       comparator_1_eq, comparator_2_eq, comparator_2_lt, d_ff_1_q, ecall, Go, halt, IR1_t, IR2_t, IR3_t,
       IRA, IRB, IRC, JAL, JALR, LH, MemToReg, nand_1_out, not_1_out, not_2_out, not_3_out, not_4_out,
       or_1_out, or_5_out, or_6_out, RST, tunnel, tunnel_t, W1, W2, W3, \单周期硬布线控制器_1_alu_src ,
       \单周期硬布线控制器_1_sw ;
  wire [1:0] priority_encoder_1_out;
  wire [3:0] \单周期硬布线控制器_1_alu_op ;
  wire [4:0] multiplexer_2_out, multiplexer_3_out;
  wire [12:0] CNT_num;
  wire [15:0] multiplexer_6_out, \总周期数 ;
  wire [31:0] adder_2_out, adder_3_out, ALUResult, bit_extender_1_out, branch, immgen_1_imm,
       multiplexer_1_out, multiplexer_4_out, multiplexer_7_out, PC_4, ram_1_data, regifile_1_r1,
       shifter_1_out, shifter_2_out;

  Button \u_继续运行  (.out(Go));
  Button _1 (.out(IRA));
  Button _2 (.out(IRB));
  Button _3 (.out(IRC));
  LED #(.active("true")) led_1 (.in(W1));
  LED #(.active("true")) led_2 (.in(W2));
  LED #(.active("true")) led_3 (.in(W3));
  Hex_Digit_Display hex_digit_display_1 (.value(LedData[31:28]));  // open: dp
  Hex_Digit_Display hex_digit_display_2 (.value(LedData[23:20]));  // open: dp
  Hex_Digit_Display hex_digit_display_3 (.value(LedData[27:24]));  // open: dp
  Multiplexer #(.select(1), .width(32), .disabled("Z"), .enable("false")) multiplexer_1 (
    .in0(PC_4), .in1(branch), .out(multiplexer_1_out), .sel(or_1_out));
  Hex_Digit_Display hex_digit_display_4 (.value(LedData[19:16]));  // open: dp
  Hex_Digit_Display hex_digit_display_5 (.value(LedData[15:12]));  // open: dp
  not not_1 (not_1_out, halt);
  Hex_Digit_Display hex_digit_display_6 (.value(LedData[11:8]));  // open: dp
  Hex_Digit_Display hex_digit_display_7 (.value(LedData[7:4]));  // open: dp
  // Probe on \总周期数 
  and and_1 (and_1_out, Blt, tunnel);
  or or_1 (or_1_out, and_1_out, and_2_out, and_3_out, JAL, JALR);
  Register #(.width(32), .trigger("rising"), .Select("low")) u_PC (
    .D(multiplexer_1_out), .en(not_1_out), .Q(PC), .clk(CLK), .clr(RST));
  not not_2 (not_2_out, halt);
  Counter #(.width(16), .max('hffff), .ongoal("wrap"), .trigger("rising"), .behavior("new")) counter_1 (
    .count(not_2_out), .Q(\总周期数 ), .clk(CLK));  // open: load, D, carry, clr, preset, down
  Hex_Digit_Display hex_digit_display_8 (.value(LedData[3:0]));  // open: dp
  and and_2 (and_2_out, Beq, tunnel_t);
  and and_3 (and_3_out, ~tunnel_t, Ben);  // AND_Gate
  Adder #(.width(32)) adder_1 (.a(PC), .b(32'h4), .out(PC_4));  // open: cin, cout
  // RiscV_Probe riscv_probe_1: pin names not known; wires that end beside it: IR
  ROM #(.addrWidth(10), .dataWidth(32), .Select("high")) rom_1 (.addr(PC[11:2]), .data(IR));
  or or_2 (IR1_t, IR1, IRA);
  or or_3 (IR2_t, IR2, IRB);
  \单周期硬布线控制器  \u_单周期硬布线控制器_1  (
    .Funct({IR[30], IR[25], IR[14:12]}), .OP(IR[6:2]), .ALU_OP(\单周期硬布线控制器_1_alu_op ), .MemToReg(MemToReg),
    .MemWrite(MemWrite), .ALU_SRC(\单周期硬布线控制器_1_alu_src ), .RegWrite(RegWrite), .ecall(ecall),
    .Sw(\单周期硬布线控制器_1_sw ), .Jalr(JALR), .Beq(Beq), .JAL(JAL), .Bne(Ben), .in_3(IR[21]), .AUIPC(AUIPC),
    .LH(LH), .BLT(Blt));  // open: uret, csrrci, csrrsi
  Multiplexer #(.select(1), .width(5), .disabled("Z"), .enable("false")) multiplexer_2 (
    .in0(IR[19:15]), .in1(5'b10001), .out(multiplexer_2_out), .sel(ecall));
  Multiplexer #(.select(1), .width(5), .disabled("Z"), .enable("false")) multiplexer_3 (
    .in0(IR[24:20]), .in1(5'b01010), .out(multiplexer_3_out), .sel(ecall));
  ImmGen immgen_1 (.Sw(\单周期硬布线控制器_1_sw ), .Auipc(AUIPC), .B_Type(or_5_out), .jal(JAL), .IR(IR), .Imm(immgen_1_imm));
  or or_4 (IR3_t, IR3, IRC);
  or or_5 (or_5_out, Blt, Ben, Beq);
  Shifter #(.width(32), .shift("ll")) shifter_1 (.in(immgen_1_imm), .\dist (5'b00001), .out(shifter_1_out));
  Shifter #(.width(32), .shift("ll")) shifter_2 (.in(immgen_1_imm), .\dist (5'b01100), .out(shifter_2_out));
  Regifile regifile_1 (
    .Din(RDin), .Clk(CLK), .R1(regifile_1_r1), .R2(MDin), .WE(RegWrite), .W_num(IR[11:7]),
    .R1_num(multiplexer_2_out), .R2_num(multiplexer_3_out));
  Multiplexer #(.select(1), .width(32), .disabled("Z"), .enable("false")) multiplexer_4 (
    .in0(MDin), .in1(immgen_1_imm), .out(multiplexer_4_out), .sel(\单周期硬布线控制器_1_alu_src ));
  Adder #(.width(32)) adder_2 (.a(shifter_1_out), .b(PC), .out(adder_2_out));  // open: cin, cout
  Adder #(.width(32)) adder_3 (.a(shifter_2_out), .b(PC), .out(adder_3_out));  // open: cin, cout
  Comparator #(.width(32), .mode("twosComplement")) comparator_1 (
    .a(regifile_1_r1), .b(32'h22), .eq(comparator_1_eq));  // open: gt, lt
  Multiplexer #(.select(1), .width(32), .disabled("Z"), .enable("false")) multiplexer_5 (
    .in0(adder_2_out), .in1(ALUResult), .out(branch), .sel(JALR));
  ALU alu_1 (
    .X(regifile_1_r1), .Y(multiplexer_4_out), .AluOP(\单周期硬布线控制器_1_alu_op ), .Equal(tunnel_t),
    .Result(ALUResult), .out_6(tunnel));  // open: Result_2, out_4
  not not_3 (not_3_out, comparator_1_eq);
  and and_4 (and_4_out, comparator_1_eq, ecall);
  and and_5 (and_5_out, ecall, not_3_out);
  not not_4 (not_4_out, Go);
  and and_6 (halt, and_5_out, not_4_out);
  Register #(.width(32), .trigger("rising"), .Select("low")) register_1 (
    .D(MDin), .en(and_4_out), .Q(LedData), .clk(CLK));  // open: clr
  D_Flip_Flop #(.trigger("high"), .Pre_Clr_Positions("LEGACY"), .NegatePresetClear("false"), .enable("true"), .NewFFLayout("false")) d_ff_1 (.Q(d_ff_1_q));  // open: clk, D, Qn, preset, en, reset
  // Probe on 13'hc
  RAM #(.addrWidth(10), .dataWidth(32), .bus("separate"), .Select("high")) ram_1 (
    .addr(ALUResult[11:2]), .din(MDin), .data(ram_1_data), .str(MemWrite), .sel(1'b1), .clk(CLK), .ld(1'b1));  // open: clr
  Comparator #(.width(13), .mode("twosComplement")) comparator_2 (
    .a(CNT_num), .b(13'hc), .eq(comparator_2_eq), .lt(comparator_2_lt));  // open: gt
  Clock #(.highDuration(1), .lowDuration(1)) clock_1 (.out(clock_1_out));
  or or_6 (or_6_out, JAL, JALR);
  Multiplexer #(.select(1), .width(16), .disabled("Z"), .enable("false")) multiplexer_6 (
    .in0(ram_1_data[15:0]), .in1(ram_1_data[31:16]), .out(multiplexer_6_out), .sel(ALUResult[1]));
  Counter #(.width(13), .max('h1fff), .ongoal("stay"), .trigger("rising"), .behavior("old")) counter_2 (
    .count(comparator_2_lt), .Q(CNT_num), .clk(clock_1_out));  // open: load, D, carry, clr, preset
  Priority_Encoder #(.select(2), .disabled("Z")) priority_encoder_1 (
    .in0(1'b1), .in1(MemToReg), .in2(or_6_out), .in3(AUIPC), .out(priority_encoder_1_out));  // open: gs, en_out, en_in
  Multiplexer #(.select(1), .width(32), .disabled("Z"), .enable("false")) multiplexer_7 (
    .in0(ram_1_data), .in1(bit_extender_1_out), .out(multiplexer_7_out), .sel(LH));
  assign bit_extender_1_out = {{16{multiplexer_6_out[15]}}, multiplexer_6_out};  // Bit_Extender bit_extender_1
  nand nand_1 (nand_1_out, d_ff_1_q, comparator_2_eq);
  assign CLK = nand_1_out ? clock_1_out : 1'bz;  // Controlled_Buffer controlled_buffer_1
  Pull_Resistor #(.pull(1)) pull_resistor_1 (.node(CLK));
  Multiplexer #(.select(2), .width(32), .disabled("Z"), .enable("false")) multiplexer_8 (
    .in0(ALUResult), .in1(multiplexer_7_out), .in2(PC_4), .in3(adder_3_out), .out(RDin),
    .sel(priority_encoder_1_out));

  // Notes on the sheet:
  //   中断源
  //   中断等待指示
  //   数码管输出应该用寄存器锁存，否则显示数据只能一闪而过
  //   数码管输出
  //   指令存储器
  //   指令探针
  //   contents of rom_1 (hex, n*v repeats v):
  //   100493 100006f 100493 200913 300993 100006f 100493 200913 300993 100006f 100493 200913 300993
  //   100006f 100493 200913 300993 408000ef 100413 100493 1f49493 900533 2200893 73 24d493 48463 fedff06f
  //   900533 2200893 73 100493 249493 900533 2200893 73 48463 fedff06f 100493 1f49493 900533 2200893 73
  //   4034d493 900533 2200893 73 4044d493 900533 2200893 73 4044d493 900533 2200893 73 4044d493 900533
  //   2200893 73 4044d493 900533 2200893 73 4044d493 900533 2200893 73 4044d493 900533 2200893 73 4044d493
  //   900533 2200893 73 100413 1f41993 41f9d993 433 c00913 300b13 140413 f47413 800293 100313 499993
  //   89e9b3 1300533 2200893 73 406282b3 fe0294e3 140413 f00f93 1f47433 1c41413 800293 100313 49d993
  //   89e9b3 1300533 2200893 73 406282b3 fe0294e3 1c45413 406b0b33 b0463 f95ff06f 2b3 fff2c293 829293
  //   ff2e293 500533 2200893 73 fff00413 493 84a023 140413 448493 84a023 140413 448493 84a023 140413
  //   448493 84a023 140413 448493 84a023 140413 448493 84a023 140413 448493 84a023 140413 448493 84a023
  //   140413 448493 84a023 140413 448493 84a023 140413 448493 84a023 140413 448493 84a023 140413 448493
  //   84a023 140413 448493 84a023 140413 448493 84a023 140413 448493 84a023 140413 448493 140413 433
  //   3c00493 42983 4aa03 149a2b3 28663 134a023 1442023 ffc48493 fe9412e3 800533 2200893 73 440413 3c00493
  //   fc9416e3 a00893 73 fff00293 7700493 849493 7748493 900533 2200893 73 1000e13 54c4b3 900533 2200893
  //   73 fffe0e13 fe0e16e3 a00893 73 13 430497 900533 2200893 73 430497 900533 2200893 73 430497 900533
  //   2200893 73 430497 900533 2200893 73 430497 900533 2200893 73 430497 900533 2200893 73 430497 900533
  //   2200893 73 430497 900533 2200893 73 a00893 73 313 1000e13 8400493 849493 8348493 400913 891913
  //   490913 849493 8248493 849493 8148493 891913 490913 891913 490913 932023 12484b3 430313 fffe0e13
  //   fe0e18e3 2000e13 313 31483 900533 2200893 73 230313 fffe0e13 fe0e14e3 a00893 73 ff100493 900533
  //   2200893 73 148493 fe04c8e3 a00893 73 413 140413 800533 2200893 73 240413 800533 2200893 73 340413
  //   800533 2200893 73 440413 800533 2200893 73 540413 800533 2200893 73 640413 800533 2200893 73 740413
  //   800533 2200893 73 840413 800533 2200893 2200893 73 8067
  //   rs1
  //   rs2
  //   指令字
  //   rd
  //   Beq
  //   Bne
  //   AluOP
  //   AluSrcB
  //   Sw
  //   为方便自动评测，需要输出PC，IR，寄存器堆写如数据RDin
  //   RAM写使能MemWrite、RAM写入数据MDin等信号
  //   控制位
  //   暂停节拍，不能为0
  //   数据存储器
  //   戳工具置1进入计数暂停模式，ctrl+k时钟自动运行到对应节拍暂停
  //   ctrl+k关闭时钟连续运行，将控制位置零，进入单步调试模式调试
  //   用这个时钟源需要去掉电路中的其他时钟源
  //   可计数暂停的时钟源
endmodule

// 单周期硬布线控制器
module \单周期硬布线控制器  (
  input  [4:0] OP,
  input  [4:0] Funct,
  input  in_3,
  output [3:0] ALU_OP,
  output uret,
  output MemToReg,
  output ecall,
  output MemWrite,
  output ALU_SRC,
  output RegWrite,
  output Sw,
  output Beq,
  output Bne,
  output JAL,
  output Jalr,
  output AUIPC,
  output LH,
  output BLT,
  output csrrsi,
  output csrrci
);

  wire \控制信号自动生成_1_ecall ;

  \运算控制器自动生成  \u_运算控制器自动生成_1  (
    .OP2(OP[0]), .OP3(OP[1]), .OP4(OP[2]), .OP5(OP[3]), .OP6(OP[4]), .F12(Funct[0]), .F13(Funct[1]),
    .F14(Funct[2]), .F25(Funct[3]), .F30(Funct[4]), .S0(ALU_OP[0]), .S1(ALU_OP[1]), .S2(ALU_OP[2]),
    .S3(ALU_OP[3]));
  \控制信号自动生成  \u_控制信号自动生成_1  (
    .OP2(OP[0]), .OP3(OP[1]), .OP4(OP[2]), .OP5(OP[3]), .OP6(OP[4]), .MemToReg(MemToReg), .F12(Funct[0]),
    .F13(Funct[1]), .F14(Funct[2]), .F25(Funct[3]), .F30(Funct[4]), .MemWrite(MemWrite), .ALU_SRC(ALU_SRC),
    .RegWrite(RegWrite), .ecall(\控制信号自动生成_1_ecall ), .Sw(Sw), .BEQ(Beq), .BNE(Bne), .JAL(JAL), .JALR(Jalr),
    .AUIPC(AUIPC), .LH(LH), .BLT(BLT), .csrrsi(csrrsi), .csrrci(csrrci));
  and and_1 (uret, in_3, \控制信号自动生成_1_ecall );
  and and_2 (ecall, ~in_3, \控制信号自动生成_1_ecall );  // AND_Gate

  // Other names for the same wires on the sheet: IR21 = in_3; OP_CODE[4:0] = OP

  // Notes on the sheet:
  //   控制信号生成，产生数据通路需要的其他控制信号
  //   运算器控制器，根据指令生成运算器功能选择信号
endmodule

// 运算器控制器
module \运算控制器自动生成  (
  input  OP2,
  input  OP3,
  input  OP4,
  input  OP5,
  input  OP6,
  input  F12,
  input  F13,
  input  F14,
  input  F25,
  input  F30,
  output S0,
  output S1,
  output S2,
  output S3
);

  wire and_1_out, and_2_out, and_3_out, and_4_out, and_5_out, and_6_out, and_7_out, and_8_out, and_9_out,
       and_10_out, and_11_out, and_12_out, and_13_out, and_14_out, and_15_out, and_16_out, and_17_out,
       and_18_out, and_19_out, and_20_out, and_21_out, and_22_out, and_23_out, and_24_out, and_25_out,
       and_26_out, and_27_out, and_28_out, and_29_out, and_30_out, and_31_out, and_32_out, and_33_out,
       and_34_out, and_35_out, and_36_out, and_37_out, and_38_out, and_39_out, not_1_out, not_2_out,
       not_3_out, not_4_out, not_5_out, not_6_out, not_7_out, not_8_out, not_9_out, not_10_out, not_11_out,
       not_12_out, not_13_out, not_14_out, not_15_out, not_16_out, not_17_out, not_18_out, not_19_out,
       not_20_out, not_21_out, not_22_out, not_23_out, not_24_out, not_25_out, not_26_out, not_27_out,
       not_28_out, not_29_out, not_30_out, not_31_out, not_32_out, not_33_out, not_34_out, not_35_out,
       not_36_out, not_37_out, not_38_out, not_39_out, not_40_out, not_41_out, not_42_out, not_43_out,
       not_44_out, not_45_out, not_46_out, not_47_out, not_48_out, not_49_out, not_50_out, not_51_out,
       not_52_out, not_53_out, not_54_out, not_55_out, not_56_out, not_57_out, not_58_out, not_59_out,
       not_60_out, not_61_out, not_62_out, not_63_out, not_64_out, not_65_out, not_66_out, not_67_out,
       not_68_out, not_69_out, not_70_out, not_71_out, not_72_out, not_73_out, not_74_out, not_75_out,
       not_76_out, not_77_out, not_78_out, not_79_out, not_80_out, not_81_out, not_82_out, not_83_out,
       not_84_out, not_85_out, not_86_out, not_87_out, not_88_out, not_89_out, not_90_out, not_91_out,
       not_92_out, not_93_out, not_94_out, not_95_out, not_96_out, not_97_out, not_98_out, not_99_out,
       not_100_out, not_101_out, not_102_out, not_103_out, not_104_out, not_105_out, not_106_out,
       not_107_out, not_108_out, not_109_out, not_110_out, not_111_out, not_112_out, not_113_out,
       not_114_out, not_115_out, not_116_out, not_117_out, not_118_out, not_119_out, not_120_out,
       not_121_out, not_122_out, not_123_out, not_124_out, not_125_out, not_126_out, not_127_out,
       not_128_out, not_129_out, not_130_out, not_131_out, not_132_out, not_133_out, not_134_out,
       not_135_out, not_136_out, not_137_out, not_138_out, not_139_out, not_140_out, not_141_out,
       not_142_out, not_143_out, not_144_out, not_145_out, not_146_out, not_147_out, not_148_out,
       not_149_out, not_150_out, not_151_out, not_152_out, not_153_out, not_154_out, not_155_out,
       not_156_out, not_157_out, not_158_out, not_159_out, not_160_out, not_161_out, not_162_out,
       not_163_out, not_164_out, not_165_out, not_166_out, not_167_out, not_168_out, not_169_out,
       not_170_out, not_171_out, not_172_out, not_173_out, not_174_out, not_175_out, not_176_out,
       not_177_out, not_178_out, not_179_out, not_180_out, not_181_out, not_182_out, not_183_out,
       not_184_out, not_185_out, not_186_out, not_187_out, not_188_out, not_189_out, not_190_out,
       not_191_out, not_192_out, not_193_out, not_194_out, not_195_out, not_196_out, not_197_out,
       not_198_out, not_199_out, not_200_out, not_201_out, not_202_out, not_203_out, not_204_out,
       not_205_out, not_206_out, not_207_out, not_208_out, not_209_out, not_210_out, not_211_out,
       not_212_out, not_213_out, not_214_out, not_215_out, not_216_out, not_217_out, not_218_out,
       not_219_out, not_220_out, not_221_out, not_222_out, not_223_out, not_224_out, not_225_out;

  not not_1 (not_1_out, F30);
  not not_2 (not_2_out, F25);
  not not_3 (not_3_out, F14);
  not not_4 (not_4_out, F13);
  not not_5 (not_5_out, F12);
  not not_6 (not_6_out, OP6);
  not not_7 (not_7_out, OP3);
  not not_8 (not_8_out, OP2);
  not not_9 (not_9_out, F30);
  not not_10 (not_10_out, F25);
  not not_11 (not_11_out, OP6);
  not not_12 (not_12_out, OP3);
  not not_13 (not_13_out, OP2);
  not not_14 (not_14_out, F30);
  not not_15 (not_15_out, F25);
  not not_16 (not_16_out, F14);
  not not_17 (not_17_out, F12);
  not not_18 (not_18_out, OP6);
  not not_19 (not_19_out, OP3);
  not not_20 (not_20_out, OP2);
  not not_21 (not_21_out, F14);
  not not_22 (not_22_out, F13);
  not not_23 (not_23_out, F12);
  not not_24 (not_24_out, OP6);
  not not_25 (not_25_out, OP5);
  not not_26 (not_26_out, OP3);
  not not_27 (not_27_out, OP2);
  not not_28 (not_28_out, OP6);
  not not_29 (not_29_out, OP5);
  not not_30 (not_30_out, OP3);
  not not_31 (not_31_out, OP2);
  not not_32 (not_32_out, F13);
  not not_33 (not_33_out, F12);
  not not_34 (not_34_out, OP6);
  not not_35 (not_35_out, OP5);
  not not_36 (not_36_out, OP3);
  not not_37 (not_37_out, OP2);
  not not_38 (not_38_out, F14);
  not not_39 (not_39_out, F12);
  not not_40 (not_40_out, OP6);
  not not_41 (not_41_out, OP5);
  not not_42 (not_42_out, OP3);
  not not_43 (not_43_out, OP2);
  not not_44 (not_44_out, F25);
  not not_45 (not_45_out, F13);
  not not_46 (not_46_out, OP6);
  not not_47 (not_47_out, OP5);
  not not_48 (not_48_out, OP3);
  not not_49 (not_49_out, OP2);
  not not_50 (not_50_out, F30);
  not not_51 (not_51_out, F25);
  not not_52 (not_52_out, F13);
  not not_53 (not_53_out, F12);
  not not_54 (not_54_out, OP6);
  not not_55 (not_55_out, OP3);
  not not_56 (not_56_out, OP2);
  not not_57 (not_57_out, OP6);
  not not_58 (not_58_out, OP5);
  not not_59 (not_59_out, OP3);
  not not_60 (not_60_out, F13);
  not not_61 (not_61_out, F12);
  not not_62 (not_62_out, OP4);
  not not_63 (not_63_out, OP3);
  not not_64 (not_64_out, OP2);
  not not_65 (not_65_out, F25);
  not not_66 (not_66_out, F14);
  not not_67 (not_67_out, F13);
  not not_68 (not_68_out, F12);
  not not_69 (not_69_out, OP6);
  not not_70 (not_70_out, OP3);
  not not_71 (not_71_out, OP2);
  not not_72 (not_72_out, F30);
  not not_73 (not_73_out, F25);
  not not_74 (not_74_out, OP6);
  not not_75 (not_75_out, OP3);
  not not_76 (not_76_out, OP2);
  not not_77 (not_77_out, F30);
  not not_78 (not_78_out, F25);
  not not_79 (not_79_out, F14);
  not not_80 (not_80_out, F12);
  not not_81 (not_81_out, OP6);
  not not_82 (not_82_out, OP3);
  not not_83 (not_83_out, OP2);
  not not_84 (not_84_out, OP6);
  not not_85 (not_85_out, OP5);
  not not_86 (not_86_out, OP3);
  not not_87 (not_87_out, OP2);
  not not_88 (not_88_out, F14);
  not not_89 (not_89_out, F12);
  not not_90 (not_90_out, OP6);
  not not_91 (not_91_out, OP5);
  not not_92 (not_92_out, OP3);
  not not_93 (not_93_out, OP2);
  not not_94 (not_94_out, F30);
  not not_95 (not_95_out, F25);
  not not_96 (not_96_out, F13);
  not not_97 (not_97_out, OP6);
  not not_98 (not_98_out, OP5);
  not not_99 (not_99_out, OP3);
  not not_100 (not_100_out, OP2);
  not not_101 (not_101_out, F14);
  not not_102 (not_102_out, F13);
  not not_103 (not_103_out, F12);
  not not_104 (not_104_out, OP4);
  not not_105 (not_105_out, OP3);
  not not_106 (not_106_out, OP2);
  not not_107 (not_107_out, F14);
  not not_108 (not_108_out, F13);
  not not_109 (not_109_out, OP4);
  not not_110 (not_110_out, OP3);
  not not_111 (not_111_out, OP2);
  not not_112 (not_112_out, F14);
  not not_113 (not_113_out, F13);
  not not_114 (not_114_out, F12);
  not not_115 (not_115_out, OP4);
  not not_116 (not_116_out, OP3);
  not not_117 (not_117_out, F13);
  not not_118 (not_118_out, F12);
  not not_119 (not_119_out, OP4);
  not not_120 (not_120_out, OP3);
  not not_121 (not_121_out, OP2);
  not not_122 (not_122_out, F30);
  not not_123 (not_123_out, F25);
  not not_124 (not_124_out, F14);
  not not_125 (not_125_out, F13);
  not not_126 (not_126_out, F12);
  not not_127 (not_127_out, OP6);
  not not_128 (not_128_out, OP3);
  not not_129 (not_129_out, OP2);
  not not_130 (not_130_out, F25);
  not not_131 (not_131_out, F14);
  not not_132 (not_132_out, F13);
  not not_133 (not_133_out, F12);
  not not_134 (not_134_out, OP6);
  not not_135 (not_135_out, OP3);
  not not_136 (not_136_out, OP2);
  not not_137 (not_137_out, F30);
  not not_138 (not_138_out, F25);
  not not_139 (not_139_out, OP6);
  not not_140 (not_140_out, OP3);
  not not_141 (not_141_out, OP2);
  not not_142 (not_142_out, F30);
  not not_143 (not_143_out, F25);
  not not_144 (not_144_out, F14);
  not not_145 (not_145_out, OP6);
  not not_146 (not_146_out, OP3);
  not not_147 (not_147_out, OP2);
  not not_148 (not_148_out, F14);
  not not_149 (not_149_out, F13);
  not not_150 (not_150_out, F12);
  not not_151 (not_151_out, OP6);
  not not_152 (not_152_out, OP5);
  not not_153 (not_153_out, OP3);
  not not_154 (not_154_out, OP2);
  not not_155 (not_155_out, OP6);
  not not_156 (not_156_out, OP5);
  not not_157 (not_157_out, OP3);
  not not_158 (not_158_out, OP2);
  not not_159 (not_159_out, F14);
  not not_160 (not_160_out, F13);
  not not_161 (not_161_out, F12);
  not not_162 (not_162_out, OP4);
  not not_163 (not_163_out, OP3);
  not not_164 (not_164_out, OP2);
  not not_165 (not_165_out, F14);
  not not_166 (not_166_out, F13);
  not not_167 (not_167_out, OP4);
  not not_168 (not_168_out, OP3);
  not not_169 (not_169_out, OP2);
  not not_170 (not_170_out, F14);
  not not_171 (not_171_out, F13);
  not not_172 (not_172_out, F12);
  not not_173 (not_173_out, OP4);
  not not_174 (not_174_out, OP3);
  not not_175 (not_175_out, OP6);
  not not_176 (not_176_out, OP5);
  not not_177 (not_177_out, OP3);
  not not_178 (not_178_out, F30);
  not not_179 (not_179_out, F25);
  not not_180 (not_180_out, F12);
  not not_181 (not_181_out, OP6);
  not not_182 (not_182_out, OP3);
  not not_183 (not_183_out, OP2);
  not not_184 (not_184_out, F30);
  not not_185 (not_185_out, F25);
  not not_186 (not_186_out, F14);
  not not_187 (not_187_out, F12);
  not not_188 (not_188_out, OP6);
  not not_189 (not_189_out, OP3);
  not not_190 (not_190_out, OP2);
  not not_191 (not_191_out, F30);
  not not_192 (not_192_out, F25);
  not not_193 (not_193_out, F14);
  not not_194 (not_194_out, OP6);
  not not_195 (not_195_out, OP3);
  not not_196 (not_196_out, OP2);
  not not_197 (not_197_out, F12);
  not not_198 (not_198_out, OP6);
  not not_199 (not_199_out, OP5);
  not not_200 (not_200_out, OP3);
  not not_201 (not_201_out, OP2);
  not not_202 (not_202_out, F13);
  not not_203 (not_203_out, F12);
  not not_204 (not_204_out, OP6);
  not not_205 (not_205_out, OP5);
  not not_206 (not_206_out, OP3);
  not not_207 (not_207_out, OP2);
  not not_208 (not_208_out, F14);
  not not_209 (not_209_out, F12);
  not not_210 (not_210_out, OP6);
  not not_211 (not_211_out, OP5);
  not not_212 (not_212_out, OP3);
  not not_213 (not_213_out, OP2);
  not not_214 (not_214_out, F30);
  not not_215 (not_215_out, F25);
  not not_216 (not_216_out, F13);
  not not_217 (not_217_out, F12);
  not not_218 (not_218_out, OP6);
  not not_219 (not_219_out, OP3);
  not not_220 (not_220_out, OP2);
  not not_221 (not_221_out, F13);
  not not_222 (not_222_out, F12);
  not not_223 (not_223_out, OP4);
  not not_224 (not_224_out, OP3);
  not not_225 (not_225_out, OP2);
  and and_1 (and_1_out, not_1_out, not_2_out, not_3_out, not_4_out, not_5_out, not_6_out, OP5, OP4, not_7_out, not_8_out);
  and and_2 (and_2_out, not_9_out, not_10_out, F14, F13, F12, not_11_out, OP5, OP4, not_12_out, not_13_out);
  and and_3 (and_3_out, not_14_out, not_15_out, not_16_out, F13, not_17_out, not_18_out, OP5, OP4, not_19_out, not_20_out);
  and and_4 (and_4_out, not_21_out, not_22_out, not_23_out, not_24_out, not_25_out, OP4, not_26_out, not_27_out);
  and and_5 (and_5_out, F14, F13, F12, not_28_out, not_29_out, OP4, not_30_out, not_31_out);
  and and_6 (and_6_out, F14, not_32_out, not_33_out, not_34_out, not_35_out, OP4, not_36_out, not_37_out);
  and and_7 (and_7_out, not_38_out, F13, not_39_out, not_40_out, not_41_out, OP4, not_42_out, not_43_out);
  and and_8 (and_8_out, F30, not_44_out, F14, not_45_out, F12, not_46_out, not_47_out, OP4, not_48_out, not_49_out);
  and and_9 (and_9_out, not_50_out, not_51_out, F14, not_52_out, not_53_out, not_54_out, OP5, OP4, not_55_out, not_56_out);
  and and_10 (and_10_out, not_57_out, not_58_out, OP4, not_59_out, OP2);
  and and_11 (and_11_out, F14, not_60_out, not_61_out, OP6, OP5, not_62_out, not_63_out, not_64_out);
  and and_12 (and_12_out, F30, not_65_out, not_66_out, not_67_out, not_68_out, not_69_out, OP5, OP4, not_70_out, not_71_out);
  and and_13 (and_13_out, not_72_out, not_73_out, F14, F13, F12, not_74_out, OP5, OP4, not_75_out, not_76_out);
  and and_14 (and_14_out, not_77_out, not_78_out, not_79_out, F13, not_80_out, not_81_out, OP5, OP4, not_82_out, not_83_out);
  and and_15 (and_15_out, F14, F13, F12, not_84_out, not_85_out, OP4, not_86_out, not_87_out);
  and and_16 (and_16_out, not_88_out, F13, not_89_out, not_90_out, not_91_out, OP4, not_92_out, not_93_out);
  and and_17 (and_17_out, not_94_out, not_95_out, F14, not_96_out, F12, not_97_out, not_98_out, OP4, not_99_out, not_100_out);
  and and_18 (and_18_out, not_101_out, not_102_out, not_103_out, OP6, OP5, not_104_out, not_105_out, not_106_out);
  and and_19 (and_19_out, not_107_out, not_108_out, F12, OP6, OP5, not_109_out, not_110_out, not_111_out);
  and and_20 (and_20_out, not_112_out, not_113_out, not_114_out, OP6, OP5, not_115_out, not_116_out, OP2);
  and and_21 (and_21_out, F14, not_117_out, not_118_out, OP6, OP5, not_119_out, not_120_out, not_121_out);
  and and_22 (and_22_out, not_122_out, not_123_out, not_124_out, not_125_out, not_126_out, not_127_out, OP5, OP4, not_128_out, not_129_out);
  and and_23 (and_23_out, F30, not_130_out, not_131_out, not_132_out, not_133_out, not_134_out, OP5, OP4, not_135_out, not_136_out);
  and and_24 (and_24_out, not_137_out, not_138_out, F14, F13, F12, not_139_out, OP5, OP4, not_140_out, not_141_out);
  and and_25 (and_25_out, not_142_out, not_143_out, not_144_out, F13, F12, not_145_out, OP5, OP4, not_146_out, not_147_out);
  and and_26 (and_26_out, not_148_out, not_149_out, not_150_out, not_151_out, not_152_out, OP4, not_153_out, not_154_out);
  and and_27 (and_27_out, F14, F13, F12, not_155_out, not_156_out, OP4, not_157_out, not_158_out);
  and and_28 (and_28_out, not_159_out, not_160_out, not_161_out, OP6, OP5, not_162_out, not_163_out, not_164_out);
  and and_29 (and_29_out, not_165_out, not_166_out, F12, OP6, OP5, not_167_out, not_168_out, not_169_out);
  and and_30 (and_30_out, not_170_out, not_171_out, not_172_out, OP6, OP5, not_173_out, not_174_out, OP2);
  and and_31 (and_31_out, not_175_out, not_176_out, OP4, not_177_out, OP2);
  and and_32 (and_32_out, not_178_out, not_179_out, F14, F13, not_180_out, not_181_out, OP5, OP4, not_182_out, not_183_out);
  and and_33 (and_33_out, not_184_out, not_185_out, not_186_out, F13, not_187_out, not_188_out, OP5, OP4, not_189_out, not_190_out);
  and and_34 (and_34_out, not_191_out, not_192_out, not_193_out, F13, F12, not_194_out, OP5, OP4, not_195_out, not_196_out);
  and and_35 (and_35_out, F14, F13, not_197_out, not_198_out, not_199_out, OP4, not_200_out, not_201_out);
  and and_36 (and_36_out, F14, not_202_out, not_203_out, not_204_out, not_205_out, OP4, not_206_out, not_207_out);
  and and_37 (and_37_out, not_208_out, F13, not_209_out, not_210_out, not_211_out, OP4, not_212_out, not_213_out);
  and and_38 (and_38_out, not_214_out, not_215_out, F14, not_216_out, not_217_out, not_218_out, OP5, OP4, not_219_out, not_220_out);
  and and_39 (and_39_out, F14, not_221_out, not_222_out, OP6, OP5, not_223_out, not_224_out, not_225_out);
  or or_1 (S0, and_1_out, and_2_out, and_3_out, and_4_out, and_5_out, and_6_out, and_7_out, and_8_out, and_9_out, and_10_out, and_11_out);
  or or_2 (S1, and_12_out, and_13_out, and_14_out, and_15_out, and_16_out, and_17_out, and_18_out, and_19_out, and_20_out, and_21_out);
  or or_3 (S2, and_22_out, and_23_out, and_24_out, and_25_out, and_26_out, and_27_out, and_28_out, and_29_out, and_30_out, and_31_out);
  or or_4 (S3, and_32_out, and_33_out, and_34_out, and_35_out, and_36_out, and_37_out, and_38_out, and_39_out);
endmodule

// 控制信号生成
module \控制信号自动生成  (
  input  OP2,
  input  OP3,
  input  OP4,
  input  OP5,
  input  OP6,
  input  F12,
  input  F13,
  input  F14,
  input  F25,
  input  F30,
  output MemToReg,
  output MemWrite,
  output ALU_SRC,
  output RegWrite,
  output ecall,
  output Sw,
  output BEQ,
  output BNE,
  output JAL,
  output JALR,
  output AUIPC,
  output LH,
  output BLT,
  output csrrsi,
  output csrrci
);

  wire and_1_out, and_2_out, and_4_out, and_5_out, and_6_out, and_7_out, and_8_out, and_9_out, and_10_out,
       and_11_out, and_12_out, and_13_out, and_14_out, and_15_out, and_16_out, and_17_out, and_18_out,
       and_19_out, and_20_out, and_21_out, and_22_out, and_23_out, and_24_out, and_25_out, and_26_out,
       and_27_out, and_28_out, not_1_out, not_2_out, not_3_out, not_4_out, not_5_out, not_6_out, not_7_out,
       not_8_out, not_9_out, not_10_out, not_11_out, not_12_out, not_13_out, not_14_out, not_15_out,
       not_16_out, not_17_out, not_18_out, not_19_out, not_20_out, not_21_out, not_22_out, not_23_out,
       not_24_out, not_25_out, not_26_out, not_27_out, not_28_out, not_29_out, not_30_out, not_31_out,
       not_32_out, not_33_out, not_34_out, not_35_out, not_36_out, not_37_out, not_38_out, not_39_out,
       not_40_out, not_41_out, not_42_out, not_43_out, not_44_out, not_45_out, not_46_out, not_47_out,
       not_48_out, not_49_out, not_50_out, not_51_out, not_52_out, not_53_out, not_54_out, not_55_out,
       not_56_out, not_57_out, not_58_out, not_59_out, not_60_out, not_61_out, not_62_out, not_63_out,
       not_64_out, not_65_out, not_66_out, not_67_out, not_68_out, not_69_out, not_70_out, not_71_out,
       not_72_out, not_73_out, not_74_out, not_75_out, not_76_out, not_77_out, not_78_out, not_79_out,
       not_80_out, not_81_out, not_82_out, not_83_out, not_84_out, not_85_out, not_86_out, not_87_out,
       not_88_out, not_89_out, not_90_out, not_91_out, not_92_out, not_93_out, not_94_out, not_95_out,
       not_96_out, not_97_out, not_98_out, not_99_out, not_100_out, not_101_out, not_102_out, not_103_out,
       not_104_out, not_105_out, not_106_out, not_107_out, not_108_out, not_109_out, not_110_out,
       not_111_out, not_112_out, not_113_out, not_114_out, not_115_out, not_116_out, not_117_out,
       not_118_out, not_119_out, not_120_out, not_121_out, not_122_out, not_123_out, not_124_out,
       not_125_out, not_126_out, not_127_out, not_128_out, not_129_out, not_130_out, not_131_out,
       not_132_out, not_133_out, not_134_out, not_135_out, not_136_out, not_137_out, not_138_out,
       not_139_out, not_140_out, not_141_out, not_142_out, not_143_out, not_144_out, not_145_out,
       not_146_out, not_147_out, not_148_out, not_149_out, not_150_out, not_151_out, not_152_out,
       not_153_out, not_154_out, not_155_out, not_156_out, not_157_out, not_158_out, not_159_out,
       not_160_out, not_161_out, not_162_out, not_163_out, not_164_out, not_165_out, not_166_out,
       not_167_out, not_168_out, not_169_out, not_170_out, not_171_out, not_172_out, not_173_out,
       not_174_out, not_175_out, not_176_out, not_177_out, not_178_out, not_179_out, not_180_out,
       not_181_out, not_182_out, not_183_out, not_184_out, not_185_out, not_186_out, not_187_out,
       not_188_out, not_189_out, not_190_out, not_191_out, not_192_out, not_193_out, not_194_out,
       not_195_out, not_196_out, not_197_out;

  not not_1 (not_1_out, OP2);
  not not_2 (not_2_out, OP3);
  not not_3 (not_3_out, OP4);
  not not_4 (not_4_out, OP5);
  not not_5 (not_5_out, OP6);
  not not_6 (not_6_out, F12);
  not not_7 (not_7_out, F14);
  not not_8 (not_8_out, OP2);
  not not_9 (not_9_out, OP3);
  not not_10 (not_10_out, OP4);
  not not_11 (not_11_out, OP5);
  not not_12 (not_12_out, OP6);
  not not_13 (not_13_out, F13);
  not not_14 (not_14_out, F14);
  not not_15 (not_15_out, OP2);
  not not_16 (not_16_out, OP3);
  not not_17 (not_17_out, OP4);
  not not_18 (not_18_out, OP6);
  not not_19 (not_19_out, F12);
  not not_20 (not_20_out, F14);
  not not_21 (not_21_out, F14);
  not not_22 (not_22_out, F13);
  not not_23 (not_23_out, F12);
  not not_24 (not_24_out, OP6);
  not not_25 (not_25_out, OP5);
  not not_26 (not_26_out, OP3);
  not not_27 (not_27_out, OP2);
  not not_28 (not_28_out, OP6);
  not not_29 (not_29_out, OP5);
  not not_30 (not_30_out, OP3);
  not not_31 (not_31_out, OP2);
  not not_32 (not_32_out, F12);
  not not_33 (not_33_out, OP6);
  not not_34 (not_34_out, OP5);
  not not_35 (not_35_out, OP3);
  not not_36 (not_36_out, OP2);
  not not_37 (not_37_out, F13);
  not not_38 (not_38_out, F12);
  not not_39 (not_39_out, OP6);
  not not_40 (not_40_out, OP5);
  not not_41 (not_41_out, OP3);
  not not_42 (not_42_out, OP2);
  not not_43 (not_43_out, F14);
  not not_44 (not_44_out, F12);
  not not_45 (not_45_out, OP6);
  not not_46 (not_46_out, OP5);
  not not_47 (not_47_out, OP3);
  not not_48 (not_48_out, OP2);
  not not_49 (not_49_out, F30);
  not not_50 (not_50_out, F25);
  not not_51 (not_51_out, F14);
  not not_52 (not_52_out, F13);
  not not_53 (not_53_out, OP6);
  not not_54 (not_54_out, OP5);
  not not_55 (not_55_out, OP3);
  not not_56 (not_56_out, OP2);
  not not_57 (not_57_out, F30);
  not not_58 (not_58_out, F25);
  not not_59 (not_59_out, F13);
  not not_60 (not_60_out, OP6);
  not not_61 (not_61_out, OP5);
  not not_62 (not_62_out, OP3);
  not not_63 (not_63_out, OP2);
  not not_64 (not_64_out, F25);
  not not_65 (not_65_out, F13);
  not not_66 (not_66_out, OP6);
  not not_67 (not_67_out, OP5);
  not not_68 (not_68_out, OP3);
  not not_69 (not_69_out, OP2);
  not not_70 (not_70_out, F14);
  not not_71 (not_71_out, F12);
  not not_72 (not_72_out, OP6);
  not not_73 (not_73_out, OP5);
  not not_74 (not_74_out, OP4);
  not not_75 (not_75_out, OP3);
  not not_76 (not_76_out, OP2);
  not not_77 (not_77_out, F14);
  not not_78 (not_78_out, F12);
  not not_79 (not_79_out, OP6);
  not not_80 (not_80_out, OP4);
  not not_81 (not_81_out, OP3);
  not not_82 (not_82_out, OP2);
  not not_83 (not_83_out, OP4);
  not not_84 (not_84_out, OP6);
  not not_85 (not_85_out, OP5);
  not not_86 (not_86_out, OP3);
  not not_87 (not_87_out, F14);
  not not_88 (not_88_out, F13);
  not not_89 (not_89_out, OP6);
  not not_90 (not_90_out, OP5);
  not not_91 (not_91_out, OP4);
  not not_92 (not_92_out, OP3);
  not not_93 (not_93_out, OP2);
  not not_94 (not_94_out, OP2);
  not not_95 (not_95_out, OP3);
  not not_96 (not_96_out, OP5);
  not not_97 (not_97_out, OP6);
  not not_98 (not_98_out, F12);
  not not_99 (not_99_out, F14);
  not not_100 (not_100_out, OP2);
  not not_101 (not_101_out, OP3);
  not not_102 (not_102_out, OP4);
  not not_103 (not_103_out, OP5);
  not not_104 (not_104_out, OP6);
  not not_105 (not_105_out, F13);
  not not_106 (not_106_out, F14);
  not not_107 (not_107_out, OP2);
  not not_108 (not_108_out, OP3);
  not not_109 (not_109_out, OP6);
  not not_110 (not_110_out, F12);
  not not_111 (not_111_out, F13);
  not not_112 (not_112_out, F14);
  not not_113 (not_113_out, F25);
  not not_114 (not_114_out, OP2);
  not not_115 (not_115_out, OP3);
  not not_116 (not_116_out, OP6);
  not not_117 (not_117_out, F12);
  not not_118 (not_118_out, F25);
  not not_119 (not_119_out, F30);
  not not_120 (not_120_out, OP3);
  not not_121 (not_121_out, OP5);
  not not_122 (not_122_out, OP6);
  not not_123 (not_123_out, F12);
  not not_124 (not_124_out, OP3);
  not not_125 (not_125_out, OP5);
  not not_126 (not_126_out, OP6);
  not not_127 (not_127_out, F13);
  not not_128 (not_128_out, F25);
  not not_129 (not_129_out, F30);
  not not_130 (not_130_out, OP3);
  not not_131 (not_131_out, OP5);
  not not_132 (not_132_out, OP6);
  not not_133 (not_133_out, F25);
  not not_134 (not_134_out, OP3);
  not not_135 (not_135_out, OP5);
  not not_136 (not_136_out, OP6);
  not not_137 (not_137_out, OP2);
  not not_138 (not_138_out, OP3);
  not not_139 (not_139_out, OP6);
  not not_140 (not_140_out, F25);
  not not_141 (not_141_out, F30);
  not not_142 (not_142_out, OP4);
  not not_143 (not_143_out, F12);
  not not_144 (not_144_out, F13);
  not not_145 (not_145_out, F14);
  not not_146 (not_146_out, OP3);
  not not_147 (not_147_out, OP5);
  not not_148 (not_148_out, OP6);
  not not_149 (not_149_out, OP4);
  not not_150 (not_150_out, OP2);
  not not_151 (not_151_out, OP3);
  not not_152 (not_152_out, F12);
  not not_153 (not_153_out, F13);
  not not_154 (not_154_out, F14);
  not not_155 (not_155_out, OP2);
  not not_156 (not_156_out, OP3);
  not not_157 (not_157_out, OP4);
  not not_158 (not_158_out, OP6);
  not not_159 (not_159_out, F12);
  not not_160 (not_160_out, F14);
  not not_161 (not_161_out, OP2);
  not not_162 (not_162_out, OP3);
  not not_163 (not_163_out, OP4);
  not not_164 (not_164_out, F12);
  not not_165 (not_165_out, F13);
  not not_166 (not_166_out, F14);
  not not_167 (not_167_out, OP2);
  not not_168 (not_168_out, OP3);
  not not_169 (not_169_out, OP4);
  not not_170 (not_170_out, F13);
  not not_171 (not_171_out, F14);
  not not_172 (not_172_out, OP4);
  not not_173 (not_173_out, OP3);
  not not_174 (not_174_out, OP4);
  not not_175 (not_175_out, F12);
  not not_176 (not_176_out, F13);
  not not_177 (not_177_out, F14);
  not not_178 (not_178_out, OP3);
  not not_179 (not_179_out, OP5);
  not not_180 (not_180_out, OP6);
  not not_181 (not_181_out, OP2);
  not not_182 (not_182_out, OP3);
  not not_183 (not_183_out, OP4);
  not not_184 (not_184_out, OP5);
  not not_185 (not_185_out, OP6);
  not not_186 (not_186_out, F13);
  not not_187 (not_187_out, F14);
  not not_188 (not_188_out, OP2);
  not not_189 (not_189_out, OP3);
  not not_190 (not_190_out, OP4);
  not not_191 (not_191_out, F12);
  not not_192 (not_192_out, F13);
  not not_193 (not_193_out, OP2);
  not not_194 (not_194_out, OP3);
  not not_195 (not_195_out, F12);
  not not_196 (not_196_out, OP2);
  not not_197 (not_197_out, OP3);
  and and_1 (and_1_out, not_1_out, not_2_out, not_3_out, not_4_out, not_5_out, not_6_out, F13, not_7_out);
  and and_2 (and_2_out, not_8_out, not_9_out, not_10_out, not_11_out, not_12_out, F12, not_13_out, not_14_out);
  and and_3 (MemWrite, not_15_out, not_16_out, not_17_out, OP5, not_18_out, not_19_out, F13, not_20_out);
  and and_4 (and_4_out, not_21_out, not_22_out, not_23_out, not_24_out, not_25_out, OP4, not_26_out, not_27_out);
  and and_5 (and_5_out, F14, F13, F12, not_28_out, not_29_out, OP4, not_30_out, not_31_out);
  and and_6 (and_6_out, F14, F13, not_32_out, not_33_out, not_34_out, OP4, not_35_out, not_36_out);
  and and_7 (and_7_out, F14, not_37_out, not_38_out, not_39_out, not_40_out, OP4, not_41_out, not_42_out);
  and and_8 (and_8_out, not_43_out, F13, not_44_out, not_45_out, not_46_out, OP4, not_47_out, not_48_out);
  and and_9 (and_9_out, not_49_out, not_50_out, not_51_out, not_52_out, F12, not_53_out, not_54_out, OP4, not_55_out, not_56_out);
  and and_10 (and_10_out, not_57_out, not_58_out, F14, not_59_out, F12, not_60_out, not_61_out, OP4, not_62_out, not_63_out);
  and and_11 (and_11_out, F30, not_64_out, F14, not_65_out, F12, not_66_out, not_67_out, OP4, not_68_out, not_69_out);
  and and_12 (and_12_out, not_70_out, F13, not_71_out, not_72_out, not_73_out, not_74_out, not_75_out, not_76_out);
  and and_13 (and_13_out, not_77_out, F13, not_78_out, not_79_out, OP5, not_80_out, not_81_out, not_82_out);
  and and_14 (and_14_out, OP6, OP5, not_83_out, OP3, OP2);
  and and_15 (and_15_out, not_84_out, not_85_out, OP4, not_86_out, OP2);
  and and_16 (and_16_out, not_87_out, not_88_out, F12, not_89_out, not_90_out, not_91_out, not_92_out, not_93_out);
  and and_17 (and_17_out, not_94_out, not_95_out, not_96_out, not_97_out, not_98_out, F13, not_99_out);
  and and_18 (and_18_out, not_100_out, not_101_out, not_102_out, not_103_out, not_104_out, F12, not_105_out, not_106_out);
  and and_19 (and_19_out, not_107_out, not_108_out, OP4, not_109_out, not_110_out, not_111_out, not_112_out, not_113_out);
  and and_20 (and_20_out, not_114_out, not_115_out, OP4, not_116_out, not_117_out, not_118_out, not_119_out);
  and and_21 (and_21_out, not_120_out, OP4, not_121_out, not_122_out, not_123_out);
  and and_22 (and_22_out, not_124_out, OP4, not_125_out, not_126_out, not_127_out, not_128_out, not_129_out);
  and and_23 (and_23_out, not_130_out, OP4, not_131_out, not_132_out, F14, not_133_out);
  and and_24 (and_24_out, not_134_out, OP4, not_135_out, not_136_out, F13, F14);
  and and_25 (and_25_out, not_137_out, not_138_out, OP4, OP5, not_139_out, F13, not_140_out, not_141_out);
  and and_26 (and_26_out, OP2, not_142_out, OP5, OP6, not_143_out, not_144_out, not_145_out);
  and and_27 (and_27_out, OP2, not_146_out, OP4, not_147_out, not_148_out);
  and and_28 (and_28_out, OP2, OP3, not_149_out, OP5, OP6);
  and and_29 (ecall, not_150_out, not_151_out, OP4, OP5, OP6, not_152_out, not_153_out, not_154_out);
  and and_30 (Sw, not_155_out, not_156_out, not_157_out, OP5, not_158_out, not_159_out, F13, not_160_out);
  and and_31 (BEQ, not_161_out, not_162_out, not_163_out, OP5, OP6, not_164_out, not_165_out, not_166_out);
  and and_32 (BNE, not_167_out, not_168_out, not_169_out, OP5, OP6, F12, not_170_out, not_171_out);
  and and_33 (JAL, OP2, OP3, not_172_out, OP5, OP6);
  and and_34 (JALR, OP2, not_173_out, not_174_out, OP5, OP6, not_175_out, not_176_out, not_177_out);
  and and_35 (AUIPC, OP2, not_178_out, OP4, not_179_out, not_180_out);
  and and_36 (LH, not_181_out, not_182_out, not_183_out, not_184_out, not_185_out, F12, not_186_out, not_187_out);
  and and_37 (BLT, not_188_out, not_189_out, not_190_out, OP5, OP6, not_191_out, not_192_out, F14);
  and and_38 (csrrsi, not_193_out, not_194_out, OP4, OP5, OP6, not_195_out, F13, F14);
  and and_39 (csrrci, not_196_out, not_197_out, OP4, OP5, OP6, F12, F13, F14);
  or or_1 (MemToReg, and_1_out, and_2_out);
  or or_2 (ALU_SRC, and_4_out, and_5_out, and_6_out, and_7_out, and_8_out, and_9_out, and_10_out, and_11_out, and_12_out, and_13_out, and_14_out, and_15_out, and_16_out);
  or or_3 (RegWrite, and_17_out, and_18_out, and_19_out, and_20_out, and_21_out, and_22_out, and_23_out, and_24_out, and_25_out, and_26_out, and_27_out, and_28_out);
endmodule

// ALU
module ALU (
  input  [31:0] X,
  input  [31:0] Y,
  input  [3:0] AluOP,
  output out_4,
  output Equal,
  output out_6,
  output [31:0] Result,
  output [31:0] Result_2
);

  wire [0:0] comparator_1_lt, comparator_2_lt;
  wire [31:0] adder_1_out, AND_out, divider_1_out, divider_1_rem, multiplier_1_cout, multiplier_1_out,
       NOR_out, OR_out, shifter_1_out, shifter_2_out, shifter_3_out, subtractor_1_out, XOR_out;

  assign AND_out = X & Y;  // AND_Gate AND, 32 bits wide
  assign OR_out = X | Y;  // OR_Gate OR, 32 bits wide
  Shifter #(.width(32), .shift("ll")) shifter_1 (.in(X), .\dist (Y[4:0]), .out(shifter_1_out));
  Shifter #(.width(32), .shift("ar")) shifter_2 (.in(X), .\dist (Y[4:0]), .out(shifter_2_out));
  Shifter #(.width(32), .shift("lr")) shifter_3 (.in(X), .\dist (Y[4:0]), .out(shifter_3_out));
  Multiplier #(.width(32)) multiplier_1 (.a(X), .b(Y), .out(multiplier_1_out), .cout(multiplier_1_cout));  // open: cin
  Divider #(.width(32)) divider_1 (.a(X), .b(Y), .out(divider_1_out), .rem(divider_1_rem));  // open: upper
  Adder #(.width(32)) adder_1 (.a(X), .b(Y), .out(adder_1_out));  // open: cin, cout
  Subtractor #(.width(32)) subtractor_1 (.a(X), .b(Y), .out(subtractor_1_out));  // open: bin, bout
  assign XOR_out = X ^ Y;  // XOR_Gate XOR, 32 bits wide
  assign NOR_out = ~(X | Y);  // NOR_Gate NOR, 32 bits wide
  Comparator #(.width(32), .mode("twosComplement")) comparator_1 (
    .a(X), .b(Y), .eq(Equal), .lt(comparator_1_lt[0]));  // open: gt
  Comparator #(.width(32), .mode("unsigned")) comparator_2 (.a(X), .b(Y), .lt(comparator_2_lt[0]));  // open: gt, eq
  Multiplexer #(.select(4), .width(32), .disabled("Z"), .enable("false")) multiplexer_1 (
    .in0(shifter_1_out), .in1(shifter_2_out), .in2(shifter_3_out), .in3(multiplier_1_out),
    .in4(divider_1_out), .in5(adder_1_out), .in6(subtractor_1_out), .in7(AND_out), .in8(OR_out),
    .in9(XOR_out), .in10(NOR_out), .in11({{31{1'b0}}, comparator_1_lt[0]}),
    .in12({{31{1'b0}}, comparator_2_lt[0]}), .in13({32{1'b0}}), .in14({32{1'b0}}), .in15({32{1'b0}}),
    .out(Result), .sel(AluOP));
  Multiplexer #(.select(4), .width(32), .disabled("Z"), .enable("false")) multiplexer_2 (
    .in0({32{1'b0}}), .in1({32{1'b0}}), .in2({32{1'b0}}), .in3(multiplier_1_cout), .in4(divider_1_rem),
    .in5({32{1'b0}}), .in6({32{1'b0}}), .in7({32{1'b0}}), .in8({32{1'b0}}), .in9({32{1'b0}}),
    .in10({32{1'b0}}), .in11({32{1'b0}}), .in12({32{1'b0}}), .in13({32{1'b0}}), .in14({32{1'b0}}),
    .in15({32{1'b0}}), .out(Result_2), .sel(AluOP));
  Multiplexer #(.select(4), .width(1), .disabled("Z"), .enable("false")) multiplexer_3 (
    .in0(1'b0), .in1(1'b0), .in2(1'b0), .in3(1'b0), .in4(1'b0), .in5(1'b0), .in6(1'b0), .in7(1'b0),
    .in8(1'b0), .in9(1'b0), .in10(1'b0), .in11(comparator_1_lt[0]), .in12(comparator_2_lt[0]), .in13(1'b0),
    .in14(1'b0), .in15(1'b0), .out(out_6), .sel(AluOP));
  not not_1 (out_4, out_6);

  // Other names for the same wires on the sheet: Result2[31:0] = Result_2; S[3:0] = AluOP; tunnel = out_6;
  //   tunnel_t = out_4

  // Notes on the sheet:
  //   不要改变此引脚区域内容，也不要改变ALU封装形式
  //   输入引脚
  //   输出引脚
endmodule

module Regifile (
  input  [31:0] Din,
  input  Clk,
  input  WE,
  input  [4:0] R1_num,
  input  [4:0] W_num,
  input  [4:0] R2_num,
  output [31:0] R1,
  output [31:0] R2
);

  // RegisterFile registerfile_1: pin names not known; wires that end beside it: Din, Clk, WE, W_num, R1_num, R2_num, R1, R2
endmodule

module \理想流水线  (
  output RegWrite,
  output MemWrite,
  output [31:0] IF_PC,
  output [31:0] ID_PC,
  output [31:0] EX_PC,
  output [31:0] M_PC,
  output [31:0] WB_PC,
  output [31:0] RDin,
  output [31:0] MDin,
  output [31:0] LedData
);

  wire alu_1_equal, and_1_out, and_2_out, and_3_out, and_4_out, and_5_out, CLK, clock_1_out, comparator_1_eq,
       comparator_1_lt, comparator_2_eq, d_ff_1_q, EX_MEM_halt, EX_MEM_lh_2, EX_MEM_memtoreg_2,
       EX_MEM_regwrite_2, Go, halt, ID_EX_alusrcb_2, ID_EX_beq_2, ID_EX_blt_2, ID_EX_bne_2, ID_EX_ecall_2,
       ID_EX_jal_2, ID_EX_jalr_2, ID_EX_memtoreg_2, ID_EX_memwrite_2, ID_EX_regwrite_2, IR1, IR2, IR3,
       MEM_WB_halt_2, MEM_WB_memtoreg_2, nand_1_out, not_1_out, not_2_out, or_1_out, or_2_out, RST, tunnel,
       W1, W2, W3, WB_halt, \单周期硬布线控制器_1_alu_src , \单周期硬布线控制器_1_auipc , \单周期硬布线控制器_1_beq , \单周期硬布线控制器_1_blt ,
       \单周期硬布线控制器_1_bne , \单周期硬布线控制器_1_ecall , \单周期硬布线控制器_1_jal , \单周期硬布线控制器_1_jalr , \单周期硬布线控制器_1_lh ,
       \单周期硬布线控制器_1_memtoreg , \单周期硬布线控制器_1_memwrite , \单周期硬布线控制器_1_regwrite , \单周期硬布线控制器_1_sw ;
  wire [3:0] ID_EX_aluop_2, \单周期硬布线控制器_1_alu_op ;
  wire [4:0] EX_MEM_rd_2, EX_rd, ID_EX_rd_2, multiplexer_2_out, multiplexer_3_out;
  wire [12:0] CNT_num;
  wire [15:0] \LoadUse次数 , multiplexer_6_out, \总周期数 , \插入气泡数 , \无条件分支数 , \条件分支成功数 ;
  wire [31:0] adder_2_out, ALUResult, bit_extender_1_out, branch, EX_IR, EX_MEM_result_2, ID_EX_imm_2,
       ID_EX_r1_2, ID_EX_r2_2, ID_IR, IF_IR, immgen_1_imm, MEM_IR, MEM_WB_result_2, MEM_WB_writedata_2,
       multiplexer_1_out, multiplexer_4_out, multiplexer_7_out, PC_4, ram_1_data, regifile_1_r1,
       regifile_1_r2, shifter_1_out, WB_IR;

  Button \u_总复位  (.out(RST));
  Button _1 (.out(IR1));
  Button _2 (.out(IR2));
  Button _3 (.out(IR3));
  // Probe on \总周期数 
  // Probe on \总周期数 
  Button \u_继续运行  (.out(Go));
  LED #(.active("true")) led_1 (.in(W1));
  LED #(.active("true")) led_2 (.in(W2));
  LED #(.active("true")) led_3 (.in(W3));
  Hex_Digit_Display hex_digit_display_1 (.value(LedData[31:28]));  // open: dp
  // Probe on IF_PC[19:0]
  // RiscV_Probe riscv_probe_1: pin names not known; wires that end beside it: IF_IR
  Hex_Digit_Display hex_digit_display_2 (.value(LedData[23:20]));  // open: dp
  Hex_Digit_Display hex_digit_display_3 (.value(LedData[27:24]));  // open: dp
  // Probe on ID_PC[19:0]
  // RiscV_Probe riscv_probe_2: pin names not known; wires that end beside it: ID_IR
  Multiplexer #(.select(1), .width(32), .disabled("Z"), .enable("false")) multiplexer_1 (
    .in0(PC_4), .in1(branch), .out(multiplexer_1_out), .sel(or_2_out));
  Register #(.width(32), .trigger("rising"), .Select("low")) PC (
    .D(multiplexer_1_out), .en(not_1_out), .Q(IF_PC), .clk(CLK), .clr(RST));
  not not_1 (not_1_out, WB_halt);
  Hex_Digit_Display hex_digit_display_4 (.value(LedData[19:16]));  // open: dp
  Hex_Digit_Display hex_digit_display_5 (.value(LedData[15:12]));  // open: dp
  Hex_Digit_Display hex_digit_display_6 (.value(LedData[11:8]));  // open: dp
  Hex_Digit_Display hex_digit_display_7 (.value(LedData[7:4]));  // open: dp
  // Probe on EX_PC[19:0]
  // RiscV_Probe riscv_probe_3: pin names not known; wires that end beside it: EX_IR
  Adder #(.width(32)) adder_1 (.a(IF_PC), .b(32'h4), .out(PC_4));  // open: cin, cout
  Hex_Digit_Display hex_digit_display_8 (.value(LedData[3:0]));  // open: dp
  ROM #(.addrWidth(10), .dataWidth(32), .Select("high")) \u_指令存储器  (.addr(IF_PC[11:2]), .data(IF_IR));
  not not_2 (not_2_out, halt);
  Counter #(.width(16), .max('hffff), .ongoal("wrap"), .trigger("rising"), .behavior("new")) counter_1 (
    .count(not_2_out), .Q(\总周期数 ), .clk(CLK));  // open: load, D, carry, clr, preset, down
  // Probe on \总周期数 
  // Probe on M_PC[19:0]
  // RiscV_Probe riscv_probe_4: pin names not known; wires that end beside it: MEM_IR
  IF_ID IF_ID (
    .IR(IF_IR), .PC(IF_PC), .IR_2(ID_IR), .PC_2(ID_PC), .clk(CLK), .rst(RST));  // open: flush, en, pre, pre_2
  // Probe on \总周期数 
  // Probe on \无条件分支数 
  // Probe on \条件分支成功数 
  // Probe on \插入气泡数 
  // Probe on \LoadUse次数 
  // Probe on IF_PC[11:0]
  // Probe on WB_PC[19:0]
  // RiscV_Probe riscv_probe_5: pin names not known; wires that end beside it: WB_IR
  \单周期硬布线控制器  \u_单周期硬布线控制器_1  (
    .Funct({ID_IR[30], ID_IR[25], ID_IR[14:12]}), .OP(ID_IR[6:2]), .ALU_OP(\单周期硬布线控制器_1_alu_op ),
    .MemToReg(\单周期硬布线控制器_1_memtoreg ), .MemWrite(\单周期硬布线控制器_1_memwrite ), .ALU_SRC(\单周期硬布线控制器_1_alu_src ),
    .RegWrite(\单周期硬布线控制器_1_regwrite ), .ecall(\单周期硬布线控制器_1_ecall ), .Sw(\单周期硬布线控制器_1_sw ),
    .Jalr(\单周期硬布线控制器_1_jalr ), .Beq(\单周期硬布线控制器_1_beq ), .JAL(\单周期硬布线控制器_1_jal ), .Bne(\单周期硬布线控制器_1_bne ),
    .in_3(ID_IR[21]), .AUIPC(\单周期硬布线控制器_1_auipc ), .LH(\单周期硬布线控制器_1_lh ), .BLT(\单周期硬布线控制器_1_blt ));  // open: uret, csrrci, csrrsi
  Multiplexer #(.select(1), .width(5), .disabled("Z"), .enable("false")) multiplexer_2 (
    .in0(ID_IR[19:15]), .in1(5'b10001), .out(multiplexer_2_out), .sel(\单周期硬布线控制器_1_ecall ));
  Multiplexer #(.select(1), .width(5), .disabled("Z"), .enable("false")) multiplexer_3 (
    .in0(ID_IR[24:20]), .in1(5'b01010), .out(multiplexer_3_out), .sel(\单周期硬布线控制器_1_ecall ));
  // Probe on EX_PC[11:0]
  // Probe on ID_PC[11:0]
  or or_1 (or_1_out, \单周期硬布线控制器_1_blt , \单周期硬布线控制器_1_bne , \单周期硬布线控制器_1_beq );
  // Probe on M_PC[11:0]
  D_Flip_Flop #(.trigger("high"), .Pre_Clr_Positions("LEGACY"), .NegatePresetClear("false"), .enable("true"), .NewFFLayout("false")) d_ff_1 (.Q(d_ff_1_q));  // open: clk, D, Qn, preset, en, reset
  // Probe on 13'hd
  ImmGen immgen_1 (
    .Sw(\单周期硬布线控制器_1_sw ), .Auipc(\单周期硬布线控制器_1_auipc ), .B_Type(or_1_out), .jal(\单周期硬布线控制器_1_jal ),
    .IR(ID_IR), .Imm(immgen_1_imm));
  // Probe on WB_PC[11:0]
  Comparator #(.width(13), .mode("twosComplement")) comparator_1 (
    .a(CNT_num), .b(13'hd), .eq(comparator_1_eq), .lt(comparator_1_lt));  // open: gt
  Clock #(.highDuration(1), .lowDuration(1)) clock_1 (.out(clock_1_out));
  nand nand_1 (nand_1_out, d_ff_1_q, comparator_1_eq);
  Counter #(.width(13), .max('h1fff), .ongoal("stay"), .trigger("rising"), .behavior("old")) counter_2 (
    .count(comparator_1_lt), .Q(CNT_num), .clk(clock_1_out));  // open: load, D, carry, clr, preset
  or or_2 (or_2_out, and_3_out, and_1_out, and_2_out, ID_EX_jalr_2, ID_EX_jal_2);
  Regifile regifile_1 (
    .Din(RDin), .Clk(CLK), .R1(regifile_1_r1), .R2(regifile_1_r2), .WE(RegWrite), .W_num(EX_rd),
    .R1_num(multiplexer_2_out), .R2_num(multiplexer_3_out));
  assign CLK = nand_1_out ? clock_1_out : 1'bz;  // Controlled_Buffer controlled_buffer_1
  ID_EX ID_EX (
    .Beq(\单周期硬布线控制器_1_beq ), .Bne(\单周期硬布线控制器_1_bne ), .MemToReg(\单周期硬布线控制器_1_memtoreg ),
    .MemWrite(\单周期硬布线控制器_1_memwrite ), .AluSrcB(\单周期硬布线控制器_1_alu_src ), .RegWrite(\单周期硬布线控制器_1_regwrite ),
    .ecall(\单周期硬布线控制器_1_ecall ), .JAL(\单周期硬布线控制器_1_jal ), .Jalr(\单周期硬布线控制器_1_jalr ), .R1(regifile_1_r1),
    .R2(regifile_1_r2), .rd(ID_IR[11:7]), .PC(ID_PC), .IR(ID_IR), .Beq_2(ID_EX_beq_2), .Bne_2(ID_EX_bne_2),
    .MemToReg_2(ID_EX_memtoreg_2), .MemWrite_2(ID_EX_memwrite_2), .AluSrcB_2(ID_EX_alusrcb_2),
    .RegWrite_2(ID_EX_regwrite_2), .ecall_2(ID_EX_ecall_2), .JAL_2(ID_EX_jal_2), .Jalr_2(ID_EX_jalr_2),
    .R1_2(ID_EX_r1_2), .R2_2(ID_EX_r2_2), .rd_2(ID_EX_rd_2), .imm_2(ID_EX_imm_2), .PC_2(EX_PC), .IR_2(EX_IR),
    .clk(CLK), .rst(RST), .Lh(\单周期硬布线控制器_1_lh ), .Lh_2(\单周期硬布线控制器_1_lh ), .Auipc(\单周期硬布线控制器_1_auipc ),
    .Blt(\单周期硬布线控制器_1_blt ), .Blt_2(ID_EX_blt_2), .imm(immgen_1_imm), .AluOP(\单周期硬布线控制器_1_alu_op ),
    .AluOP_2(ID_EX_aluop_2));  // open: Auipc_2, flush, en, pre, pre_2
  Pull_Resistor #(.pull(1)) pull_resistor_1 (.node(CLK));
  and and_1 (and_1_out, ID_EX_bne_2, ~alu_1_equal);  // AND_Gate
  and and_2 (and_2_out, ID_EX_beq_2, alu_1_equal);
  Multiplexer #(.select(1), .width(32), .disabled("Z"), .enable("false")) multiplexer_4 (
    .in0(ID_EX_r2_2), .in1(ID_EX_imm_2), .out(multiplexer_4_out), .sel(ID_EX_alusrcb_2));
  and and_3 (and_3_out, ID_EX_blt_2, tunnel);
  ALU alu_1 (
    .X(ID_EX_r1_2), .Y(multiplexer_4_out), .AluOP(ID_EX_aluop_2), .Equal(alu_1_equal), .Result(ALUResult),
    .out_6(tunnel));  // open: Result_2, out_4
  Comparator #(.width(32), .mode("twosComplement")) comparator_2 (
    .a(ID_EX_r1_2), .b(32'h22), .eq(comparator_2_eq));  // open: gt, lt
  Shifter #(.width(32), .shift("ll")) shifter_1 (.in(ID_EX_imm_2), .\dist (5'b00001), .out(shifter_1_out));
  Adder #(.width(32)) adder_2 (.a(shifter_1_out), .b(EX_PC), .out(adder_2_out));  // open: cin, cout
  and and_4 (and_4_out, comparator_2_eq, ID_EX_ecall_2);
  Multiplexer #(.select(1), .width(32), .disabled("Z"), .enable("false")) multiplexer_5 (
    .in0(ALUResult), .in1(adder_2_out), .out(branch), .sel(ID_EX_jalr_2));
  and and_5 (and_5_out, ID_EX_ecall_2, ~comparator_2_eq);  // AND_Gate
  Register #(.width(32), .trigger("rising"), .Select("low")) register_1 (
    .D(ID_EX_r2_2), .en(and_4_out), .Q(LedData), .clk(CLK));  // open: clr
  EX_MEM EX_MEM (
    .MemToReg(ID_EX_memtoreg_2), .MemWrite(ID_EX_memwrite_2), .RegWrite(ID_EX_regwrite_2), .IR(EX_IR),
    .MemToReg_2(EX_MEM_memtoreg_2), .MemWrite_2(MemWrite), .RegWrite_2(EX_MEM_regwrite_2), .IR_2(MEM_IR),
    .PC(EX_PC), .PC_2(M_PC), .rst(RST), .clk(CLK), .Result(ALUResult), .Result_2(EX_MEM_result_2),
    .WriteData(ID_EX_r2_2), .WriteData_2(MDin), .lh(\单周期硬布线控制器_1_lh ), .lh_2(EX_MEM_lh_2), .rd(ID_EX_rd_2),
    .rd_2(EX_MEM_rd_2), .hait(and_5_out), .halt(EX_MEM_halt));  // open: en
  RAM #(.addrWidth(10), .dataWidth(32), .bus("separate"), .Select("high")) ram_1 (
    .addr(EX_MEM_result_2[11:2]), .din(MDin), .data(ram_1_data), .str(MemWrite), .sel(1'b1), .clk(CLK),
    .ld(1'b1), .clr(RST));
  assign bit_extender_1_out = {{16{multiplexer_6_out[15]}}, multiplexer_6_out};  // Bit_Extender bit_extender_1
  Multiplexer #(.select(1), .width(16), .disabled("Z"), .enable("false")) multiplexer_6 (
    .in0(ram_1_data[15:0]), .in1(ram_1_data[31:16]), .out(multiplexer_6_out), .sel(EX_MEM_result_2[1]));
  MEM_WB MEM_WB (
    .MemToReg(EX_MEM_memtoreg_2), .MemToReg_2(MEM_WB_memtoreg_2), .RegWrite(EX_MEM_regwrite_2),
    .RegWrite_2(RegWrite), .Result(EX_MEM_result_2), .Result_2(MEM_WB_result_2),
    .WriteData(multiplexer_7_out), .WriteData_2(MEM_WB_writedata_2), .rd_2(EX_rd), .IR(MEM_IR), .IR_2(WB_IR),
    .PC(M_PC), .PC_2(WB_PC), .rst(RST), .clk(CLK), .rd(EX_MEM_rd_2), .halt_2(MEM_WB_halt_2),
    .halt(EX_MEM_halt));  // open: en
  Multiplexer #(.select(1), .width(32), .disabled("Z"), .enable("false")) multiplexer_7 (
    .in0(ram_1_data), .in1(bit_extender_1_out), .out(multiplexer_7_out), .sel(EX_MEM_lh_2));
  and and_6 (WB_halt, ~Go, MEM_WB_halt_2);  // AND_Gate
  Multiplexer #(.select(1), .width(32), .disabled("Z"), .enable("false")) multiplexer_8 (
    .in0(MEM_WB_result_2), .in1(MEM_WB_writedata_2), .out(RDin), .sel(MEM_WB_memtoreg_2));

  // Other names for the same wires on the sheet: MEM_PC[31:0] = M_PC

  // Notes on the sheet:
  //   中断源
  //   时空图监测，可删除
  //   中断等待指示
  //   数码管输出
  //   IF阶段
  //   contents of 指令存储器 (hex, n*v repeats v):
  //   100493 100006f 100493 200913 300993 100006f 100493 200913 300993 100006f 100493 200913 300993
  //   100006f 100493 200913 300993 408000ef 100413 100493 1f49493 900533 2200893 73 24d493 48463 fedff06f
  //   900533 2200893 73 100493 249493 900533 2200893 73 48463 fedff06f 100493 1f49493 900533 2200893 73
  //   4034d493 900533 2200893 73 4044d493 900533 2200893 73 4044d493 900533 2200893 73 4044d493 900533
  //   2200893 73 4044d493 900533 2200893 73 4044d493 900533 2200893 73 4044d493 900533 2200893 73 4044d493
  //   900533 2200893 73 100413 1f41993 41f9d993 433 c00913 300b13 140413 f47413 800293 100313 499993
  //   89e9b3 1300533 2200893 73 406282b3 fe0294e3 140413 f00f93 1f47433 1c41413 800293 100313 49d993
  //   89e9b3 1300533 2200893 73 406282b3 fe0294e3 1c45413 406b0b33 b0463 f95ff06f 2b3 fff2c293 829293
  //   ff2e293 500533 2200893 73 fff00413 493 84a023 140413 448493 84a023 140413 448493 84a023 140413
  //   448493 84a023 140413 448493 84a023 140413 448493 84a023 140413 448493 84a023 140413 448493 84a023
  //   140413 448493 84a023 140413 448493 84a023 140413 448493 84a023 140413 448493 84a023 140413 448493
  //   84a023 140413 448493 84a023 140413 448493 84a023 140413 448493 84a023 140413 448493 140413 433
  //   3c00493 42983 4aa03 149a2b3 28663 134a023 1442023 ffc48493 fe9412e3 800533 2200893 73 440413 3c00493
  //   fc9416e3 a00893 73 fff00293 7700493 849493 7748493 900533 2200893 73 1000e13 54c4b3 900533 2200893
  //   73 fffe0e13 fe0e16e3 a00893 73 13 430497 900533 2200893 73 430497 900533 2200893 73 430497 900533
  //   2200893 73 430497 900533 2200893 73 430497 900533 2200893 73 430497 900533 2200893 73 430497 900533
  //   2200893 73 430497 900533 2200893 73 a00893 73 313 1000e13 8400493 849493 8348493 400913 891913
  //   490913 849493 8248493 849493 8148493 891913 490913 891913 490913 932023 12484b3 430313 fffe0e13
  //   fe0e18e3 2000e13 313 31483 900533 2200893 73 230313 fffe0e13 fe0e14e3 a00893 73 ff100493 900533
  //   2200893 73 148493 fe04c8e3 a00893 73 413 140413 800533 2200893 73 240413 800533 2200893 73 340413
  //   800533 2200893 73 440413 800533 2200893 73 540413 800533 2200893 73 640413 800533 2200893 73 740413
  //   800533 2200893 73 840413 800533 2200893 2200893 73 8067
  //   rs1
  //   rs2
  //   rd
  //   控制位
  //   流水调试日志用
  //   暂停节拍，不能为0
  //   ID阶段
  //   戳工具置1进入计数暂停模式，ctrl+k时钟自动运行到对应节拍暂停
  //   ctrl+k关闭时钟连续运行，将控制位置零，进入单步调试模式调试
  //   用这个时钟源需要去掉电路中的其他时钟源
  //   可计数暂停的时钟源
  //   EX阶段
  //   为方便自动评测，需要输出流水线各段保存的PC值，注意是PC不是PC+4，另外ID段寄存器写入信息，Mem段内存写入信息也要输出
  //   数据存储器
  //   MEM阶段
endmodule

module \气泡流水线  (
  output RegWrite,
  output MemWrite,
  output [31:0] IF_PC,
  output [31:0] ID_PC,
  output [31:0] EX_PC,
  output [31:0] M_PC,
  output [31:0] WB_PC,
  output [31:0] RDin,
  output [31:0] MDin,
  output [31:0] LedData
);

  wire alu_1_equal, alu_1_out_6, and_1_out, and_2_out, and_3_out, and_4_out, and_5_out, CLK, clock_1_out,
       comparator_1_eq, comparator_1_lt, comparator_2_eq, d_ff_1_q, EX_MEM_halt, EX_MEM_lh_2,
       EX_MEM_memtoreg_2, EX_MEM_regwrite_2, Go, ID_EX_alusrcb_2, ID_EX_auipc_2, ID_EX_beq_2, ID_EX_blt_2,
       ID_EX_bne_2, ID_EX_ecall_2, ID_EX_jal_2, ID_EX_jalr_2, ID_EX_lh_2, ID_EX_memtoreg_2, ID_EX_memwrite_2,
       ID_EX_regwrite_2, IR1, IR2, IR3, MEM_WB_halt_2, MEM_WB_memtoreg_2, nand_1_out, not_1_out, not_2_out,
       not_3_out, not_4_out, or_1_out, or_2_out, or_3_out, or_4_out, or_5_out, or_6_out, or_7_out, or_8_out,
       RST, stall, W1, W2, W3, WB_halt, \单周期硬布线控制器_1_alu_src , \单周期硬布线控制器_1_auipc , \单周期硬布线控制器_1_beq ,
       \单周期硬布线控制器_1_blt , \单周期硬布线控制器_1_bne , \单周期硬布线控制器_1_ecall , \单周期硬布线控制器_1_jal , \单周期硬布线控制器_1_jalr ,
       \单周期硬布线控制器_1_lh , \单周期硬布线控制器_1_memtoreg , \单周期硬布线控制器_1_memwrite , \单周期硬布线控制器_1_regwrite ,
       \单周期硬布线控制器_1_sw ;
  wire [3:0] ID_EX_aluop_2, \单周期硬布线控制器_1_alu_op ;
  wire [4:0] EX_MEM_rd_2, ID_EX_rd_2, multiplexer_2_out, multiplexer_3_out, WB_rd;
  wire [12:0] CNT_num;
  wire [15:0] \LoadUse次数 , multiplexer_8_out, \总周期数 , \插入气泡数 , \无条件分支数 , \条件分支成功数 ;
  wire [31:0] adder_2_out, adder_3_out, alu_1_result, bit_extender_1_out, branch, EX_IR, EX_MEM_result_2,
       ID_EX_imm_2, ID_EX_r1_2, ID_EX_r2_2, ID_IR, IF_IR, immgen_1_imm, MEM_IR, MEM_WB_result_2,
       MEM_WB_writedata_2, multiplexer_1_out, multiplexer_4_out, multiplexer_5_out, multiplexer_7_out,
       multiplexer_9_out, PC_4, ram_1_data, regifile_1_r1, regifile_1_r2, shifter_1_out, WB_IR;

  Button \u_总复位  (.out(RST));
  Button _1 (.out(IR1));
  Button _2 (.out(IR2));
  Button _3 (.out(IR3));
  // Probe on \总周期数 
  // Probe on \总周期数 
  Button \u_继续运行  (.out(Go));
  LED #(.active("true")) led_1 (.in(W1));
  LED #(.active("true")) led_2 (.in(W2));
  LED #(.active("true")) led_3 (.in(W3));
  Hex_Digit_Display hex_digit_display_1 (.value(LedData[31:28]));  // open: dp
  // Probe on IF_PC[19:0]
  // RiscV_Probe riscv_probe_1: pin names not known; wires that end beside it: IF_IR
  Hex_Digit_Display hex_digit_display_2 (.value(LedData[23:20]));  // open: dp
  Hex_Digit_Display hex_digit_display_3 (.value(LedData[27:24]));  // open: dp
  // Probe on ID_PC[19:0]
  // RiscV_Probe riscv_probe_2: pin names not known; wires that end beside it: ID_IR
  or or_1 (or_1_out, WB_halt, stall);
  not not_1 (not_1_out, or_1_out);
  Multiplexer #(.select(1), .width(32), .disabled("Z"), .enable("false")) multiplexer_1 (
    .in0(PC_4), .in1(branch), .out(multiplexer_1_out), .sel(or_4_out));
  Register #(.width(32), .trigger("rising"), .Select("low")) PC (
    .D(multiplexer_1_out), .en(not_1_out), .Q(IF_PC), .clk(CLK), .clr(RST));
  Hex_Digit_Display hex_digit_display_4 (.value(LedData[15:12]));  // open: dp
  Hex_Digit_Display hex_digit_display_5 (.value(LedData[19:16]));  // open: dp
  Counter #(.width(16), .max('hffff), .ongoal("wrap"), .trigger("rising"), .behavior("new")) counter_1 (
    .Q(\插入气泡数 ), .clk(stall));  // open: load, D, count, carry, clr, preset, down
  not not_2 (not_2_out, WB_halt);
  Hex_Digit_Display hex_digit_display_6 (.value(LedData[11:8]));  // open: dp
  Hex_Digit_Display hex_digit_display_7 (.value(LedData[7:4]));  // open: dp
  // Probe on EX_PC[19:0]
  // RiscV_Probe riscv_probe_3: pin names not known; wires that end beside it: EX_IR
  Adder #(.width(32)) adder_1 (.a(IF_PC), .b(32'h4), .out(PC_4));  // open: cin, cout
  Counter #(.width(16), .max('hffff), .ongoal("wrap"), .trigger("rising"), .behavior("new")) counter_2 (
    .count(not_2_out), .Q(\总周期数 ), .clk(CLK));  // open: load, D, carry, clr, preset, down
  Hex_Digit_Display hex_digit_display_8 (.value(LedData[3:0]));  // open: dp
  ROM #(.addrWidth(10), .dataWidth(32), .Select("high")) \u_指令存储器  (.addr(IF_PC[11:2]), .data(IF_IR));
  // Probe on \总周期数 
  // Probe on M_PC[19:0]
  // RiscV_Probe riscv_probe_4: pin names not known; wires that end beside it: MEM_IR
  IF_ID IF_ID (
    .IR(IF_IR), .PC(IF_PC), .IR_2(ID_IR), .PC_2(ID_PC), .clk(CLK), .rst(RST), .flush(or_4_out), .en(not_3_out));  // open: pre, pre_2
  or or_2 (or_2_out, stall, WB_halt);
  not not_3 (not_3_out, or_2_out);
  // Probe on \总周期数 
  // Probe on \无条件分支数 
  // Probe on \条件分支成功数 
  // Probe on \插入气泡数 
  // Probe on \LoadUse次数 
  // Probe on IF_PC[11:0]
  // Probe on WB_PC[19:0]
  // RiscV_Probe riscv_probe_5: pin names not known; wires that end beside it: WB_IR
  \单周期硬布线控制器  \u_单周期硬布线控制器_1  (
    .Funct({ID_IR[30], ID_IR[25], ID_IR[14:12]}), .OP(ID_IR[6:2]), .ALU_OP(\单周期硬布线控制器_1_alu_op ),
    .MemToReg(\单周期硬布线控制器_1_memtoreg ), .MemWrite(\单周期硬布线控制器_1_memwrite ), .ALU_SRC(\单周期硬布线控制器_1_alu_src ),
    .RegWrite(\单周期硬布线控制器_1_regwrite ), .ecall(\单周期硬布线控制器_1_ecall ), .Sw(\单周期硬布线控制器_1_sw ),
    .Jalr(\单周期硬布线控制器_1_jalr ), .Beq(\单周期硬布线控制器_1_beq ), .JAL(\单周期硬布线控制器_1_jal ), .Bne(\单周期硬布线控制器_1_bne ),
    .in_3(ID_IR[21]), .AUIPC(\单周期硬布线控制器_1_auipc ), .LH(\单周期硬布线控制器_1_lh ), .BLT(\单周期硬布线控制器_1_blt ));  // open: uret, csrrci, csrrsi
  Multiplexer #(.select(1), .width(5), .disabled("Z"), .enable("false")) multiplexer_2 (
    .in0(ID_IR[19:15]), .in1(5'b10001), .out(multiplexer_2_out), .sel(\单周期硬布线控制器_1_ecall ));
  Multiplexer #(.select(1), .width(5), .disabled("Z"), .enable("false")) multiplexer_3 (
    .in0(ID_IR[24:20]), .in1(5'b01010), .out(multiplexer_3_out), .sel(\单周期硬布线控制器_1_ecall ));
  // Probe on ID_PC[11:0]
  // Probe on EX_PC[11:0]
  or or_3 (or_3_out, \单周期硬布线控制器_1_blt , \单周期硬布线控制器_1_bne , \单周期硬布线控制器_1_beq );
  // Probe on M_PC[11:0]
  D_Flip_Flop #(.trigger("high"), .Pre_Clr_Positions("LEGACY"), .NegatePresetClear("false"), .enable("true"), .NewFFLayout("false")) d_ff_1 (.Q(d_ff_1_q));  // open: clk, D, Qn, preset, en, reset
  // Probe on 13'h10
  \气泡处理  \u_气泡处理_1  (
    .stall(stall), .IR(ID_IR), .rs1(multiplexer_2_out), .rs2(multiplexer_3_out), .EX_rd(ID_EX_rd_2),
    .EX_RegWrite(ID_EX_regwrite_2), .MEM_rd(EX_MEM_rd_2), .MEM_RegWrite(EX_MEM_regwrite_2));
  ImmGen immgen_1 (
    .Sw(\单周期硬布线控制器_1_sw ), .Auipc(\单周期硬布线控制器_1_auipc ), .B_Type(or_3_out), .jal(\单周期硬布线控制器_1_jal ),
    .IR(ID_IR), .Imm(immgen_1_imm));
  // Probe on WB_PC[11:0]
  Comparator #(.width(13), .mode("twosComplement")) comparator_1 (
    .a(CNT_num), .b(13'h10), .eq(comparator_1_eq), .lt(comparator_1_lt));  // open: gt
  Clock #(.highDuration(1), .lowDuration(1)) clock_1 (.out(clock_1_out));
  not not_4 (not_4_out, WB_halt);
  nand nand_1 (nand_1_out, d_ff_1_q, comparator_1_eq);
  Counter #(.width(13), .max('h1fff), .ongoal("stay"), .trigger("rising"), .behavior("old")) counter_3 (
    .count(comparator_1_lt), .Q(CNT_num), .clk(clock_1_out));  // open: load, D, carry, clr, preset
  Regifile regifile_1 (
    .Din(RDin), .Clk(CLK), .R1(regifile_1_r1), .R2(regifile_1_r2), .WE(RegWrite), .W_num(WB_rd),
    .R1_num(multiplexer_2_out), .R2_num(multiplexer_3_out));
  assign CLK = nand_1_out ? clock_1_out : 1'bz;  // Controlled_Buffer controlled_buffer_1
  or or_4 (or_4_out, or_6_out, or_7_out);
  or or_5 (or_5_out, stall, or_4_out);
  ID_EX ID_EX (
    .Beq(\单周期硬布线控制器_1_beq ), .Bne(\单周期硬布线控制器_1_bne ), .MemToReg(\单周期硬布线控制器_1_memtoreg ),
    .MemWrite(\单周期硬布线控制器_1_memwrite ), .AluSrcB(\单周期硬布线控制器_1_alu_src ), .RegWrite(\单周期硬布线控制器_1_regwrite ),
    .ecall(\单周期硬布线控制器_1_ecall ), .JAL(\单周期硬布线控制器_1_jal ), .Jalr(\单周期硬布线控制器_1_jalr ), .R1(regifile_1_r1),
    .R2(regifile_1_r2), .rd(ID_IR[11:7]), .PC(ID_PC), .IR(ID_IR), .Beq_2(ID_EX_beq_2), .Bne_2(ID_EX_bne_2),
    .MemToReg_2(ID_EX_memtoreg_2), .MemWrite_2(ID_EX_memwrite_2), .AluSrcB_2(ID_EX_alusrcb_2),
    .RegWrite_2(ID_EX_regwrite_2), .ecall_2(ID_EX_ecall_2), .JAL_2(ID_EX_jal_2), .Jalr_2(ID_EX_jalr_2),
    .R1_2(ID_EX_r1_2), .R2_2(ID_EX_r2_2), .rd_2(ID_EX_rd_2), .imm_2(ID_EX_imm_2), .PC_2(EX_PC), .IR_2(EX_IR),
    .clk(CLK), .rst(RST), .Lh(\单周期硬布线控制器_1_lh ), .Lh_2(ID_EX_lh_2), .Auipc(\单周期硬布线控制器_1_auipc ),
    .Auipc_2(ID_EX_auipc_2), .Blt(\单周期硬布线控制器_1_blt ), .Blt_2(ID_EX_blt_2), .imm(immgen_1_imm),
    .AluOP(\单周期硬布线控制器_1_alu_op ), .AluOP_2(ID_EX_aluop_2), .flush(or_5_out), .en(not_4_out));  // open: pre, pre_2
  Pull_Resistor #(.pull(1)) pull_resistor_1 (.node(CLK));
  Counter #(.width(16), .max('hffff), .ongoal("wrap"), .trigger("rising"), .behavior("new")) counter_4 (
    .Q(\条件分支成功数 ), .clk(or_6_out));  // open: load, D, count, carry, clr, preset, down
  Counter #(.width(16), .max('hffff), .ongoal("wrap"), .trigger("rising"), .behavior("new")) counter_5 (
    .Q(\无条件分支数 ), .clk(or_7_out));  // open: load, D, count, carry, clr, preset, down
  or or_6 (or_6_out, and_4_out, and_2_out, and_1_out);
  or or_7 (or_7_out, ID_EX_jalr_2, ID_EX_jal_2);
  Multiplexer #(.select(1), .width(32), .disabled("Z"), .enable("false")) multiplexer_4 (
    .in0(ID_EX_r2_2), .in1(ID_EX_imm_2), .out(multiplexer_4_out), .sel(ID_EX_alusrcb_2));
  and and_1 (and_1_out, ID_EX_beq_2, alu_1_equal);
  and and_2 (and_2_out, ID_EX_bne_2, ~alu_1_equal);  // AND_Gate
  Multiplexer #(.select(1), .width(32), .disabled("Z"), .enable("false")) multiplexer_5 (
    .in0(ID_EX_r1_2), .in1(EX_PC), .out(multiplexer_5_out), .sel(ID_EX_auipc_2));
  ALU alu_1 (
    .X(multiplexer_5_out), .Y(multiplexer_4_out), .AluOP(ID_EX_aluop_2), .Equal(alu_1_equal),
    .Result(alu_1_result), .out_6(alu_1_out_6));  // open: Result_2, out_4
  Shifter #(.width(32), .shift("ll")) shifter_1 (.in(ID_EX_imm_2), .\dist (5'b00001), .out(shifter_1_out));
  Comparator #(.width(32), .mode("twosComplement")) comparator_2 (
    .a(ID_EX_r1_2), .b(32'h22), .eq(comparator_2_eq));  // open: gt, lt
  and and_3 (and_3_out, comparator_2_eq, ID_EX_ecall_2);
  and and_4 (and_4_out, ID_EX_blt_2, alu_1_out_6);
  Adder #(.width(32)) adder_2 (.a(shifter_1_out), .b(EX_PC), .out(adder_2_out));  // open: cin, cout
  Multiplexer #(.select(1), .width(32), .disabled("Z"), .enable("false")) multiplexer_6 (
    .in0(adder_2_out), .in1(alu_1_result), .out(branch), .sel(ID_EX_jalr_2));
  and and_5 (and_5_out, ID_EX_ecall_2, ~comparator_2_eq);  // AND_Gate
  Adder #(.width(32)) adder_3 (.a(32'h4), .b(EX_PC), .out(adder_3_out));  // open: cin, cout
  Register #(.width(32), .trigger("rising"), .Select("low")) register_1 (
    .D(ID_EX_r2_2), .en(and_3_out), .Q(LedData), .clk(CLK));  // open: clr
  or or_8 (or_8_out, ID_EX_jalr_2, ID_EX_jal_2);
  EX_MEM EX_MEM (
    .MemToReg(ID_EX_memtoreg_2), .MemWrite(ID_EX_memwrite_2), .RegWrite(ID_EX_regwrite_2), .IR(EX_IR),
    .MemToReg_2(EX_MEM_memtoreg_2), .MemWrite_2(MemWrite), .RegWrite_2(EX_MEM_regwrite_2), .IR_2(MEM_IR),
    .PC(EX_PC), .PC_2(M_PC), .rst(RST), .clk(CLK), .Result(multiplexer_7_out), .Result_2(EX_MEM_result_2),
    .WriteData(ID_EX_r2_2), .WriteData_2(MDin), .lh(ID_EX_lh_2), .lh_2(EX_MEM_lh_2), .rd(ID_EX_rd_2),
    .rd_2(EX_MEM_rd_2), .en(not_4_out), .hait(and_5_out), .halt(EX_MEM_halt));
  Multiplexer #(.select(1), .width(32), .disabled("Z"), .enable("false")) multiplexer_7 (
    .in0(alu_1_result), .in1(adder_3_out), .out(multiplexer_7_out), .sel(or_8_out));
  RAM #(.addrWidth(10), .dataWidth(32), .bus("separate"), .Select("high")) ram_1 (
    .addr(EX_MEM_result_2[11:2]), .din(MDin), .data(ram_1_data), .str(MemWrite), .sel(1'b1), .clk(CLK),
    .ld(1'b1), .clr(RST));
  Multiplexer #(.select(1), .width(16), .disabled("Z"), .enable("false")) multiplexer_8 (
    .in0(ram_1_data[15:0]), .in1(ram_1_data[31:16]), .out(multiplexer_8_out), .sel(EX_MEM_result_2[1]));
  assign bit_extender_1_out = {{16{multiplexer_8_out[15]}}, multiplexer_8_out};  // Bit_Extender bit_extender_1
  MEM_WB MEM_WB (
    .MemToReg(EX_MEM_memtoreg_2), .MemToReg_2(MEM_WB_memtoreg_2), .RegWrite(EX_MEM_regwrite_2),
    .RegWrite_2(RegWrite), .Result(EX_MEM_result_2), .Result_2(MEM_WB_result_2),
    .WriteData(multiplexer_9_out), .WriteData_2(MEM_WB_writedata_2), .rd_2(WB_rd), .IR(MEM_IR), .IR_2(WB_IR),
    .PC(M_PC), .PC_2(WB_PC), .rst(RST), .clk(CLK), .rd(EX_MEM_rd_2), .en(not_4_out), .halt_2(MEM_WB_halt_2),
    .halt(EX_MEM_halt));
  Multiplexer #(.select(1), .width(32), .disabled("Z"), .enable("false")) multiplexer_9 (
    .in0(ram_1_data), .in1(bit_extender_1_out), .out(multiplexer_9_out), .sel(EX_MEM_lh_2));
  and and_6 (WB_halt, ~Go, MEM_WB_halt_2);  // AND_Gate
  Multiplexer #(.select(1), .width(32), .disabled("Z"), .enable("false")) multiplexer_10 (
    .in0(MEM_WB_result_2), .in1(MEM_WB_writedata_2), .out(RDin), .sel(MEM_WB_memtoreg_2));

  // Other names for the same wires on the sheet: MEM_PC[31:0] = M_PC

  // Notes on the sheet:
  //   中断源
  //   时空图监测，可删除
  //   中断等待指示
  //   数码管输出
  //   IF阶段
  //   contents of 指令存储器 (hex, n*v repeats v):
  //   100493 100006f 100493 200913 300993 100006f 100493 200913 300993 100006f 100493 200913 300993
  //   100006f 100493 200913 300993 408000ef 100413 100493 1f49493 900533 2200893 73 24d493 48463 fedff06f
  //   900533 2200893 73 100493 249493 900533 2200893 73 48463 fedff06f 100493 1f49493 900533 2200893 73
  //   4034d493 900533 2200893 73 4044d493 900533 2200893 73 4044d493 900533 2200893 73 4044d493 900533
  //   2200893 73 4044d493 900533 2200893 73 4044d493 900533 2200893 73 4044d493 900533 2200893 73 4044d493
  //   900533 2200893 73 100413 1f41993 41f9d993 433 c00913 300b13 140413 f47413 800293 100313 499993
  //   89e9b3 1300533 2200893 73 406282b3 fe0294e3 140413 f00f93 1f47433 1c41413 800293 100313 49d993
  //   89e9b3 1300533 2200893 73 406282b3 fe0294e3 1c45413 406b0b33 b0463 f95ff06f 2b3 fff2c293 829293
  //   ff2e293 500533 2200893 73 fff00413 493 84a023 140413 448493 84a023 140413 448493 84a023 140413
  //   448493 84a023 140413 448493 84a023 140413 448493 84a023 140413 448493 84a023 140413 448493 84a023
  //   140413 448493 84a023 140413 448493 84a023 140413 448493 84a023 140413 448493 84a023 140413 448493
  //   84a023 140413 448493 84a023 140413 448493 84a023 140413 448493 84a023 140413 448493 140413 433
  //   3c00493 42983 4aa03 149a2b3 28663 134a023 1442023 ffc48493 fe9412e3 800533 2200893 73 440413 3c00493
  //   fc9416e3 a00893 73 fff00293 7700493 849493 7748493 900533 2200893 73 1000e13 54c4b3 900533 2200893
  //   73 fffe0e13 fe0e16e3 a00893 73 13 430497 900533 2200893 73 430497 900533 2200893 73 430497 900533
  //   2200893 73 430497 900533 2200893 73 430497 900533 2200893 73 430497 900533 2200893 73 430497 900533
  //   2200893 73 430497 900533 2200893 73 a00893 73 313 1000e13 8400493 849493 8348493 400913 891913
  //   490913 849493 8248493 849493 8148493 891913 490913 891913 490913 932023 12484b3 430313 fffe0e13
  //   fe0e18e3 2000e13 313 31483 900533 2200893 73 230313 fffe0e13 fe0e14e3 a00893 73 ff100493 900533
  //   2200893 73 148493 fe04c8e3 a00893 73 413 140413 800533 2200893 73 240413 800533 2200893 73 340413
  //   800533 2200893 73 440413 800533 2200893 73 540413 800533 2200893 73 640413 800533 2200893 73 740413
  //   800533 2200893 73 840413 800533 2200893 2200893 73 8067
  //   rs1
  //   rs2
  //   rd
  //   控制位
  //   ID阶段
  //   流水调试日志用
  //   暂停节拍，不能为0
  //   戳工具置1进入计数暂停模式，ctrl+k时钟自动运行到对应节拍暂停
  //   ctrl+k关闭时钟连续运行，将控制位置零，进入单步调试模式调试
  //   可计数暂停的时钟源
  //   EX阶段
  //   为方便自动评测，需要输出流水线各段保存的PC值，注意是PC不是PC+4，另外ID段寄存器写入信息，Mem段内存写入信息也要输出
  //   数据存储器
  //   MEM阶段
endmodule

module \重定向流水线  (
  output RegWrite,
  output MemWrite,
  output [31:0] IF_PC,
  output [31:0] ID_PC,
  output [31:0] EX_PC,
  output [31:0] M_PC,
  output [31:0] WB_PC,
  output [31:0] RDin,
  output [31:0] MDin,
  output [31:0] LedData
);

  wire alu_1_equal, alu_1_out_6, and_1_out, and_2_out, and_3_out, and_4_out, and_5_out, and_6_out, Branch,
       BranchTaken, CLK, clock_1_out, comparator_1_eq, comparator_1_lt, comparator_2_eq, d_ff_1_q,
       EX_MEM_halt, EX_MEM_lh_2, EX_MEM_memtoreg_2, EX_MEM_regwrite_2, Go, \id_ex_重定向_1_alusrcb_2 ,
       \id_ex_重定向_1_auipc_2 , \id_ex_重定向_1_beq_2 , \id_ex_重定向_1_blt_2 , \id_ex_重定向_1_bne_2 ,
       \id_ex_重定向_1_ecall_2 , \id_ex_重定向_1_jal_2 , \id_ex_重定向_1_jalr_2 , \id_ex_重定向_1_lh_2 ,
       \id_ex_重定向_1_memtoreg_2 , \id_ex_重定向_1_memwrite_2 , \id_ex_重定向_1_regwrite_2 , IR1, IR2, IR3, Jmp,
       LoadUse, MEM_WB_halt_2, MEM_WB_memtoreg_2, nand_1_out, not_1_out, not_2_out, not_3_out, or_1_out,
       or_2_out, or_3_out, or_5_out, or_8_out, or_9_out, RST, stall, W1, W2, W3, WB_halt,
       \单周期硬布线控制器_1_alu_src , \单周期硬布线控制器_1_auipc , \单周期硬布线控制器_1_beq , \单周期硬布线控制器_1_blt , \单周期硬布线控制器_1_bne ,
       \单周期硬布线控制器_1_ecall , \单周期硬布线控制器_1_jal , \单周期硬布线控制器_1_jalr , \单周期硬布线控制器_1_lh , \单周期硬布线控制器_1_memtoreg ,
       \单周期硬布线控制器_1_memwrite , \单周期硬布线控制器_1_regwrite , \单周期硬布线控制器_1_sw ;
  wire [1:0] \id_ex_重定向_1_rs1_f_2 , \id_ex_重定向_1_rs2_f_2 , \重定向处理_1_rs1_f , \重定向处理_1_rs2_f ;
  wire [3:0] \id_ex_重定向_1_aluop_2 , \单周期硬布线控制器_1_alu_op ;
  wire [4:0] EX_MEM_rd_2, \id_ex_重定向_1_rd_2 , multiplexer_2_out, multiplexer_3_out, WB_rd;
  wire [12:0] CNT_num;
  wire [15:0] counter_4_q, counter_5_q, \LoadUse次数 , multiplexer_10_out, \总周期数 , \插入气泡数 , \无条件分支数 , \条件分支成功数 ;
  wire [31:0] adder_2_out, adder_4_out, alu_1_result, bit_extender_1_out, branch_t, EX_IR,
       \id_ex_重定向_1_imm_2 , \id_ex_重定向_1_r1_2 , \id_ex_重定向_1_r2_2 , ID_IR, IF_IR, immgen_1_imm,
       MEM_ALUResult, MEM_IR, MEM_WB_result_2, MEM_WB_writedata_2, multiplexer_1_out, multiplexer_4_out,
       multiplexer_5_out, multiplexer_6_out, multiplexer_7_out, multiplexer_9_out, multiplexer_11_out, PC_4,
       ram_1_data, regifile_1_r1, regifile_1_r2, shifter_1_out, WB_IR;

  Button \u_总复位  (.out(RST));
  Button _1 (.out(IR1));
  Button _2 (.out(IR2));
  Button _3 (.out(IR3));
  // Probe on \总周期数 
  // Probe on \总周期数 
  Button \u_继续运行  (.out(Go));
  LED #(.active("true")) led_1 (.in(W1));
  LED #(.active("true")) led_2 (.in(W2));
  LED #(.active("true")) led_3 (.in(W3));
  Hex_Digit_Display hex_digit_display_1 (.value(LedData[31:28]));  // open: dp
  // Probe on IF_PC[19:0]
  // RiscV_Probe riscv_probe_1: pin names not known; wires that end beside it: IF_IR
  Hex_Digit_Display hex_digit_display_2 (.value(LedData[23:20]));  // open: dp
  Hex_Digit_Display hex_digit_display_3 (.value(LedData[27:24]));  // open: dp
  // Probe on ID_PC[19:0]
  // RiscV_Probe riscv_probe_2: pin names not known; wires that end beside it: ID_IR
  or or_1 (or_1_out, WB_halt, stall);
  not not_1 (not_1_out, or_1_out);
  Multiplexer #(.select(1), .width(32), .disabled("Z"), .enable("false")) multiplexer_1 (
    .in0(PC_4), .in1(branch_t), .out(multiplexer_1_out), .sel(BranchTaken));
  Register #(.width(32), .trigger("rising"), .Select("low")) PC (
    .D(multiplexer_1_out), .en(not_1_out), .Q(IF_PC), .clk(CLK), .clr(RST));
  Hex_Digit_Display hex_digit_display_4 (.value(LedData[19:16]));  // open: dp
  Hex_Digit_Display hex_digit_display_5 (.value(LedData[15:12]));  // open: dp
  Hex_Digit_Display hex_digit_display_6 (.value(LedData[11:8]));  // open: dp
  Hex_Digit_Display hex_digit_display_7 (.value(LedData[7:4]));  // open: dp
  // Probe on EX_PC[19:0]
  // RiscV_Probe riscv_probe_3: pin names not known; wires that end beside it: EX_IR
  Adder #(.width(32)) adder_1 (.a(IF_PC), .b(32'h4), .out(PC_4));  // open: cin, cout
  Hex_Digit_Display hex_digit_display_8 (.value(LedData[3:0]));  // open: dp
  ROM #(.addrWidth(10), .dataWidth(32), .Select("high")) \u_指令存储器  (.addr(IF_PC[11:2]), .data(IF_IR));
  // Probe on \总周期数 
  // Probe on M_PC[19:0]
  // RiscV_Probe riscv_probe_4: pin names not known; wires that end beside it: MEM_IR
  IF_ID IF_ID (
    .IR(IF_IR), .PC(IF_PC), .IR_2(ID_IR), .PC_2(ID_PC), .clk(CLK), .rst(RST), .flush(BranchTaken),
    .en(not_2_out));  // open: pre, pre_2
  or or_2 (or_2_out, stall, WB_halt);
  not not_2 (not_2_out, or_2_out);
  // Probe on \总周期数 
  // Probe on \无条件分支数 
  // Probe on \条件分支成功数 
  // Probe on \插入气泡数 
  // Probe on \LoadUse次数 
  // Probe on IF_PC[11:0]
  // Probe on WB_PC[19:0]
  // RiscV_Probe riscv_probe_5: pin names not known; wires that end beside it: WB_IR
  \单周期硬布线控制器  \u_单周期硬布线控制器_1  (
    .Funct({ID_IR[30], ID_IR[25], ID_IR[14:12]}), .OP(ID_IR[6:2]), .ALU_OP(\单周期硬布线控制器_1_alu_op ),
    .MemToReg(\单周期硬布线控制器_1_memtoreg ), .MemWrite(\单周期硬布线控制器_1_memwrite ), .ALU_SRC(\单周期硬布线控制器_1_alu_src ),
    .RegWrite(\单周期硬布线控制器_1_regwrite ), .ecall(\单周期硬布线控制器_1_ecall ), .Sw(\单周期硬布线控制器_1_sw ),
    .Jalr(\单周期硬布线控制器_1_jalr ), .Beq(\单周期硬布线控制器_1_beq ), .JAL(\单周期硬布线控制器_1_jal ), .Bne(\单周期硬布线控制器_1_bne ),
    .in_3(ID_IR[21]), .AUIPC(\单周期硬布线控制器_1_auipc ), .LH(\单周期硬布线控制器_1_lh ), .BLT(\单周期硬布线控制器_1_blt ));  // open: uret, csrrci, csrrsi
  Multiplexer #(.select(1), .width(5), .disabled("Z"), .enable("false")) multiplexer_2 (
    .in0(ID_IR[19:15]), .in1(5'b10001), .out(multiplexer_2_out), .sel(\单周期硬布线控制器_1_ecall ));
  Multiplexer #(.select(1), .width(5), .disabled("Z"), .enable("false")) multiplexer_3 (
    .in0(ID_IR[24:20]), .in1(5'b01010), .out(multiplexer_3_out), .sel(\单周期硬布线控制器_1_ecall ));
  // Probe on ID_PC[11:0]
  // Probe on EX_PC[11:0]
  or or_3 (or_3_out, \单周期硬布线控制器_1_blt , \单周期硬布线控制器_1_bne , \单周期硬布线控制器_1_beq );
  // Probe on M_PC[11:0]
  D_Flip_Flop #(.trigger("high"), .Pre_Clr_Positions("LEGACY"), .NegatePresetClear("false"), .enable("true"), .NewFFLayout("false")) d_ff_1 (.Q(d_ff_1_q));  // open: clk, D, Qn, preset, en, reset
  // Probe on 13'ha1a
  ImmGen immgen_1 (
    .Sw(\单周期硬布线控制器_1_sw ), .Auipc(\单周期硬布线控制器_1_auipc ), .B_Type(or_3_out), .jal(\单周期硬布线控制器_1_jal ),
    .IR(ID_IR), .Imm(immgen_1_imm));
  // Probe on WB_PC[11:0]
  Comparator #(.width(13), .mode("twosComplement")) comparator_1 (
    .a(CNT_num), .b(13'ha1a), .eq(comparator_1_eq), .lt(comparator_1_lt));  // open: gt
  Clock #(.highDuration(1), .lowDuration(1)) clock_1 (.out(clock_1_out));
  not not_3 (not_3_out, WB_halt);
  nand nand_1 (nand_1_out, d_ff_1_q, comparator_1_eq);
  Counter #(.width(13), .max('h1fff), .ongoal("stay"), .trigger("rising"), .behavior("old")) counter_1 (
    .count(comparator_1_lt), .Q(CNT_num), .clk(clock_1_out));  // open: load, D, carry, clr, preset
  Regifile regifile_1 (
    .Din(RDin), .Clk(CLK), .R1(regifile_1_r1), .R2(regifile_1_r2), .WE(RegWrite), .W_num(WB_rd),
    .R1_num(multiplexer_2_out), .R2_num(multiplexer_3_out));
  Counter #(.width(16), .max('hffff), .ongoal("wrap"), .trigger("rising"), .behavior("new")) counter_2 (
    .Q(\条件分支成功数 ), .clk(Branch));  // open: load, D, count, carry, clr, preset, down
  assign CLK = nand_1_out ? clock_1_out : 1'bz;  // Controlled_Buffer controlled_buffer_1
  or or_4 (BranchTaken, Branch, Jmp);
  or or_5 (or_5_out, stall, BranchTaken);
  \ID_EX_重定向  \id_ex_重定向_1  (
    .rs1_f(\重定向处理_1_rs1_f ), .rs2_f(\重定向处理_1_rs2_f ), .Lh(\单周期硬布线控制器_1_lh ), .Auipc(\单周期硬布线控制器_1_auipc ),
    .Blt(\单周期硬布线控制器_1_blt ), .Beq(\单周期硬布线控制器_1_beq ), .Bne(\单周期硬布线控制器_1_bne ),
    .MemToReg(\单周期硬布线控制器_1_memtoreg ), .MemWrite(\单周期硬布线控制器_1_memwrite ), .AluSrcB(\单周期硬布线控制器_1_alu_src ),
    .RegWrite(\单周期硬布线控制器_1_regwrite ), .ecall(\单周期硬布线控制器_1_ecall ), .JAL(\单周期硬布线控制器_1_jal ),
    .Jalr(\单周期硬布线控制器_1_jalr ), .AluOP(\单周期硬布线控制器_1_alu_op ), .rd(ID_IR[11:7]), .R1(regifile_1_r1),
    .R2(regifile_1_r2), .imm(immgen_1_imm), .PC(ID_IR), .IR(ID_PC), .rs1_f_2(\id_ex_重定向_1_rs1_f_2 ),
    .rs2_f_2(\id_ex_重定向_1_rs2_f_2 ), .Lh_2(\id_ex_重定向_1_lh_2 ), .Auipc_2(\id_ex_重定向_1_auipc_2 ),
    .Blt_2(\id_ex_重定向_1_blt_2 ), .Beq_2(\id_ex_重定向_1_beq_2 ), .Bne_2(\id_ex_重定向_1_bne_2 ),
    .MemToReg_2(\id_ex_重定向_1_memtoreg_2 ), .MemWrite_2(\id_ex_重定向_1_memwrite_2 ),
    .AluSrcB_2(\id_ex_重定向_1_alusrcb_2 ), .RegWrite_2(\id_ex_重定向_1_regwrite_2 ),
    .ecall_2(\id_ex_重定向_1_ecall_2 ), .JAL_2(\id_ex_重定向_1_jal_2 ), .Jalr_2(\id_ex_重定向_1_jalr_2 ),
    .AluOP_2(\id_ex_重定向_1_aluop_2 ), .rd_2(\id_ex_重定向_1_rd_2 ), .R1_2(\id_ex_重定向_1_r1_2 ),
    .R2_2(\id_ex_重定向_1_r2_2 ), .imm_2(\id_ex_重定向_1_imm_2 ), .PC_2(EX_IR), .IR_2(EX_PC), .flush(or_5_out),
    .rst(RST), .en(not_3_out), .clk(CLK));  // open: pre, pre_2
  Pull_Resistor #(.pull(1)) pull_resistor_1 (.node(CLK));
  or or_6 (Branch, and_4_out, and_1_out, and_2_out);
  or or_7 (Jmp, \id_ex_重定向_1_jal_2 , \id_ex_重定向_1_jalr_2 );
  Multiplexer #(.select(2), .width(32), .disabled("Z"), .enable("false")) multiplexer_4 (
    .in0(\id_ex_重定向_1_r1_2 ), .in1(RDin), .in2(MEM_ALUResult), .in3(MEM_ALUResult), .out(multiplexer_4_out),
    .sel(\id_ex_重定向_1_rs1_f_2 ));
  Multiplexer #(.select(2), .width(32), .disabled("Z"), .enable("false")) multiplexer_5 (
    .in0(\id_ex_重定向_1_r2_2 ), .in1(RDin), .in2(MEM_ALUResult), .in3(MEM_ALUResult), .out(multiplexer_5_out),
    .sel(\id_ex_重定向_1_rs2_f_2 ));
  Counter #(.width(16), .max('hffff), .ongoal("wrap"), .trigger("rising"), .behavior("new")) counter_3 (
    .Q(\无条件分支数 ), .clk(Jmp));  // open: load, D, count, carry, clr, preset, down
  Multiplexer #(.select(1), .width(32), .disabled("Z"), .enable("false")) multiplexer_6 (
    .in0(multiplexer_5_out), .in1(\id_ex_重定向_1_imm_2 ), .out(multiplexer_6_out), .sel(\id_ex_重定向_1_alusrcb_2 ));
  or or_8 (or_8_out, BranchTaken, stall);
  and and_1 (and_1_out, \id_ex_重定向_1_bne_2 , ~alu_1_equal);  // AND_Gate
  and and_2 (and_2_out, \id_ex_重定向_1_beq_2 , alu_1_equal);
  Multiplexer #(.select(1), .width(32), .disabled("Z"), .enable("false")) multiplexer_7 (
    .in0(multiplexer_4_out), .in1(EX_PC), .out(multiplexer_7_out), .sel(\id_ex_重定向_1_auipc_2 ));
  ALU alu_1 (
    .X(multiplexer_7_out), .Y(multiplexer_6_out), .AluOP(\id_ex_重定向_1_aluop_2 ), .Equal(alu_1_equal),
    .Result(alu_1_result), .out_6(alu_1_out_6));  // open: Result_2, out_4
  Shifter #(.width(32), .shift("ll")) shifter_1 (.in(\id_ex_重定向_1_imm_2 ), .\dist (5'b00001), .out(shifter_1_out));
  Adder #(.width(32)) adder_2 (.a(shifter_1_out), .b(EX_PC), .out(adder_2_out));  // open: cin, cout
  Comparator #(.width(32), .mode("twosComplement")) comparator_2 (
    .a(multiplexer_4_out), .b(32'h22), .eq(comparator_2_eq));  // open: gt, lt
  and and_3 (and_3_out, comparator_2_eq, \id_ex_重定向_1_ecall_2 );
  Counter #(.width(16), .max('hffff), .ongoal("wrap"), .trigger("rising"), .behavior("new")) counter_4 (
    .Q(counter_4_q), .clk(or_8_out));  // open: load, D, count, carry, clr, preset, down
  Counter #(.width(16), .max('hffff), .ongoal("wrap"), .trigger("rising"), .behavior("new")) counter_5 (
    .Q(counter_5_q), .clk(BranchTaken));  // open: load, D, count, carry, clr, preset, down
  and and_4 (and_4_out, \id_ex_重定向_1_blt_2 , alu_1_out_6);
  Multiplexer #(.select(1), .width(32), .disabled("Z"), .enable("false")) multiplexer_8 (
    .in0(adder_2_out), .in1(alu_1_result), .out(branch_t), .sel(\id_ex_重定向_1_jalr_2 ));
  and and_5 (and_5_out, \id_ex_重定向_1_ecall_2 , ~comparator_2_eq);  // AND_Gate
  Register #(.width(32), .trigger("rising"), .Select("low")) register_1 (
    .D(multiplexer_5_out), .en(and_3_out), .Q(LedData), .clk(CLK));  // open: clr
  Adder #(.width(16)) adder_3 (.a(counter_4_q), .b(counter_5_q), .out(\插入气泡数 ));  // open: cin, cout
  or or_9 (or_9_out, \id_ex_重定向_1_jal_2 , \id_ex_重定向_1_jalr_2 );
  Multiplexer #(.select(1), .width(32), .disabled("Z"), .enable("false")) multiplexer_9 (
    .in0(alu_1_result), .in1(adder_4_out), .out(multiplexer_9_out), .sel(or_9_out));
  Adder #(.width(32)) adder_4 (.a(32'h4), .b(EX_PC), .out(adder_4_out));  // open: cin, cout
  Counter #(.width(16), .max('hffff), .ongoal("wrap"), .trigger("rising"), .behavior("new")) counter_6 (
    .Q(\LoadUse次数 ), .clk(LoadUse));  // open: load, D, count, carry, clr, preset, down
  EX_MEM EX_MEM (
    .MemToReg(\id_ex_重定向_1_memtoreg_2 ), .MemWrite(\id_ex_重定向_1_memwrite_2 ),
    .RegWrite(\id_ex_重定向_1_regwrite_2 ), .IR(EX_IR), .MemToReg_2(EX_MEM_memtoreg_2), .MemWrite_2(MemWrite),
    .RegWrite_2(EX_MEM_regwrite_2), .IR_2(MEM_IR), .PC(EX_PC), .PC_2(M_PC), .rst(RST), .clk(CLK),
    .Result(multiplexer_9_out), .Result_2(MEM_ALUResult), .WriteData(multiplexer_5_out), .WriteData_2(MDin),
    .lh(\id_ex_重定向_1_lh_2 ), .lh_2(EX_MEM_lh_2), .rd(\id_ex_重定向_1_rd_2 ), .rd_2(EX_MEM_rd_2), .en(not_3_out),
    .hait(and_5_out), .halt(EX_MEM_halt));
  Counter #(.width(16), .max('hffff), .ongoal("wrap"), .trigger("rising"), .behavior("new")) counter_7 (
    .Q(\总周期数 ), .clk(and_6_out));  // open: load, D, count, carry, clr, preset, down
  and and_6 (and_6_out, ~WB_halt, CLK);  // AND_Gate
  \重定向处理  \u_重定向处理_1  (
    .IR(ID_IR), .rs1_f(\重定向处理_1_rs1_f ), .rs1(multiplexer_2_out), .rs2(multiplexer_3_out),
    .EX_rd(\id_ex_重定向_1_rd_2 ), .MEM_rd(EX_MEM_rd_2), .EX_RegWrite(\id_ex_重定向_1_regwrite_2 ),
    .MEM_RegWrite(EX_MEM_regwrite_2), .EX_MemToReg(\id_ex_重定向_1_memtoreg_2 ), .rs2_f(\重定向处理_1_rs2_f ),
    .Stall(stall), .LoadUse(LoadUse));
  RAM #(.addrWidth(10), .dataWidth(32), .bus("separate"), .Select("high")) ram_1 (
    .addr(MEM_ALUResult[11:2]), .din(MDin), .data(ram_1_data), .str(MemWrite), .sel(1'b1), .clk(CLK),
    .ld(1'b1), .clr(RST));
  Multiplexer #(.select(1), .width(16), .disabled("Z"), .enable("false")) multiplexer_10 (
    .in0(ram_1_data[15:0]), .in1(ram_1_data[31:16]), .out(multiplexer_10_out), .sel(MEM_ALUResult[1]));
  assign bit_extender_1_out = {{16{multiplexer_10_out[15]}}, multiplexer_10_out};  // Bit_Extender bit_extender_1
  MEM_WB MEM_WB (
    .MemToReg(EX_MEM_memtoreg_2), .MemToReg_2(MEM_WB_memtoreg_2), .RegWrite(EX_MEM_regwrite_2),
    .RegWrite_2(RegWrite), .Result(MEM_ALUResult), .Result_2(MEM_WB_result_2),
    .WriteData(multiplexer_11_out), .WriteData_2(MEM_WB_writedata_2), .rd_2(WB_rd), .IR(MEM_IR),
    .IR_2(WB_IR), .PC(M_PC), .PC_2(WB_PC), .rst(RST), .clk(CLK), .rd(EX_MEM_rd_2), .en(not_3_out),
    .halt_2(MEM_WB_halt_2), .halt(EX_MEM_halt));
  Multiplexer #(.select(1), .width(32), .disabled("Z"), .enable("false")) multiplexer_11 (
    .in0(ram_1_data), .in1(bit_extender_1_out), .out(multiplexer_11_out), .sel(EX_MEM_lh_2));
  Multiplexer #(.select(1), .width(32), .disabled("Z"), .enable("false")) multiplexer_12 (
    .in0(MEM_WB_result_2), .in1(MEM_WB_writedata_2), .out(RDin), .sel(MEM_WB_memtoreg_2));
  and and_7 (WB_halt, ~Go, MEM_WB_halt_2);  // AND_Gate

  // Other names for the same wires on the sheet: MEM_PC[31:0] = M_PC

  // Notes on the sheet:
  //   中断源
  //   时空图监测，可删除
  //   中断等待指示
  //   数码管输出
  //   IF阶段
  //   contents of 指令存储器 (hex, n*v repeats v):
  //   100493 100006f 100493 200913 300993 100006f 100493 200913 300993 100006f 100493 200913 300993
  //   100006f 100493 200913 300993 408000ef 100413 100493 1f49493 900533 2200893 73 24d493 48463 fedff06f
  //   900533 2200893 73 100493 249493 900533 2200893 73 48463 fedff06f 100493 1f49493 900533 2200893 73
  //   4034d493 900533 2200893 73 4044d493 900533 2200893 73 4044d493 900533 2200893 73 4044d493 900533
  //   2200893 73 4044d493 900533 2200893 73 4044d493 900533 2200893 73 4044d493 900533 2200893 73 4044d493
  //   900533 2200893 73 100413 1f41993 41f9d993 433 c00913 300b13 140413 f47413 800293 100313 499993
  //   89e9b3 1300533 2200893 73 406282b3 fe0294e3 140413 f00f93 1f47433 1c41413 800293 100313 49d993
  //   89e9b3 1300533 2200893 73 406282b3 fe0294e3 1c45413 406b0b33 b0463 f95ff06f 2b3 fff2c293 829293
  //   ff2e293 500533 2200893 73 fff00413 493 84a023 140413 448493 84a023 140413 448493 84a023 140413
  //   448493 84a023 140413 448493 84a023 140413 448493 84a023 140413 448493 84a023 140413 448493 84a023
  //   140413 448493 84a023 140413 448493 84a023 140413 448493 84a023 140413 448493 84a023 140413 448493
  //   84a023 140413 448493 84a023 140413 448493 84a023 140413 448493 84a023 140413 448493 140413 433
  //   3c00493 42983 4aa03 149a2b3 28663 134a023 1442023 ffc48493 fe9412e3 800533 2200893 73 440413 3c00493
  //   fc9416e3 a00893 73 fff00293 7700493 849493 7748493 900533 2200893 73 1000e13 54c4b3 900533 2200893
  //   73 fffe0e13 fe0e16e3 a00893 73 13 430497 900533 2200893 73 430497 900533 2200893 73 430497 900533
  //   2200893 73 430497 900533 2200893 73 430497 900533 2200893 73 430497 900533 2200893 73 430497 900533
  //   2200893 73 430497 900533 2200893 73 a00893 73 313 1000e13 8400493 849493 8348493 400913 891913
  //   490913 849493 8248493 849493 8148493 891913 490913 891913 490913 932023 12484b3 430313 fffe0e13
  //   fe0e18e3 2000e13 313 31483 900533 2200893 73 230313 fffe0e13 fe0e14e3 a00893 73 ff100493 900533
  //   2200893 73 148493 fe04c8e3 a00893 73 413 140413 800533 2200893 73 240413 800533 2200893 73 340413
  //   800533 2200893 73 440413 800533 2200893 73 540413 800533 2200893 73 640413 800533 2200893 73 740413
  //   800533 2200893 73 840413 800533 2200893 2200893 73 8067
  //   rs1
  //   rs2
  //   rd
  //   控制位
  //   ID阶段
  //   流水调试日志用
  //   暂停节拍，不能为0
  //   戳工具置1进入计数暂停模式，ctrl+k时钟自动运行到对应节拍暂停
  //   ctrl+k关闭时钟连续运行，将控制位置零，进入单步调试模式调试
  //   可计数暂停的时钟源
  //   为方便自动评测，需要输出流水线各段保存的PC值，注意是PC不是PC+4，另外ID段寄存器写入信息，Mem段内存写入信息也要输出
  //   EX阶段
  //   MEM阶段
  //   数据存储器
  //   WB阶段
endmodule
module \流水线_动态分支预测  (
  output RegWrite,
  output MemWrite,
  output [31:0] IF_PC,
  output [31:0] ID_PC,
  output [31:0] EX_PC,
  output [31:0] M_PC,
  output [31:0] WB_PC,
  output [31:0] RDin,
  output [31:0] MDin,
  output [31:0] LedData
);

  wire alu_1_equal, alu_1_out_6, and_1_out, and_2_out, and_3_out, and_4_out, and_5_out, and_6_out, B, Branch,
       BranchTaken, CLK, clock_1_out, comparator_1_eq, comparator_2_eq, comparator_2_lt, comparator_3_eq,
       d_ff_1_q, EX_MEM_halt, EX_MEM_lh_2, EX_MEM_memtoreg_2, EX_MEM_regwrite_2, ex_predict_err,
       ex_predict_jmp, Go, \id_ex_重定向_1_alusrcb_2 , \id_ex_重定向_1_auipc_2 , \id_ex_重定向_1_beq_2 ,
       \id_ex_重定向_1_blt_2 , \id_ex_重定向_1_bne_2 , \id_ex_重定向_1_ecall_2 , \id_ex_重定向_1_lh_2 ,
       \id_ex_重定向_1_memtoreg_2 , \id_ex_重定向_1_memwrite_2 , \id_ex_重定向_1_regwrite_2 , IF_ID_pre_2, IR1, IR2,
       IR3, Jal, Jalr, Jmp, LoadUse, MEM_WB_halt_2, MEM_WB_memtoreg_2, nand_1_out, not_2_out, not_3_out,
       not_4_out, or_1_out, or_2_out, or_3_out, or_4_out, or_5_out, or_6_out, or_7_out, or_8_out, or_13_out,
       predict_jmp, RST, stall, W1, W2, W3, WB_halt, \单周期硬布线控制器_1_alu_src , \单周期硬布线控制器_1_auipc ,
       \单周期硬布线控制器_1_beq , \单周期硬布线控制器_1_blt , \单周期硬布线控制器_1_bne , \单周期硬布线控制器_1_ecall , \单周期硬布线控制器_1_jal ,
       \单周期硬布线控制器_1_jalr , \单周期硬布线控制器_1_lh , \单周期硬布线控制器_1_memtoreg , \单周期硬布线控制器_1_memwrite ,
       \单周期硬布线控制器_1_regwrite , \单周期硬布线控制器_1_sw ;
  wire [1:0] \id_ex_重定向_1_rs1_f_2 , \id_ex_重定向_1_rs2_f_2 , \重定向处理_1_rs1_f , \重定向处理_1_rs2_f ;
  wire [3:0] \id_ex_重定向_1_aluop_2 , \单周期硬布线控制器_1_alu_op ;
  wire [4:0] EX_MEM_rd_2, \id_ex_重定向_1_rd_2 , multiplexer_7_out, multiplexer_8_out, WB_rd;
  wire [12:0] CNT_num;
  wire [15:0] counter_4_q, counter_5_q, \LoadUse次数 , multiplexer_15_out, \总周期数 , \插入气泡数 , \无条件分支数 , \条件分支成功数 ;
  wire [31:0] adder_1_out, adder_5_out, bit_extender_1_out, branch_t, branchadd, EX_IR, \id_ex_重定向_1_imm_2 ,
       \id_ex_重定向_1_r1_2 , \id_ex_重定向_1_r2_2 , ID_IR, IF_IR, Imm, immgen_1_imm, jalradd, jmp_add,
       MEM_ALUResult, MEM_IR, MEM_WB_result_2, MEM_WB_writedata_2, multiplexer_1_out, multiplexer_3_out,
       multiplexer_4_out, multiplexer_5_out, multiplexer_6_out, multiplexer_9_out, multiplexer_10_out,
       multiplexer_11_out, multiplexer_12_out, multiplexer_14_out, multiplexer_16_out, PC_4, ram_1_data,
       regifile_1_r1, regifile_1_r2, shifter_1_out, WB_IR;

  Button \u_总复位  (.out(RST));
  Button _1 (.out(IR1));
  Button _2 (.out(IR2));
  Button _3 (.out(IR3));
  // Probe on \总周期数 
  // Probe on \总周期数 
  Button \u_继续运行  (.out(Go));
  LED #(.active("true")) led_1 (.in(W1));
  LED #(.active("true")) led_2 (.in(W2));
  LED #(.active("true")) led_3 (.in(W3));
  Hex_Digit_Display hex_digit_display_1 (.value(LedData[31:28]));  // open: dp
  // Probe on IF_PC[19:0]
  // RiscV_Probe riscv_probe_1: pin names not known; wires that end beside it: IF_IR
  Multiplexer #(.select(1), .width(32), .disabled("Z"), .enable("false")) multiplexer_1 (
    .in0(PC_4), .in1(Imm), .out(multiplexer_1_out), .sel(Jal));
  Hex_Digit_Display hex_digit_display_2 (.value(LedData[27:24]));  // open: dp
  Hex_Digit_Display hex_digit_display_3 (.value(LedData[23:20]));  // open: dp
  // Probe on ID_PC[19:0]
  // RiscV_Probe riscv_probe_2: pin names not known; wires that end beside it: ID_IR
  Multiplexer #(.select(1), .width(32), .disabled("Z"), .enable("false")) multiplexer_2 (
    .in0(multiplexer_1_out), .in1(Imm), .out(branchadd), .sel(B));
  Hex_Digit_Display hex_digit_display_4 (.value(LedData[15:12]));  // open: dp
  Hex_Digit_Display hex_digit_display_5 (.value(LedData[19:16]));  // open: dp
  or or_1 (or_1_out, Jal, Branch);
  Adder #(.width(32)) adder_1 (.a(EX_PC), .b(32'h4), .out(adder_1_out));  // open: cin, cout
  Hex_Digit_Display hex_digit_display_6 (.value(LedData[7:4]));  // open: dp
  Hex_Digit_Display hex_digit_display_7 (.value(LedData[11:8]));  // open: dp
  // Probe on EX_PC[19:0]
  // RiscV_Probe riscv_probe_3: pin names not known; wires that end beside it: EX_IR
  Comparator #(.width(1), .mode("twosComplement")) comparator_1 (
    .a(BranchTaken), .b(ex_predict_jmp), .eq(comparator_1_eq));  // open: gt, lt
  not not_1 (ex_predict_err, comparator_1_eq);
  Multiplexer #(.select(1), .width(32), .disabled("Z"), .enable("false")) multiplexer_3 (
    .in0(adder_1_out), .in1(branchadd), .out(multiplexer_3_out), .sel(or_1_out));
  Hex_Digit_Display hex_digit_display_8 (.value(LedData[3:0]));  // open: dp
  Multiplexer #(.select(1), .width(32), .disabled("Z"), .enable("false")) multiplexer_4 (
    .in0(multiplexer_6_out), .in1(multiplexer_3_out), .out(multiplexer_4_out), .sel(ex_predict_err));
  Multiplexer #(.select(1), .width(32), .disabled("Z"), .enable("false")) multiplexer_5 (
    .in0(multiplexer_4_out), .in1(jalradd), .out(multiplexer_5_out), .sel(Jalr));
  // Probe on \总周期数 
  // Probe on M_PC[19:0]
  // RiscV_Probe riscv_probe_4: pin names not known; wires that end beside it: MEM_IR
  or or_2 (or_2_out, WB_halt, stall);
  not not_2 (not_2_out, or_2_out);
  Register #(.width(32), .trigger("rising"), .Select("low")) PC (
    .D(multiplexer_5_out), .en(not_2_out), .Q(IF_PC), .clk(CLK), .clr(RST));
  // Probe on \总周期数 
  // Probe on \无条件分支数 
  // Probe on \条件分支成功数 
  // Probe on \插入气泡数 
  // Probe on \LoadUse次数 
  or or_3 (or_3_out, Jal, Branch);
  Adder #(.width(32)) adder_2 (.a(IF_PC), .b(32'h4), .out(PC_4));  // open: cin, cout
  // Probe on IF_PC[11:0]
  // Probe on WB_PC[19:0]
  // RiscV_Probe riscv_probe_5: pin names not known; wires that end beside it: WB_IR
  or or_4 (or_4_out, B, Jal);
  BHT bht_1 (
    .Clk(CLK), .EX_Branch(or_4_out), .PC(IF_PC), .EX_PC(EX_PC), .EX_BranchAddr(branchadd),
    .EX_Branched(or_3_out), .JumpAddr(jmp_add), .PredictJump(predict_jmp));
  // Probe on ID_PC[11:0]
  // Probe on EX_PC[11:0]
  Multiplexer #(.select(1), .width(32), .disabled("Z"), .enable("false")) multiplexer_6 (
    .in0(PC_4), .in1(jmp_add), .out(multiplexer_6_out), .sel(predict_jmp));
  ROM #(.addrWidth(10), .dataWidth(32), .Select("high")) \u_指令存储器  (.addr(IF_PC[11:2]), .data(IF_IR));
  or or_5 (or_5_out, stall, WB_halt);
  // Probe on M_PC[11:0]
  D_Flip_Flop #(.trigger("high"), .Pre_Clr_Positions("LEGACY"), .NegatePresetClear("false"), .enable("true"), .NewFFLayout("false")) d_ff_1 (.Q(d_ff_1_q));  // open: clk, D, Qn, preset, en, reset
  // Probe on 13'ha1a
  IF_ID IF_ID (
    .IR(IF_IR), .PC(IF_PC), .IR_2(ID_IR), .PC_2(ID_PC), .clk(CLK), .rst(RST), .flush(ex_predict_err),
    .en(not_3_out), .pre(predict_jmp), .pre_2(IF_ID_pre_2));
  not not_3 (not_3_out, or_5_out);
  // Probe on WB_PC[11:0]
  Comparator #(.width(13), .mode("twosComplement")) comparator_2 (
    .a(CNT_num), .b(13'ha1a), .eq(comparator_2_eq), .lt(comparator_2_lt));  // open: gt
  Clock #(.highDuration(1), .lowDuration(1)) clock_1 (.out(clock_1_out));
  nand nand_1 (nand_1_out, d_ff_1_q, comparator_2_eq);
  Counter #(.width(13), .max('h1fff), .ongoal("stay"), .trigger("rising"), .behavior("old")) counter_1 (
    .count(comparator_2_lt), .Q(CNT_num), .clk(clock_1_out));  // open: load, D, carry, clr, preset
  \单周期硬布线控制器  \u_单周期硬布线控制器_1  (
    .Funct({ID_IR[30], ID_IR[25], ID_IR[14:12]}), .OP(ID_IR[6:2]), .ALU_OP(\单周期硬布线控制器_1_alu_op ),
    .MemToReg(\单周期硬布线控制器_1_memtoreg ), .MemWrite(\单周期硬布线控制器_1_memwrite ), .ALU_SRC(\单周期硬布线控制器_1_alu_src ),
    .RegWrite(\单周期硬布线控制器_1_regwrite ), .ecall(\单周期硬布线控制器_1_ecall ), .Sw(\单周期硬布线控制器_1_sw ),
    .Jalr(\单周期硬布线控制器_1_jalr ), .Beq(\单周期硬布线控制器_1_beq ), .JAL(\单周期硬布线控制器_1_jal ), .Bne(\单周期硬布线控制器_1_bne ),
    .in_3(ID_IR[21]), .AUIPC(\单周期硬布线控制器_1_auipc ), .LH(\单周期硬布线控制器_1_lh ), .BLT(\单周期硬布线控制器_1_blt ));  // open: uret, csrrci, csrrsi
  Multiplexer #(.select(1), .width(5), .disabled("Z"), .enable("false")) multiplexer_7 (
    .in0(ID_IR[19:15]), .in1(5'b10001), .out(multiplexer_7_out), .sel(\单周期硬布线控制器_1_ecall ));
  Multiplexer #(.select(1), .width(5), .disabled("Z"), .enable("false")) multiplexer_8 (
    .in0(ID_IR[24:20]), .in1(5'b01010), .out(multiplexer_8_out), .sel(\单周期硬布线控制器_1_ecall ));
  Counter #(.width(16), .max('hffff), .ongoal("wrap"), .trigger("rising"), .behavior("new")) counter_2 (
    .Q(\条件分支成功数 ), .clk(Branch));  // open: load, D, count, carry, clr, preset, down
  assign CLK = nand_1_out ? clock_1_out : 1'bz;  // Controlled_Buffer controlled_buffer_1
  or or_6 (or_6_out, \单周期硬布线控制器_1_blt , \单周期硬布线控制器_1_bne , \单周期硬布线控制器_1_beq );
  ImmGen immgen_1 (
    .Sw(\单周期硬布线控制器_1_sw ), .Auipc(\单周期硬布线控制器_1_auipc ), .B_Type(or_6_out), .jal(\单周期硬布线控制器_1_jal ),
    .IR(ID_IR), .Imm(immgen_1_imm));
  Pull_Resistor #(.pull(1)) pull_resistor_1 (.node(CLK));
  not not_4 (not_4_out, WB_halt);
  Counter #(.width(16), .max('hffff), .ongoal("wrap"), .trigger("rising"), .behavior("new")) counter_3 (
    .Q(\无条件分支数 ), .clk(Jmp));  // open: load, D, count, carry, clr, preset, down
  Regifile regifile_1 (
    .Din(RDin), .Clk(CLK), .R1(regifile_1_r1), .R2(regifile_1_r2), .WE(RegWrite), .W_num(WB_rd),
    .R1_num(multiplexer_7_out), .R2_num(multiplexer_8_out));
  or or_7 (or_7_out, BranchTaken, stall);
  or or_8 (or_8_out, stall, ex_predict_err);
  Counter #(.width(16), .max('hffff), .ongoal("wrap"), .trigger("rising"), .behavior("new")) counter_4 (
    .Q(counter_4_q), .clk(or_7_out));  // open: load, D, count, carry, clr, preset, down
  Counter #(.width(16), .max('hffff), .ongoal("wrap"), .trigger("rising"), .behavior("new")) counter_5 (
    .Q(counter_5_q), .clk(BranchTaken));  // open: load, D, count, carry, clr, preset, down
  or or_9 (BranchTaken, Branch, Jmp);
  \ID_EX_重定向  \id_ex_重定向_1  (
    .rs1_f(\重定向处理_1_rs1_f ), .rs2_f(\重定向处理_1_rs2_f ), .Lh(\单周期硬布线控制器_1_lh ), .Auipc(\单周期硬布线控制器_1_auipc ),
    .Blt(\单周期硬布线控制器_1_blt ), .Beq(\单周期硬布线控制器_1_beq ), .Bne(\单周期硬布线控制器_1_bne ),
    .MemToReg(\单周期硬布线控制器_1_memtoreg ), .MemWrite(\单周期硬布线控制器_1_memwrite ), .AluSrcB(\单周期硬布线控制器_1_alu_src ),
    .RegWrite(\单周期硬布线控制器_1_regwrite ), .ecall(\单周期硬布线控制器_1_ecall ), .JAL(\单周期硬布线控制器_1_jal ),
    .Jalr(\单周期硬布线控制器_1_jalr ), .AluOP(\单周期硬布线控制器_1_alu_op ), .rd(ID_IR[11:7]), .R1(regifile_1_r1),
    .R2(regifile_1_r2), .imm(immgen_1_imm), .PC(ID_IR), .IR(ID_PC), .rs1_f_2(\id_ex_重定向_1_rs1_f_2 ),
    .rs2_f_2(\id_ex_重定向_1_rs2_f_2 ), .Lh_2(\id_ex_重定向_1_lh_2 ), .Auipc_2(\id_ex_重定向_1_auipc_2 ),
    .Blt_2(\id_ex_重定向_1_blt_2 ), .Beq_2(\id_ex_重定向_1_beq_2 ), .Bne_2(\id_ex_重定向_1_bne_2 ),
    .MemToReg_2(\id_ex_重定向_1_memtoreg_2 ), .MemWrite_2(\id_ex_重定向_1_memwrite_2 ),
    .AluSrcB_2(\id_ex_重定向_1_alusrcb_2 ), .RegWrite_2(\id_ex_重定向_1_regwrite_2 ),
    .ecall_2(\id_ex_重定向_1_ecall_2 ), .JAL_2(Jal), .Jalr_2(Jalr), .AluOP_2(\id_ex_重定向_1_aluop_2 ),
    .rd_2(\id_ex_重定向_1_rd_2 ), .R1_2(\id_ex_重定向_1_r1_2 ), .R2_2(\id_ex_重定向_1_r2_2 ),
    .imm_2(\id_ex_重定向_1_imm_2 ), .PC_2(EX_IR), .IR_2(EX_PC), .flush(or_8_out), .rst(RST), .en(not_4_out),
    .clk(CLK), .pre(IF_ID_pre_2), .pre_2(ex_predict_jmp));
  Multiplexer #(.select(2), .width(32), .disabled("Z"), .enable("false")) multiplexer_9 (
    .in0(\id_ex_重定向_1_r1_2 ), .in1(RDin), .in2(MEM_ALUResult), .in3(MEM_ALUResult), .out(multiplexer_9_out),
    .sel(\id_ex_重定向_1_rs1_f_2 ));
  Multiplexer #(.select(2), .width(32), .disabled("Z"), .enable("false")) multiplexer_10 (
    .in0(\id_ex_重定向_1_r2_2 ), .in1(RDin), .in2(MEM_ALUResult), .in3(MEM_ALUResult), .out(multiplexer_10_out),
    .sel(\id_ex_重定向_1_rs2_f_2 ));
  Adder #(.width(16)) adder_3 (.a(counter_4_q), .b(counter_5_q), .out(\插入气泡数 ));  // open: cin, cout
  or or_10 (Branch, and_2_out, and_3_out, and_1_out);
  or or_11 (Jmp, Jal, Jalr);
  Counter #(.width(16), .max('hffff), .ongoal("wrap"), .trigger("rising"), .behavior("new")) counter_6 (
    .Q(\LoadUse次数 ), .clk(LoadUse));  // open: load, D, count, carry, clr, preset, down
  or or_12 (B, \id_ex_重定向_1_beq_2 , \id_ex_重定向_1_bne_2 , \id_ex_重定向_1_blt_2 );
  and and_1 (and_1_out, \id_ex_重定向_1_beq_2 , alu_1_equal);
  Multiplexer #(.select(1), .width(32), .disabled("Z"), .enable("false")) multiplexer_11 (
    .in0(multiplexer_9_out), .in1(EX_PC), .out(multiplexer_11_out), .sel(\id_ex_重定向_1_auipc_2 ));
  Multiplexer #(.select(1), .width(32), .disabled("Z"), .enable("false")) multiplexer_12 (
    .in0(multiplexer_10_out), .in1(\id_ex_重定向_1_imm_2 ), .out(multiplexer_12_out),
    .sel(\id_ex_重定向_1_alusrcb_2 ));
  Shifter #(.width(32), .shift("ll")) shifter_1 (.in(\id_ex_重定向_1_imm_2 ), .\dist (5'b00001), .out(shifter_1_out));
  Comparator #(.width(32), .mode("twosComplement")) comparator_3 (
    .a(multiplexer_9_out), .b(32'h22), .eq(comparator_3_eq));  // open: gt, lt
  and and_2 (and_2_out, \id_ex_重定向_1_blt_2 , alu_1_out_6);
  and and_3 (and_3_out, \id_ex_重定向_1_bne_2 , ~alu_1_equal);  // AND_Gate
  ALU alu_1 (
    .X(multiplexer_11_out), .Y(multiplexer_12_out), .AluOP(\id_ex_重定向_1_aluop_2 ), .Equal(alu_1_equal),
    .Result(jalradd), .out_6(alu_1_out_6));  // open: Result_2, out_4
  Adder #(.width(32)) adder_4 (.a(shifter_1_out), .b(EX_PC), .out(Imm));  // open: cin, cout
  and and_4 (and_4_out, comparator_3_eq, \id_ex_重定向_1_ecall_2 );
  Counter #(.width(16), .max('hffff), .ongoal("wrap"), .trigger("rising"), .behavior("new")) counter_7 (
    .Q(\总周期数 ), .clk(and_5_out));  // open: load, D, count, carry, clr, preset, down
  and and_5 (and_5_out, ~WB_halt, CLK);  // AND_Gate
  Multiplexer #(.select(1), .width(32), .disabled("Z"), .enable("false")) multiplexer_13 (
    .in0(Imm), .in1(jalradd), .out(branch_t), .sel(Jalr));
  and and_6 (and_6_out, \id_ex_重定向_1_ecall_2 , ~comparator_3_eq);  // AND_Gate
  Register #(.width(32), .trigger("rising"), .Select("low")) register_1 (
    .D(multiplexer_10_out), .en(and_4_out), .Q(LedData), .clk(CLK));  // open: clr
  or or_13 (or_13_out, Jal, Jalr);
  Multiplexer #(.select(1), .width(32), .disabled("Z"), .enable("false")) multiplexer_14 (
    .in0(jalradd), .in1(adder_5_out), .out(multiplexer_14_out), .sel(or_13_out));
  Adder #(.width(32)) adder_5 (.a(32'h4), .b(EX_PC), .out(adder_5_out));  // open: cin, cout
  EX_MEM EX_MEM (
    .MemToReg(\id_ex_重定向_1_memtoreg_2 ), .MemWrite(\id_ex_重定向_1_memwrite_2 ),
    .RegWrite(\id_ex_重定向_1_regwrite_2 ), .IR(EX_IR), .MemToReg_2(EX_MEM_memtoreg_2), .MemWrite_2(MemWrite),
    .RegWrite_2(EX_MEM_regwrite_2), .IR_2(MEM_IR), .PC(EX_PC), .PC_2(M_PC), .rst(RST), .clk(CLK),
    .Result(multiplexer_14_out), .Result_2(MEM_ALUResult), .WriteData(multiplexer_10_out),
    .WriteData_2(MDin), .lh(\id_ex_重定向_1_lh_2 ), .lh_2(EX_MEM_lh_2), .rd(\id_ex_重定向_1_rd_2 ),
    .rd_2(EX_MEM_rd_2), .en(not_4_out), .hait(and_6_out), .halt(EX_MEM_halt));
  RAM #(.addrWidth(10), .dataWidth(32), .bus("separate"), .Select("high")) ram_1 (
    .addr(MEM_ALUResult[11:2]), .din(MDin), .data(ram_1_data), .str(MemWrite), .sel(1'b1), .clk(CLK),
    .ld(1'b1), .clr(RST));
  \重定向处理  \u_重定向处理_1  (
    .IR(ID_IR), .rs1_f(\重定向处理_1_rs1_f ), .rs1(multiplexer_7_out), .rs2(multiplexer_8_out),
    .EX_rd(\id_ex_重定向_1_rd_2 ), .MEM_rd(EX_MEM_rd_2), .EX_RegWrite(\id_ex_重定向_1_regwrite_2 ),
    .MEM_RegWrite(EX_MEM_regwrite_2), .EX_MemToReg(\id_ex_重定向_1_memtoreg_2 ), .rs2_f(\重定向处理_1_rs2_f ),
    .Stall(stall), .LoadUse(LoadUse));
  assign bit_extender_1_out = {{16{multiplexer_15_out[15]}}, multiplexer_15_out};  // Bit_Extender bit_extender_1
  Multiplexer #(.select(1), .width(16), .disabled("Z"), .enable("false")) multiplexer_15 (
    .in0(ram_1_data[15:0]), .in1(ram_1_data[31:16]), .out(multiplexer_15_out), .sel(MEM_ALUResult[1]));
  MEM_WB MEM_WB (
    .MemToReg(EX_MEM_memtoreg_2), .MemToReg_2(MEM_WB_memtoreg_2), .RegWrite(EX_MEM_regwrite_2),
    .RegWrite_2(RegWrite), .Result(MEM_ALUResult), .Result_2(MEM_WB_result_2),
    .WriteData(multiplexer_16_out), .WriteData_2(MEM_WB_writedata_2), .rd_2(WB_rd), .IR(MEM_IR),
    .IR_2(WB_IR), .PC(M_PC), .PC_2(WB_PC), .rst(RST), .clk(CLK), .rd(EX_MEM_rd_2), .en(not_4_out),
    .halt_2(MEM_WB_halt_2), .halt(EX_MEM_halt));
  Multiplexer #(.select(1), .width(32), .disabled("Z"), .enable("false")) multiplexer_16 (
    .in0(ram_1_data), .in1(bit_extender_1_out), .out(multiplexer_16_out), .sel(EX_MEM_lh_2));
  Multiplexer #(.select(1), .width(32), .disabled("Z"), .enable("false")) multiplexer_17 (
    .in0(MEM_WB_result_2), .in1(MEM_WB_writedata_2), .out(RDin), .sel(MEM_WB_memtoreg_2));
  and and_7 (WB_halt, ~Go, MEM_WB_halt_2);  // AND_Gate

  // Other names for the same wires on the sheet: MEM_PC[31:0] = M_PC

  // Notes on the sheet:
  //   中断源
  //   时空图监测，可删除
  //   中断等待指示
  //   数码管输出
  //   IF阶段
  //   控制位
  //   contents of 指令存储器 (hex, n*v repeats v):
  //   100493 100006f 100493 200913 300993 100006f 100493 200913 300993 100006f 100493 200913 300993
  //   100006f 100493 200913 300993 408000ef 100413 100493 1f49493 900533 2200893 73 24d493 48463 fedff06f
  //   900533 2200893 73 100493 249493 900533 2200893 73 48463 fedff06f 100493 1f49493 900533 2200893 73
  //   4034d493 900533 2200893 73 4044d493 900533 2200893 73 4044d493 900533 2200893 73 4044d493 900533
  //   2200893 73 4044d493 900533 2200893 73 4044d493 900533 2200893 73 4044d493 900533 2200893 73 4044d493
  //   900533 2200893 73 100413 1f41993 41f9d993 433 c00913 300b13 140413 f47413 800293 100313 499993
  //   89e9b3 1300533 2200893 73 406282b3 fe0294e3 140413 f00f93 1f47433 1c41413 800293 100313 49d993
  //   89e9b3 1300533 2200893 73 406282b3 fe0294e3 1c45413 406b0b33 b0463 f95ff06f 2b3 fff2c293 829293
  //   ff2e293 500533 2200893 73 fff00413 493 84a023 140413 448493 84a023 140413 448493 84a023 140413
  //   448493 84a023 140413 448493 84a023 140413 448493 84a023 140413 448493 84a023 140413 448493 84a023
  //   140413 448493 84a023 140413 448493 84a023 140413 448493 84a023 140413 448493 84a023 140413 448493
  //   84a023 140413 448493 84a023 140413 448493 84a023 140413 448493 84a023 140413 448493 140413 433
  //   3c00493 42983 4aa03 149a2b3 28663 134a023 1442023 ffc48493 fe9412e3 800533 2200893 73 440413 3c00493
  //   fc9416e3 a00893 73 fff00293 7700493 849493 7748493 900533 2200893 73 1000e13 54c4b3 900533 2200893
  //   73 fffe0e13 fe0e16e3 a00893 73 13 430497 900533 2200893 73 430497 900533 2200893 73 430497 900533
  //   2200893 73 430497 900533 2200893 73 430497 900533 2200893 73 430497 900533 2200893 73 430497 900533
  //   2200893 73 430497 900533 2200893 73 a00893 73 313 1000e13 8400493 849493 8348493 400913 891913
  //   490913 849493 8248493 849493 8148493 891913 490913 891913 490913 932023 12484b3 430313 fffe0e13
  //   fe0e18e3 2000e13 313 31483 900533 2200893 73 230313 fffe0e13 fe0e14e3 a00893 73 ff100493 900533
  //   2200893 73 148493 fe04c8e3 a00893 73 413 140413 800533 2200893 73 240413 800533 2200893 73 340413
  //   800533 2200893 73 440413 800533 2200893 73 540413 800533 2200893 73 640413 800533 2200893 73 740413
  //   800533 2200893 73 840413 800533 2200893 2200893 73 8067
  //   流水调试日志用
  //   暂停节拍，不能为0
  //   戳工具置1进入计数暂停模式，ctrl+k时钟自动运行到对应节拍暂停
  //   ctrl+k关闭时钟连续运行，将控制位置零，进入单步调试模式调试
  //   rs1
  //   rs2
  //   rd
  //   可计数暂停的时钟源
  //   ID阶段
  //   为方便自动评测，需要输出流水线各段保存的PC值，注意是PC不是PC+4，另外ID段寄存器写入信息，Mem段内存写入信息也要输出
  //   EX阶段
  //   数据存储器
  //   MEM阶段
  //   WB阶段
endmodule

module \单周期_单级中断  (
  input  IR1,
  input  IR2,
  input  IR3,
  output RegWrite,
  output MemWrite,
  output [31:0] PC,
  output [31:0] IR,
  output [31:0] RDin,
  output [31:0] MDin,
  output [31:0] LedData
);

  wire and_1_out, and_2_out, and_3_out, and_4_out, and_5_out, AUIPC, Ben, Beq, Blt, CLK, clock_1_out,
       comparator_1_eq, comparator_2_eq, comparator_3_eq, comparator_4_eq, comparator_5_eq, comparator_6_eq,
       comparator_6_lt, controlled_inverter_1_out, controlled_inverter_2_out, controlled_inverter_3_out,
       d_ff_1_q, ecall, Go, halt, INT, IR1_t, IR2_t, IR3_t, IRA, IRB, IRC, JAL, JALR, LH, MemToReg,
       nand_1_out, not_1_out, not_2_out, not_3_out, not_4_out, or_1_out, or_2_out, or_6_out, or_7_out,
       tunnel, tunnel_t, URET, W1, W2, W3, \单周期硬布线控制器_1_alu_src , \单周期硬布线控制器_1_sw ;
  wire [1:0] priority_encoder_1_out;
  wire [3:0] \单周期硬布线控制器_1_alu_op ;
  wire [4:0] multiplexer_4_out, multiplexer_5_out;
  wire [12:0] CNT_num;
  wire [15:0] multiplexer_8_out, \总周期数 ;
  wire [31:0] adder_2_out, adder_3_out, ALUResult, bit_extender_1_out, branch, EPC, immgen_1_imm, INT_add,
       multiplexer_2_out, multiplexer_3_out, multiplexer_6_out, multiplexer_9_out, PC_4, ram_1_data,
       regifile_1_r1, RPC, shifter_1_out, shifter_2_out;

  Button \u_继续运行  (.out(Go));
  Button _1 (.out(IRA));
  Button _2 (.out(IRB));
  Button _3 (.out(IRC));
  LED #(.active("true")) led_1 (.in(W1));
  LED #(.active("true")) led_2 (.in(W2));
  LED #(.active("true")) led_3 (.in(W3));
  Hex_Digit_Display hex_digit_display_1 (.value(LedData[31:28]));  // open: dp
  Comparator #(.width(16), .mode("twosComplement")) comparator_1 (
    .a(16'h23b), .b(\总周期数 ), .eq(comparator_1_eq));  // open: gt, lt
  Comparator #(.width(16), .mode("twosComplement")) comparator_2 (
    .a(\总周期数 ), .b(16'h1), .eq(comparator_2_eq));  // open: gt, lt
  Comparator #(.width(16), .mode("twosComplement")) comparator_3 (
    .a(\总周期数 ), .b(16'h4), .eq(comparator_3_eq));  // open: gt, lt
  Comparator #(.width(16), .mode("twosComplement")) comparator_4 (
    .a(\总周期数 ), .b(16'h7), .eq(comparator_4_eq));  // open: gt, lt
  Multiplexer #(.select(1), .width(32), .disabled("Z"), .enable("false")) multiplexer_1 (
    .in0(PC_4), .in1(branch), .out(RPC), .sel(or_2_out));
  Hex_Digit_Display hex_digit_display_2 (.value(LedData[27:24]));  // open: dp
  Hex_Digit_Display hex_digit_display_3 (.value(LedData[23:20]));  // open: dp
  or or_1 (or_1_out, comparator_1_eq, comparator_2_eq);
  assign controlled_inverter_1_out = or_1_out ? ~CLK : 1'bz;  // Controlled_Inverter controlled_inverter_1
  assign controlled_inverter_2_out = comparator_3_eq ? ~CLK : 1'bz;  // Controlled_Inverter controlled_inverter_2
  assign controlled_inverter_3_out = comparator_4_eq ? ~CLK : 1'bz;  // Controlled_Inverter controlled_inverter_3
  Multiplexer #(.select(1), .width(32), .disabled("Z"), .enable("false")) multiplexer_2 (
    .in0(RPC), .in1(INT_add), .out(multiplexer_2_out), .sel(INT));
  Multiplexer #(.select(1), .width(32), .disabled("Z"), .enable("false")) multiplexer_3 (
    .in0(multiplexer_2_out), .in1(EPC), .out(multiplexer_3_out), .sel(URET));
  not not_1 (not_1_out, halt);
  Hex_Digit_Display hex_digit_display_4 (.value(LedData[19:16]));  // open: dp
  Hex_Digit_Display hex_digit_display_5 (.value(LedData[15:12]));  // open: dp
  Pull_Resistor #(.pull(0)) pull_resistor_1 (.node(controlled_inverter_1_out));
  Pull_Resistor #(.pull(0)) pull_resistor_2 (.node(controlled_inverter_2_out));
  Pull_Resistor #(.pull(0)) pull_resistor_3 (.node(controlled_inverter_3_out));
  or or_2 (or_2_out, and_1_out, and_2_out, and_3_out, JAL, JALR);
  Register #(.width(32), .trigger("rising"), .Select("low")) u_PC (
    .D(multiplexer_3_out), .en(not_1_out), .Q(PC), .clk(CLK));  // open: clr
  Hex_Digit_Display hex_digit_display_6 (.value(LedData[11:8]));  // open: dp
  Hex_Digit_Display hex_digit_display_7 (.value(LedData[7:4]));  // open: dp
  // Probe on \总周期数 
  and and_1 (and_1_out, Blt, tunnel);
  and and_2 (and_2_out, Beq, tunnel_t);
  and and_3 (and_3_out, ~tunnel_t, Ben);  // AND_Gate
  Adder #(.width(32)) adder_1 (.a(PC), .b(32'h4), .out(PC_4));  // open: cin, cout
  not not_2 (not_2_out, halt);
  Counter #(.width(16), .max('hffff), .ongoal("wrap"), .trigger("rising"), .behavior("new")) counter_1 (
    .count(not_2_out), .Q(\总周期数 ), .clk(CLK));  // open: load, D, carry, clr, preset, down
  Hex_Digit_Display hex_digit_display_8 (.value(LedData[3:0]));  // open: dp
  \单级中断逻辑电路  \u_单级中断逻辑电路_1  (
    .IRA(IR1_t), .W1(W1), .IRB(IR2_t), .W2(W2), .IRC(IR3_t), .W3(W3), .clk(CLK), .INT_Add(INT_add),
    .INT(INT), .URET(URET), .NPC(RPC), .EPC(EPC));
  // RiscV_Probe riscv_probe_1: pin names not known; wires that end beside it: IR
  ROM #(.addrWidth(10), .dataWidth(32), .Select("high")) rom_1 (.addr(PC[11:2]), .data(IR));
  or or_3 (IR1_t, IR1, IRA);
  or or_4 (IR2_t, IR2, IRB);
  \单周期硬布线控制器  \u_单周期硬布线控制器_1  (
    .Funct({IR[30], IR[25], IR[14:12]}), .OP(IR[6:2]), .ALU_OP(\单周期硬布线控制器_1_alu_op ), .MemToReg(MemToReg),
    .MemWrite(MemWrite), .ALU_SRC(\单周期硬布线控制器_1_alu_src ), .RegWrite(RegWrite), .ecall(ecall),
    .Sw(\单周期硬布线控制器_1_sw ), .Jalr(JALR), .Beq(Beq), .JAL(JAL), .Bne(Ben), .in_3(IR[21]), .uret(URET),
    .AUIPC(AUIPC), .LH(LH), .BLT(Blt));  // open: csrrci, csrrsi
  Multiplexer #(.select(1), .width(5), .disabled("Z"), .enable("false")) multiplexer_4 (
    .in0(IR[19:15]), .in1(5'b10001), .out(multiplexer_4_out), .sel(ecall));
  Multiplexer #(.select(1), .width(5), .disabled("Z"), .enable("false")) multiplexer_5 (
    .in0(IR[24:20]), .in1(5'b01010), .out(multiplexer_5_out), .sel(ecall));
  ImmGen immgen_1 (.Sw(\单周期硬布线控制器_1_sw ), .Auipc(AUIPC), .B_Type(or_6_out), .jal(JAL), .IR(IR), .Imm(immgen_1_imm));
  or or_5 (IR3_t, IR3, IRC);
  or or_6 (or_6_out, Blt, Ben, Beq);
  Regifile regifile_1 (
    .Din(RDin), .Clk(CLK), .R1(regifile_1_r1), .R2(MDin), .WE(RegWrite), .W_num(IR[11:7]),
    .R1_num(multiplexer_4_out), .R2_num(multiplexer_5_out));
  Shifter #(.width(32), .shift("ll")) shifter_1 (.in(immgen_1_imm), .\dist (5'b00001), .out(shifter_1_out));
  Shifter #(.width(32), .shift("ll")) shifter_2 (.in(immgen_1_imm), .\dist (5'b01100), .out(shifter_2_out));
  Multiplexer #(.select(1), .width(32), .disabled("Z"), .enable("false")) multiplexer_6 (
    .in0(MDin), .in1(immgen_1_imm), .out(multiplexer_6_out), .sel(\单周期硬布线控制器_1_alu_src ));
  Adder #(.width(32)) adder_2 (.a(shifter_1_out), .b(PC), .out(adder_2_out));  // open: cin, cout
  Multiplexer #(.select(1), .width(32), .disabled("Z"), .enable("false")) multiplexer_7 (
    .in0(adder_2_out), .in1(ALUResult), .out(branch), .sel(JALR));
  Adder #(.width(32)) adder_3 (.a(shifter_2_out), .b(PC), .out(adder_3_out));  // open: cin, cout
  ALU alu_1 (
    .X(regifile_1_r1), .Y(multiplexer_6_out), .AluOP(\单周期硬布线控制器_1_alu_op ), .Equal(tunnel_t),
    .Result(ALUResult), .out_6(tunnel));  // open: Result_2, out_4
  not not_3 (not_3_out, comparator_5_eq);
  Comparator #(.width(32), .mode("twosComplement")) comparator_5 (
    .a(regifile_1_r1), .b(32'h22), .eq(comparator_5_eq));  // open: gt, lt
  and and_4 (and_4_out, ecall, not_3_out);
  and and_5 (and_5_out, comparator_5_eq, ecall);
  and and_6 (halt, and_4_out, not_4_out);
  not not_4 (not_4_out, Go);
  Register #(.width(32), .trigger("rising"), .Select("low")) register_1 (
    .D(MDin), .en(and_5_out), .Q(LedData), .clk(CLK));  // open: clr
  RAM #(.addrWidth(10), .dataWidth(32), .bus("separate"), .Select("high")) ram_1 (
    .addr(ALUResult[11:2]), .din(MDin), .data(ram_1_data), .str(MemWrite), .sel(1'b1), .clk(CLK), .ld(1'b1));  // open: clr
  D_Flip_Flop #(.trigger("high"), .Pre_Clr_Positions("LEGACY"), .NegatePresetClear("false"), .enable("true"), .NewFFLayout("false")) d_ff_1 (.Q(d_ff_1_q));  // open: clk, D, Qn, preset, en, reset
  // Probe on 13'hc
  Multiplexer #(.select(1), .width(16), .disabled("Z"), .enable("false")) multiplexer_8 (
    .in0(ram_1_data[15:0]), .in1(ram_1_data[31:16]), .out(multiplexer_8_out), .sel(ALUResult[1]));
  Comparator #(.width(13), .mode("twosComplement")) comparator_6 (
    .a(CNT_num), .b(13'hc), .eq(comparator_6_eq), .lt(comparator_6_lt));  // open: gt
  Clock #(.highDuration(1), .lowDuration(1)) clock_1 (.out(clock_1_out));
  or or_7 (or_7_out, JAL, JALR);
  assign bit_extender_1_out = {{16{multiplexer_8_out[15]}}, multiplexer_8_out};  // Bit_Extender bit_extender_1
  Counter #(.width(13), .max('h1fff), .ongoal("stay"), .trigger("rising"), .behavior("old")) counter_2 (
    .count(comparator_6_lt), .Q(CNT_num), .clk(clock_1_out));  // open: load, D, carry, clr, preset
  Priority_Encoder #(.select(2), .disabled("Z")) priority_encoder_1 (
    .in0(1'b1), .in1(MemToReg), .in2(or_7_out), .in3(AUIPC), .out(priority_encoder_1_out));  // open: gs, en_out, en_in
  Multiplexer #(.select(1), .width(32), .disabled("Z"), .enable("false")) multiplexer_9 (
    .in0(ram_1_data), .in1(bit_extender_1_out), .out(multiplexer_9_out), .sel(LH));
  nand nand_1 (nand_1_out, d_ff_1_q, comparator_6_eq);
  Multiplexer #(.select(2), .width(32), .disabled("Z"), .enable("false")) multiplexer_10 (
    .in0(ALUResult), .in1(multiplexer_9_out), .in2(PC_4), .in3(adder_3_out), .out(RDin),
    .sel(priority_encoder_1_out));
  assign CLK = nand_1_out ? clock_1_out : 1'bz;  // Controlled_Buffer controlled_buffer_1
  Pull_Resistor #(.pull(1)) pull_resistor_4 (.node(CLK));

  // Notes on the sheet:
  //   中断源
  //   中断等待指示
  //   总复位信号应将除ROM以外所有存储组件全部清零
  //   单级中断测试信号模拟器
  //   数码管输出
  //   数码管输出应该用寄存器锁存，否则显示数据只能一闪而过
  //   指令探针
  //   指令存储器
  //   指令字
  //   contents of rom_1 (hex, n*v repeats v):
  //   7d000113 100413 1f41993 41f9d993 433 c00913 800b13 140413 f47413 800293 100313 499993 89e9b3 1300533
  //   2200893 73 406282b3 fe0294e3 140413 f00f93 1f47433 1c41413 800293 100313 49d993 89e9b3 1300533
  //   2200893 73 406282b3 fe0294e3 1c45413 406b0b33 b0463 f95ff06f 2b3 fff2c293 1029293 fff2e293 500533
  //   2200893 73 f5dff06f 1112023 410113 a12023 410113 812023 410113 1312023 410113 1412023 410113 1512023
  //   410113 1612023 410113 100b13 300a13 100a93 1600433 441413 14469b3 1300533 2200893 73 fe0416e3
  //   415a0a33 fe0a10e3 ffc10113 12b03 ffc10113 12a83 ffc10113 12a03 ffc10113 12983 ffc10113 12403
  //   ffc10113 12503 ffc10113 12883 200073 1112023 410113 a12023 410113 812023 410113 1312023 410113
  //   1412023 410113 1512023 410113 1612023 410113 200b13 300a13 100a93 1600433 441413 14469b3 1300533
  //   2200893 73 fe0416e3 415a0a33 fe0a10e3 ffc10113 12b03 ffc10113 12a83 ffc10113 12a03 ffc10113 12983
  //   ffc10113 12403 ffc10113 12503 ffc10113 12883 200073 1112023 410113 a12023 410113 812023 410113
  //   1312023 410113 1412023 410113 1512023 410113 1612023 410113 300b13 300a13 100a93 1600433 441413
  //   14469b3 1300533 2200893 73 fe0416e3 415a0a33 fe0a10e3 ffc10113 12b03 ffc10113 12a83 ffc10113 12a03
  //   ffc10113 12983 ffc10113 12403 ffc10113 12503 ffc10113 12883 200073
  //   rs1
  //   rs2
  //   rd
  //   Beq
  //   Bne
  //   AluOP
  //   AluSrcB
  //   Sw
  //   为方便自动评测，需要输出PC，IR，寄存器堆写如数据RDin
  //   RAM写使能MemWrite、RAM写入数据MDin等信号
  //   数据存储器
  //   控制位
  //   暂停节拍，不能为0
  //   戳工具置1进入计数暂停模式，ctrl+k时钟自动运行到对应节拍暂停
  //   ctrl+k关闭时钟连续运行，将控制位置零，进入单步调试模式调试
  //   可计数暂停的时钟源
endmodule

module \单周期_多级中断  (
  input  IR1,
  input  IR2,
  input  IR3,
  output RegWrite,
  output MemWrite,
  output [31:0] PC,
  output [31:0] IR,
  output [31:0] RDin,
  output [31:0] MDin,
  output [31:0] LedData
);

  wire and_1_out, and_2_out, and_3_out, and_4_out, and_5_out, AUIPC, Ben, Beq, Blt, CLK, clock_1_out,
       comparator_1_eq, comparator_2_eq, comparator_3_eq, comparator_4_eq, comparator_5_eq, comparator_6_eq,
       comparator_7_eq, comparator_7_lt, csrrci, csrrsi, d_ff_1_q, ecall, Go, halt, INT, IR1_t, IR2_t, IR3_t,
       IRA, IRB, IRC, JAL, JALR, LH, MemToReg, nand_1_out, not_1_out, not_2_out, not_3_out, not_4_out,
       or_1_out, or_2_out, or_3_out, or_7_out, or_8_out, pull_resistor_1_node, pull_resistor_2_node,
       pull_resistor_3_node, tunnel, tunnel_t, URET, W1, W2, W3, \单周期硬布线控制器_1_alu_src , \单周期硬布线控制器_1_sw ;
  wire [1:0] priority_encoder_1_out;
  wire [3:0] \单周期硬布线控制器_1_alu_op ;
  wire [4:0] multiplexer_4_out, multiplexer_5_out;
  wire [12:0] CNT_num;
  wire [15:0] multiplexer_8_out, \总周期数 ;
  wire [31:0] adder_2_out, adder_3_out, ALUResult, bit_extender_1_out, branch, EPC, immgen_1_imm, INT_add,
       multiplexer_2_out, multiplexer_3_out, multiplexer_6_out, multiplexer_9_out, NPC, PC_4, R1, ram_1_data,
       shifter_1_out, shifter_2_out;

  Button \u_继续运行  (.out(Go));
  Button _1 (.out(IRA));
  Button _2 (.out(IRB));
  Button _3 (.out(IRC));
  LED #(.active("true")) led_1 (.in(W1));
  LED #(.active("true")) led_2 (.in(W2));
  LED #(.active("true")) led_3 (.in(W3));
  Hex_Digit_Display hex_digit_display_1 (.value(LedData[31:28]));  // open: dp
  Comparator #(.width(16), .mode("twosComplement")) comparator_1 (
    .a(\总周期数 ), .b(16'h7), .eq(comparator_1_eq));  // open: gt, lt
  Comparator #(.width(16), .mode("twosComplement")) comparator_2 (
    .a(\总周期数 ), .b(16'h241), .eq(comparator_2_eq));  // open: gt, lt
  Hex_Digit_Display hex_digit_display_2 (.value(LedData[27:24]));  // open: dp
  Hex_Digit_Display hex_digit_display_3 (.value(LedData[23:20]));  // open: dp
  Comparator #(.width(16), .mode("twosComplement")) comparator_3 (
    .a(16'h258), .b(\总周期数 ), .eq(comparator_3_eq));  // open: gt, lt
  or or_1 (or_1_out, comparator_3_eq, comparator_4_eq);
  Comparator #(.width(16), .mode("twosComplement")) comparator_4 (
    .a(\总周期数 ), .b(16'h1), .eq(comparator_4_eq));  // open: gt, lt
  Comparator #(.width(16), .mode("twosComplement")) comparator_5 (
    .a(\总周期数 ), .b(16'h4), .eq(comparator_5_eq));  // open: gt, lt
  or or_2 (or_2_out, comparator_1_eq, comparator_2_eq);
  Multiplexer #(.select(1), .width(32), .disabled("Z"), .enable("false")) multiplexer_1 (
    .in0(PC_4), .in1(branch), .out(NPC), .sel(or_3_out));
  Hex_Digit_Display hex_digit_display_4 (.value(LedData[19:16]));  // open: dp
  Hex_Digit_Display hex_digit_display_5 (.value(LedData[15:12]));  // open: dp
  Pull_Resistor #(.pull(0)) pull_resistor_1 (.node(pull_resistor_1_node));
  assign pull_resistor_1_node = or_1_out ? ~CLK : 1'bz;  // Controlled_Inverter controlled_inverter_1
  Pull_Resistor #(.pull(0)) pull_resistor_2 (.node(pull_resistor_2_node));
  assign pull_resistor_2_node = comparator_5_eq ? ~CLK : 1'bz;  // Controlled_Inverter controlled_inverter_2
  Pull_Resistor #(.pull(0)) pull_resistor_3 (.node(pull_resistor_3_node));
  assign pull_resistor_3_node = or_2_out ? ~CLK : 1'bz;  // Controlled_Inverter controlled_inverter_3
  Multiplexer #(.select(1), .width(32), .disabled("Z"), .enable("false")) multiplexer_2 (
    .in0(NPC), .in1(INT_add), .out(multiplexer_2_out), .sel(INT));
  Multiplexer #(.select(1), .width(32), .disabled("Z"), .enable("false")) multiplexer_3 (
    .in0(multiplexer_2_out), .in1(EPC), .out(multiplexer_3_out), .sel(URET));
  not not_1 (not_1_out, halt);
  Hex_Digit_Display hex_digit_display_6 (.value(LedData[11:8]));  // open: dp
  Hex_Digit_Display hex_digit_display_7 (.value(LedData[7:4]));  // open: dp
  // Probe on \总周期数 
  or or_3 (or_3_out, and_1_out, and_2_out, and_3_out, JAL, JALR);
  Register #(.width(32), .trigger("rising"), .Select("low")) u_PC (
    .D(multiplexer_3_out), .en(not_1_out), .Q(PC), .clk(CLK));  // open: clr
  Hex_Digit_Display hex_digit_display_8 (.value(LedData[3:0]));  // open: dp
  and and_1 (and_1_out, Blt, tunnel);
  and and_2 (and_2_out, Beq, tunnel_t);
  and and_3 (and_3_out, ~tunnel_t, Ben);  // AND_Gate
  Adder #(.width(32)) adder_1 (.a(PC), .b(32'h4), .out(PC_4));  // open: cin, cout
  \多级中断逻辑电路  \u_多级中断逻辑电路_1  (
    .W1(W1), .IRA(IR1_t), .NPC(NPC), .W2(W2), .INT_Add(INT_add), .IRB(IR2_t), .W3(W3), .IRC(IR3_t),
    .INT(INT), .clk(CLK), .csrrci(csrrci), .EPC(EPC), .URET(URET), .csrrsi(csrrsi));
  // RiscV_Probe riscv_probe_1: pin names not known; wires that end beside it: IR
  or or_4 (IR1_t, IR1, IRA);
  ROM #(.addrWidth(10), .dataWidth(32), .Select("high")) rom_1 (.addr(PC[11:2]), .data(IR));
  or or_5 (IR2_t, IR2, IRB);
  \单周期硬布线控制器  \u_单周期硬布线控制器_1  (
    .Funct({IR[30], IR[25], IR[14:12]}), .OP(IR[6:2]), .ALU_OP(\单周期硬布线控制器_1_alu_op ), .MemToReg(MemToReg),
    .MemWrite(MemWrite), .ALU_SRC(\单周期硬布线控制器_1_alu_src ), .RegWrite(RegWrite), .ecall(ecall),
    .Sw(\单周期硬布线控制器_1_sw ), .Jalr(JALR), .Beq(Beq), .JAL(JAL), .Bne(Ben), .in_3(IR[21]), .uret(URET),
    .AUIPC(AUIPC), .LH(LH), .BLT(Blt), .csrrci(csrrci), .csrrsi(csrrsi));
  Multiplexer #(.select(1), .width(5), .disabled("Z"), .enable("false")) multiplexer_4 (
    .in0(IR[19:15]), .in1(5'b10001), .out(multiplexer_4_out), .sel(ecall));
  Multiplexer #(.select(1), .width(5), .disabled("Z"), .enable("false")) multiplexer_5 (
    .in0(IR[24:20]), .in1(5'b01010), .out(multiplexer_5_out), .sel(ecall));
  or or_6 (IR3_t, IR3, IRC);
  ImmGen immgen_1 (.Sw(\单周期硬布线控制器_1_sw ), .Auipc(AUIPC), .B_Type(or_7_out), .jal(JAL), .IR(IR), .Imm(immgen_1_imm));
  or or_7 (or_7_out, Blt, Ben, Beq);
  Regifile regifile_1 (
    .Din(RDin), .Clk(CLK), .R1(R1), .R2(MDin), .WE(RegWrite), .W_num(IR[11:7]), .R1_num(multiplexer_4_out),
    .R2_num(multiplexer_5_out));
  Shifter #(.width(32), .shift("ll")) shifter_1 (.in(immgen_1_imm), .\dist (5'b00001), .out(shifter_1_out));
  not not_2 (not_2_out, halt);
  Counter #(.width(16), .max('hffff), .ongoal("wrap"), .trigger("rising"), .behavior("new")) counter_1 (
    .count(not_2_out), .Q(\总周期数 ), .clk(CLK));  // open: load, D, carry, clr, preset, down
  Multiplexer #(.select(1), .width(32), .disabled("Z"), .enable("false")) multiplexer_6 (
    .in0(MDin), .in1(immgen_1_imm), .out(multiplexer_6_out), .sel(\单周期硬布线控制器_1_alu_src ));
  Adder #(.width(32)) adder_2 (.a(shifter_1_out), .b(PC), .out(adder_2_out));  // open: cin, cout
  ALU alu_1 (
    .X(R1), .Y(multiplexer_6_out), .AluOP(\单周期硬布线控制器_1_alu_op ), .Equal(tunnel_t), .Result(ALUResult),
    .out_6(tunnel));  // open: Result_2, out_4
  Multiplexer #(.select(1), .width(32), .disabled("Z"), .enable("false")) multiplexer_7 (
    .in0(adder_2_out), .in1(ALUResult), .out(branch), .sel(JALR));
  Comparator #(.width(32), .mode("twosComplement")) comparator_6 (
    .a(R1), .b(32'h22), .eq(comparator_6_eq));  // open: gt, lt
  D_Flip_Flop #(.trigger("high"), .Pre_Clr_Positions("LEGACY"), .NegatePresetClear("false"), .enable("true"), .NewFFLayout("false")) d_ff_1 (.Q(d_ff_1_q));  // open: clk, D, Qn, preset, en, reset
  // Probe on 13'hcd
  and and_4 (and_4_out, ecall, not_3_out);
  not not_3 (not_3_out, comparator_6_eq);
  and and_5 (and_5_out, ecall, comparator_6_eq);
  RAM #(.addrWidth(10), .dataWidth(32), .bus("separate"), .Select("high")) ram_1 (
    .addr(ALUResult[11:2]), .din(MDin), .data(ram_1_data), .str(MemWrite), .sel(1'b1), .clk(CLK), .ld(1'b1));  // open: clr
  Comparator #(.width(13), .mode("twosComplement")) comparator_7 (
    .a(CNT_num), .b(13'hcd), .eq(comparator_7_eq), .lt(comparator_7_lt));  // open: gt
  Clock #(.highDuration(1), .lowDuration(1)) clock_1 (.out(clock_1_out));
  and and_6 (halt, and_4_out, not_4_out);
  not not_4 (not_4_out, Go);
  Register #(.width(32), .trigger("rising"), .Select("low")) register_1 (
    .D(MDin), .en(and_5_out), .Q(LedData), .clk(CLK));  // open: clr
  Multiplexer #(.select(1), .width(16), .disabled("Z"), .enable("false")) multiplexer_8 (
    .in0(ram_1_data[15:0]), .in1(ram_1_data[31:16]), .out(multiplexer_8_out), .sel(ALUResult[1]));
  Shifter #(.width(32), .shift("ll")) shifter_2 (.in(immgen_1_imm), .\dist (5'b01100), .out(shifter_2_out));
  Counter #(.width(13), .max('h1fff), .ongoal("stay"), .trigger("rising"), .behavior("old")) counter_2 (
    .count(comparator_7_lt), .Q(CNT_num), .clk(clock_1_out));  // open: load, D, carry, clr, preset
  or or_8 (or_8_out, JAL, JALR);
  assign bit_extender_1_out = {{16{multiplexer_8_out[15]}}, multiplexer_8_out};  // Bit_Extender bit_extender_1
  Adder #(.width(32)) adder_3 (.a(shifter_2_out), .b(PC), .out(adder_3_out));  // open: cin, cout
  nand nand_1 (nand_1_out, d_ff_1_q, comparator_7_eq);
  Priority_Encoder #(.select(2), .disabled("Z")) priority_encoder_1 (
    .in0(1'b1), .in1(MemToReg), .in2(or_8_out), .in3(AUIPC), .out(priority_encoder_1_out));  // open: gs, en_out, en_in
  Multiplexer #(.select(1), .width(32), .disabled("Z"), .enable("false")) multiplexer_9 (
    .in0(ram_1_data), .in1(bit_extender_1_out), .out(multiplexer_9_out), .sel(LH));
  assign CLK = nand_1_out ? clock_1_out : 1'bz;  // Controlled_Buffer controlled_buffer_1
  Pull_Resistor #(.pull(1)) pull_resistor_4 (.node(CLK));
  Multiplexer #(.select(2), .width(32), .disabled("Z"), .enable("false")) multiplexer_10 (
    .in0(ALUResult), .in1(multiplexer_9_out), .in2(PC_4), .in3(adder_3_out), .out(RDin),
    .sel(priority_encoder_1_out));

  // Other names for the same wires on the sheet: R2[31:0] = MDin

  // Notes on the sheet:
  //   中断源
  //   中断等待指示
  //   总复位信号应将除ROM以外所有存储组件全部清零
  //   多级中断测试信号模拟器
  //   数码管输出
  //   数码管输出应该用寄存器锁存，否则显示数据只能一闪而过
  //   指令探针
  //   指令存储器
  //   指令字
  //   contents of rom_1 (hex, n*v repeats v):
  //   7d000113 100413 1f41993 41f9d993 433 c00913 800b13 140413 f47413 800293 100313 499993 89e9b3 1300533
  //   2200893 73 406282b3 fe0294e3 140413 f00f93 1f47433 1c41413 800293 100313 49d993 89e9b3 1300533
  //   2200893 73 406282b3 fe0294e3 1c45413 406b0b33 b0463 f95ff06f 2b3 fff2c293 1029293 fff2e293 500533
  //   2200893 73 f5dff06f 1112023 410113 a12023 410113 812023 410113 1312023 410113 1412023 410113 1512023
  //   410113 1612023 410113 40e073 100b13 300a13 100a93 1600433 441413 14469b3 1300533 2200893 73 fe0416e3
  //   415a0a33 fe0a10e3 40f073 ffc10113 12b03 ffc10113 12a83 ffc10113 12a03 ffc10113 12983 ffc10113 12403
  //   ffc10113 12503 ffc10113 12883 200073 1112023 410113 a12023 410113 812023 410113 1312023 410113
  //   1412023 410113 1512023 410113 1612023 410113 40e073 200b13 300a13 100a93 1600433 441413 14469b3
  //   1300533 2200893 73 fe0416e3 415a0a33 fe0a10e3 40f073 ffc10113 12b03 ffc10113 12a83 ffc10113 12a03
  //   ffc10113 12983 ffc10113 12403 ffc10113 12503 ffc10113 12883 200073 1112023 410113 a12023 410113
  //   812023 410113 1312023 410113 1412023 410113 1512023 410113 1612023 410113 40e073 300b13 300a13
  //   100a93 1600433 441413 14469b3 1300533 2200893 73 fe0416e3 415a0a33 fe0a10e3 40f073 ffc10113 12b03
  //   ffc10113 12a83 ffc10113 12a03 ffc10113 12983 ffc10113 12403 ffc10113 12503 ffc10113 12883 200073
  //   rs1
  //   rs2
  //   rd
  //   Beq
  //   Bne
  //   AluOP
  //   AluSrcB
  //   Sw
  //   为方便自动评测，需要输出PC，IR，寄存器堆写如数据RDin
  //   RAM写使能MemWrite、RAM写入数据MDin等信号
  //   控制位
  //   暂停节拍，不能为0
  //   数据存储器
  //   戳工具置1进入计数暂停模式，ctrl+k时钟自动运行到对应节拍暂停
  //   ctrl+k关闭时钟连续运行，将控制位置零，进入单步调试模式调试
  //   可计数暂停的时钟源
endmodule

module \流水线_多级中断  (
  output RegWrite,
  output MemWrite,
  output [31:0] IF_PC,
  output [31:0] ID_PC,
  output [31:0] EX_PC,
  output [31:0] M_PC,
  output [31:0] WB_PC,
  output [31:0] RDin,
  output [31:0] MDin,
  output [31:0] LedData
);

  wire alu_1_equal, alu_1_out_6, and_1_out, and_2_out, and_3_out, and_4_out, and_5_out, and_6_out, Branch,
       BranchTaken, CLK, clock_1_out, comparator_1_eq, comparator_2_eq, comparator_3_eq, comparator_4_eq,
       comparator_5_eq, comparator_6_eq, comparator_6_lt, comparator_7_eq, controlled_inverter_3_out, csrrci,
       csrrsi, d_ff_1_q, EX_MEM_halt, EX_MEM_lh_2, EX_MEM_memtoreg_2, EX_MEM_regwrite_2, Go,
       \id_ex_重定向_1_alusrcb_2 , \id_ex_重定向_1_auipc_2 , \id_ex_重定向_1_beq_2 , \id_ex_重定向_1_blt_2 ,
       \id_ex_重定向_1_bne_2 , \id_ex_重定向_1_ecall_2 , \id_ex_重定向_1_jal_2 , \id_ex_重定向_1_jalr_2 ,
       \id_ex_重定向_1_lh_2 , \id_ex_重定向_1_memtoreg_2 , \id_ex_重定向_1_memwrite_2 , \id_ex_重定向_1_regwrite_2 , INT,
       IR1, IR2, IR3, IRA, IRB, Jmp, LoadUse, MEM_WB_halt_2, MEM_WB_memtoreg_2, nand_1_out, not_1_out,
       not_2_out, not_3_out, or_1_out, or_2_out, or_3_out, or_4_out, or_5_out, or_6_out, or_8_out, or_11_out,
       riscv_probe_2_p2, riscv_probe_2_p3, RST, stall, URET, W1, W2, W3, WB_halt, \单周期硬布线控制器_1_alu_src ,
       \单周期硬布线控制器_1_auipc , \单周期硬布线控制器_1_beq , \单周期硬布线控制器_1_blt , \单周期硬布线控制器_1_bne , \单周期硬布线控制器_1_ecall ,
       \单周期硬布线控制器_1_jal , \单周期硬布线控制器_1_jalr , \单周期硬布线控制器_1_lh , \单周期硬布线控制器_1_memtoreg ,
       \单周期硬布线控制器_1_memwrite , \单周期硬布线控制器_1_regwrite , \单周期硬布线控制器_1_sw ;
  wire [1:0] \id_ex_重定向_1_rs1_f_2 , \id_ex_重定向_1_rs2_f_2 , \重定向处理_1_rs1_f , \重定向处理_1_rs2_f ;
  wire [3:0] \id_ex_重定向_1_aluop_2 , \单周期硬布线控制器_1_alu_op ;
  wire [4:0] EX_MEM_rd_2, \id_ex_重定向_1_rd_2 , multiplexer_4_out, multiplexer_5_out, WB_rd;
  wire [12:0] CNT_num;
  wire [15:0] \LoadUse次数 , multiplexer_12_out, \总周期数 , \插入气泡数 , \无条件分支数 , \条件分支成功数 ;
  wire [31:0] adder_2_out, adder_3_out, alu_1_result, bit_extender_1_out, branch_t, EPC, EX_IR,
       \id_ex_重定向_1_imm_2 , \id_ex_重定向_1_r1_2 , \id_ex_重定向_1_r2_2 , ID_IR, IF_IR, immgen_1_imm, INT_add,
       MEM_ALUResult, MEM_IR, MEM_WB_result_2, MEM_WB_writedata_2, multiplexer_2_out, multiplexer_3_out,
       multiplexer_6_out, multiplexer_7_out, multiplexer_8_out, multiplexer_9_out, multiplexer_11_out,
       multiplexer_13_out, NPC, PC_4, ram_1_data, regifile_1_r1, regifile_1_r2, shifter_1_out, WB_IR;

  Button \u_总复位  (.out(RST));
  Button _1 (.out(IR1));
  Button _2 (.out(IR2));
  Button _3 (.out(IR3));
  // Probe on \总周期数 
  // Probe on \总周期数 
  Button \u_继续运行  (.out(Go));
  LED #(.active("true")) led_1 (.in(W1));
  LED #(.active("true")) led_2 (.in(W2));
  LED #(.active("true")) led_3 (.in(W3));
  Hex_Digit_Display hex_digit_display_1 (.value(LedData[31:28]));  // open: dp
  // Probe on IF_PC[19:0]
  // RiscV_Probe riscv_probe_1: pin names not known; wires that end beside it: IF_IR
  Comparator #(.width(16), .mode("twosComplement")) comparator_1 (
    .a(16'h258), .b(\总周期数 ), .eq(comparator_1_eq));  // open: gt, lt
  Comparator #(.width(16), .mode("twosComplement")) comparator_2 (
    .a(\总周期数 ), .b(16'h1), .eq(comparator_2_eq));  // open: gt, lt
  Comparator #(.width(16), .mode("twosComplement")) comparator_3 (
    .a(\总周期数 ), .b(16'h4), .eq(comparator_3_eq));  // open: gt, lt
  Comparator #(.width(16), .mode("twosComplement")) comparator_4 (
    .a(\总周期数 ), .b(16'h7), .eq(comparator_4_eq));  // open: gt, lt
  Comparator #(.width(16), .mode("twosComplement")) comparator_5 (
    .a(\总周期数 ), .b(16'h241), .eq(comparator_5_eq));  // open: gt, lt
  Hex_Digit_Display hex_digit_display_2 (.value(LedData[27:24]));  // open: dp
  Hex_Digit_Display hex_digit_display_3 (.value(LedData[23:20]));  // open: dp
  // Probe on ID_PC[19:0]
  // RiscV_Probe riscv_probe_2: pin names not known; wires that end beside it: ID_IR, riscv_probe_2_p2, riscv_probe_2_p3, IRB, IRA
  or or_1 (or_1_out, comparator_1_eq, comparator_2_eq);
  assign riscv_probe_2_p3 = or_1_out ? ~CLK : 1'bz;  // Controlled_Inverter controlled_inverter_1
  assign riscv_probe_2_p2 = comparator_3_eq ? ~CLK : 1'bz;  // Controlled_Inverter controlled_inverter_2
  or or_2 (or_2_out, comparator_4_eq, comparator_5_eq);
  assign controlled_inverter_3_out = or_2_out ? ~CLK : 1'bz;  // Controlled_Inverter controlled_inverter_3
  Hex_Digit_Display hex_digit_display_4 (.value(LedData[15:12]));  // open: dp
  Hex_Digit_Display hex_digit_display_5 (.value(LedData[19:16]));  // open: dp
  Pull_Resistor #(.pull(0)) pull_resistor_1 (.node(riscv_probe_2_p3));
  Pull_Resistor #(.pull(0)) pull_resistor_2 (.node(riscv_probe_2_p2));
  Pull_Resistor #(.pull(0)) pull_resistor_3 (.node(controlled_inverter_3_out));
  Hex_Digit_Display hex_digit_display_6 (.value(LedData[11:8]));  // open: dp
  Hex_Digit_Display hex_digit_display_7 (.value(LedData[7:4]));  // open: dp
  // Probe on EX_PC[19:0]
  // RiscV_Probe riscv_probe_3: pin names not known; wires that end beside it: EX_IR
  Multiplexer #(.select(1), .width(32), .disabled("Z"), .enable("false")) multiplexer_1 (
    .in0(PC_4), .in1(branch_t), .out(NPC), .sel(BranchTaken));
  Hex_Digit_Display hex_digit_display_8 (.value(LedData[3:0]));  // open: dp
  Multiplexer #(.select(1), .width(32), .disabled("Z"), .enable("false")) multiplexer_2 (
    .in0(NPC), .in1(INT_add), .out(multiplexer_2_out), .sel(INT));
  // Probe on \总周期数 
  // Probe on M_PC[19:0]
  // RiscV_Probe riscv_probe_4: pin names not known; wires that end beside it: MEM_IR
  \多级中断逻辑电路  \u_多级中断逻辑电路_1  (
    .W1(W1), .IRA(IR1), .NPC(NPC), .W2(W2), .INT_Add(INT_add), .IRB(IR2), .W3(W3), .IRC(IR3), .INT(INT),
    .clk(CLK), .csrrci(csrrci), .EPC(EPC), .URET(URET), .csrrsi(csrrsi));
  or or_3 (or_3_out, WB_halt, stall);
  not not_1 (not_1_out, or_3_out);
  Multiplexer #(.select(1), .width(32), .disabled("Z"), .enable("false")) multiplexer_3 (
    .in0(multiplexer_2_out), .in1(EPC), .out(multiplexer_3_out), .sel(URET));
  // Probe on \总周期数 
  // Probe on \无条件分支数 
  // Probe on \条件分支成功数 
  // Probe on \插入气泡数 
  // Probe on \LoadUse次数 
  Register #(.width(32), .trigger("rising"), .Select("low")) PC (
    .D(multiplexer_3_out), .en(not_1_out), .Q(IF_PC), .clk(CLK), .clr(RST));
  // Probe on IF_PC[11:0]
  // Probe on WB_PC[19:0]
  // RiscV_Probe riscv_probe_5: pin names not known; wires that end beside it: WB_IR
  Adder #(.width(32)) adder_1 (.a(IF_PC), .b(32'h4), .out(PC_4));  // open: cin, cout
  // Probe on ID_PC[11:0]
  // Probe on EX_PC[11:0]
  Counter #(.width(16), .max('hffff), .ongoal("wrap"), .trigger("rising"), .behavior("new")) counter_1 (
    .Q(\条件分支成功数 ), .clk(Branch));  // open: load, D, count, carry, clr, preset, down
  ROM #(.addrWidth(10), .dataWidth(32), .Select("high")) \u_指令存储器  (.addr(IF_PC[11:2]), .data(IF_IR));
  // Probe on M_PC[11:0]
  D_Flip_Flop #(.trigger("high"), .Pre_Clr_Positions("LEGACY"), .NegatePresetClear("false"), .enable("true"), .NewFFLayout("false")) d_ff_1 (.Q(d_ff_1_q));  // open: clk, D, Qn, preset, en, reset
  // Probe on 13'h10
  not not_2 (not_2_out, or_4_out);
  or or_4 (or_4_out, stall, WB_halt);
  // Probe on WB_PC[11:0]
  Comparator #(.width(13), .mode("twosComplement")) comparator_6 (
    .a(CNT_num), .b(13'h10), .eq(comparator_6_eq), .lt(comparator_6_lt));  // open: gt
  Clock #(.highDuration(1), .lowDuration(1)) clock_1 (.out(clock_1_out));
  Counter #(.width(16), .max('hffff), .ongoal("wrap"), .trigger("rising"), .behavior("new")) counter_2 (
    .Q(\无条件分支数 ), .clk(Jmp));  // open: load, D, count, carry, clr, preset, down
  IF_ID IF_ID (
    .IR(IF_IR), .PC(IF_PC), .IR_2(ID_IR), .PC_2(ID_PC), .clk(CLK), .rst(RST), .flush(BranchTaken),
    .en(not_2_out));  // open: pre, pre_2
  nand nand_1 (nand_1_out, d_ff_1_q, comparator_6_eq);
  Counter #(.width(13), .max('h1fff), .ongoal("stay"), .trigger("rising"), .behavior("old")) counter_3 (
    .count(comparator_6_lt), .Q(CNT_num), .clk(clock_1_out));  // open: load, D, carry, clr, preset
  \单周期硬布线控制器  \u_单周期硬布线控制器_1  (
    .Funct({ID_IR[30], ID_IR[25], ID_IR[14:12]}), .OP(ID_IR[6:2]), .ALU_OP(\单周期硬布线控制器_1_alu_op ),
    .MemToReg(\单周期硬布线控制器_1_memtoreg ), .MemWrite(\单周期硬布线控制器_1_memwrite ), .ALU_SRC(\单周期硬布线控制器_1_alu_src ),
    .RegWrite(\单周期硬布线控制器_1_regwrite ), .ecall(\单周期硬布线控制器_1_ecall ), .Sw(\单周期硬布线控制器_1_sw ),
    .Jalr(\单周期硬布线控制器_1_jalr ), .Beq(\单周期硬布线控制器_1_beq ), .JAL(\单周期硬布线控制器_1_jal ), .Bne(\单周期硬布线控制器_1_bne ),
    .in_3(ID_IR[21]), .uret(URET), .AUIPC(\单周期硬布线控制器_1_auipc ), .LH(\单周期硬布线控制器_1_lh ),
    .BLT(\单周期硬布线控制器_1_blt ), .csrrci(csrrci), .csrrsi(csrrsi));
  assign CLK = nand_1_out ? clock_1_out : 1'bz;  // Controlled_Buffer controlled_buffer_1
  Counter #(.width(16), .max('hffff), .ongoal("wrap"), .trigger("rising"), .behavior("new")) counter_4 (
    .Q(\插入气泡数 ), .clk(or_5_out));  // open: load, D, count, carry, clr, preset, down
  or or_5 (or_5_out, BranchTaken, stall);
  Multiplexer #(.select(1), .width(5), .disabled("Z"), .enable("false")) multiplexer_4 (
    .in0(ID_IR[19:15]), .in1(5'b10001), .out(multiplexer_4_out), .sel(\单周期硬布线控制器_1_ecall ));
  Multiplexer #(.select(1), .width(5), .disabled("Z"), .enable("false")) multiplexer_5 (
    .in0(ID_IR[24:20]), .in1(5'b01010), .out(multiplexer_5_out), .sel(\单周期硬布线控制器_1_ecall ));
  or or_6 (or_6_out, \单周期硬布线控制器_1_blt , \单周期硬布线控制器_1_bne , \单周期硬布线控制器_1_beq );
  Pull_Resistor #(.pull(1)) pull_resistor_4 (.node(CLK));
  ImmGen immgen_1 (
    .Sw(\单周期硬布线控制器_1_sw ), .Auipc(\单周期硬布线控制器_1_auipc ), .B_Type(or_6_out), .jal(\单周期硬布线控制器_1_jal ),
    .IR(ID_IR), .Imm(immgen_1_imm));
  Counter #(.width(16), .max('hffff), .ongoal("wrap"), .trigger("rising"), .behavior("new")) counter_5 (
    .Q(\LoadUse次数 ), .clk(stall));  // open: load, D, count, carry, clr, preset, down
  not not_3 (not_3_out, WB_halt);
  Regifile regifile_1 (
    .Din(RDin), .Clk(CLK), .R1(regifile_1_r1), .R2(regifile_1_r2), .WE(RegWrite), .W_num(WB_rd),
    .R1_num(multiplexer_4_out), .R2_num(multiplexer_5_out));
  Counter #(.width(16), .max('hffff), .ongoal("wrap"), .trigger("rising"), .behavior("new")) counter_6 (
    .Q(\总周期数 ), .clk(and_1_out));  // open: load, D, count, carry, clr, preset, down
  and and_1 (and_1_out, ~WB_halt, CLK);  // AND_Gate
  or or_7 (BranchTaken, Branch, Jmp);
  or or_8 (or_8_out, stall, BranchTaken);
  \ID_EX_重定向  \id_ex_重定向_1  (
    .rs1_f(\重定向处理_1_rs1_f ), .rs2_f(\重定向处理_1_rs2_f ), .Lh(\单周期硬布线控制器_1_lh ), .Auipc(\单周期硬布线控制器_1_auipc ),
    .Blt(\单周期硬布线控制器_1_blt ), .Beq(\单周期硬布线控制器_1_beq ), .Bne(\单周期硬布线控制器_1_bne ),
    .MemToReg(\单周期硬布线控制器_1_memtoreg ), .MemWrite(\单周期硬布线控制器_1_memwrite ), .AluSrcB(\单周期硬布线控制器_1_alu_src ),
    .RegWrite(\单周期硬布线控制器_1_regwrite ), .ecall(\单周期硬布线控制器_1_ecall ), .JAL(\单周期硬布线控制器_1_jal ),
    .Jalr(\单周期硬布线控制器_1_jalr ), .AluOP(\单周期硬布线控制器_1_alu_op ), .rd(ID_IR[11:7]), .R1(regifile_1_r1),
    .R2(regifile_1_r2), .imm(immgen_1_imm), .PC(ID_IR), .IR(ID_PC), .rs1_f_2(\id_ex_重定向_1_rs1_f_2 ),
    .rs2_f_2(\id_ex_重定向_1_rs2_f_2 ), .Lh_2(\id_ex_重定向_1_lh_2 ), .Auipc_2(\id_ex_重定向_1_auipc_2 ),
    .Blt_2(\id_ex_重定向_1_blt_2 ), .Beq_2(\id_ex_重定向_1_beq_2 ), .Bne_2(\id_ex_重定向_1_bne_2 ),
    .MemToReg_2(\id_ex_重定向_1_memtoreg_2 ), .MemWrite_2(\id_ex_重定向_1_memwrite_2 ),
    .AluSrcB_2(\id_ex_重定向_1_alusrcb_2 ), .RegWrite_2(\id_ex_重定向_1_regwrite_2 ),
    .ecall_2(\id_ex_重定向_1_ecall_2 ), .JAL_2(\id_ex_重定向_1_jal_2 ), .Jalr_2(\id_ex_重定向_1_jalr_2 ),
    .AluOP_2(\id_ex_重定向_1_aluop_2 ), .rd_2(\id_ex_重定向_1_rd_2 ), .R1_2(\id_ex_重定向_1_r1_2 ),
    .R2_2(\id_ex_重定向_1_r2_2 ), .imm_2(\id_ex_重定向_1_imm_2 ), .PC_2(EX_IR), .IR_2(EX_PC), .flush(or_8_out),
    .rst(RST), .en(not_3_out), .clk(CLK));  // open: pre, pre_2
  or or_9 (Branch, and_5_out, and_3_out, and_2_out);
  or or_10 (Jmp, \id_ex_重定向_1_jal_2 , \id_ex_重定向_1_jalr_2 );
  Multiplexer #(.select(2), .width(32), .disabled("Z"), .enable("false")) multiplexer_6 (
    .in0(\id_ex_重定向_1_r1_2 ), .in1(RDin), .in2(MEM_ALUResult), .in3(MEM_ALUResult), .out(multiplexer_6_out),
    .sel(\id_ex_重定向_1_rs1_f_2 ));
  Multiplexer #(.select(2), .width(32), .disabled("Z"), .enable("false")) multiplexer_7 (
    .in0(\id_ex_重定向_1_r2_2 ), .in1(RDin), .in2(MEM_ALUResult), .in3(MEM_ALUResult), .out(multiplexer_7_out),
    .sel(\id_ex_重定向_1_rs2_f_2 ));
  Multiplexer #(.select(1), .width(32), .disabled("Z"), .enable("false")) multiplexer_8 (
    .in0(multiplexer_7_out), .in1(\id_ex_重定向_1_imm_2 ), .out(multiplexer_8_out), .sel(\id_ex_重定向_1_alusrcb_2 ));
  and and_2 (and_2_out, \id_ex_重定向_1_beq_2 , alu_1_equal);
  and and_3 (and_3_out, \id_ex_重定向_1_bne_2 , ~alu_1_equal);  // AND_Gate
  Multiplexer #(.select(1), .width(32), .disabled("Z"), .enable("false")) multiplexer_9 (
    .in0(multiplexer_6_out), .in1(EX_PC), .out(multiplexer_9_out), .sel(\id_ex_重定向_1_auipc_2 ));
  Shifter #(.width(32), .shift("ll")) shifter_1 (.in(\id_ex_重定向_1_imm_2 ), .\dist (5'b00001), .out(shifter_1_out));
  Comparator #(.width(32), .mode("twosComplement")) comparator_7 (
    .a(multiplexer_6_out), .b(32'h22), .eq(comparator_7_eq));  // open: gt, lt
  and and_4 (and_4_out, comparator_7_eq, \id_ex_重定向_1_ecall_2 );
  and and_5 (and_5_out, \id_ex_重定向_1_blt_2 , alu_1_out_6);
  ALU alu_1 (
    .X(multiplexer_9_out), .Y(multiplexer_8_out), .AluOP(\id_ex_重定向_1_aluop_2 ), .Equal(alu_1_equal),
    .Result(alu_1_result), .out_6(alu_1_out_6));  // open: Result_2, out_4
  Adder #(.width(32)) adder_2 (.a(shifter_1_out), .b(EX_PC), .out(adder_2_out));  // open: cin, cout
  Multiplexer #(.select(1), .width(32), .disabled("Z"), .enable("false")) multiplexer_10 (
    .in0(adder_2_out), .in1(alu_1_result), .out(branch_t), .sel(\id_ex_重定向_1_jalr_2 ));
  and and_6 (and_6_out, \id_ex_重定向_1_ecall_2 , ~comparator_7_eq);  // AND_Gate
  Register #(.width(32), .trigger("rising"), .Select("low")) register_1 (
    .D(multiplexer_7_out), .en(and_4_out), .Q(LedData), .clk(CLK));  // open: clr
  or or_11 (or_11_out, \id_ex_重定向_1_jal_2 , \id_ex_重定向_1_jalr_2 );
  Adder #(.width(32)) adder_3 (.a(32'h4), .b(EX_PC), .out(adder_3_out));  // open: cin, cout
  EX_MEM EX_MEM (
    .MemToReg(\id_ex_重定向_1_memtoreg_2 ), .MemWrite(\id_ex_重定向_1_memwrite_2 ),
    .RegWrite(\id_ex_重定向_1_regwrite_2 ), .IR(EX_IR), .MemToReg_2(EX_MEM_memtoreg_2), .MemWrite_2(MemWrite),
    .RegWrite_2(EX_MEM_regwrite_2), .IR_2(MEM_IR), .PC(EX_PC), .PC_2(M_PC), .rst(RST), .clk(CLK),
    .Result(multiplexer_11_out), .Result_2(MEM_ALUResult), .WriteData(multiplexer_7_out), .WriteData_2(MDin),
    .lh(\id_ex_重定向_1_lh_2 ), .lh_2(EX_MEM_lh_2), .rd(\id_ex_重定向_1_rd_2 ), .rd_2(EX_MEM_rd_2), .en(not_3_out),
    .hait(and_6_out), .halt(EX_MEM_halt));
  Multiplexer #(.select(1), .width(32), .disabled("Z"), .enable("false")) multiplexer_11 (
    .in0(alu_1_result), .in1(adder_3_out), .out(multiplexer_11_out), .sel(or_11_out));
  \重定向处理  \u_重定向处理_1  (
    .IR(ID_IR), .rs1_f(\重定向处理_1_rs1_f ), .rs1(multiplexer_4_out), .rs2(multiplexer_5_out),
    .EX_rd(\id_ex_重定向_1_rd_2 ), .MEM_rd(EX_MEM_rd_2), .EX_RegWrite(\id_ex_重定向_1_regwrite_2 ),
    .MEM_RegWrite(EX_MEM_regwrite_2), .EX_MemToReg(\id_ex_重定向_1_memtoreg_2 ), .rs2_f(\重定向处理_1_rs2_f ),
    .Stall(stall), .LoadUse(LoadUse));
  RAM #(.addrWidth(10), .dataWidth(32), .bus("separate"), .Select("high")) ram_1 (
    .addr(MEM_ALUResult[11:2]), .din(MDin), .data(ram_1_data), .str(MemWrite), .sel(1'b1), .clk(CLK),
    .ld(1'b1), .clr(RST));
  Multiplexer #(.select(1), .width(16), .disabled("Z"), .enable("false")) multiplexer_12 (
    .in0(ram_1_data[15:0]), .in1(ram_1_data[31:16]), .out(multiplexer_12_out), .sel(MEM_ALUResult[1]));
  MEM_WB MEM_WB (
    .MemToReg(EX_MEM_memtoreg_2), .MemToReg_2(MEM_WB_memtoreg_2), .RegWrite(EX_MEM_regwrite_2),
    .RegWrite_2(RegWrite), .Result(MEM_ALUResult), .Result_2(MEM_WB_result_2),
    .WriteData(multiplexer_13_out), .WriteData_2(MEM_WB_writedata_2), .rd_2(WB_rd), .IR(MEM_IR),
    .IR_2(WB_IR), .PC(M_PC), .PC_2(WB_PC), .rst(RST), .clk(CLK), .rd(EX_MEM_rd_2), .en(not_3_out),
    .halt_2(MEM_WB_halt_2), .halt(EX_MEM_halt));
  Multiplexer #(.select(1), .width(32), .disabled("Z"), .enable("false")) multiplexer_13 (
    .in0(ram_1_data), .in1(bit_extender_1_out), .out(multiplexer_13_out), .sel(EX_MEM_lh_2));
  assign bit_extender_1_out = {{16{multiplexer_12_out[15]}}, multiplexer_12_out};  // Bit_Extender bit_extender_1
  Multiplexer #(.select(1), .width(32), .disabled("Z"), .enable("false")) multiplexer_14 (
    .in0(MEM_WB_result_2), .in1(MEM_WB_writedata_2), .out(RDin), .sel(MEM_WB_memtoreg_2));
  and and_7 (WB_halt, ~Go, MEM_WB_halt_2);  // AND_Gate

  // Other names for the same wires on the sheet: MEM_PC[31:0] = M_PC

  // Notes on the sheet:
  //   中断源
  //   时空图监测，可删除
  //   中断等待指示
  //   多级中断测试信号模拟器
  //   数码管输出
  //   IF阶段
  //   控制位
  //   contents of 指令存储器 (hex, n*v repeats v):
  //   7d000113 100413 1f41993 41f9d993 433 c00913 800b13 140413 f47413 800293 100313 499993 89e9b3 1300533
  //   2200893 73 406282b3 fe0294e3 140413 f00f93 1f47433 1c41413 800293 100313 49d993 89e9b3 1300533
  //   2200893 73 406282b3 fe0294e3 1c45413 406b0b33 b0463 f95ff06f 2b3 fff2c293 1029293 fff2e293 500533
  //   2200893 73 f5dff06f 1112023 410113 a12023 410113 812023 410113 1312023 410113 1412023 410113 1512023
  //   410113 1612023 410113 40e073 100b13 300a13 100a93 1600433 441413 14469b3 1300533 2200893 73 fe0416e3
  //   415a0a33 fe0a10e3 40f073 ffc10113 12b03 ffc10113 12a83 ffc10113 12a03 ffc10113 12983 ffc10113 12403
  //   ffc10113 12503 ffc10113 12883 200073 1112023 410113 a12023 410113 812023 410113 1312023 410113
  //   1412023 410113 1512023 410113 1612023 410113 40e073 200b13 300a13 100a93 1600433 441413 14469b3
  //   1300533 2200893 73 fe0416e3 415a0a33 fe0a10e3 40f073 ffc10113 12b03 ffc10113 12a83 ffc10113 12a03
  //   ffc10113 12983 ffc10113 12403 ffc10113 12503 ffc10113 12883 200073 1112023 410113 a12023 410113
  //   812023 410113 1312023 410113 1412023 410113 1512023 410113 1612023 410113 40e073 300b13 300a13
  //   100a93 1600433 441413 14469b3 1300533 2200893 73 fe0416e3 415a0a33 fe0a10e3 40f073 ffc10113 12b03
  //   ffc10113 12a83 ffc10113 12a03 ffc10113 12983 ffc10113 12403 ffc10113 12503 ffc10113 12883 200073
  //   流水调试日志用
  //   暂停节拍，不能为0
  //   戳工具置1进入计数暂停模式，ctrl+k时钟自动运行到对应节拍暂停
  //   ctrl+k关闭时钟连续运行，将控制位置零，进入单步调试模式调试
  //   rs1
  //   rs2
  //   rd
  //   可计数暂停的时钟源
  //   ID阶段
  //   为方便自动评测，需要输出流水线各段保存的PC值，注意是PC不是PC+4，另外ID段寄存器写入信息，Mem段内存写入信息也要输出
  //   EX阶段
  //   MEM阶段
  //   数据存储器
  //   WB阶段
endmodule

module IF_ID (
  input  pre,
  input  [31:0] IR,
  input  [31:0] PC,
  input  clk,
  input  rst,
  input  en,
  input  flush,
  output pre_2,
  output [31:0] IR_2,
  output [31:0] PC_2
);

  wire multiplexer_1_out, or_1_out;
  wire [31:0] multiplexer_2_out, multiplexer_3_out;

  Multiplexer #(.select(1), .width(1), .disabled("Z"), .enable("false")) multiplexer_1 (
    .in0(pre), .in1(1'b0), .out(multiplexer_1_out), .sel(or_1_out));
  Multiplexer #(.select(1), .width(32), .disabled("Z"), .enable("false")) multiplexer_2 (
    .in0(IR), .in1({32{1'b0}}), .out(multiplexer_2_out), .sel(or_1_out));
  Multiplexer #(.select(1), .width(32), .disabled("Z"), .enable("false")) multiplexer_3 (
    .in0(PC), .in1({32{1'b0}}), .out(multiplexer_3_out), .sel(or_1_out));
  or or_1 (or_1_out, flush, rst);
  Register #(.width(1), .trigger("rising"), .Select("low")) register_1 (
    .D(multiplexer_1_out), .en(en), .Q(pre_2), .clk(clk));  // open: clr
  Register #(.width(32), .trigger("rising"), .Select("low")) register_2 (
    .D(multiplexer_2_out), .en(en), .Q(IR_2), .clk(clk));  // open: clr
  Register #(.width(32), .trigger("rising"), .Select("low")) register_3 (
    .D(multiplexer_3_out), .en(en), .Q(PC_2), .clk(clk));  // open: clr
endmodule

module ID_EX (
  input  pre,
  input  Lh,
  input  Auipc,
  input  Blt,
  input  Beq,
  input  Bne,
  input  MemToReg,
  input  MemWrite,
  input  AluSrcB,
  input  RegWrite,
  input  ecall,
  input  JAL,
  input  Jalr,
  input  [3:0] AluOP,
  input  [4:0] rd,
  input  [31:0] R1,
  input  [31:0] R2,
  input  [31:0] imm,
  input  [31:0] PC,
  input  [31:0] IR,
  input  en,
  input  clk,
  input  rst,
  input  flush,
  output pre_2,
  output Lh_2,
  output Auipc_2,
  output Blt_2,
  output Beq_2,
  output Bne_2,
  output MemToReg_2,
  output MemWrite_2,
  output AluSrcB_2,
  output RegWrite_2,
  output ecall_2,
  output JAL_2,
  output Jalr_2,
  output [3:0] AluOP_2,
  output [4:0] rd_2,
  output [31:0] R1_2,
  output [31:0] R2_2,
  output [31:0] imm_2,
  output [31:0] PC_2,
  output [31:0] IR_2
);

  wire multiplexer_1_out, multiplexer_2_out, multiplexer_3_out, multiplexer_4_out, multiplexer_5_out,
       multiplexer_6_out, multiplexer_7_out, multiplexer_8_out, multiplexer_9_out, multiplexer_10_out,
       multiplexer_11_out, multiplexer_12_out, multiplexer_13_out, or_1_out;
  wire [3:0] multiplexer_14_out;
  wire [4:0] multiplexer_15_out;
  wire [31:0] multiplexer_16_out, multiplexer_17_out, multiplexer_18_out, multiplexer_19_out,
       multiplexer_20_out;

  Multiplexer #(.select(1), .width(1), .disabled("Z"), .enable("false")) multiplexer_1 (
    .in0(pre), .in1(1'b0), .out(multiplexer_1_out), .sel(or_1_out));
  Multiplexer #(.select(1), .width(1), .disabled("Z"), .enable("false")) multiplexer_2 (
    .in0(Lh), .in1(1'b0), .out(multiplexer_2_out), .sel(or_1_out));
  Multiplexer #(.select(1), .width(1), .disabled("Z"), .enable("false")) multiplexer_3 (
    .in0(Auipc), .in1(1'b0), .out(multiplexer_3_out), .sel(or_1_out));
  Multiplexer #(.select(1), .width(1), .disabled("Z"), .enable("false")) multiplexer_4 (
    .in0(Blt), .in1(1'b0), .out(multiplexer_4_out), .sel(or_1_out));
  Multiplexer #(.select(1), .width(1), .disabled("Z"), .enable("false")) multiplexer_5 (
    .in0(Beq), .in1(1'b0), .out(multiplexer_5_out), .sel(or_1_out));
  Multiplexer #(.select(1), .width(1), .disabled("Z"), .enable("false")) multiplexer_6 (
    .in0(Bne), .in1(1'b0), .out(multiplexer_6_out), .sel(or_1_out));
  Multiplexer #(.select(1), .width(1), .disabled("Z"), .enable("false")) multiplexer_7 (
    .in0(MemToReg), .in1(1'b0), .out(multiplexer_7_out), .sel(or_1_out));
  Multiplexer #(.select(1), .width(1), .disabled("Z"), .enable("false")) multiplexer_8 (
    .in0(MemWrite), .in1(1'b0), .out(multiplexer_8_out), .sel(or_1_out));
  Multiplexer #(.select(1), .width(1), .disabled("Z"), .enable("false")) multiplexer_9 (
    .in0(AluSrcB), .in1(1'b0), .out(multiplexer_9_out), .sel(or_1_out));
  Multiplexer #(.select(1), .width(1), .disabled("Z"), .enable("false")) multiplexer_10 (
    .in0(RegWrite), .in1(1'b0), .out(multiplexer_10_out), .sel(or_1_out));
  Multiplexer #(.select(1), .width(1), .disabled("Z"), .enable("false")) multiplexer_11 (
    .in0(ecall), .in1(1'b0), .out(multiplexer_11_out), .sel(or_1_out));
  Multiplexer #(.select(1), .width(1), .disabled("Z"), .enable("false")) multiplexer_12 (
    .in0(JAL), .in1(1'b0), .out(multiplexer_12_out), .sel(or_1_out));
  Multiplexer #(.select(1), .width(1), .disabled("Z"), .enable("false")) multiplexer_13 (
    .in0(Jalr), .in1(1'b0), .out(multiplexer_13_out), .sel(or_1_out));
  Multiplexer #(.select(1), .width(4), .disabled("Z"), .enable("false")) multiplexer_14 (
    .in0(AluOP), .in1(4'b0000), .out(multiplexer_14_out), .sel(or_1_out));
  Multiplexer #(.select(1), .width(5), .disabled("Z"), .enable("false")) multiplexer_15 (
    .in0(rd), .in1({5{1'b0}}), .out(multiplexer_15_out), .sel(or_1_out));
  Multiplexer #(.select(1), .width(32), .disabled("Z"), .enable("false")) multiplexer_16 (
    .in0(R1), .in1({32{1'b0}}), .out(multiplexer_16_out), .sel(or_1_out));
  Multiplexer #(.select(1), .width(32), .disabled("Z"), .enable("false")) multiplexer_17 (
    .in0(R2), .in1({32{1'b0}}), .out(multiplexer_17_out), .sel(or_1_out));
  Multiplexer #(.select(1), .width(32), .disabled("Z"), .enable("false")) multiplexer_18 (
    .in0(imm), .in1({32{1'b0}}), .out(multiplexer_18_out), .sel(or_1_out));
  Multiplexer #(.select(1), .width(32), .disabled("Z"), .enable("false")) multiplexer_19 (
    .in0(PC), .in1({32{1'b0}}), .out(multiplexer_19_out), .sel(or_1_out));
  Multiplexer #(.select(1), .width(32), .disabled("Z"), .enable("false")) multiplexer_20 (
    .in0(IR), .in1({32{1'b0}}), .out(multiplexer_20_out), .sel(or_1_out));
  or or_1 (or_1_out, flush, rst);
  Register #(.width(1), .trigger("rising"), .Select("low")) register_1 (
    .D(multiplexer_1_out), .en(en), .Q(pre_2), .clk(clk));  // open: clr
  Register #(.width(1), .trigger("rising"), .Select("low")) register_2 (
    .D(multiplexer_2_out), .en(en), .Q(Lh_2), .clk(clk));  // open: clr
  Register #(.width(1), .trigger("rising"), .Select("low")) register_3 (
    .D(multiplexer_3_out), .en(en), .Q(Auipc_2), .clk(clk));  // open: clr
  Register #(.width(1), .trigger("rising"), .Select("low")) register_4 (
    .D(multiplexer_4_out), .en(en), .Q(Blt_2), .clk(clk));  // open: clr
  Register #(.width(1), .trigger("rising"), .Select("low")) register_5 (
    .D(multiplexer_5_out), .en(en), .Q(Beq_2), .clk(clk));  // open: clr
  Register #(.width(1), .trigger("rising"), .Select("low")) register_6 (
    .D(multiplexer_6_out), .en(en), .Q(Bne_2), .clk(clk));  // open: clr
  Register #(.width(1), .trigger("rising"), .Select("low")) register_7 (
    .D(multiplexer_7_out), .en(en), .Q(MemToReg_2), .clk(clk));  // open: clr
  Register #(.width(1), .trigger("rising"), .Select("low")) register_8 (
    .D(multiplexer_8_out), .en(en), .Q(MemWrite_2), .clk(clk));  // open: clr
  Register #(.width(1), .trigger("rising"), .Select("low")) register_9 (
    .D(multiplexer_9_out), .en(en), .Q(AluSrcB_2), .clk(clk));  // open: clr
  Register #(.width(1), .trigger("rising"), .Select("low")) register_10 (
    .D(multiplexer_10_out), .en(en), .Q(RegWrite_2), .clk(clk));  // open: clr
  Register #(.width(1), .trigger("rising"), .Select("low")) register_11 (
    .D(multiplexer_11_out), .en(en), .Q(ecall_2), .clk(clk));  // open: clr
  Register #(.width(1), .trigger("rising"), .Select("low")) register_12 (
    .D(multiplexer_12_out), .en(en), .Q(JAL_2), .clk(clk));  // open: clr
  Register #(.width(1), .trigger("rising"), .Select("low")) register_13 (
    .D(multiplexer_13_out), .en(en), .Q(Jalr_2), .clk(clk));  // open: clr
  Register #(.width(4), .trigger("rising"), .Select("low")) register_14 (
    .D(multiplexer_14_out), .en(en), .Q(AluOP_2), .clk(clk));  // open: clr
  Register #(.width(5), .trigger("rising"), .Select("low")) register_15 (
    .D(multiplexer_15_out), .en(en), .Q(rd_2), .clk(clk));  // open: clr
  Register #(.width(32), .trigger("rising"), .Select("low")) register_16 (
    .D(multiplexer_16_out), .en(en), .Q(R1_2), .clk(clk));  // open: clr
  Register #(.width(32), .trigger("rising"), .Select("low")) register_17 (
    .D(multiplexer_17_out), .en(en), .Q(R2_2), .clk(clk));  // open: clr
  Register #(.width(32), .trigger("rising"), .Select("low")) register_18 (
    .D(multiplexer_18_out), .en(en), .Q(imm_2), .clk(clk));  // open: clr
  Register #(.width(32), .trigger("rising"), .Select("low")) register_19 (
    .D(multiplexer_19_out), .en(en), .Q(PC_2), .clk(clk));  // open: clr
  Register #(.width(32), .trigger("rising"), .Select("low")) register_20 (
    .D(multiplexer_20_out), .en(en), .Q(IR_2), .clk(clk));  // open: clr
endmodule

module EX_MEM (
  input  lh,
  input  MemToReg,
  input  MemWrite,
  input  RegWrite,
  input  hait,
  input  [4:0] rd,
  input  [31:0] Result,
  input  [31:0] WriteData,
  input  [31:0] IR,
  input  [31:0] PC,
  input  rst,
  input  en,
  input  clk,
  output lh_2,
  output MemToReg_2,
  output MemWrite_2,
  output RegWrite_2,
  output halt,
  output [4:0] rd_2,
  output [31:0] Result_2,
  output [31:0] WriteData_2,
  output [31:0] IR_2,
  output [31:0] PC_2
);

  wire multiplexer_1_out, multiplexer_2_out, multiplexer_3_out, multiplexer_4_out, multiplexer_5_out;
  wire [4:0] multiplexer_6_out;
  wire [31:0] multiplexer_7_out, multiplexer_8_out, multiplexer_9_out, multiplexer_10_out;

  Multiplexer #(.select(1), .width(1), .disabled("Z"), .enable("false")) multiplexer_1 (
    .in0(lh), .in1(1'b0), .out(multiplexer_1_out), .sel(rst));
  Multiplexer #(.select(1), .width(1), .disabled("Z"), .enable("false")) multiplexer_2 (
    .in0(MemToReg), .in1(1'b0), .out(multiplexer_2_out), .sel(rst));
  Multiplexer #(.select(1), .width(1), .disabled("Z"), .enable("false")) multiplexer_3 (
    .in0(MemWrite), .in1(1'b0), .out(multiplexer_3_out), .sel(rst));
  Multiplexer #(.select(1), .width(1), .disabled("Z"), .enable("false")) multiplexer_4 (
    .in0(RegWrite), .in1(1'b0), .out(multiplexer_4_out), .sel(rst));
  Multiplexer #(.select(1), .width(1), .disabled("Z"), .enable("false")) multiplexer_5 (
    .in0(hait), .in1(1'b0), .out(multiplexer_5_out), .sel(rst));
  Multiplexer #(.select(1), .width(5), .disabled("Z"), .enable("false")) multiplexer_6 (
    .in0(rd), .in1({5{1'b0}}), .out(multiplexer_6_out), .sel(rst));
  Multiplexer #(.select(1), .width(32), .disabled("Z"), .enable("false")) multiplexer_7 (
    .in0(Result), .in1({32{1'b0}}), .out(multiplexer_7_out), .sel(rst));
  Multiplexer #(.select(1), .width(32), .disabled("Z"), .enable("false")) multiplexer_8 (
    .in0(WriteData), .in1({32{1'b0}}), .out(multiplexer_8_out), .sel(rst));
  Multiplexer #(.select(1), .width(32), .disabled("Z"), .enable("false")) multiplexer_9 (
    .in0(IR), .in1({32{1'b0}}), .out(multiplexer_9_out), .sel(rst));
  Multiplexer #(.select(1), .width(32), .disabled("Z"), .enable("false")) multiplexer_10 (
    .in0(PC), .in1({32{1'b0}}), .out(multiplexer_10_out), .sel(rst));
  Register #(.width(1), .trigger("rising"), .Select("low")) register_1 (
    .D(multiplexer_1_out), .en(en), .Q(lh_2), .clk(clk));  // open: clr
  Register #(.width(1), .trigger("rising"), .Select("low")) register_2 (
    .D(multiplexer_2_out), .en(en), .Q(MemToReg_2), .clk(clk));  // open: clr
  Register #(.width(1), .trigger("rising"), .Select("low")) register_3 (
    .D(multiplexer_3_out), .en(en), .Q(MemWrite_2), .clk(clk));  // open: clr
  Register #(.width(1), .trigger("rising"), .Select("low")) register_4 (
    .D(multiplexer_4_out), .en(en), .Q(RegWrite_2), .clk(clk));  // open: clr
  Register #(.width(1), .trigger("rising"), .Select("low")) register_5 (
    .D(multiplexer_5_out), .en(en), .Q(halt), .clk(clk));  // open: clr
  Register #(.width(5), .trigger("rising"), .Select("low")) register_6 (
    .D(multiplexer_6_out), .en(en), .Q(rd_2), .clk(clk));  // open: clr
  Register #(.width(32), .trigger("rising"), .Select("low")) register_7 (
    .D(multiplexer_7_out), .en(en), .Q(Result_2), .clk(clk));  // open: clr
  Register #(.width(32), .trigger("rising"), .Select("low")) register_8 (
    .D(multiplexer_8_out), .en(en), .Q(WriteData_2), .clk(clk));  // open: clr
  Register #(.width(32), .trigger("rising"), .Select("low")) register_9 (
    .D(multiplexer_9_out), .en(en), .Q(IR_2), .clk(clk));  // open: clr
  Register #(.width(32), .trigger("rising"), .Select("low")) register_10 (
    .D(multiplexer_10_out), .en(en), .Q(PC_2), .clk(clk));  // open: clr
endmodule

module MEM_WB (
  input  MemToReg,
  input  RegWrite,
  input  halt,
  input  [4:0] rd,
  input  [31:0] Result,
  input  [31:0] WriteData,
  input  [31:0] IR,
  input  [31:0] PC,
  input  rst,
  input  clk,
  input  en,
  output MemToReg_2,
  output RegWrite_2,
  output halt_2,
  output [4:0] rd_2,
  output [31:0] Result_2,
  output [31:0] WriteData_2,
  output [31:0] IR_2,
  output [31:0] PC_2
);

  wire multiplexer_1_out, multiplexer_2_out, multiplexer_3_out;
  wire [4:0] multiplexer_4_out;
  wire [31:0] multiplexer_5_out, multiplexer_6_out, multiplexer_7_out, multiplexer_8_out;

  Multiplexer #(.select(1), .width(1), .disabled("Z"), .enable("false")) multiplexer_1 (
    .in0(MemToReg), .in1(1'b0), .out(multiplexer_1_out), .sel(rst));
  Multiplexer #(.select(1), .width(1), .disabled("Z"), .enable("false")) multiplexer_2 (
    .in0(RegWrite), .in1(1'b0), .out(multiplexer_2_out), .sel(rst));
  Multiplexer #(.select(1), .width(1), .disabled("Z"), .enable("false")) multiplexer_3 (
    .in0(halt), .in1(1'b0), .out(multiplexer_3_out), .sel(rst));
  Multiplexer #(.select(1), .width(5), .disabled("Z"), .enable("false")) multiplexer_4 (
    .in0(rd), .in1({5{1'b0}}), .out(multiplexer_4_out), .sel(rst));
  Multiplexer #(.select(1), .width(32), .disabled("Z"), .enable("false")) multiplexer_5 (
    .in0(Result), .in1({32{1'b0}}), .out(multiplexer_5_out), .sel(rst));
  Multiplexer #(.select(1), .width(32), .disabled("Z"), .enable("false")) multiplexer_6 (
    .in0(WriteData), .in1({32{1'b0}}), .out(multiplexer_6_out), .sel(rst));
  Multiplexer #(.select(1), .width(32), .disabled("Z"), .enable("false")) multiplexer_7 (
    .in0(IR), .in1({32{1'b0}}), .out(multiplexer_7_out), .sel(rst));
  Multiplexer #(.select(1), .width(32), .disabled("Z"), .enable("false")) multiplexer_8 (
    .in0(PC), .in1({32{1'b0}}), .out(multiplexer_8_out), .sel(rst));
  Register #(.width(1), .trigger("rising"), .Select("low")) register_1 (
    .D(multiplexer_1_out), .en(en), .Q(MemToReg_2), .clk(clk));  // open: clr
  Register #(.width(1), .trigger("rising"), .Select("low")) register_2 (
    .D(multiplexer_2_out), .en(en), .Q(RegWrite_2), .clk(clk));  // open: clr
  Register #(.width(1), .trigger("rising"), .Select("low")) register_3 (
    .D(multiplexer_3_out), .en(en), .Q(halt_2), .clk(clk));  // open: clr
  Register #(.width(5), .trigger("rising"), .Select("low")) register_4 (
    .D(multiplexer_4_out), .en(en), .Q(rd_2), .clk(clk));  // open: clr
  Register #(.width(32), .trigger("rising"), .Select("low")) register_5 (
    .D(multiplexer_5_out), .en(en), .Q(Result_2), .clk(clk));  // open: clr
  Register #(.width(32), .trigger("rising"), .Select("low")) register_6 (
    .D(multiplexer_6_out), .en(en), .Q(WriteData_2), .clk(clk));  // open: clr
  Register #(.width(32), .trigger("rising"), .Select("low")) register_7 (
    .D(multiplexer_7_out), .en(en), .Q(IR_2), .clk(clk));  // open: clr
  Register #(.width(32), .trigger("rising"), .Select("low")) register_8 (
    .D(multiplexer_8_out), .en(en), .Q(PC_2), .clk(clk));  // open: clr
endmodule

module ImmGen (
  input  Sw,
  input  Auipc,
  input  B_Type,
  input  jal,
  input  [31:0] IR,
  output [31:0] Imm
);

  wire [2:0] priority_encoder_1_out;
  wire [31:0] bit_extender_1_out, bit_extender_2_out, bit_extender_3_out, bit_extender_4_out,
       bit_extender_5_out, shifter_1_out;

  assign bit_extender_1_out = {{12{IR[31]}}, IR[31:12]};  // Bit_Extender bit_extender_1
  assign bit_extender_2_out = {{20{IR[31]}}, IR[31:20]};  // Bit_Extender bit_extender_2
  assign bit_extender_3_out = {{20{IR[31]}}, {IR[31:25], IR[11:7]}};  // Bit_Extender bit_extender_3
  Shifter #(.width(32), .shift("ll")) shifter_1 (.in(bit_extender_1_out), .\dist (5'b01100), .out(shifter_1_out));
  assign bit_extender_4_out = {{20{IR[31]}}, {IR[31], IR[7], IR[30:25], IR[11:8]}};  // Bit_Extender bit_extender_4
  assign bit_extender_5_out = {{12{IR[31]}}, {IR[31], IR[19:12], IR[20], IR[30:21]}};  // Bit_Extender bit_extender_5
  Priority_Encoder #(.select(3), .disabled("Z")) priority_encoder_1 (
    .in0(1'b1), .in1(Sw), .in2(Auipc), .in3(B_Type), .in4(jal), .out(priority_encoder_1_out));  // open: in5, in6, in7, gs, en_out, en_in
  // Probe on priority_encoder_1_out
  Multiplexer #(.select(3), .width(32), .disabled("Z"), .enable("false")) multiplexer_1 (
    .in0(bit_extender_2_out), .in1(bit_extender_3_out), .in2(shifter_1_out), .in3(bit_extender_4_out),
    .in4(bit_extender_5_out), .out(Imm), .sel(priority_encoder_1_out));  // open: in5, in6, in7

  // Notes on the sheet:
  //   imm_U
  //   imm_I
  //   imm_S
  //   imm_B
  //   imm_J
endmodule

module \寄存器使用  (
  input  [31:0] IR,
  output r2_used,
  output r1_used
);

  wire comparator_1_eq, comparator_2_eq, comparator_3_eq, comparator_4_eq, comparator_5_eq, comparator_6_eq,
       not_1_out, not_2_out, or_1_out, or_2_out;

  Comparator #(.width(5), .mode("twosComplement")) comparator_1 (
    .a(IR[6:2]), .b(5'b00100), .eq(comparator_1_eq));  // open: gt, lt
  Comparator #(.width(5), .mode("twosComplement")) comparator_2 (
    .a(IR[6:2]), .b({5{1'b0}}), .eq(comparator_2_eq));  // open: gt, lt
  Comparator #(.width(5), .mode("twosComplement")) comparator_3 (
    .a(IR[6:2]), .b(5'b11001), .eq(comparator_3_eq));  // open: gt, lt
  Comparator #(.width(5), .mode("twosComplement")) comparator_4 (
    .a(IR[6:2]), .b(5'b11011), .eq(comparator_4_eq));  // open: gt, lt
  Comparator #(.width(5), .mode("twosComplement")) comparator_5 (
    .a(IR[6:2]), .b(5'b00101), .eq(comparator_5_eq));  // open: gt, lt
  Comparator #(.width(5), .mode("twosComplement")) comparator_6 (
    .a(IR[6:2]), .b(5'b01101), .eq(comparator_6_eq));  // open: gt, lt
  or or_1 (or_1_out, comparator_1_eq, comparator_2_eq, comparator_3_eq);
  or or_2 (or_2_out, comparator_4_eq, comparator_5_eq, comparator_6_eq);
  not not_1 (not_1_out, or_1_out);
  not not_2 (not_2_out, or_2_out);
  and and_1 (r2_used, IR[0], not_1_out, not_2_out);
  and and_2 (r1_used, IR[0], not_2_out);
endmodule

module \气泡处理  (
  input  [31:0] IR,
  input  [4:0] rs1,
  input  [4:0] rs2,
  input  [4:0] EX_rd,
  input  EX_RegWrite,
  input  [4:0] MEM_rd,
  input  MEM_RegWrite,
  output stall
);

  wire and_1_out, and_2_out, and_3_out, and_4_out, comparator_1_eq, comparator_2_eq, comparator_3_eq,
       comparator_4_eq, comparator_5_eq, comparator_6_eq, not_1_out, not_2_out, \寄存器使用_1_r1_used ,
       \寄存器使用_1_r2_used ;

  \寄存器使用  \u_寄存器使用_1  (.IR(IR), .r2_used(\寄存器使用_1_r2_used ), .r1_used(\寄存器使用_1_r1_used ));
  Comparator #(.width(5), .mode("twosComplement")) comparator_1 (
    .a(rs1), .b(EX_rd), .eq(comparator_1_eq));  // open: gt, lt
  Comparator #(.width(5), .mode("twosComplement")) comparator_2 (
    .a(rs2), .b(EX_rd), .eq(comparator_2_eq));  // open: gt, lt
  Comparator #(.width(5), .mode("twosComplement")) comparator_3 (
    .a(EX_rd), .b({5{1'b0}}), .eq(comparator_3_eq));  // open: gt, lt
  Comparator #(.width(5), .mode("twosComplement")) comparator_4 (
    .a(rs1), .b(MEM_rd), .eq(comparator_4_eq));  // open: gt, lt
  Comparator #(.width(5), .mode("twosComplement")) comparator_5 (
    .a(rs2), .b(MEM_rd), .eq(comparator_5_eq));  // open: gt, lt
  Comparator #(.width(5), .mode("twosComplement")) comparator_6 (
    .a(MEM_rd), .b({5{1'b0}}), .eq(comparator_6_eq));  // open: gt, lt
  not not_1 (not_1_out, comparator_3_eq);
  not not_2 (not_2_out, comparator_6_eq);
  and and_1 (and_1_out, \寄存器使用_1_r1_used , comparator_1_eq, not_1_out, EX_RegWrite);
  and and_2 (and_2_out, comparator_2_eq, not_1_out, \寄存器使用_1_r2_used , EX_RegWrite);
  and and_3 (and_3_out, \寄存器使用_1_r1_used , comparator_4_eq, not_2_out, MEM_RegWrite);
  and and_4 (and_4_out, comparator_5_eq, MEM_RegWrite, \寄存器使用_1_r2_used , not_2_out);
  or or_1 (stall, and_1_out, and_2_out, and_3_out, and_4_out);
endmodule

module \ID_EX_重定向  (
  input  pre,
  input  [1:0] rs1_f,
  input  [1:0] rs2_f,
  input  Lh,
  input  Auipc,
  input  Blt,
  input  Beq,
  input  Bne,
  input  MemToReg,
  input  MemWrite,
  input  AluSrcB,
  input  RegWrite,
  input  ecall,
  input  JAL,
  input  Jalr,
  input  [3:0] AluOP,
  input  [4:0] rd,
  input  [31:0] R1,
  input  [31:0] R2,
  input  [31:0] imm,
  input  [31:0] PC,
  input  [31:0] IR,
  input  en,
  input  clk,
  input  rst,
  input  flush,
  output pre_2,
  output [1:0] rs1_f_2,
  output [1:0] rs2_f_2,
  output Lh_2,
  output Auipc_2,
  output Blt_2,
  output Beq_2,
  output Bne_2,
  output MemToReg_2,
  output MemWrite_2,
  output AluSrcB_2,
  output RegWrite_2,
  output ecall_2,
  output JAL_2,
  output Jalr_2,
  output [3:0] AluOP_2,
  output [4:0] rd_2,
  output [31:0] R1_2,
  output [31:0] R2_2,
  output [31:0] imm_2,
  output [31:0] PC_2,
  output [31:0] IR_2
);

  wire multiplexer_2_out, multiplexer_5_out, multiplexer_6_out, multiplexer_7_out, multiplexer_8_out,
       multiplexer_9_out, multiplexer_10_out, multiplexer_11_out, multiplexer_12_out, multiplexer_13_out,
       multiplexer_14_out, multiplexer_15_out, multiplexer_16_out, or_1_out;
  wire [1:0] multiplexer_3_out, multiplexer_4_out;
  wire [3:0] multiplexer_17_out;
  wire [4:0] multiplexer_1_out;
  wire [31:0] multiplexer_18_out, multiplexer_19_out, multiplexer_20_out, multiplexer_21_out,
       multiplexer_22_out;

  Multiplexer #(.select(1), .width(5), .disabled("Z"), .enable("false")) multiplexer_1 (
    .in0(rd), .in1({5{1'b0}}), .out(multiplexer_1_out), .sel(or_1_out));
  Multiplexer #(.select(1), .width(1), .disabled("Z"), .enable("false")) multiplexer_2 (
    .in0(pre), .in1(1'b0), .out(multiplexer_2_out), .sel(or_1_out));
  Register #(.width(1), .trigger("rising"), .Select("low")) register_1 (
    .D(multiplexer_2_out), .en(en), .Q(pre_2), .clk(clk));  // open: clr
  Register #(.width(2), .trigger("rising"), .Select("low")) register_2 (
    .D(multiplexer_3_out), .en(en), .Q(rs1_f_2), .clk(clk));  // open: clr
  Multiplexer #(.select(1), .width(2), .disabled("Z"), .enable("false")) multiplexer_3 (
    .in0(rs1_f), .in1(2'b00), .out(multiplexer_3_out), .sel(or_1_out));
  Multiplexer #(.select(1), .width(2), .disabled("Z"), .enable("false")) multiplexer_4 (
    .in0(rs2_f), .in1(2'b00), .out(multiplexer_4_out), .sel(or_1_out));
  Register #(.width(2), .trigger("rising"), .Select("low")) register_3 (
    .D(multiplexer_4_out), .en(en), .Q(rs2_f_2), .clk(clk));  // open: clr
  Register #(.width(1), .trigger("rising"), .Select("low")) register_4 (
    .D(multiplexer_5_out), .en(en), .Q(Lh_2), .clk(clk));  // open: clr
  Multiplexer #(.select(1), .width(1), .disabled("Z"), .enable("false")) multiplexer_5 (
    .in0(Lh), .in1(1'b0), .out(multiplexer_5_out), .sel(or_1_out));
  Register #(.width(1), .trigger("rising"), .Select("low")) register_5 (
    .D(multiplexer_6_out), .en(en), .Q(Auipc_2), .clk(clk));  // open: clr
  Multiplexer #(.select(1), .width(1), .disabled("Z"), .enable("false")) multiplexer_6 (
    .in0(Auipc), .in1(1'b0), .out(multiplexer_6_out), .sel(or_1_out));
  Register #(.width(1), .trigger("rising"), .Select("low")) register_6 (
    .D(multiplexer_7_out), .en(en), .Q(Blt_2), .clk(clk));  // open: clr
  Multiplexer #(.select(1), .width(1), .disabled("Z"), .enable("false")) multiplexer_7 (
    .in0(Blt), .in1(1'b0), .out(multiplexer_7_out), .sel(or_1_out));
  Register #(.width(1), .trigger("rising"), .Select("low")) register_7 (
    .D(multiplexer_8_out), .en(en), .Q(Beq_2), .clk(clk));  // open: clr
  Multiplexer #(.select(1), .width(1), .disabled("Z"), .enable("false")) multiplexer_8 (
    .in0(Beq), .in1(1'b0), .out(multiplexer_8_out), .sel(or_1_out));
  Multiplexer #(.select(1), .width(1), .disabled("Z"), .enable("false")) multiplexer_9 (
    .in0(Bne), .in1(1'b0), .out(multiplexer_9_out), .sel(or_1_out));
  Register #(.width(1), .trigger("rising"), .Select("low")) register_8 (
    .D(multiplexer_9_out), .en(en), .Q(Bne_2), .clk(clk));  // open: clr
  Multiplexer #(.select(1), .width(1), .disabled("Z"), .enable("false")) multiplexer_10 (
    .in0(MemToReg), .in1(1'b0), .out(multiplexer_10_out), .sel(or_1_out));
  Register #(.width(1), .trigger("rising"), .Select("low")) register_9 (
    .D(multiplexer_10_out), .en(en), .Q(MemToReg_2), .clk(clk));  // open: clr
  Multiplexer #(.select(1), .width(1), .disabled("Z"), .enable("false")) multiplexer_11 (
    .in0(MemWrite), .in1(1'b0), .out(multiplexer_11_out), .sel(or_1_out));
  Register #(.width(1), .trigger("rising"), .Select("low")) register_10 (
    .D(multiplexer_11_out), .en(en), .Q(MemWrite_2), .clk(clk));  // open: clr
  Multiplexer #(.select(1), .width(1), .disabled("Z"), .enable("false")) multiplexer_12 (
    .in0(AluSrcB), .in1(1'b0), .out(multiplexer_12_out), .sel(or_1_out));
  Register #(.width(1), .trigger("rising"), .Select("low")) register_11 (
    .D(multiplexer_12_out), .en(en), .Q(AluSrcB_2), .clk(clk));  // open: clr
  Multiplexer #(.select(1), .width(1), .disabled("Z"), .enable("false")) multiplexer_13 (
    .in0(RegWrite), .in1(1'b0), .out(multiplexer_13_out), .sel(or_1_out));
  Register #(.width(1), .trigger("rising"), .Select("low")) register_12 (
    .D(multiplexer_13_out), .en(en), .Q(RegWrite_2), .clk(clk));  // open: clr
  Register #(.width(1), .trigger("rising"), .Select("low")) register_13 (
    .D(multiplexer_14_out), .en(en), .Q(ecall_2), .clk(clk));  // open: clr
  Multiplexer #(.select(1), .width(1), .disabled("Z"), .enable("false")) multiplexer_14 (
    .in0(ecall), .in1(1'b0), .out(multiplexer_14_out), .sel(or_1_out));
  Register #(.width(1), .trigger("rising"), .Select("low")) register_14 (
    .D(multiplexer_15_out), .en(en), .Q(JAL_2), .clk(clk));  // open: clr
  Multiplexer #(.select(1), .width(1), .disabled("Z"), .enable("false")) multiplexer_15 (
    .in0(JAL), .in1(1'b0), .out(multiplexer_15_out), .sel(or_1_out));
  Multiplexer #(.select(1), .width(1), .disabled("Z"), .enable("false")) multiplexer_16 (
    .in0(Jalr), .in1(1'b0), .out(multiplexer_16_out), .sel(or_1_out));
  Register #(.width(1), .trigger("rising"), .Select("low")) register_15 (
    .D(multiplexer_16_out), .en(en), .Q(Jalr_2), .clk(clk));  // open: clr
  Multiplexer #(.select(1), .width(4), .disabled("Z"), .enable("false")) multiplexer_17 (
    .in0(AluOP), .in1(4'b0000), .out(multiplexer_17_out), .sel(or_1_out));
  Register #(.width(4), .trigger("rising"), .Select("low")) register_16 (
    .D(multiplexer_17_out), .en(en), .Q(AluOP_2), .clk(clk));  // open: clr
  Register #(.width(5), .trigger("rising"), .Select("low")) register_17 (
    .D(multiplexer_1_out), .en(en), .Q(rd_2), .clk(clk));  // open: clr
  Register #(.width(32), .trigger("rising"), .Select("low")) register_18 (
    .D(multiplexer_18_out), .en(en), .Q(R1_2), .clk(clk));  // open: clr
  Multiplexer #(.select(1), .width(32), .disabled("Z"), .enable("false")) multiplexer_18 (
    .in0(R1), .in1({32{1'b0}}), .out(multiplexer_18_out), .sel(or_1_out));
  Register #(.width(32), .trigger("rising"), .Select("low")) register_19 (
    .D(multiplexer_19_out), .en(en), .Q(R2_2), .clk(clk));  // open: clr
  Multiplexer #(.select(1), .width(32), .disabled("Z"), .enable("false")) multiplexer_19 (
    .in0(R2), .in1({32{1'b0}}), .out(multiplexer_19_out), .sel(or_1_out));
  Multiplexer #(.select(1), .width(32), .disabled("Z"), .enable("false")) multiplexer_20 (
    .in0(imm), .in1({32{1'b0}}), .out(multiplexer_20_out), .sel(or_1_out));
  Register #(.width(32), .trigger("rising"), .Select("low")) register_20 (
    .D(multiplexer_20_out), .en(en), .Q(imm_2), .clk(clk));  // open: clr
  Register #(.width(32), .trigger("rising"), .Select("low")) register_21 (
    .D(multiplexer_21_out), .en(en), .Q(PC_2), .clk(clk));  // open: clr
  Multiplexer #(.select(1), .width(32), .disabled("Z"), .enable("false")) multiplexer_21 (
    .in0(PC), .in1({32{1'b0}}), .out(multiplexer_21_out), .sel(or_1_out));
  Multiplexer #(.select(1), .width(32), .disabled("Z"), .enable("false")) multiplexer_22 (
    .in0(IR), .in1({32{1'b0}}), .out(multiplexer_22_out), .sel(or_1_out));
  Register #(.width(32), .trigger("rising"), .Select("low")) register_22 (
    .D(multiplexer_22_out), .en(en), .Q(IR_2), .clk(clk));  // open: clr
  or or_1 (or_1_out, flush, rst);
endmodule

module \重定向处理  (
  input  [4:0] rs1,
  input  [31:0] IR,
  input  [4:0] rs2,
  input  EX_RegWrite,
  input  [4:0] EX_rd,
  input  MEM_RegWrite,
  input  [4:0] MEM_rd,
  input  EX_MemToReg,
  output [1:0] rs1_f,
  output [1:0] rs2_f,
  output Stall,
  output LoadUse
);

  wire and_5_out, and_6_out, comparator_1_eq, comparator_2_eq, comparator_3_eq, comparator_4_eq,
       comparator_5_eq, comparator_6_eq, comparator_7_gt, not_1_out, not_2_out, r1_used, r2_used;
  wire [1:0] or_2_out;

  Comparator #(.width(5), .mode("twosComplement")) comparator_1 (
    .a(rs1), .b(EX_rd), .eq(comparator_1_eq));  // open: gt, lt
  Comparator #(.width(5), .mode("twosComplement")) comparator_2 (
    .a(rs2), .b(EX_rd), .eq(comparator_2_eq));  // open: gt, lt
  not not_1 (not_1_out, comparator_3_eq);
  Comparator #(.width(5), .mode("twosComplement")) comparator_3 (
    .a(EX_rd), .b({5{1'b0}}), .eq(comparator_3_eq));  // open: gt, lt
  Comparator #(.width(5), .mode("twosComplement")) comparator_4 (
    .a(rs1), .b(MEM_rd), .eq(comparator_4_eq));  // open: gt, lt
  Comparator #(.width(5), .mode("twosComplement")) comparator_5 (
    .a(rs2), .b(MEM_rd), .eq(comparator_5_eq));  // open: gt, lt
  Comparator #(.width(5), .mode("twosComplement")) comparator_6 (
    .a(MEM_rd), .b({5{1'b0}}), .eq(comparator_6_eq));  // open: gt, lt
  not not_2 (not_2_out, comparator_6_eq);
  \寄存器使用  \u_寄存器使用_1  (.IR(IR), .r2_used(r2_used), .r1_used(r1_used));
  and and_1 (rs1_f[1], r1_used, comparator_1_eq, not_1_out, EX_RegWrite);
  and and_2 (rs2_f[1], comparator_2_eq, not_1_out, r2_used, EX_RegWrite);
  and and_3 (rs1_f[0], r1_used, comparator_4_eq, not_2_out, MEM_RegWrite);
  and and_4 (rs2_f[0], comparator_5_eq, MEM_RegWrite, r2_used, not_2_out);
  and and_5 (and_5_out, r1_used, EX_MemToReg, comparator_1_eq, not_1_out);
  and and_6 (and_6_out, comparator_2_eq, EX_MemToReg, not_1_out, r2_used);
  or or_1 (Stall, and_5_out, and_6_out);
  assign or_2_out = rs1_f | rs2_f;  // OR_Gate or_2, 2 bits wide
  Comparator #(.width(2), .mode("unsigned")) comparator_7 (
    .a(or_2_out), .b(2'b00), .gt(comparator_7_gt));  // open: eq, lt
  or or_3 (LoadUse, Stall, comparator_7_gt);

  // Notes on the sheet:
  //   输入引脚
  //   输出引脚
endmodule

module \单级中断逻辑电路  (
  input  IRA,
  input  [31:0] NPC,
  input  IRB,
  input  IRC,
  input  clk,
  input  URET,
  output W1,
  output W2,
  output [31:0] INT_Add,
  output W3,
  output INT,
  output [31:0] EPC
);

  wire and_1_out, and_2_out, and_3_out, and_4_out, d_ff_1_q, d_ff_2_q, d_ff_3_q, demultiplexer_1_out0,
       demultiplexer_1_out1, demultiplexer_1_out2, IE, Int_Sign, IR1_2_q, IR1_3_q, IR1_q, or_4_out, or_5_out,
       or_6_out;
  wire [1:0] Int_ID, register_1_q;

  or or_1 (W1, IR1_q, d_ff_1_q);
  or or_2 (W2, IR1_2_q, d_ff_2_q);
  or or_3 (W3, IR1_3_q, d_ff_3_q);
  D_Flip_Flop #(.trigger("rising"), .Pre_Clr_Positions("LEGACY"), .NegatePresetClear("false"), .enable("true"), .NewFFLayout("false")) d_ff_1 (
    .clk(IRA), .D(1'b1), .Q(d_ff_1_q), .reset(IR1_q));  // open: Qn, preset, en
  D_Flip_Flop #(.trigger("rising"), .Pre_Clr_Positions("LEGACY"), .NegatePresetClear("false"), .enable("true"), .NewFFLayout("false")) d_ff_2 (
    .clk(IRB), .D(1'b1), .Q(d_ff_2_q), .reset(IR1_2_q));  // open: Qn, preset, en
  D_Flip_Flop #(.trigger("rising"), .Pre_Clr_Positions("LEGACY"), .NegatePresetClear("false"), .enable("true"), .NewFFLayout("false")) d_ff_3 (
    .clk(IRC), .D(1'b1), .Q(d_ff_3_q), .reset(IR1_3_q));  // open: Qn, preset, en
  or or_4 (or_4_out, d_ff_1_q, IR1_q);
  or or_5 (or_5_out, d_ff_2_q, IR1_2_q);
  or or_6 (or_6_out, d_ff_3_q, IR1_3_q);
  Register #(.width(2), .trigger("rising"), .Select("low")) register_1 (
    .D(Int_ID), .en(INT), .Q(register_1_q), .clk(clk));  // open: clr
  Demultiplexer #(.select(2), .width(1), .tristate("false"), .disabled("Z"), .enable("false")) demultiplexer_1 (
    .out0(demultiplexer_1_out0), .out1(demultiplexer_1_out1), .out2(demultiplexer_1_out2), .in(URET),
    .sel(register_1_q));  // open: out3
  and and_1 (and_1_out, or_4_out, ~demultiplexer_1_out0);  // AND_Gate
  and and_2 (and_2_out, or_5_out, ~demultiplexer_1_out1);  // AND_Gate
  and and_3 (and_3_out, or_6_out, ~demultiplexer_1_out2);  // AND_Gate
  D_Flip_Flop #(.trigger("rising"), .Pre_Clr_Positions("LEGACY"), .NegatePresetClear("false"), .enable("true"), .NewFFLayout("false")) IR1 (
    .clk(clk), .D(and_1_out), .Q(IR1_q));  // open: Qn, preset, en, reset
  D_Flip_Flop #(.trigger("rising"), .Pre_Clr_Positions("LEGACY"), .NegatePresetClear("false"), .enable("true"), .NewFFLayout("false")) IR1_2 (
    .clk(clk), .D(and_2_out), .Q(IR1_2_q));  // open: Qn, preset, en, reset
  D_Flip_Flop #(.trigger("rising"), .Pre_Clr_Positions("LEGACY"), .NegatePresetClear("false"), .enable("true"), .NewFFLayout("false")) IR1_3 (
    .clk(clk), .D(and_3_out), .Q(IR1_3_q));  // open: Qn, preset, en, reset
  Priority_Encoder #(.select(2), .disabled("Z")) priority_encoder_1 (
    .in0(IR1_q), .in1(IR1_2_q), .in2(IR1_3_q), .out(Int_ID));  // open: in3, gs, en_out, en_in
  or or_7 (Int_Sign, IR1_q, IR1_2_q, IR1_3_q);
  and and_4 (and_4_out, Int_Sign, ~URET);  // AND_Gate
  Register #(.width(32), .trigger("rising"), .Select("low")) u_EPC (
    .D(NPC), .en(INT), .Q(EPC), .clk(clk));  // open: clr
  Multiplexer #(.select(2), .width(32), .disabled("Z"), .enable("false")) multiplexer_1 (
    .in0(32'h30ac), .in1(32'h3150), .in2(32'h31f4), .out(INT_Add), .sel(Int_ID));  // open: in3
  Register #(.width(1), .trigger("rising"), .Select("low")) u_IE (.D(and_4_out), .Q(IE), .clk(clk));  // open: en, clr
  and and_5 (INT, Int_Sign, ~IE);  // AND_Gate

  // Notes on the sheet:
  //   输入引脚
  //   输出引脚
endmodule
module \多级中断逻辑电路  (
  input  IRA,
  input  [31:0] NPC,
  input  IRB,
  input  IRC,
  input  clk,
  input  csrrci,
  input  URET,
  input  csrrsi,
  output W1,
  output W2,
  output [31:0] INT_Add,
  output W3,
  output INT,
  output [31:0] EPC
);

  wire and_1_out, and_2_out, and_3_out, and_4_out, and_5_out, and_6_out, d_ff_1_q, d_ff_2_q, d_ff_3_q,
       demultiplexer_1_out1, demultiplexer_1_out2, demultiplexer_1_out3, IE, Int_Sign, IR1_2_q, IR1_3_q,
       IR1_q, or_4_out, or_5_out, or_6_out, or_7_out, or_8_out, or_9_out, or_10_out, \屏蔽器_1_x , \屏蔽器_1_y ,
       \屏蔽器_1_z ;
  wire [1:0] Int_ID, Int_ID2_q, Int_ID3_q, multiplexer_3_out, multiplexer_5_out, multiplexer_7_out,
       Next_Int_ID;
  wire [31:0] EPC2_q, EPC3_q, multiplexer_2_out, multiplexer_4_out, multiplexer_6_out;

  or or_1 (W1, IR1_q, d_ff_1_q);
  or or_2 (W2, IR1_2_q, d_ff_2_q);
  or or_3 (W3, IR1_3_q, d_ff_3_q);
  D_Flip_Flop #(.trigger("rising"), .Pre_Clr_Positions("LEGACY"), .NegatePresetClear("false"), .enable("true"), .NewFFLayout("false")) d_ff_1 (
    .clk(IRA), .D(1'b1), .Q(d_ff_1_q), .reset(IR1_q));  // open: Qn, preset, en
  D_Flip_Flop #(.trigger("rising"), .Pre_Clr_Positions("LEGACY"), .NegatePresetClear("false"), .enable("true"), .NewFFLayout("false")) d_ff_2 (
    .clk(IRB), .D(1'b1), .Q(d_ff_2_q), .reset(IR1_2_q));  // open: Qn, preset, en
  D_Flip_Flop #(.trigger("rising"), .Pre_Clr_Positions("LEGACY"), .NegatePresetClear("false"), .enable("true"), .NewFFLayout("false")) d_ff_3 (
    .clk(IRC), .D(1'b1), .Q(d_ff_3_q), .reset(IR1_3_q));  // open: Qn, preset, en
  or or_4 (or_4_out, d_ff_1_q, IR1_q);
  or or_5 (or_5_out, d_ff_2_q, IR1_2_q);
  or or_6 (or_6_out, d_ff_3_q, IR1_3_q);
  Demultiplexer #(.select(2), .width(1), .tristate("false"), .disabled("Z"), .enable("false")) demultiplexer_1 (
    .out1(demultiplexer_1_out1), .out2(demultiplexer_1_out2), .out3(demultiplexer_1_out3), .in(URET),
    .sel(Int_ID));  // open: out0
  and and_1 (and_1_out, or_4_out, ~demultiplexer_1_out1);  // AND_Gate
  and and_2 (and_2_out, or_5_out, ~demultiplexer_1_out2);  // AND_Gate
  and and_3 (and_3_out, or_6_out, ~demultiplexer_1_out3);  // AND_Gate
  D_Flip_Flop #(.trigger("rising"), .Pre_Clr_Positions("LEGACY"), .NegatePresetClear("false"), .enable("true"), .NewFFLayout("false")) IR1 (
    .clk(clk), .D(and_1_out), .Q(IR1_q));  // open: Qn, preset, en, reset
  D_Flip_Flop #(.trigger("rising"), .Pre_Clr_Positions("LEGACY"), .NegatePresetClear("false"), .enable("true"), .NewFFLayout("false")) IR1_2 (
    .clk(clk), .D(and_2_out), .Q(IR1_2_q));  // open: Qn, preset, en, reset
  D_Flip_Flop #(.trigger("rising"), .Pre_Clr_Positions("LEGACY"), .NegatePresetClear("false"), .enable("true"), .NewFFLayout("false")) IR1_3 (
    .clk(clk), .D(and_3_out), .Q(IR1_3_q));  // open: Qn, preset, en, reset
  and and_4 (and_4_out, IR1_q, ~\屏蔽器_1_x );  // AND_Gate
  and and_5 (and_5_out, IR1_2_q, ~\屏蔽器_1_y );  // AND_Gate
  and and_6 (and_6_out, IR1_3_q, ~\屏蔽器_1_z );  // AND_Gate
  \屏蔽器  \u_屏蔽器_1  (.x(\屏蔽器_1_x ), .y(\屏蔽器_1_y ), .z(\屏蔽器_1_z ), .ID(Int_ID));
  Priority_Encoder #(.select(2), .disabled("Z")) priority_encoder_1 (
    .in1(and_4_out), .in2(and_5_out), .in3(and_6_out), .out(Next_Int_ID), .gs(Int_Sign));  // open: in0, en_out, en_in
  or or_7 (or_7_out, INT, csrrci);
  or or_8 (or_8_out, INT, csrrci, csrrsi, URET);
  Register #(.width(1), .trigger("rising"), .Select("low")) u_IE (
    .D(or_7_out), .en(or_8_out), .Q(IE), .clk(clk));  // open: clr
  and and_7 (INT, Int_Sign, ~IE);  // AND_Gate
  Multiplexer #(.select(2), .width(32), .disabled("Z"), .enable("false")) multiplexer_1 (
    .in1(32'h30ac), .in2(32'h3158), .in3(32'h3204), .out(INT_Add), .sel(Next_Int_ID));  // open: in0
  Multiplexer #(.select(1), .width(32), .disabled("Z"), .enable("false")) multiplexer_2 (
    .in0(NPC), .in1(EPC2_q), .out(multiplexer_2_out), .sel(URET));
  or or_9 (or_9_out, INT, URET);
  Multiplexer #(.select(1), .width(2), .disabled("Z"), .enable("false")) multiplexer_3 (
    .in0(Next_Int_ID), .in1(Int_ID2_q), .out(multiplexer_3_out), .sel(URET));
  or or_10 (or_10_out, INT, URET);
  Register #(.width(32), .trigger("rising"), .Select("low")) EPC1 (
    .D(multiplexer_2_out), .en(or_9_out), .Q(EPC), .clk(clk));  // open: clr
  Register #(.width(2), .trigger("rising"), .Select("low")) Int_ID1 (
    .D(multiplexer_3_out), .en(or_10_out), .Q(Int_ID), .clk(clk));  // open: clr
  Multiplexer #(.select(1), .width(32), .disabled("Z"), .enable("false")) multiplexer_4 (
    .in0(EPC), .in1(EPC3_q), .out(multiplexer_4_out), .sel(URET));
  Multiplexer #(.select(1), .width(2), .disabled("Z"), .enable("false")) multiplexer_5 (
    .in0(Int_ID), .in1(Int_ID3_q), .out(multiplexer_5_out), .sel(URET));
  Register #(.width(32), .trigger("rising"), .Select("low")) EPC2 (
    .D(multiplexer_4_out), .en(or_9_out), .Q(EPC2_q), .clk(clk));  // open: clr
  Register #(.width(2), .trigger("rising"), .Select("low")) Int_ID2 (
    .D(multiplexer_5_out), .en(or_10_out), .Q(Int_ID2_q), .clk(clk));  // open: clr
  Multiplexer #(.select(1), .width(32), .disabled("Z"), .enable("false")) multiplexer_6 (
    .in0(EPC2_q), .in1({32{1'b0}}), .out(multiplexer_6_out), .sel(URET));
  Register #(.width(32), .trigger("rising"), .Select("low")) EPC3 (
    .D(multiplexer_6_out), .en(or_9_out), .Q(EPC3_q), .clk(clk));  // open: clr
  Register #(.width(2), .trigger("rising"), .Select("low")) Int_ID3 (
    .D(multiplexer_7_out), .en(or_10_out), .Q(Int_ID3_q), .clk(clk));  // open: clr
  Multiplexer #(.select(1), .width(2), .disabled("Z"), .enable("false")) multiplexer_7 (
    .in0(Int_ID2_q), .in1(2'b00), .out(multiplexer_7_out), .sel(URET));

  // Notes on the sheet:
  //   输入引脚
  //   输出引脚
endmodule

module \屏蔽器  (
  input  [1:0] ID,
  output x,
  output y,
  output z
);

  or or_1 (x, ID[0], ID[1]);
  and and_1 (z, ID[1], ID[0]);

  assign y = ID[1];
endmodule

module \中断按键参考电路  (
  input  \同步清零信号 ,
  output \与中断屏蔽位与 
);

  wire \_1号中断_out , and_1_out, clock_1_out, d_ff_1_q, or_1_out, or_2_out;

  Clock #(.highDuration(1), .lowDuration(1)) clock_1 (.out(clock_1_out));
  Button \_1号中断  (.out(\_1号中断_out ));
  or or_1 (or_1_out, \与中断屏蔽位与 , d_ff_1_q);
  LED #(.active("true")) \_1号中断等待指示灯  (.in(or_1_out));
  D_Flip_Flop #(.trigger("rising"), .Pre_Clr_Positions("LEGACY"), .NegatePresetClear("false"), .enable("true"), .NewFFLayout("false")) d_ff_1 (
    .clk(\_1号中断_out ), .D(1'b1), .Q(d_ff_1_q), .reset(\与中断屏蔽位与 ));  // open: Qn, preset, en
  or or_2 (or_2_out, d_ff_1_q, \与中断屏蔽位与 );
  and and_1 (and_1_out, or_2_out, ~\同步清零信号 );  // AND_Gate
  D_Flip_Flop #(.trigger("rising"), .Pre_Clr_Positions("LEGACY"), .NegatePresetClear("false"), .enable("true"), .NewFFLayout("false")) IR1 (
    .clk(clock_1_out), .D(and_1_out), .Q(\与中断屏蔽位与 ));  // open: Qn, preset, en, reset

  // Notes on the sheet:
  //   中断信号采样参考电路
  //   Reset 
endmodule

module \封装正确性测试  (
);

  wire IR1, IR2, IR3, MemW, RegW;
  wire [31:0] EX_PC, ID_PC, IF_PC, IR, LED, MDin, MDinr, MEM_PC, PC, RDin, RDinr, WB_PC;

  \单周期RISC_V  \u_单周期risc_v_1  (
    .IR1(IR1), .IR2(IR2), .IR3(IR3), .RegWrite(RegW), .MemWrite(MemW), .PC(PC), .IR(IR), .RDin(RDin),
    .MDin(MDin), .LedData(LED));
  \气泡流水线  \u_气泡流水线_1  (
    .RegWrite(RegW), .MemWrite(MemW), .IF_PC(IF_PC), .ID_PC(ID_PC), .EX_PC(EX_PC), .M_PC(MEM_PC),
    .WB_PC(WB_PC), .RDin(RDinr), .MDin(MDinr), .LedData(LED));
  \单周期_单级中断  \u_单周期_单级中断_1  (
    .IR1(IR1), .IR2(IR2), .IR3(IR3), .RegWrite(RegW), .MemWrite(MemW), .PC(PC), .IR(IR), .RDin(RDin),
    .MDin(MDin), .LedData(LED));
  \理想流水线  \u_理想流水线_1  (
    .RegWrite(RegW), .MemWrite(MemW), .IF_PC(IF_PC), .ID_PC(ID_PC), .EX_PC(EX_PC), .M_PC(MEM_PC),
    .WB_PC(WB_PC), .RDin(RDinr), .MDin(MDinr), .LedData(LED));
  \重定向流水线  \u_重定向流水线_1  (
    .RegWrite(RegW), .MemWrite(MemW), .IF_PC(IF_PC), .ID_PC(ID_PC), .EX_PC(EX_PC), .M_PC(MEM_PC),
    .WB_PC(WB_PC), .RDin(RDinr), .MDin(MDinr), .LedData(LED));
  \单周期_多级中断  \u_单周期_多级中断_1  (
    .IR1(IR1), .IR2(IR2), .IR3(IR3), .RegWrite(RegW), .MemWrite(MemW), .PC(PC), .IR(IR), .RDin(RDin),
    .MDin(MDin), .LedData(LED));

  // Notes on the sheet:
  //   单周期封装测试
  //   气泡流水封装测试
  //   单周期+单级中断封装测试
  //   请检查上面封装有无位宽不匹配，引脚标签是否和连接的标签相对应，否则无法在educoder平台上正确测试
  //   理想流水封装测试
  //   重定向流水封装测试
  //   单周期+多级中断封装测试
endmodule

// MAX2
module MAX2 (
  input  [15:0] Y,
  input  [15:0] X,
  input  [2:0] Y_num,
  input  [2:0] X_num,
  output [15:0] MAX,
  output [2:0] MAX_num
);

  wire comparator_1_eq, comparator_1_gt, or_1_out;

  Comparator #(.width(16), .mode("unsigned")) comparator_1 (
    .a(X), .b(Y), .gt(comparator_1_gt), .eq(comparator_1_eq));  // open: lt
  Multiplexer #(.select(1), .width(16), .disabled("Z"), .enable("false")) multiplexer_1 (
    .in0(Y), .in1(X), .out(MAX), .sel(or_1_out));
  or or_1 (or_1_out, comparator_1_gt, comparator_1_eq);
  Multiplexer #(.select(1), .width(3), .disabled("Z"), .enable("false")) multiplexer_2 (
    .in0(Y_num), .in1(X_num), .out(MAX_num), .sel(or_1_out));
endmodule

module BHT (
  input  Clk,
  input  EX_Branch,
  input  [31:0] PC,
  input  [31:0] EX_PC,
  input  [31:0] EX_BranchAddr,
  input  EX_Branched,
  output [31:0] JumpAddr,
  output PredictJump
);

  wire A0, A1, A2, A3, A4, A5, A6, A7, and_1_out, comparator_1_eq, comparator_2_eq, comparator_3_eq,
       comparator_4_eq, comparator_5_eq, comparator_6_eq, comparator_7_eq, comparator_8_eq, comparator_9_eq,
       comparator_10_eq, comparator_11_eq, comparator_12_eq, comparator_13_eq, comparator_14_eq,
       comparator_15_eq, comparator_16_eq, decoder_1_out0, decoder_1_out1, decoder_1_out2, decoder_1_out3,
       decoder_1_out4, decoder_1_out5, decoder_1_out6, decoder_1_out7, decoder_2_out0, decoder_2_out1,
       decoder_2_out2, decoder_2_out3, decoder_2_out4, decoder_2_out5, decoder_2_out6, decoder_2_out7,
       EX_Hit, EX_Miss, IF_Hit, IF_Miss, L0, L1, L2, L3, L4, L5, L6, L7, M0, M1, M2, M3, M4, M5, M6, M7,
       not_1_out, not_2_out, not_3_out, not_4_out, not_5_out, not_6_out, not_7_out, not_8_out, or_1_out,
       or_2_out, or_3_out, or_4_out, or_5_out, or_6_out, or_7_out, or_8_out, or_9_out, or_10_out, or_11_out,
       or_12_out, or_13_out, or_14_out, or_17_out, or_18_out, priority_encoder_1_gs, V0, V1, V2, V3, V4, V5,
       V6, V7, WriteL0, WriteL1, WriteL2, WriteL3, WriteL4, WriteL5, WriteL6, WriteL7;
  wire [0:0] controlled_buffer_1_out, controlled_buffer_2_out, controlled_buffer_3_out,
       controlled_buffer_4_out, controlled_buffer_5_out, controlled_buffer_6_out, controlled_buffer_7_out,
       controlled_buffer_8_out;
  wire [1:0] adder_1_out, adder_2_out, adder_3_out, adder_4_out, adder_5_out, adder_6_out, adder_7_out,
       adder_8_out, multiplexer_1_out, multiplexer_2_out, multiplexer_3_out, multiplexer_4_out,
       multiplexer_5_out, multiplexer_6_out, multiplexer_7_out, multiplexer_8_out, multiplexer_9_out,
       multiplexer_10_out, multiplexer_11_out, multiplexer_12_out, multiplexer_13_out, multiplexer_14_out,
       multiplexer_15_out, multiplexer_16_out, multiplexer_17_out, multiplexer_18_out, multiplexer_19_out,
       multiplexer_20_out, multiplexer_21_out, multiplexer_22_out, multiplexer_23_out, multiplexer_24_out,
       multiplexer_25_out, multiplexer_26_out, multiplexer_27_out, multiplexer_28_out, multiplexer_29_out,
       multiplexer_30_out, multiplexer_31_out, multiplexer_32_out, multiplexer_33_out, multiplexer_34_out,
       multiplexer_35_out, multiplexer_36_out, multiplexer_37_out, multiplexer_38_out, multiplexer_39_out,
       multiplexer_40_out, Predict0, Predict1, Predict2, Predict3, Predict4, Predict5, Predict6, Predict7;
  wire [2:0] max2_1_max_num, max2_2_max_num, max2_3_max_num, max2_4_max_num, max2_5_max_num, max2_6_max_num,
       max2_7_max_num, priority_encoder_1_out;
  wire [15:0] C0, C1, C2, C3, C4, C5, C6, C7, max2_1_max, max2_2_max, max2_3_max, max2_4_max, max2_5_max,
       max2_6_max;
  wire [31:0] Tag0, Tag1, Tag2, Tag3, Tag4, Tag5, Tag6, Tag7, \分支目标地址_2_q , \分支目标地址_3_q , \分支目标地址_4_q ,
       \分支目标地址_5_q , \分支目标地址_6_q , \分支目标地址_7_q , \分支目标地址_8_q , \分支目标地址_q ;

  Register #(.width(1), .trigger("rising"), .Select("low")) VALID (
    .D(1'b1), .en(WriteL0), .Q(V0), .clk(Clk));  // open: clr
  Register #(.width(1), .trigger("rising"), .Select("low")) VALID_2 (
    .D(1'b1), .en(WriteL1), .Q(V1), .clk(Clk));  // open: clr
  Register #(.width(1), .trigger("rising"), .Select("low")) VALID_3 (
    .D(1'b1), .en(WriteL2), .Q(V2), .clk(Clk));  // open: clr
  Register #(.width(1), .trigger("rising"), .Select("low")) VALID_4 (
    .D(1'b1), .en(WriteL3), .Q(V3), .clk(Clk));  // open: clr
  Register #(.width(1), .trigger("rising"), .Select("low")) VALID_5 (
    .D(1'b1), .en(WriteL4), .Q(V4), .clk(Clk));  // open: clr
  Register #(.width(1), .trigger("rising"), .Select("low")) VALID_6 (
    .D(1'b1), .en(WriteL5), .Q(V5), .clk(Clk));  // open: clr
  Register #(.width(1), .trigger("rising"), .Select("low")) VALID_7 (
    .D(1'b1), .en(WriteL6), .Q(V6), .clk(Clk));  // open: clr
  Register #(.width(1), .trigger("rising"), .Select("low")) VALID_8 (
    .D(1'b1), .en(WriteL7), .Q(V7), .clk(Clk));  // open: clr
  not not_1 (not_1_out, V0);
  not not_2 (not_2_out, V1);
  not not_3 (not_3_out, V2);
  not not_4 (not_4_out, V3);
  not not_5 (not_5_out, V4);
  not not_6 (not_6_out, V5);
  not not_7 (not_7_out, V6);
  not not_8 (not_8_out, V7);
  MAX2 max2_1 (.Y(C1), .X(C0), .Y_num(3'b001), .X_num(3'b000), .MAX(max2_1_max), .MAX_num(max2_1_max_num));
  MAX2 max2_2 (.Y(C3), .X(C2), .Y_num(3'b011), .X_num(3'b010), .MAX(max2_2_max), .MAX_num(max2_2_max_num));
  MAX2 max2_3 (.Y(C5), .X(C4), .Y_num(3'b101), .X_num(3'b100), .MAX(max2_3_max), .MAX_num(max2_3_max_num));
  MAX2 max2_4 (.Y(C7), .X(C6), .Y_num(3'b111), .X_num(3'b110), .MAX(max2_4_max), .MAX_num(max2_4_max_num));
  Pull_Resistor #(.pull(0)) pull_resistor_1 (.node(PredictJump));
  assign {PredictJump, controlled_buffer_1_out[0]} = L0 ? Predict0 : 2'bz;  // Controlled_Buffer controlled_buffer_1
  assign {PredictJump, controlled_buffer_2_out[0]} = L1 ? Predict1 : 2'bz;  // Controlled_Buffer controlled_buffer_2
  assign {PredictJump, controlled_buffer_3_out[0]} = L2 ? Predict2 : 2'bz;  // Controlled_Buffer controlled_buffer_3
  assign {PredictJump, controlled_buffer_4_out[0]} = L3 ? Predict3 : 2'bz;  // Controlled_Buffer controlled_buffer_4
  assign {PredictJump, controlled_buffer_5_out[0]} = L4 ? Predict4 : 2'bz;  // Controlled_Buffer controlled_buffer_5
  assign {PredictJump, controlled_buffer_6_out[0]} = L5 ? Predict5 : 2'bz;  // Controlled_Buffer controlled_buffer_6
  assign {PredictJump, controlled_buffer_7_out[0]} = L6 ? Predict6 : 2'bz;  // Controlled_Buffer controlled_buffer_7
  assign {PredictJump, controlled_buffer_8_out[0]} = L7 ? Predict7 : 2'bz;  // Controlled_Buffer controlled_buffer_8
  Priority_Encoder #(.select(3), .disabled("Z")) priority_encoder_1 (
    .in0(not_1_out), .in1(not_2_out), .in2(not_3_out), .in3(not_4_out), .in4(not_5_out), .in5(not_6_out),
    .in6(not_7_out), .in7(not_8_out), .out(priority_encoder_1_out), .gs(priority_encoder_1_gs));  // open: en_out, en_in
  MAX2 max2_5 (
    .Y(max2_2_max), .X(max2_1_max), .Y_num(max2_2_max_num), .X_num(max2_1_max_num), .MAX(max2_5_max),
    .MAX_num(max2_5_max_num));
  MAX2 max2_6 (
    .Y(max2_4_max), .X(max2_3_max), .Y_num(max2_4_max_num), .X_num(max2_3_max_num), .MAX(max2_6_max),
    .MAX_num(max2_6_max_num));
  and and_1 (and_1_out, V0, V1, V2, V3, V4, V5, V6, V7);
  or or_1 (or_1_out, L1, L2, L3, L4, L5, L6, L7, WriteL1, WriteL2, WriteL3, WriteL4, WriteL5, WriteL6, WriteL7);
  or or_2 (or_2_out, L0, L1, L2, L3, L5, L6, L7, WriteL0, WriteL1, WriteL2, WriteL3, WriteL5, WriteL6, WriteL7);
  Register #(.width(32), .trigger("rising"), .Select("low")) \u_分支指令地址  (
    .D(EX_PC), .en(WriteL0), .Q(Tag0), .clk(Clk));  // open: clr
  Register #(.width(32), .trigger("rising"), .Select("low")) \u_分支指令地址_2  (
    .D(EX_PC), .en(WriteL1), .Q(Tag1), .clk(Clk));  // open: clr
  Register #(.width(32), .trigger("rising"), .Select("low")) \u_分支指令地址_3  (
    .D(EX_PC), .en(WriteL2), .Q(Tag2), .clk(Clk));  // open: clr
  Register #(.width(32), .trigger("rising"), .Select("low")) \u_分支指令地址_4  (
    .D(EX_PC), .en(WriteL3), .Q(Tag3), .clk(Clk));  // open: clr
  Register #(.width(32), .trigger("rising"), .Select("low")) \u_分支指令地址_5  (
    .D(EX_PC), .en(WriteL4), .Q(Tag4), .clk(Clk));  // open: clr
  Register #(.width(32), .trigger("rising"), .Select("low")) \u_分支指令地址_6  (
    .D(EX_PC), .en(WriteL5), .Q(Tag5), .clk(Clk));  // open: clr
  Register #(.width(32), .trigger("rising"), .Select("low")) \u_分支指令地址_7  (
    .D(EX_PC), .en(WriteL6), .Q(Tag6), .clk(Clk));  // open: clr
  Register #(.width(32), .trigger("rising"), .Select("low")) \u_分支指令地址_8  (
    .D(EX_PC), .en(WriteL7), .Q(Tag7), .clk(Clk));  // open: clr
  Decoder #(.select(3), .tristate("false"), .disabled(0), .enable("true")) decoder_1 (
    .out0(decoder_1_out0), .out1(decoder_1_out1), .out2(decoder_1_out2), .out3(decoder_1_out3),
    .out4(decoder_1_out4), .out5(decoder_1_out5), .out6(decoder_1_out6), .out7(decoder_1_out7),
    .sel(priority_encoder_1_out), .en(priority_encoder_1_gs));
  Decoder #(.select(3), .tristate("false"), .disabled(0), .enable("true")) decoder_2 (
    .out0(decoder_2_out0), .out1(decoder_2_out1), .out2(decoder_2_out2), .out3(decoder_2_out3),
    .out4(decoder_2_out4), .out5(decoder_2_out5), .out6(decoder_2_out6), .out7(decoder_2_out7),
    .sel(max2_7_max_num), .en(and_1_out));
  MAX2 max2_7 (
    .Y(max2_6_max), .X(max2_5_max), .Y_num(max2_6_max_num), .X_num(max2_5_max_num), .MAX_num(max2_7_max_num));  // open: MAX
  Multiplexer #(.select(1), .width(2), .disabled("Z"), .enable("false")) multiplexer_1 (
    .in0(2'b00), .in1(2'b01), .out(multiplexer_1_out), .sel(EX_Branched));
  Multiplexer #(.select(1), .width(2), .disabled("Z"), .enable("false")) multiplexer_2 (
    .in0(2'b11), .in1(2'b01), .out(multiplexer_2_out), .sel(EX_Branched));
  Multiplexer #(.select(1), .width(2), .disabled("Z"), .enable("false")) multiplexer_3 (
    .in0(2'b01), .in1(2'b00), .out(multiplexer_3_out), .sel(EX_Branched));
  Multiplexer #(.select(1), .width(2), .disabled("Z"), .enable("false")) multiplexer_4 (
    .in0(2'b01), .in1(2'b11), .out(multiplexer_4_out), .sel(EX_Branched));
  Multiplexer #(.select(1), .width(2), .disabled("Z"), .enable("false")) multiplexer_5 (
    .in0(2'b00), .in1(2'b01), .out(multiplexer_5_out), .sel(EX_Branched));
  Multiplexer #(.select(1), .width(2), .disabled("Z"), .enable("false")) multiplexer_6 (
    .in0(2'b11), .in1(2'b01), .out(multiplexer_6_out), .sel(EX_Branched));
  Multiplexer #(.select(1), .width(2), .disabled("Z"), .enable("false")) multiplexer_7 (
    .in0(2'b01), .in1(2'b00), .out(multiplexer_7_out), .sel(EX_Branched));
  Multiplexer #(.select(1), .width(2), .disabled("Z"), .enable("false")) multiplexer_8 (
    .in0(2'b01), .in1(2'b11), .out(multiplexer_8_out), .sel(EX_Branched));
  Counter #(.width(16), .max('hffff), .ongoal("wrap"), .trigger("rising"), .behavior("old")) \u_置换标记  (
    .count(A0), .Q(C0), .clk(Clk), .clr(L0));  // open: load, D, carry, preset
  Counter #(.width(16), .max('hffff), .ongoal("wrap"), .trigger("rising"), .behavior("old")) \u_置换标记_2  (
    .count(A1), .Q(C1), .clk(Clk), .clr(L1));  // open: load, D, carry, preset
  Counter #(.width(16), .max('hffff), .ongoal("wrap"), .trigger("rising"), .behavior("old")) \u_置换标记_3  (
    .count(A2), .Q(C2), .clk(Clk), .clr(L2));  // open: load, D, carry, preset
  Counter #(.width(16), .max('hffff), .ongoal("wrap"), .trigger("rising"), .behavior("old")) \u_置换标记_4  (
    .count(A3), .Q(C3), .clk(Clk), .clr(L3));  // open: load, D, carry, preset
  Counter #(.width(16), .max('hffff), .ongoal("wrap"), .trigger("rising"), .behavior("old")) \u_置换标记_5  (
    .count(A4), .Q(C4), .clk(Clk), .clr(L4));  // open: load, D, carry, preset
  Counter #(.width(16), .max('hffff), .ongoal("wrap"), .trigger("rising"), .behavior("old")) \u_置换标记_6  (
    .count(A5), .Q(C5), .clk(Clk), .clr(L5));  // open: load, D, carry, preset
  Counter #(.width(16), .max('hffff), .ongoal("wrap"), .trigger("rising"), .behavior("old")) \u_置换标记_7  (
    .count(A6), .Q(C6), .clk(Clk), .clr(L6));  // open: load, D, carry, preset
  Counter #(.width(16), .max('hffff), .ongoal("wrap"), .trigger("rising"), .behavior("old")) \u_置换标记_8  (
    .count(A7), .Q(C7), .clk(Clk), .clr(L7));  // open: load, D, carry, preset
  and and_2 (A0, or_1_out, V0);
  and and_3 (A4, or_2_out, V4);
  Multiplexer #(.select(2), .width(2), .disabled("Z"), .enable("false")) multiplexer_9 (
    .in0(multiplexer_1_out), .in1(multiplexer_2_out), .in2(multiplexer_3_out), .in3(multiplexer_4_out),
    .out(multiplexer_9_out), .sel(Predict0));
  Adder #(.width(2)) adder_1 (.a(Predict0), .b(multiplexer_9_out), .out(adder_1_out));  // open: cin, cout
  Adder #(.width(2)) adder_2 (.a(Predict4), .b(multiplexer_10_out), .out(adder_2_out));  // open: cin, cout
  Multiplexer #(.select(2), .width(2), .disabled("Z"), .enable("false")) multiplexer_10 (
    .in0(multiplexer_5_out), .in1(multiplexer_6_out), .in2(multiplexer_7_out), .in3(multiplexer_8_out),
    .out(multiplexer_10_out), .sel(Predict4));
  or or_3 (or_3_out, decoder_1_out0, decoder_2_out0);
  or or_4 (or_4_out, decoder_1_out1, decoder_2_out1);
  or or_5 (or_5_out, decoder_1_out2, decoder_2_out2);
  or or_6 (or_6_out, decoder_1_out3, decoder_2_out3);
  or or_7 (or_7_out, decoder_1_out4, decoder_2_out4);
  or or_8 (or_8_out, decoder_1_out5, decoder_2_out5);
  or or_9 (or_9_out, decoder_1_out6, decoder_2_out6);
  or or_10 (or_10_out, decoder_1_out7, decoder_2_out7);
  Register #(.width(2), .trigger("rising"), .Select("low")) \u_分支预测历史位  (
    .D(adder_1_out), .en(M0), .Q(Predict0), .clk(Clk));  // open: clr
  Register #(.width(2), .trigger("rising"), .Select("low")) \u_分支预测历史位_2  (
    .D(adder_2_out), .en(M4), .Q(Predict4), .clk(Clk));  // open: clr
  Register #(.width(32), .trigger("rising"), .Select("low")) \u_分支目标地址  (
    .D(EX_BranchAddr), .en(WriteL0), .Q(\分支目标地址_q ), .clk(Clk));  // open: clr
  assign JumpAddr = L0 ? \分支目标地址_q  : 32'bz;  // Controlled_Buffer controlled_buffer_9
  assign JumpAddr = L1 ? \分支目标地址_2_q  : 32'bz;  // Controlled_Buffer controlled_buffer_10
  Register #(.width(32), .trigger("rising"), .Select("low")) \u_分支目标地址_2  (
    .D(EX_BranchAddr), .en(WriteL1), .Q(\分支目标地址_2_q ), .clk(Clk));  // open: clr
  assign JumpAddr = L2 ? \分支目标地址_3_q  : 32'bz;  // Controlled_Buffer controlled_buffer_11
  Register #(.width(32), .trigger("rising"), .Select("low")) \u_分支目标地址_3  (
    .D(EX_BranchAddr), .en(WriteL2), .Q(\分支目标地址_3_q ), .clk(Clk));  // open: clr
  assign JumpAddr = L3 ? \分支目标地址_4_q  : 32'bz;  // Controlled_Buffer controlled_buffer_12
  Register #(.width(32), .trigger("rising"), .Select("low")) \u_分支目标地址_4  (
    .D(EX_BranchAddr), .en(WriteL3), .Q(\分支目标地址_4_q ), .clk(Clk));  // open: clr
  Register #(.width(32), .trigger("rising"), .Select("low")) \u_分支目标地址_5  (
    .D(EX_BranchAddr), .en(WriteL4), .Q(\分支目标地址_5_q ), .clk(Clk));  // open: clr
  assign JumpAddr = L4 ? \分支目标地址_5_q  : 32'bz;  // Controlled_Buffer controlled_buffer_13
  assign JumpAddr = L5 ? \分支目标地址_6_q  : 32'bz;  // Controlled_Buffer controlled_buffer_14
  Register #(.width(32), .trigger("rising"), .Select("low")) \u_分支目标地址_6  (
    .D(EX_BranchAddr), .en(WriteL5), .Q(\分支目标地址_6_q ), .clk(Clk));  // open: clr
  Register #(.width(32), .trigger("rising"), .Select("low")) \u_分支目标地址_7  (
    .D(EX_BranchAddr), .en(WriteL6), .Q(\分支目标地址_7_q ), .clk(Clk));  // open: clr
  assign JumpAddr = L6 ? \分支目标地址_7_q  : 32'bz;  // Controlled_Buffer controlled_buffer_15
  assign JumpAddr = L7 ? \分支目标地址_8_q  : 32'bz;  // Controlled_Buffer controlled_buffer_16
  Register #(.width(32), .trigger("rising"), .Select("low")) \u_分支目标地址_8  (
    .D(EX_BranchAddr), .en(WriteL7), .Q(\分支目标地址_8_q ), .clk(Clk));  // open: clr
  and and_4 (WriteL0, or_3_out, EX_Miss, EX_Branch);
  and and_5 (WriteL1, or_4_out, EX_Miss, EX_Branch);
  and and_6 (WriteL2, or_5_out, EX_Miss, EX_Branch);
  and and_7 (WriteL3, or_6_out, EX_Miss, EX_Branch);
  and and_8 (WriteL4, or_7_out, EX_Miss, EX_Branch);
  and and_9 (WriteL5, or_8_out, EX_Miss, EX_Branch);
  and and_10 (WriteL6, or_9_out, EX_Miss, EX_Branch);
  and and_11 (WriteL7, or_10_out, EX_Miss, EX_Branch);
  or or_11 (or_11_out, L0, L2, L3, L4, L5, L6, L7, WriteL0, WriteL2, WriteL3, WriteL4, WriteL5, WriteL6, WriteL7);
  or or_12 (or_12_out, L0, L1, L2, L3, L4, L6, L7, WriteL0, WriteL1, WriteL2, WriteL3, WriteL4, WriteL6, WriteL7);
  and and_12 (A1, or_11_out, V1);
  and and_13 (A5, or_12_out, V5);
  Multiplexer #(.select(1), .width(2), .disabled("Z"), .enable("false")) multiplexer_11 (
    .in0(2'b00), .in1(2'b01), .out(multiplexer_11_out), .sel(EX_Branched));
  Multiplexer #(.select(1), .width(2), .disabled("Z"), .enable("false")) multiplexer_12 (
    .in0(2'b11), .in1(2'b01), .out(multiplexer_12_out), .sel(EX_Branched));
  Multiplexer #(.select(1), .width(2), .disabled("Z"), .enable("false")) multiplexer_13 (
    .in0(2'b01), .in1(2'b00), .out(multiplexer_13_out), .sel(EX_Branched));
  Multiplexer #(.select(1), .width(2), .disabled("Z"), .enable("false")) multiplexer_14 (
    .in0(2'b01), .in1(2'b11), .out(multiplexer_14_out), .sel(EX_Branched));
  Multiplexer #(.select(1), .width(2), .disabled("Z"), .enable("false")) multiplexer_15 (
    .in0(2'b00), .in1(2'b01), .out(multiplexer_15_out), .sel(EX_Branched));
  Multiplexer #(.select(1), .width(2), .disabled("Z"), .enable("false")) multiplexer_16 (
    .in0(2'b11), .in1(2'b01), .out(multiplexer_16_out), .sel(EX_Branched));
  Multiplexer #(.select(1), .width(2), .disabled("Z"), .enable("false")) multiplexer_17 (
    .in0(2'b01), .in1(2'b00), .out(multiplexer_17_out), .sel(EX_Branched));
  Multiplexer #(.select(1), .width(2), .disabled("Z"), .enable("false")) multiplexer_18 (
    .in0(2'b01), .in1(2'b11), .out(multiplexer_18_out), .sel(EX_Branched));
  Multiplexer #(.select(2), .width(2), .disabled("Z"), .enable("false")) multiplexer_19 (
    .in0(multiplexer_11_out), .in1(multiplexer_12_out), .in2(multiplexer_13_out), .in3(multiplexer_14_out),
    .out(multiplexer_19_out), .sel(Predict1));
  Multiplexer #(.select(2), .width(2), .disabled("Z"), .enable("false")) multiplexer_20 (
    .in0(multiplexer_15_out), .in1(multiplexer_16_out), .in2(multiplexer_17_out), .in3(multiplexer_18_out),
    .out(multiplexer_20_out), .sel(Predict5));
  Comparator #(.width(32), .mode("twosComplement")) comparator_1 (
    .a(PC), .b(Tag0), .eq(comparator_1_eq));  // open: gt, lt
  Comparator #(.width(32), .mode("twosComplement")) comparator_2 (
    .a(PC), .b(Tag1), .eq(comparator_2_eq));  // open: gt, lt
  Comparator #(.width(32), .mode("twosComplement")) comparator_3 (
    .a(PC), .b(Tag2), .eq(comparator_3_eq));  // open: gt, lt
  Comparator #(.width(32), .mode("twosComplement")) comparator_4 (
    .a(PC), .b(Tag3), .eq(comparator_4_eq));  // open: gt, lt
  Comparator #(.width(32), .mode("twosComplement")) comparator_5 (
    .a(PC), .b(Tag4), .eq(comparator_5_eq));  // open: gt, lt
  Comparator #(.width(32), .mode("twosComplement")) comparator_6 (
    .a(PC), .b(Tag5), .eq(comparator_6_eq));  // open: gt, lt
  Comparator #(.width(32), .mode("twosComplement")) comparator_7 (
    .a(PC), .b(Tag6), .eq(comparator_7_eq));  // open: gt, lt
  Comparator #(.width(32), .mode("twosComplement")) comparator_8 (
    .a(PC), .b(Tag7), .eq(comparator_8_eq));  // open: gt, lt
  Comparator #(.width(32), .mode("twosComplement")) comparator_9 (
    .a(EX_PC), .b(Tag0), .eq(comparator_9_eq));  // open: gt, lt
  Comparator #(.width(32), .mode("twosComplement")) comparator_10 (
    .a(EX_PC), .b(Tag1), .eq(comparator_10_eq));  // open: gt, lt
  Comparator #(.width(32), .mode("twosComplement")) comparator_11 (
    .a(EX_PC), .b(Tag2), .eq(comparator_11_eq));  // open: gt, lt
  Comparator #(.width(32), .mode("twosComplement")) comparator_12 (
    .a(EX_PC), .b(Tag3), .eq(comparator_12_eq));  // open: gt, lt
  Comparator #(.width(32), .mode("twosComplement")) comparator_13 (
    .a(EX_PC), .b(Tag4), .eq(comparator_13_eq));  // open: gt, lt
  Comparator #(.width(32), .mode("twosComplement")) comparator_14 (
    .a(EX_PC), .b(Tag5), .eq(comparator_14_eq));  // open: gt, lt
  Comparator #(.width(32), .mode("twosComplement")) comparator_15 (
    .a(EX_PC), .b(Tag6), .eq(comparator_15_eq));  // open: gt, lt
  Comparator #(.width(32), .mode("twosComplement")) comparator_16 (
    .a(EX_PC), .b(Tag7), .eq(comparator_16_eq));  // open: gt, lt
  Register #(.width(2), .trigger("rising"), .Select("low")) \u_分支预测历史位_3  (
    .D(adder_3_out), .en(M1), .Q(Predict1), .clk(Clk));  // open: clr
  Adder #(.width(2)) adder_3 (.a(Predict1), .b(multiplexer_19_out), .out(adder_3_out));  // open: cin, cout
  Adder #(.width(2)) adder_4 (.a(Predict5), .b(multiplexer_20_out), .out(adder_4_out));  // open: cin, cout
  or or_13 (or_13_out, L0, L1, L3, L4, L5, L6, L7, WriteL0, WriteL1, WriteL3, WriteL4, WriteL5, WriteL6, WriteL7);
  or or_14 (or_14_out, L0, L1, L2, L3, L4, L5, L7, WriteL0, WriteL1, WriteL2, WriteL3, WriteL4, WriteL5, WriteL7);
  Register #(.width(2), .trigger("rising"), .Select("low")) \u_分支预测历史位_4  (
    .D(adder_4_out), .en(M5), .Q(Predict5), .clk(Clk));  // open: clr
  and and_14 (L0, comparator_1_eq, V0);
  and and_15 (L1, comparator_2_eq, V1);
  and and_16 (L2, comparator_3_eq, V2);
  and and_17 (L3, comparator_4_eq, V3);
  and and_18 (L4, comparator_5_eq, V4);
  and and_19 (L5, comparator_6_eq, V5);
  and and_20 (L6, comparator_7_eq, V6);
  and and_21 (L7, comparator_8_eq, V7);
  and and_22 (M0, comparator_9_eq, V0);
  and and_23 (M1, comparator_10_eq, V1);
  and and_24 (M2, comparator_11_eq, V2);
  and and_25 (M3, comparator_12_eq, V3);
  and and_26 (M4, comparator_13_eq, V4);
  and and_27 (M5, comparator_14_eq, V5);
  and and_28 (M6, comparator_15_eq, V6);
  and and_29 (M7, comparator_16_eq, V7);
  and and_30 (A2, or_13_out, V2);
  and and_31 (A6, or_14_out, V6);
  or or_15 (IF_Hit, L0, L1, L2, L3, L4, L5, L6, L7);
  or or_16 (EX_Hit, M0, M1, M2, M3, M4, M5, M6, M7);
  Multiplexer #(.select(1), .width(2), .disabled("Z"), .enable("false")) multiplexer_21 (
    .in0(2'b00), .in1(2'b01), .out(multiplexer_21_out), .sel(EX_Branched));
  Multiplexer #(.select(1), .width(2), .disabled("Z"), .enable("false")) multiplexer_22 (
    .in0(2'b11), .in1(2'b01), .out(multiplexer_22_out), .sel(EX_Branched));
  Multiplexer #(.select(1), .width(2), .disabled("Z"), .enable("false")) multiplexer_23 (
    .in0(2'b01), .in1(2'b00), .out(multiplexer_23_out), .sel(EX_Branched));
  Multiplexer #(.select(1), .width(2), .disabled("Z"), .enable("false")) multiplexer_24 (
    .in0(2'b01), .in1(2'b11), .out(multiplexer_24_out), .sel(EX_Branched));
  Multiplexer #(.select(1), .width(2), .disabled("Z"), .enable("false")) multiplexer_25 (
    .in0(2'b00), .in1(2'b01), .out(multiplexer_25_out), .sel(EX_Branched));
  Multiplexer #(.select(1), .width(2), .disabled("Z"), .enable("false")) multiplexer_26 (
    .in0(2'b11), .in1(2'b01), .out(multiplexer_26_out), .sel(EX_Branched));
  Multiplexer #(.select(1), .width(2), .disabled("Z"), .enable("false")) multiplexer_27 (
    .in0(2'b01), .in1(2'b00), .out(multiplexer_27_out), .sel(EX_Branched));
  Multiplexer #(.select(1), .width(2), .disabled("Z"), .enable("false")) multiplexer_28 (
    .in0(2'b01), .in1(2'b11), .out(multiplexer_28_out), .sel(EX_Branched));
  not not_9 (IF_Miss, IF_Hit);
  not not_10 (EX_Miss, EX_Hit);
  Adder #(.width(2)) adder_5 (.a(Predict2), .b(multiplexer_29_out), .out(adder_5_out));  // open: cin, cout
  Multiplexer #(.select(2), .width(2), .disabled("Z"), .enable("false")) multiplexer_29 (
    .in0(multiplexer_21_out), .in1(multiplexer_22_out), .in2(multiplexer_23_out), .in3(multiplexer_24_out),
    .out(multiplexer_29_out), .sel(Predict2));
  Multiplexer #(.select(2), .width(2), .disabled("Z"), .enable("false")) multiplexer_30 (
    .in0(multiplexer_25_out), .in1(multiplexer_26_out), .in2(multiplexer_27_out), .in3(multiplexer_28_out),
    .out(multiplexer_30_out), .sel(Predict6));
  or or_17 (or_17_out, L0, L1, L2, L4, L5, L6, L7, WriteL0, WriteL1, WriteL2, WriteL4, WriteL5, WriteL6, WriteL7);
  or or_18 (or_18_out, L0, L1, L2, L3, L4, L5, L6, WriteL0, WriteL1, WriteL2, WriteL3, WriteL4, WriteL5, WriteL6);
  Register #(.width(2), .trigger("rising"), .Select("low")) \u_分支预测历史位_5  (
    .D(adder_5_out), .en(M2), .Q(Predict2), .clk(Clk));  // open: clr
  Register #(.width(2), .trigger("rising"), .Select("low")) \u_分支预测历史位_6  (
    .D(adder_6_out), .en(M6), .Q(Predict6), .clk(Clk));  // open: clr
  Adder #(.width(2)) adder_6 (.a(Predict6), .b(multiplexer_30_out), .out(adder_6_out));  // open: cin, cout
  and and_32 (A3, or_17_out, V3);
  and and_33 (A7, or_18_out, V7);
  Multiplexer #(.select(1), .width(2), .disabled("Z"), .enable("false")) multiplexer_31 (
    .in0(2'b00), .in1(2'b01), .out(multiplexer_31_out), .sel(EX_Branched));
  Multiplexer #(.select(1), .width(2), .disabled("Z"), .enable("false")) multiplexer_32 (
    .in0(2'b11), .in1(2'b01), .out(multiplexer_32_out), .sel(EX_Branched));
  Multiplexer #(.select(1), .width(2), .disabled("Z"), .enable("false")) multiplexer_33 (
    .in0(2'b01), .in1(2'b00), .out(multiplexer_33_out), .sel(EX_Branched));
  Multiplexer #(.select(1), .width(2), .disabled("Z"), .enable("false")) multiplexer_34 (
    .in0(2'b01), .in1(2'b11), .out(multiplexer_34_out), .sel(EX_Branched));
  Multiplexer #(.select(1), .width(2), .disabled("Z"), .enable("false")) multiplexer_35 (
    .in0(2'b00), .in1(2'b01), .out(multiplexer_35_out), .sel(EX_Branched));
  Multiplexer #(.select(1), .width(2), .disabled("Z"), .enable("false")) multiplexer_36 (
    .in0(2'b11), .in1(2'b01), .out(multiplexer_36_out), .sel(EX_Branched));
  Multiplexer #(.select(1), .width(2), .disabled("Z"), .enable("false")) multiplexer_37 (
    .in0(2'b01), .in1(2'b00), .out(multiplexer_37_out), .sel(EX_Branched));
  Multiplexer #(.select(1), .width(2), .disabled("Z"), .enable("false")) multiplexer_38 (
    .in0(2'b01), .in1(2'b11), .out(multiplexer_38_out), .sel(EX_Branched));
  Multiplexer #(.select(2), .width(2), .disabled("Z"), .enable("false")) multiplexer_39 (
    .in0(multiplexer_31_out), .in1(multiplexer_32_out), .in2(multiplexer_33_out), .in3(multiplexer_34_out),
    .out(multiplexer_39_out), .sel(Predict3));
  Multiplexer #(.select(2), .width(2), .disabled("Z"), .enable("false")) multiplexer_40 (
    .in0(multiplexer_35_out), .in1(multiplexer_36_out), .in2(multiplexer_37_out), .in3(multiplexer_38_out),
    .out(multiplexer_40_out), .sel(Predict7));
  Adder #(.width(2)) adder_7 (.a(Predict3), .b(multiplexer_39_out), .out(adder_7_out));  // open: cin, cout
  Adder #(.width(2)) adder_8 (.a(Predict7), .b(multiplexer_40_out), .out(adder_8_out));  // open: cin, cout
  Register #(.width(2), .trigger("rising"), .Select("low")) \u_分支预测历史位_7  (
    .D(adder_7_out), .en(M3), .Q(Predict3), .clk(Clk));  // open: clr
  Register #(.width(2), .trigger("rising"), .Select("low")) \u_分支预测历史位_8  (
    .D(adder_8_out), .en(M7), .Q(Predict7), .clk(Clk));  // open: clr

  // Other names for the same wires on the sheet: Tag[31:0] = EX_PC

  // Notes on the sheet:
  //   Cache槽
  //   读缺失逻辑/块载入逻辑
  //   查找逻辑
endmodule
