// Logisim project cpu21-riscv_wy2.circ as structural Verilog: 24 circuits, main circuit ◇单周期RISC-V
module \单周期RISC_V  (
  input  IR1,
  input  IR2,
  input  IR3,
  output RegWrite,
  output MemWrite,
  output [31:0] PC,
  output [31:0] IR,
  output [31:0] RDin,
  output [31:0] MDin,
  output [31:0] LedData
);

  wire Alu_Src, and_1_out, and_2_out, and_3_out, and_4_out, Beq, BGEU, Bne, CLK, clock_1_out,
       comparator_1_eq, comparator_2_eq, comparator_2_lt, d_ff_1_q, E, ecall, G, Go, halt, IR1_t, IR2_t,
       IR3_t, IRA, IRB, IRC, JAL, JALR, LUI, MemToReg, nand_1_out, not_1_out, not_2_out, not_3_out,
       not_4_out, or_1_out, or_2_out, or_10_out, RST, S, S_type, sb, URET, W1, W2, W3;
  wire [1:0] priority_encoder_1_out, priority_encoder_2_out;
  wire [3:0] \单周期硬布线控制器_1_alu_op ;
  wire [4:0] multiplexer_2_out, multiplexer_3_out;
  wire [12:0] CNT_num;
  wire [15:0] \总周期数 ;
  wire [31:0] ALUResult, and_6_out, and_7_out, and_8_out, and_9_out, B, bit_extender_1_out,
       bit_extender_2_out, bit_extender_3_out, bit_extender_4_out, bit_extender_5_out, J, multiplexer_1_out,
       multiplexer_4_out, multiplexer_5_out, multiplexer_6_out, multiplexer_7_out, or_6_out, or_7_out,
       or_8_out, or_9_out, PC_4, ram_1_data, regifile_1_r1, shifter_1_out, shifter_2_out, shifter_3_out,
       shifter_4_out, shifter_5_out, shifter_6_out, U;

  Button \u_继续运行  (.out(Go));
  Button _1 (.out(IRA));
  Button _2 (.out(IRB));
  Button _3 (.out(IRC));
  LED #(.active("true")) led_1 (.in(W1));
  LED #(.active("true")) led_2 (.in(W2));
  LED #(.active("true")) led_3 (.in(W3));
  Priority_Encoder #(.select(2), .disabled("Z")) priority_encoder_1 (
    .in0(1'b1), .in1(JALR), .in2(or_2_out), .in3(JAL), .out(priority_encoder_1_out));  // open: gs, en_out, en_in
  Multiplexer #(.select(2), .width(32), .disabled("Z"), .enable("false")) multiplexer_1 (
    .in0(PC_4), .in1(ALUResult), .in2(B), .in3(J), .out(multiplexer_1_out), .sel(priority_encoder_1_out));
  not not_1 (not_1_out, halt);
  Hex_Digit_Display hex_digit_display_1 (.value(LedData[31:28]));  // open: dp
  Register #(.width(32), .trigger("rising"), .Select("low")) u_PC (
    .D(multiplexer_1_out), .en(or_1_out), .Q(PC), .clk(CLK), .clr(RST));
  or or_1 (or_1_out, not_1_out, Go);
  Hex_Digit_Display hex_digit_display_2 (.value(LedData[23:20]));  // open: dp
  Hex_Digit_Display hex_digit_display_3 (.value(LedData[27:24]));  // open: dp
  and and_1 (and_1_out, BGEU, G);
  or or_2 (or_2_out, and_1_out, and_2_out, and_3_out);
  and and_2 (and_2_out, Beq, E);
  and and_3 (and_3_out, not_3_out, Bne);
  not not_2 (not_2_out, halt);
  Hex_Digit_Display hex_digit_display_4 (.value(LedData[15:12]));  // open: dp
  Hex_Digit_Display hex_digit_display_5 (.value(LedData[19:16]));  // open: dp
  not not_3 (not_3_out, E);
  // RiscV_Probe riscv_probe_1: pin names not known; wires that end beside it: IR
  Adder #(.width(32)) adder_1 (.a(PC), .b(32'h4), .out(PC_4));  // open: cin, cout
  Counter #(.width(16), .max('hffff), .ongoal("wrap"), .trigger("rising"), .behavior("new")) counter_1 (
    .count(not_2_out), .Q(\总周期数 ), .clk(CLK));  // open: load, D, carry, clr, preset, down
  Hex_Digit_Display hex_digit_display_6 (.value(LedData[7:4]));  // open: dp
  Hex_Digit_Display hex_digit_display_7 (.value(LedData[11:8]));  // open: dp
  // Probe on \总周期数 
  ROM #(.addrWidth(10), .dataWidth(32), .Select("high")) rom_1 (.addr(PC[11:2]), .data(IR));
  Hex_Digit_Display hex_digit_display_8 (.value(LedData[3:0]));  // open: dp
  \单周期硬布线控制器  \u_单周期硬布线控制器_1  (
    .Funct({IR[30], IR[25], IR[14:12]}), .OP(IR[6:2]), .ALU_OP(\单周期硬布线控制器_1_alu_op ), .MemToReg(MemToReg),
    .MemWrite(MemWrite), .ALU_SRC(Alu_Src), .RegWrite(RegWrite), .ecall(ecall), .S_type(S_type), .Jalr(JALR),
    .Beq(Beq), .JAL(JAL), .Bne(Bne), .in_3(IR[21]), .uret(URET), .LUI(LUI), .sb(sb), .BGEU(BGEU));  // open: rs1, rs2, CSR
  Multiplexer #(.select(1), .width(5), .disabled("Z"), .enable("false")) multiplexer_2 (
    .in0(IR[19:15]), .in1(5'b10001), .out(multiplexer_2_out), .sel(ecall));
  Multiplexer #(.select(1), .width(5), .disabled("Z"), .enable("false")) multiplexer_3 (
    .in0(IR[24:20]), .in1(5'b01010), .out(multiplexer_3_out), .sel(ecall));
  assign bit_extender_1_out = {{20{IR[31]}}, IR[31:20]};  // Bit_Extender bit_extender_1
  assign bit_extender_2_out = {{12{IR[31]}}, IR[31:12]};  // Bit_Extender bit_extender_2
  or or_3 (IR1_t, IR1, IRA);
  assign bit_extender_3_out = {{20{IR[31]}}, {IR[31:25], IR[11:7]}};  // Bit_Extender bit_extender_3
  assign bit_extender_4_out = {{20{IR[31]}}, {IR[31], IR[7], IR[30:25], IR[11:8]}};  // Bit_Extender bit_extender_4
  assign bit_extender_5_out = {{12{IR[31]}}, {IR[31], IR[19:12], IR[20], IR[30:21]}};  // Bit_Extender bit_extender_5
  or or_4 (IR2_t, IR2, IRB);
  Regifile regifile_1 (
    .Din(RDin), .Clk(CLK), .R1(regifile_1_r1), .R2(MDin), .WE(RegWrite), .W_num(IR[11:7]),
    .R1_num(multiplexer_2_out), .R2_num(multiplexer_3_out));
  Multiplexer #(.select(1), .width(32), .disabled("Z"), .enable("false")) multiplexer_4 (
    .in0(bit_extender_1_out), .in1(bit_extender_3_out), .out(multiplexer_4_out), .sel(S_type));
  Shifter #(.width(32), .shift("ll")) shifter_1 (.in(bit_extender_4_out), .\dist (5'b00001), .out(shifter_1_out));
  Shifter #(.width(32), .shift("ll")) shifter_2 (.in(bit_extender_5_out), .\dist (5'b00001), .out(shifter_2_out));
  Shifter #(.width(32), .shift("ll")) shifter_3 (.in(bit_extender_2_out), .\dist (5'b01100), .out(shifter_3_out));
  Adder #(.width(32)) adder_2 (.a(shifter_1_out), .b(PC), .out(B));  // open: cin, cout
  Adder #(.width(32)) adder_3 (.a(PC), .b(shifter_2_out), .out(J));  // open: cin, cout
  Adder #(.width(32)) adder_4 (.a(PC), .b(shifter_3_out), .out(U));  // open: cin, cout
  or or_5 (IR3_t, IR3, IRC);
  Multiplexer #(.select(1), .width(32), .disabled("Z"), .enable("false")) multiplexer_5 (
    .in0(MDin), .in1(multiplexer_4_out), .out(multiplexer_5_out), .sel(Alu_Src));
  Comparator #(.width(32), .mode("twosComplement")) comparator_1 (
    .a(regifile_1_r1), .b(32'h22), .eq(comparator_1_eq));  // open: gt, lt
  ALU alu_1 (
    .X(regifile_1_r1), .Y(multiplexer_5_out), .AluOP(\单周期硬布线控制器_1_alu_op ), .Equal(E), .Result(ALUResult),
    .out_4(G), .out_6(S));  // open: Result_2
  and and_4 (and_4_out, comparator_1_eq, ecall);
  not not_4 (not_4_out, comparator_1_eq);
  and and_5 (halt, ecall, not_4_out);
  Multiplexer #(.select(1), .width(32), .disabled("Z"), .enable("false")) multiplexer_6 (
    .in0(MDin), .in1(multiplexer_7_out), .out(multiplexer_6_out), .sel(sb));
  Multiplexer #(.select(2), .width(32), .disabled("Z"), .enable("false")) multiplexer_7 (
    .in0(or_8_out), .in1(or_9_out), .in2(or_6_out), .in3(or_7_out), .out(multiplexer_7_out),
    .sel(ALUResult[1:0]));
  assign or_6_out = and_7_out | shifter_5_out;  // OR_Gate or_6, 32 bits wide
  assign or_7_out = shifter_6_out | and_6_out;  // OR_Gate or_7, 32 bits wide
  Register #(.width(32), .trigger("rising"), .Select("low")) register_1 (
    .D(MDin), .en(and_4_out), .Q(LedData), .clk(CLK));  // open: clr
  assign or_8_out = and_9_out | MDin;  // OR_Gate or_8, 32 bits wide
  assign or_9_out = and_8_out | shifter_4_out;  // OR_Gate or_9, 32 bits wide
  RAM #(.addrWidth(10), .dataWidth(32), .bus("separate"), .Select("high")) ram_1 (
    .addr(ALUResult[11:2]), .din(multiplexer_6_out), .data(ram_1_data), .str(MemWrite), .sel(1'b1),
    .clk(CLK), .ld(1'b1));  // open: clr
  assign and_6_out = ram_1_data & 32'hffffff;  // AND_Gate and_6, 32 bits wide
  assign and_7_out = ram_1_data & 32'hff00ffff;  // AND_Gate and_7, 32 bits wide
  assign and_8_out = ram_1_data & 32'hffff00ff;  // AND_Gate and_8, 32 bits wide
  assign and_9_out = ram_1_data & 32'hffffff00;  // AND_Gate and_9, 32 bits wide
  Shifter #(.width(32), .shift("ll")) shifter_4 (.in(MDin), .\dist (5'b01000), .out(shifter_4_out));
  Shifter #(.width(32), .shift("ll")) shifter_5 (.in(MDin), .\dist (5'b10000), .out(shifter_5_out));
  Shifter #(.width(32), .shift("ll")) shifter_6 (.in(MDin), .\dist (5'b11000), .out(shifter_6_out));
  D_Flip_Flop #(.trigger("high"), .Pre_Clr_Positions("LEGACY"), .NegatePresetClear("false"), .enable("true"), .NewFFLayout("false")) d_ff_1 (.Q(d_ff_1_q));  // open: clk, D, Qn, preset, en, reset
  // Probe on 13'hc
  Priority_Encoder #(.select(2), .disabled("Z")) priority_encoder_2 (
    .in0(1'b1), .in1(MemToReg), .in2(or_10_out), .in3(LUI), .out(priority_encoder_2_out));  // open: gs, en_out, en_in
  Comparator #(.width(13), .mode("twosComplement")) comparator_2 (
    .a(CNT_num), .b(13'hc), .eq(comparator_2_eq), .lt(comparator_2_lt));  // open: gt
  Clock #(.highDuration(1), .lowDuration(1)) clock_1 (.out(clock_1_out));
  Multiplexer #(.select(2), .width(32), .disabled("Z"), .enable("false")) multiplexer_8 (
    .in0(ALUResult), .in1(ram_1_data), .in2(PC_4), .in3(U), .out(RDin), .sel(priority_encoder_2_out));
  or or_10 (or_10_out, JALR, JAL);
  Counter #(.width(13), .max('h1fff), .ongoal("stay"), .trigger("rising"), .behavior("old")) counter_2 (
    .count(comparator_2_lt), .Q(CNT_num), .clk(clock_1_out));  // open: load, D, carry, clr, preset
  nand nand_1 (nand_1_out, d_ff_1_q, comparator_2_eq);
  assign CLK = nand_1_out ? clock_1_out : 1'bz;  // Controlled_Buffer controlled_buffer_1
  Pull_Resistor #(.pull(1)) pull_resistor_1 (.node(CLK));

  // Notes on the sheet:
  //   中断源
  //   中断等待指示
  //   数码管输出应该用寄存器锁存，否则显示数据只能一闪而过
  //   数码管输出
  //   指令探针
  //   指令存储器
  //   周期计数器
  //   指令字
  //   contents of rom_1 (hex, n*v repeats v):
  //   313 2000e13 493 100913 930023 900533 2200893 73 12484b3 130313 fffe0e13 fe0e12e3 800e13 313 32483
  //   900533 2200893 73 430313 fffe0e13 fe0e14e3 a00893 73
  //   I型指令
  //   S型指令
  //   B型指令
  //   J型指令
  //   为方便自动评测，需要输出PC，IR，寄存器堆写如数据RDin
  //   RAM写使能MemWrite、RAM写入数据MDin等信号
  //   数据存储器
  //   控制位
  //   暂停节拍，不能为0
  //   戳工具置1进入计数暂停模式，ctrl+k时钟自动运行到对应节拍暂停
  //   ctrl+k关闭时钟连续运行，将控制位置零，进入单步调试模式调试
  //   用这个时钟源需要去掉电路中的其他时钟源
  //   可计数暂停的时钟源
endmodule

// 单周期硬布线控制器
module \单周期硬布线控制器  (
  input  [4:0] OP,
  input  [4:0] Funct,
  input  in_3,
  output [3:0] ALU_OP,
  output uret,
  output MemToReg,
  output MemWrite,
  output CSR,
  output ecall,
  output rs1,
  output rs2,
  output ALU_SRC,
  output RegWrite,
  output S_type,
  output Beq,
  output Bne,
  output Jalr,
  output JAL,
  output LUI,
  output sb,
  output BGEU
);

  wire \控制信号自动生成_1_ecall ;

  \运算控制器自动生成  \u_运算控制器自动生成_1  (
    .OP2(OP[0]), .OP3(OP[1]), .OP4(OP[2]), .OP5(OP[3]), .OP6(OP[4]), .F12(Funct[0]), .F13(Funct[1]),
    .F14(Funct[2]), .F25(Funct[3]), .F30(Funct[4]), .S0(ALU_OP[0]), .S1(ALU_OP[1]), .S2(ALU_OP[2]),
    .S3(ALU_OP[3]));
  \控制信号自动生成  \u_控制信号自动生成_1  (
    .OP2(OP[0]), .OP3(OP[1]), .MemToReg(MemToReg), .OP4(OP[2]), .OP5(OP[3]), .OP6(OP[4]), .F12(Funct[0]),
    .F13(Funct[1]), .F14(Funct[2]), .MemWrite(MemWrite), .F25(Funct[3]), .F30(Funct[4]), .CSR(CSR),
    .rs1use(rs1), .rs2use(rs2), .ALU_SRC(ALU_SRC), .RegWrite(RegWrite), .ecall(\控制信号自动生成_1_ecall ),
    .S_Type(S_type), .BEQ(Beq), .BNE(Bne), .JALR(Jalr), .JAL(JAL), .LUI(LUI), .SB(sb), .BEGU(BGEU));
  and and_1 (uret, in_3, \控制信号自动生成_1_ecall );
  and and_2 (ecall, ~in_3, \控制信号自动生成_1_ecall );  // AND_Gate

  // Other names for the same wires on the sheet: IR21 = in_3; OP_CODE[4:0] = OP

  // Notes on the sheet:
  //   运算器控制器，根据指令生成运算器功能选择信号
endmodule

// 运算器控制器
module \运算控制器自动生成  (
  input  OP2,
  input  OP3,
  input  OP4,
  input  OP5,
  input  OP6,
  input  F12,
  input  F13,
  input  F14,
  input  F25,
  input  F30,
  output S0,
  output S1,
  output S2,
  output S3
);

  wire and_1_out, and_2_out, and_3_out, and_4_out, and_5_out, and_6_out, and_7_out, and_8_out, and_9_out,
       and_10_out, and_11_out, and_12_out, and_13_out, and_14_out, and_15_out, and_16_out, and_17_out,
       and_18_out, and_19_out, and_20_out, and_21_out, and_22_out, and_23_out, and_24_out, and_25_out,
       and_26_out, and_27_out, and_28_out, and_29_out, and_30_out, and_31_out, and_32_out, and_33_out,
       and_34_out, and_35_out, and_36_out, not_1_out, not_2_out, not_3_out, not_4_out, not_5_out, not_6_out,
       not_7_out, not_8_out, not_9_out, not_10_out, not_11_out, not_12_out, not_13_out, not_14_out,
       not_15_out, not_16_out, not_17_out, not_18_out, not_19_out, not_20_out, not_21_out, not_22_out,
       not_23_out, not_24_out, not_25_out, not_26_out, not_27_out, not_28_out, not_29_out, not_30_out,
       not_31_out, not_32_out, not_33_out, not_34_out, not_35_out, not_36_out, not_37_out, not_38_out,
       not_39_out, not_40_out, not_41_out, not_42_out, not_43_out, not_44_out, not_45_out, not_46_out,
       not_47_out, not_48_out, not_49_out, not_50_out, not_51_out, not_52_out, not_53_out, not_54_out,
       not_55_out, not_56_out, not_57_out, not_58_out, not_59_out, not_60_out, not_61_out, not_62_out,
       not_63_out, not_64_out, not_65_out, not_66_out, not_67_out, not_68_out, not_69_out, not_70_out,
       not_71_out, not_72_out, not_73_out, not_74_out, not_75_out, not_76_out, not_77_out, not_78_out,
       not_79_out, not_80_out, not_81_out, not_82_out, not_83_out, not_84_out, not_85_out, not_86_out,
       not_87_out, not_88_out, not_89_out, not_90_out, not_91_out, not_92_out, not_93_out, not_94_out,
       not_95_out, not_96_out, not_97_out, not_98_out, not_99_out, not_100_out, not_101_out, not_102_out,
       not_103_out, not_104_out, not_105_out, not_106_out, not_107_out, not_108_out, not_109_out,
       not_110_out, not_111_out, not_112_out, not_113_out, not_114_out, not_115_out, not_116_out,
       not_117_out, not_118_out, not_119_out, not_120_out, not_121_out, not_122_out, not_123_out,
       not_124_out, not_125_out, not_126_out, not_127_out, not_128_out, not_129_out, not_130_out,
       not_131_out, not_132_out, not_133_out, not_134_out, not_135_out, not_136_out, not_137_out,
       not_138_out, not_139_out, not_140_out, not_141_out, not_142_out, not_143_out, not_144_out,
       not_145_out, not_146_out, not_147_out, not_148_out, not_149_out, not_150_out, not_151_out,
       not_152_out, not_153_out, not_154_out, not_155_out, not_156_out, not_157_out, not_158_out,
       not_159_out, not_160_out, not_161_out, not_162_out, not_163_out, not_164_out, not_165_out,
       not_166_out, not_167_out, not_168_out, not_169_out, not_170_out, not_171_out, not_172_out,
       not_173_out, not_174_out, not_175_out, not_176_out, not_177_out, not_178_out, not_179_out,
       not_180_out, not_181_out, not_182_out, not_183_out, not_184_out, not_185_out, not_186_out,
       not_187_out, not_188_out, not_189_out, not_190_out, not_191_out, not_192_out, not_193_out,
       not_194_out, not_195_out, not_196_out, not_197_out, not_198_out, not_199_out, not_200_out,
       not_201_out, not_202_out, not_203_out, not_204_out, not_205_out, not_206_out, not_207_out,
       not_208_out, not_209_out, not_210_out;

  not not_1 (not_1_out, F30);
  not not_2 (not_2_out, F25);
  not not_3 (not_3_out, F14);
  not not_4 (not_4_out, F13);
  not not_5 (not_5_out, F12);
  not not_6 (not_6_out, OP6);
  not not_7 (not_7_out, OP3);
  not not_8 (not_8_out, OP2);
  not not_9 (not_9_out, F30);
  not not_10 (not_10_out, F25);
  not not_11 (not_11_out, OP6);
  not not_12 (not_12_out, OP3);
  not not_13 (not_13_out, OP2);
  not not_14 (not_14_out, F30);
  not not_15 (not_15_out, F25);
  not not_16 (not_16_out, F14);
  not not_17 (not_17_out, F12);
  not not_18 (not_18_out, OP6);
  not not_19 (not_19_out, OP3);
  not not_20 (not_20_out, OP2);
  not not_21 (not_21_out, F14);
  not not_22 (not_22_out, F13);
  not not_23 (not_23_out, F12);
  not not_24 (not_24_out, OP6);
  not not_25 (not_25_out, OP5);
  not not_26 (not_26_out, OP3);
  not not_27 (not_27_out, OP2);
  not not_28 (not_28_out, OP6);
  not not_29 (not_29_out, OP5);
  not not_30 (not_30_out, OP3);
  not not_31 (not_31_out, OP2);
  not not_32 (not_32_out, F13);
  not not_33 (not_33_out, F12);
  not not_34 (not_34_out, OP6);
  not not_35 (not_35_out, OP5);
  not not_36 (not_36_out, OP3);
  not not_37 (not_37_out, OP2);
  not not_38 (not_38_out, F14);
  not not_39 (not_39_out, F12);
  not not_40 (not_40_out, OP6);
  not not_41 (not_41_out, OP5);
  not not_42 (not_42_out, OP3);
  not not_43 (not_43_out, OP2);
  not not_44 (not_44_out, F25);
  not not_45 (not_45_out, F13);
  not not_46 (not_46_out, OP6);
  not not_47 (not_47_out, OP5);
  not not_48 (not_48_out, OP3);
  not not_49 (not_49_out, OP2);
  not not_50 (not_50_out, F14);
  not not_51 (not_51_out, F13);
  not not_52 (not_52_out, F12);
  not not_53 (not_53_out, OP4);
  not not_54 (not_54_out, OP3);
  not not_55 (not_55_out, F30);
  not not_56 (not_56_out, F25);
  not not_57 (not_57_out, F13);
  not not_58 (not_58_out, F12);
  not not_59 (not_59_out, OP6);
  not not_60 (not_60_out, OP3);
  not not_61 (not_61_out, OP2);
  not not_62 (not_62_out, F25);
  not not_63 (not_63_out, F14);
  not not_64 (not_64_out, F13);
  not not_65 (not_65_out, F12);
  not not_66 (not_66_out, OP6);
  not not_67 (not_67_out, OP3);
  not not_68 (not_68_out, OP2);
  not not_69 (not_69_out, F30);
  not not_70 (not_70_out, F25);
  not not_71 (not_71_out, OP6);
  not not_72 (not_72_out, OP3);
  not not_73 (not_73_out, OP2);
  not not_74 (not_74_out, F30);
  not not_75 (not_75_out, F25);
  not not_76 (not_76_out, F14);
  not not_77 (not_77_out, F12);
  not not_78 (not_78_out, OP6);
  not not_79 (not_79_out, OP3);
  not not_80 (not_80_out, OP2);
  not not_81 (not_81_out, OP6);
  not not_82 (not_82_out, OP5);
  not not_83 (not_83_out, OP3);
  not not_84 (not_84_out, OP2);
  not not_85 (not_85_out, F14);
  not not_86 (not_86_out, F12);
  not not_87 (not_87_out, OP6);
  not not_88 (not_88_out, OP5);
  not not_89 (not_89_out, OP3);
  not not_90 (not_90_out, OP2);
  not not_91 (not_91_out, F30);
  not not_92 (not_92_out, F25);
  not not_93 (not_93_out, F13);
  not not_94 (not_94_out, OP6);
  not not_95 (not_95_out, OP5);
  not not_96 (not_96_out, OP3);
  not not_97 (not_97_out, OP2);
  not not_98 (not_98_out, F14);
  not not_99 (not_99_out, F13);
  not not_100 (not_100_out, F12);
  not not_101 (not_101_out, OP4);
  not not_102 (not_102_out, OP3);
  not not_103 (not_103_out, OP2);
  not not_104 (not_104_out, F14);
  not not_105 (not_105_out, F13);
  not not_106 (not_106_out, OP4);
  not not_107 (not_107_out, OP3);
  not not_108 (not_108_out, OP2);
  not not_109 (not_109_out, F30);
  not not_110 (not_110_out, F25);
  not not_111 (not_111_out, F14);
  not not_112 (not_112_out, F13);
  not not_113 (not_113_out, F12);
  not not_114 (not_114_out, OP6);
  not not_115 (not_115_out, OP3);
  not not_116 (not_116_out, OP2);
  not not_117 (not_117_out, F25);
  not not_118 (not_118_out, F14);
  not not_119 (not_119_out, F13);
  not not_120 (not_120_out, F12);
  not not_121 (not_121_out, OP6);
  not not_122 (not_122_out, OP3);
  not not_123 (not_123_out, OP2);
  not not_124 (not_124_out, F30);
  not not_125 (not_125_out, F25);
  not not_126 (not_126_out, OP6);
  not not_127 (not_127_out, OP3);
  not not_128 (not_128_out, OP2);
  not not_129 (not_129_out, F30);
  not not_130 (not_130_out, F25);
  not not_131 (not_131_out, F14);
  not not_132 (not_132_out, OP6);
  not not_133 (not_133_out, OP3);
  not not_134 (not_134_out, OP2);
  not not_135 (not_135_out, F14);
  not not_136 (not_136_out, F13);
  not not_137 (not_137_out, F12);
  not not_138 (not_138_out, OP6);
  not not_139 (not_139_out, OP5);
  not not_140 (not_140_out, OP3);
  not not_141 (not_141_out, OP2);
  not not_142 (not_142_out, OP6);
  not not_143 (not_143_out, OP5);
  not not_144 (not_144_out, OP3);
  not not_145 (not_145_out, OP2);
  not not_146 (not_146_out, F14);
  not not_147 (not_147_out, F13);
  not not_148 (not_148_out, F12);
  not not_149 (not_149_out, OP4);
  not not_150 (not_150_out, OP3);
  not not_151 (not_151_out, OP2);
  not not_152 (not_152_out, F14);
  not not_153 (not_153_out, F13);
  not not_154 (not_154_out, OP4);
  not not_155 (not_155_out, OP3);
  not not_156 (not_156_out, OP2);
  not not_157 (not_157_out, F14);
  not not_158 (not_158_out, F13);
  not not_159 (not_159_out, F12);
  not not_160 (not_160_out, OP4);
  not not_161 (not_161_out, OP3);
  not not_162 (not_162_out, OP4);
  not not_163 (not_163_out, OP3);
  not not_164 (not_164_out, OP2);
  not not_165 (not_165_out, F30);
  not not_166 (not_166_out, F25);
  not not_167 (not_167_out, F12);
  not not_168 (not_168_out, OP6);
  not not_169 (not_169_out, OP3);
  not not_170 (not_170_out, OP2);
  not not_171 (not_171_out, F30);
  not not_172 (not_172_out, F25);
  not not_173 (not_173_out, F14);
  not not_174 (not_174_out, F12);
  not not_175 (not_175_out, OP6);
  not not_176 (not_176_out, OP3);
  not not_177 (not_177_out, OP2);
  not not_178 (not_178_out, F30);
  not not_179 (not_179_out, F25);
  not not_180 (not_180_out, F14);
  not not_181 (not_181_out, OP6);
  not not_182 (not_182_out, OP3);
  not not_183 (not_183_out, OP2);
  not not_184 (not_184_out, F12);
  not not_185 (not_185_out, OP6);
  not not_186 (not_186_out, OP5);
  not not_187 (not_187_out, OP3);
  not not_188 (not_188_out, OP2);
  not not_189 (not_189_out, F13);
  not not_190 (not_190_out, F12);
  not not_191 (not_191_out, OP6);
  not not_192 (not_192_out, OP5);
  not not_193 (not_193_out, OP3);
  not not_194 (not_194_out, OP2);
  not not_195 (not_195_out, F14);
  not not_196 (not_196_out, F12);
  not not_197 (not_197_out, OP6);
  not not_198 (not_198_out, OP5);
  not not_199 (not_199_out, OP3);
  not not_200 (not_200_out, OP2);
  not not_201 (not_201_out, F30);
  not not_202 (not_202_out, F25);
  not not_203 (not_203_out, F13);
  not not_204 (not_204_out, F12);
  not not_205 (not_205_out, OP6);
  not not_206 (not_206_out, OP3);
  not not_207 (not_207_out, OP2);
  not not_208 (not_208_out, OP4);
  not not_209 (not_209_out, OP3);
  not not_210 (not_210_out, OP2);
  and and_1 (and_1_out, not_1_out, not_2_out, not_3_out, not_4_out, not_5_out, not_6_out, OP5, OP4, not_7_out, not_8_out);
  and and_2 (and_2_out, not_9_out, not_10_out, F14, F13, F12, not_11_out, OP5, OP4, not_12_out, not_13_out);
  and and_3 (and_3_out, not_14_out, not_15_out, not_16_out, F13, not_17_out, not_18_out, OP5, OP4, not_19_out, not_20_out);
  and and_4 (and_4_out, not_21_out, not_22_out, not_23_out, not_24_out, not_25_out, OP4, not_26_out, not_27_out);
  and and_5 (and_5_out, F14, F13, F12, not_28_out, not_29_out, OP4, not_30_out, not_31_out);
  and and_6 (and_6_out, F14, not_32_out, not_33_out, not_34_out, not_35_out, OP4, not_36_out, not_37_out);
  and and_7 (and_7_out, not_38_out, F13, not_39_out, not_40_out, not_41_out, OP4, not_42_out, not_43_out);
  and and_8 (and_8_out, F30, not_44_out, F14, not_45_out, F12, not_46_out, not_47_out, OP4, not_48_out, not_49_out);
  and and_9 (and_9_out, not_50_out, not_51_out, not_52_out, OP6, OP5, not_53_out, not_54_out, OP2);
  and and_10 (and_10_out, not_55_out, not_56_out, F14, not_57_out, not_58_out, not_59_out, OP5, OP4, not_60_out, not_61_out);
  and and_11 (and_11_out, F30, not_62_out, not_63_out, not_64_out, not_65_out, not_66_out, OP5, OP4, not_67_out, not_68_out);
  and and_12 (and_12_out, not_69_out, not_70_out, F14, F13, F12, not_71_out, OP5, OP4, not_72_out, not_73_out);
  and and_13 (and_13_out, not_74_out, not_75_out, not_76_out, F13, not_77_out, not_78_out, OP5, OP4, not_79_out, not_80_out);
  and and_14 (and_14_out, F14, F13, F12, not_81_out, not_82_out, OP4, not_83_out, not_84_out);
  and and_15 (and_15_out, not_85_out, F13, not_86_out, not_87_out, not_88_out, OP4, not_89_out, not_90_out);
  and and_16 (and_16_out, not_91_out, not_92_out, F14, not_93_out, F12, not_94_out, not_95_out, OP4, not_96_out, not_97_out);
  and and_17 (and_17_out, not_98_out, not_99_out, not_100_out, OP6, OP5, not_101_out, not_102_out, not_103_out);
  and and_18 (and_18_out, not_104_out, not_105_out, F12, OP6, OP5, not_106_out, not_107_out, not_108_out);
  and and_19 (and_19_out, not_109_out, not_110_out, not_111_out, not_112_out, not_113_out, not_114_out, OP5, OP4, not_115_out, not_116_out);
  and and_20 (and_20_out, F30, not_117_out, not_118_out, not_119_out, not_120_out, not_121_out, OP5, OP4, not_122_out, not_123_out);
  and and_21 (and_21_out, not_124_out, not_125_out, F14, F13, F12, not_126_out, OP5, OP4, not_127_out, not_128_out);
  and and_22 (and_22_out, not_129_out, not_130_out, not_131_out, F13, F12, not_132_out, OP5, OP4, not_133_out, not_134_out);
  and and_23 (and_23_out, not_135_out, not_136_out, not_137_out, not_138_out, not_139_out, OP4, not_140_out, not_141_out);
  and and_24 (and_24_out, F14, F13, F12, not_142_out, not_143_out, OP4, not_144_out, not_145_out);
  and and_25 (and_25_out, not_146_out, not_147_out, not_148_out, OP6, OP5, not_149_out, not_150_out, not_151_out);
  and and_26 (and_26_out, not_152_out, not_153_out, F12, OP6, OP5, not_154_out, not_155_out, not_156_out);
  and and_27 (and_27_out, not_157_out, not_158_out, not_159_out, OP6, OP5, not_160_out, not_161_out, OP2);
  and and_28 (and_28_out, F14, F13, F12, OP6, OP5, not_162_out, not_163_out, not_164_out);
  and and_29 (and_29_out, not_165_out, not_166_out, F14, F13, not_167_out, not_168_out, OP5, OP4, not_169_out, not_170_out);
  and and_30 (and_30_out, not_171_out, not_172_out, not_173_out, F13, not_174_out, not_175_out, OP5, OP4, not_176_out, not_177_out);
  and and_31 (and_31_out, not_178_out, not_179_out, not_180_out, F13, F12, not_181_out, OP5, OP4, not_182_out, not_183_out);
  and and_32 (and_32_out, F14, F13, not_184_out, not_185_out, not_186_out, OP4, not_187_out, not_188_out);
  and and_33 (and_33_out, F14, not_189_out, not_190_out, not_191_out, not_192_out, OP4, not_193_out, not_194_out);
  and and_34 (and_34_out, not_195_out, F13, not_196_out, not_197_out, not_198_out, OP4, not_199_out, not_200_out);
  and and_35 (and_35_out, not_201_out, not_202_out, F14, not_203_out, not_204_out, not_205_out, OP5, OP4, not_206_out, not_207_out);
  and and_36 (and_36_out, F14, F13, F12, OP6, OP5, not_208_out, not_209_out, not_210_out);
  or or_1 (S0, and_1_out, and_2_out, and_3_out, and_4_out, and_5_out, and_6_out, and_7_out, and_8_out, and_9_out, and_10_out);
  or or_2 (S1, and_11_out, and_12_out, and_13_out, and_14_out, and_15_out, and_16_out, and_17_out, and_18_out);
  or or_3 (S2, and_19_out, and_20_out, and_21_out, and_22_out, and_23_out, and_24_out, and_25_out, and_26_out, and_27_out, and_28_out);
  or or_4 (S3, and_29_out, and_30_out, and_31_out, and_32_out, and_33_out, and_34_out, and_35_out, and_36_out);
endmodule

// 控制信号生成
module \控制信号自动生成  (
  input  OP2,
  input  OP3,
  input  OP4,
  input  OP5,
  input  OP6,
  input  F12,
  input  F13,
  input  F14,
  input  F25,
  input  F30,
  output MemToReg,
  output MemWrite,
  output CSR,
  output rs1use,
  output rs2use,
  output ALU_SRC,
  output RegWrite,
  output ecall,
  output S_Type,
  output BEQ,
  output BNE,
  output JALR,
  output JAL,
  output LUI,
  output SB,
  output BEGU
);

  wire and_2_out, and_3_out, and_4_out, and_5_out, and_6_out, and_7_out, and_8_out, and_9_out, and_10_out,
       and_11_out, and_12_out, and_13_out, and_14_out, and_15_out, and_16_out, and_17_out, and_18_out,
       and_19_out, and_20_out, and_21_out, and_22_out, and_23_out, and_24_out, and_25_out, and_26_out,
       and_27_out, and_28_out, and_29_out, and_30_out, and_31_out, and_32_out, and_33_out, and_34_out,
       and_35_out, and_36_out, and_37_out, and_38_out, and_39_out, and_40_out, and_41_out, and_42_out,
       and_43_out, and_44_out, and_45_out, and_46_out, and_47_out, and_48_out, and_49_out, and_50_out,
       and_51_out, and_52_out, and_53_out, and_54_out, and_55_out, and_56_out, and_57_out, and_58_out,
       and_59_out, and_60_out, and_61_out, and_62_out, and_63_out, and_64_out, and_65_out, and_66_out,
       and_67_out, and_68_out, and_69_out, and_70_out, and_71_out, and_73_out, and_74_out, not_1_out,
       not_2_out, not_3_out, not_4_out, not_5_out, not_6_out, not_7_out, not_8_out, not_9_out, not_10_out,
       not_11_out, not_12_out, not_13_out, not_14_out, not_15_out, not_16_out, not_17_out, not_18_out,
       not_19_out, not_20_out, not_21_out, not_22_out, not_23_out, not_24_out, not_25_out, not_26_out,
       not_27_out, not_28_out, not_29_out, not_30_out, not_31_out, not_32_out, not_33_out, not_34_out,
       not_35_out, not_36_out, not_37_out, not_38_out, not_39_out, not_40_out, not_41_out, not_42_out,
       not_43_out, not_44_out, not_45_out, not_46_out, not_47_out, not_48_out, not_49_out, not_50_out,
       not_51_out, not_52_out, not_53_out, not_54_out, not_55_out, not_56_out, not_57_out, not_58_out,
       not_59_out, not_60_out, not_61_out, not_62_out, not_63_out, not_64_out, not_65_out, not_66_out,
       not_67_out, not_68_out, not_69_out, not_70_out, not_71_out, not_72_out, not_73_out, not_74_out,
       not_75_out, not_76_out, not_77_out, not_78_out, not_79_out, not_80_out, not_81_out, not_82_out,
       not_83_out, not_84_out, not_85_out, not_86_out, not_87_out, not_88_out, not_89_out, not_90_out,
       not_91_out, not_92_out, not_93_out, not_94_out, not_95_out, not_96_out, not_97_out, not_98_out,
       not_99_out, not_100_out, not_101_out, not_102_out, not_103_out, not_104_out, not_105_out, not_106_out,
       not_107_out, not_108_out, not_109_out, not_110_out, not_111_out, not_112_out, not_113_out,
       not_114_out, not_115_out, not_116_out, not_117_out, not_118_out, not_119_out, not_120_out,
       not_121_out, not_122_out, not_123_out, not_124_out, not_125_out, not_126_out, not_127_out,
       not_128_out, not_129_out, not_130_out, not_131_out, not_132_out, not_133_out, not_134_out,
       not_135_out, not_136_out, not_137_out, not_138_out, not_139_out, not_140_out, not_141_out,
       not_142_out, not_143_out, not_144_out, not_145_out, not_146_out, not_147_out, not_148_out,
       not_149_out, not_150_out, not_151_out, not_152_out, not_153_out, not_154_out, not_155_out,
       not_156_out, not_157_out, not_158_out, not_159_out, not_160_out, not_161_out, not_162_out,
       not_163_out, not_164_out, not_165_out, not_166_out, not_167_out, not_168_out, not_169_out,
       not_170_out, not_171_out, not_172_out, not_173_out, not_174_out, not_175_out, not_176_out,
       not_177_out, not_178_out, not_179_out, not_180_out, not_181_out, not_182_out, not_183_out,
       not_184_out, not_185_out, not_186_out, not_187_out, not_188_out, not_189_out, not_190_out,
       not_191_out, not_192_out, not_193_out, not_194_out, not_195_out, not_196_out, not_197_out,
       not_198_out, not_199_out, not_200_out, not_201_out, not_202_out, not_203_out, not_204_out,
       not_205_out, not_206_out, not_207_out, not_208_out, not_209_out, not_210_out, not_211_out,
       not_212_out, not_213_out, not_214_out, not_215_out, not_216_out, not_217_out, not_218_out,
       not_219_out, not_220_out, not_221_out, not_222_out, not_223_out, not_224_out, not_225_out,
       not_226_out, not_227_out, not_228_out, not_229_out, not_230_out, not_231_out, not_232_out,
       not_233_out, not_234_out, not_235_out, not_236_out, not_237_out, not_238_out, not_239_out,
       not_240_out, not_241_out, not_242_out, not_243_out, not_244_out, not_245_out, not_246_out,
       not_247_out, not_248_out, not_249_out, not_250_out, not_251_out, not_252_out, not_253_out,
       not_254_out, not_255_out, not_256_out, not_257_out, not_258_out, not_259_out, not_260_out,
       not_261_out, not_262_out, not_263_out, not_264_out, not_265_out, not_266_out, not_267_out,
       not_268_out, not_269_out, not_270_out, not_271_out, not_272_out, not_273_out, not_274_out,
       not_275_out, not_276_out, not_277_out, not_278_out, not_279_out, not_280_out, not_281_out,
       not_282_out, not_283_out, not_284_out, not_285_out, not_286_out, not_287_out, not_288_out,
       not_289_out, not_290_out, not_291_out, not_292_out, not_293_out, not_294_out, not_295_out,
       not_296_out, not_297_out, not_298_out, not_299_out, not_300_out, not_301_out, not_302_out,
       not_303_out, not_304_out, not_305_out, not_306_out, not_307_out, not_308_out, not_309_out,
       not_310_out, not_311_out, not_312_out, not_313_out, not_314_out, not_315_out, not_316_out,
       not_317_out, not_318_out, not_319_out, not_320_out, not_321_out, not_322_out, not_323_out,
       not_324_out, not_325_out, not_326_out, not_327_out, not_328_out, not_329_out, not_330_out,
       not_331_out, not_332_out, not_333_out, not_334_out, not_335_out, not_336_out, not_337_out,
       not_338_out, not_339_out, not_340_out, not_341_out, not_342_out, not_343_out, not_344_out,
       not_345_out, not_346_out, not_347_out, not_348_out, not_349_out, not_350_out, not_351_out,
       not_352_out, not_353_out, not_354_out, not_355_out, not_356_out, not_357_out, not_358_out,
       not_359_out, not_360_out, not_361_out, not_362_out, not_363_out, not_364_out, not_365_out,
       not_366_out, not_367_out, not_368_out, not_369_out, not_370_out, not_371_out, not_372_out,
       not_373_out, not_374_out, not_375_out, not_376_out, not_377_out, not_378_out, not_379_out,
       not_380_out, not_381_out, not_382_out, not_383_out, not_384_out, not_385_out, not_386_out,
       not_387_out, not_388_out, not_389_out, not_390_out, not_391_out, not_392_out, not_393_out,
       not_394_out, not_395_out, not_396_out, not_397_out, not_398_out, not_399_out, not_400_out,
       not_401_out, not_402_out, not_403_out, not_404_out, not_405_out, not_406_out, not_407_out,
       not_408_out, not_409_out, not_410_out, not_411_out, not_412_out, not_413_out, not_414_out,
       not_415_out, not_416_out, not_417_out, not_418_out, not_419_out, not_420_out, not_421_out,
       not_422_out, not_423_out, not_424_out, not_425_out, not_426_out, not_427_out, not_428_out,
       not_429_out, not_430_out, not_431_out, not_432_out, not_433_out, not_434_out, not_435_out,
       not_436_out, not_437_out, not_438_out, not_439_out, not_440_out, not_441_out, not_442_out,
       not_443_out, not_444_out, not_445_out, not_446_out, not_447_out, not_448_out, not_449_out,
       not_450_out, not_451_out, not_452_out, not_453_out, not_454_out, not_455_out, not_456_out,
       not_457_out, not_458_out, not_459_out, not_460_out, not_461_out, not_462_out, not_463_out,
       not_464_out, not_465_out, not_466_out, not_467_out, not_468_out;

  not not_1 (not_1_out, F14);
  not not_2 (not_2_out, F12);
  not not_3 (not_3_out, OP6);
  not not_4 (not_4_out, OP5);
  not not_5 (not_5_out, OP4);
  not not_6 (not_6_out, OP3);
  not not_7 (not_7_out, OP2);
  not not_8 (not_8_out, F14);
  not not_9 (not_9_out, F12);
  not not_10 (not_10_out, OP6);
  not not_11 (not_11_out, OP4);
  not not_12 (not_12_out, OP3);
  not not_13 (not_13_out, OP2);
  not not_14 (not_14_out, F14);
  not not_15 (not_15_out, F13);
  not not_16 (not_16_out, F12);
  not not_17 (not_17_out, OP6);
  not not_18 (not_18_out, OP4);
  not not_19 (not_19_out, OP3);
  not not_20 (not_20_out, OP2);
  not not_21 (not_21_out, OP2);
  not not_22 (not_22_out, OP3);
  not not_23 (not_23_out, OP2);
  not not_24 (not_24_out, OP3);
  not not_25 (not_25_out, F13);
  not not_26 (not_26_out, F14);
  not not_27 (not_27_out, F30);
  not not_28 (not_28_out, F25);
  not not_29 (not_29_out, F14);
  not not_30 (not_30_out, F13);
  not not_31 (not_31_out, F12);
  not not_32 (not_32_out, OP6);
  not not_33 (not_33_out, OP3);
  not not_34 (not_34_out, OP2);
  not not_35 (not_35_out, F25);
  not not_36 (not_36_out, F14);
  not not_37 (not_37_out, F13);
  not not_38 (not_38_out, F12);
  not not_39 (not_39_out, OP6);
  not not_40 (not_40_out, OP3);
  not not_41 (not_41_out, OP2);
  not not_42 (not_42_out, F30);
  not not_43 (not_43_out, F25);
  not not_44 (not_44_out, OP6);
  not not_45 (not_45_out, OP3);
  not not_46 (not_46_out, OP2);
  not not_47 (not_47_out, F30);
  not not_48 (not_48_out, F25);
  not not_49 (not_49_out, F12);
  not not_50 (not_50_out, OP6);
  not not_51 (not_51_out, OP3);
  not not_52 (not_52_out, OP2);
  not not_53 (not_53_out, F30);
  not not_54 (not_54_out, F25);
  not not_55 (not_55_out, F14);
  not not_56 (not_56_out, F12);
  not not_57 (not_57_out, OP6);
  not not_58 (not_58_out, OP3);
  not not_59 (not_59_out, OP2);
  not not_60 (not_60_out, F30);
  not not_61 (not_61_out, F25);
  not not_62 (not_62_out, F14);
  not not_63 (not_63_out, OP6);
  not not_64 (not_64_out, OP3);
  not not_65 (not_65_out, OP2);
  not not_66 (not_66_out, F14);
  not not_67 (not_67_out, F13);
  not not_68 (not_68_out, F12);
  not not_69 (not_69_out, OP6);
  not not_70 (not_70_out, OP5);
  not not_71 (not_71_out, OP3);
  not not_72 (not_72_out, OP2);
  not not_73 (not_73_out, OP6);
  not not_74 (not_74_out, OP5);
  not not_75 (not_75_out, OP3);
  not not_76 (not_76_out, OP2);
  not not_77 (not_77_out, F12);
  not not_78 (not_78_out, OP6);
  not not_79 (not_79_out, OP5);
  not not_80 (not_80_out, OP3);
  not not_81 (not_81_out, OP2);
  not not_82 (not_82_out, F13);
  not not_83 (not_83_out, F12);
  not not_84 (not_84_out, OP6);
  not not_85 (not_85_out, OP5);
  not not_86 (not_86_out, OP3);
  not not_87 (not_87_out, OP2);
  not not_88 (not_88_out, F14);
  not not_89 (not_89_out, F12);
  not not_90 (not_90_out, OP6);
  not not_91 (not_91_out, OP5);
  not not_92 (not_92_out, OP3);
  not not_93 (not_93_out, OP2);
  not not_94 (not_94_out, F30);
  not not_95 (not_95_out, F25);
  not not_96 (not_96_out, F14);
  not not_97 (not_97_out, F13);
  not not_98 (not_98_out, OP6);
  not not_99 (not_99_out, OP5);
  not not_100 (not_100_out, OP3);
  not not_101 (not_101_out, OP2);
  not not_102 (not_102_out, F30);
  not not_103 (not_103_out, F25);
  not not_104 (not_104_out, F13);
  not not_105 (not_105_out, OP6);
  not not_106 (not_106_out, OP5);
  not not_107 (not_107_out, OP3);
  not not_108 (not_108_out, OP2);
  not not_109 (not_109_out, F25);
  not not_110 (not_110_out, F13);
  not not_111 (not_111_out, OP6);
  not not_112 (not_112_out, OP5);
  not not_113 (not_113_out, OP3);
  not not_114 (not_114_out, OP2);
  not not_115 (not_115_out, F14);
  not not_116 (not_116_out, F12);
  not not_117 (not_117_out, OP6);
  not not_118 (not_118_out, OP5);
  not not_119 (not_119_out, OP4);
  not not_120 (not_120_out, OP3);
  not not_121 (not_121_out, OP2);
  not not_122 (not_122_out, F14);
  not not_123 (not_123_out, F12);
  not not_124 (not_124_out, OP6);
  not not_125 (not_125_out, OP4);
  not not_126 (not_126_out, OP3);
  not not_127 (not_127_out, OP2);
  not not_128 (not_128_out, F14);
  not not_129 (not_129_out, F13);
  not not_130 (not_130_out, F12);
  not not_131 (not_131_out, OP4);
  not not_132 (not_132_out, OP3);
  not not_133 (not_133_out, OP2);
  not not_134 (not_134_out, F14);
  not not_135 (not_135_out, F13);
  not not_136 (not_136_out, OP4);
  not not_137 (not_137_out, OP3);
  not not_138 (not_138_out, OP2);
  not not_139 (not_139_out, F14);
  not not_140 (not_140_out, F13);
  not not_141 (not_141_out, F12);
  not not_142 (not_142_out, OP4);
  not not_143 (not_143_out, OP3);
  not not_144 (not_144_out, F30);
  not not_145 (not_145_out, F25);
  not not_146 (not_146_out, F13);
  not not_147 (not_147_out, F12);
  not not_148 (not_148_out, OP6);
  not not_149 (not_149_out, OP3);
  not not_150 (not_150_out, OP2);
  not not_151 (not_151_out, OP6);
  not not_152 (not_152_out, OP3);
  not not_153 (not_153_out, F14);
  not not_154 (not_154_out, F13);
  not not_155 (not_155_out, F12);
  not not_156 (not_156_out, OP6);
  not not_157 (not_157_out, OP4);
  not not_158 (not_158_out, OP3);
  not not_159 (not_159_out, OP2);
  not not_160 (not_160_out, OP4);
  not not_161 (not_161_out, OP3);
  not not_162 (not_162_out, OP2);
  not not_163 (not_163_out, F30);
  not not_164 (not_164_out, F25);
  not not_165 (not_165_out, F14);
  not not_166 (not_166_out, F13);
  not not_167 (not_167_out, F12);
  not not_168 (not_168_out, OP6);
  not not_169 (not_169_out, OP3);
  not not_170 (not_170_out, OP2);
  not not_171 (not_171_out, F25);
  not not_172 (not_172_out, F14);
  not not_173 (not_173_out, F13);
  not not_174 (not_174_out, F12);
  not not_175 (not_175_out, OP6);
  not not_176 (not_176_out, OP3);
  not not_177 (not_177_out, OP2);
  not not_178 (not_178_out, F30);
  not not_179 (not_179_out, F25);
  not not_180 (not_180_out, OP6);
  not not_181 (not_181_out, OP3);
  not not_182 (not_182_out, OP2);
  not not_183 (not_183_out, F30);
  not not_184 (not_184_out, F25);
  not not_185 (not_185_out, F12);
  not not_186 (not_186_out, OP6);
  not not_187 (not_187_out, OP3);
  not not_188 (not_188_out, OP2);
  not not_189 (not_189_out, F30);
  not not_190 (not_190_out, F25);
  not not_191 (not_191_out, F14);
  not not_192 (not_192_out, F12);
  not not_193 (not_193_out, OP6);
  not not_194 (not_194_out, OP3);
  not not_195 (not_195_out, OP2);
  not not_196 (not_196_out, F30);
  not not_197 (not_197_out, F25);
  not not_198 (not_198_out, F14);
  not not_199 (not_199_out, OP6);
  not not_200 (not_200_out, OP3);
  not not_201 (not_201_out, OP2);
  not not_202 (not_202_out, F14);
  not not_203 (not_203_out, F12);
  not not_204 (not_204_out, OP6);
  not not_205 (not_205_out, OP4);
  not not_206 (not_206_out, OP3);
  not not_207 (not_207_out, OP2);
  not not_208 (not_208_out, F14);
  not not_209 (not_209_out, F13);
  not not_210 (not_210_out, F12);
  not not_211 (not_211_out, OP4);
  not not_212 (not_212_out, OP3);
  not not_213 (not_213_out, OP2);
  not not_214 (not_214_out, F14);
  not not_215 (not_215_out, F13);
  not not_216 (not_216_out, OP4);
  not not_217 (not_217_out, OP3);
  not not_218 (not_218_out, OP2);
  not not_219 (not_219_out, F30);
  not not_220 (not_220_out, F25);
  not not_221 (not_221_out, F13);
  not not_222 (not_222_out, F12);
  not not_223 (not_223_out, OP6);
  not not_224 (not_224_out, OP3);
  not not_225 (not_225_out, OP2);
  not not_226 (not_226_out, F14);
  not not_227 (not_227_out, F13);
  not not_228 (not_228_out, F12);
  not not_229 (not_229_out, OP6);
  not not_230 (not_230_out, OP4);
  not not_231 (not_231_out, OP3);
  not not_232 (not_232_out, OP2);
  not not_233 (not_233_out, OP4);
  not not_234 (not_234_out, OP3);
  not not_235 (not_235_out, OP2);
  not not_236 (not_236_out, F14);
  not not_237 (not_237_out, F13);
  not not_238 (not_238_out, F12);
  not not_239 (not_239_out, OP6);
  not not_240 (not_240_out, OP5);
  not not_241 (not_241_out, OP3);
  not not_242 (not_242_out, OP2);
  not not_243 (not_243_out, OP6);
  not not_244 (not_244_out, OP5);
  not not_245 (not_245_out, OP3);
  not not_246 (not_246_out, OP2);
  not not_247 (not_247_out, F12);
  not not_248 (not_248_out, OP6);
  not not_249 (not_249_out, OP5);
  not not_250 (not_250_out, OP3);
  not not_251 (not_251_out, OP2);
  not not_252 (not_252_out, F13);
  not not_253 (not_253_out, F12);
  not not_254 (not_254_out, OP6);
  not not_255 (not_255_out, OP5);
  not not_256 (not_256_out, OP3);
  not not_257 (not_257_out, OP2);
  not not_258 (not_258_out, F14);
  not not_259 (not_259_out, F12);
  not not_260 (not_260_out, OP6);
  not not_261 (not_261_out, OP5);
  not not_262 (not_262_out, OP3);
  not not_263 (not_263_out, OP2);
  not not_264 (not_264_out, F30);
  not not_265 (not_265_out, F25);
  not not_266 (not_266_out, F14);
  not not_267 (not_267_out, F13);
  not not_268 (not_268_out, OP6);
  not not_269 (not_269_out, OP5);
  not not_270 (not_270_out, OP3);
  not not_271 (not_271_out, OP2);
  not not_272 (not_272_out, F30);
  not not_273 (not_273_out, F25);
  not not_274 (not_274_out, F13);
  not not_275 (not_275_out, OP6);
  not not_276 (not_276_out, OP5);
  not not_277 (not_277_out, OP3);
  not not_278 (not_278_out, OP2);
  not not_279 (not_279_out, F25);
  not not_280 (not_280_out, F13);
  not not_281 (not_281_out, OP6);
  not not_282 (not_282_out, OP5);
  not not_283 (not_283_out, OP3);
  not not_284 (not_284_out, OP2);
  not not_285 (not_285_out, F14);
  not not_286 (not_286_out, F12);
  not not_287 (not_287_out, OP6);
  not not_288 (not_288_out, OP5);
  not not_289 (not_289_out, OP4);
  not not_290 (not_290_out, OP3);
  not not_291 (not_291_out, OP2);
  not not_292 (not_292_out, F14);
  not not_293 (not_293_out, F12);
  not not_294 (not_294_out, OP6);
  not not_295 (not_295_out, OP4);
  not not_296 (not_296_out, OP3);
  not not_297 (not_297_out, OP2);
  not not_298 (not_298_out, F14);
  not not_299 (not_299_out, F13);
  not not_300 (not_300_out, F12);
  not not_301 (not_301_out, OP4);
  not not_302 (not_302_out, OP3);
  not not_303 (not_303_out, F14);
  not not_304 (not_304_out, F13);
  not not_305 (not_305_out, F12);
  not not_306 (not_306_out, OP6);
  not not_307 (not_307_out, OP4);
  not not_308 (not_308_out, OP3);
  not not_309 (not_309_out, OP2);
  not not_310 (not_310_out, F30);
  not not_311 (not_311_out, F25);
  not not_312 (not_312_out, F14);
  not not_313 (not_313_out, F13);
  not not_314 (not_314_out, F12);
  not not_315 (not_315_out, OP6);
  not not_316 (not_316_out, OP3);
  not not_317 (not_317_out, OP2);
  not not_318 (not_318_out, F25);
  not not_319 (not_319_out, F14);
  not not_320 (not_320_out, F13);
  not not_321 (not_321_out, F12);
  not not_322 (not_322_out, OP6);
  not not_323 (not_323_out, OP3);
  not not_324 (not_324_out, OP2);
  not not_325 (not_325_out, F30);
  not not_326 (not_326_out, F25);
  not not_327 (not_327_out, OP6);
  not not_328 (not_328_out, OP3);
  not not_329 (not_329_out, OP2);
  not not_330 (not_330_out, F30);
  not not_331 (not_331_out, F25);
  not not_332 (not_332_out, F12);
  not not_333 (not_333_out, OP6);
  not not_334 (not_334_out, OP3);
  not not_335 (not_335_out, OP2);
  not not_336 (not_336_out, F30);
  not not_337 (not_337_out, F25);
  not not_338 (not_338_out, F14);
  not not_339 (not_339_out, F12);
  not not_340 (not_340_out, OP6);
  not not_341 (not_341_out, OP3);
  not not_342 (not_342_out, OP2);
  not not_343 (not_343_out, F30);
  not not_344 (not_344_out, F25);
  not not_345 (not_345_out, F14);
  not not_346 (not_346_out, OP6);
  not not_347 (not_347_out, OP3);
  not not_348 (not_348_out, OP2);
  not not_349 (not_349_out, F14);
  not not_350 (not_350_out, F13);
  not not_351 (not_351_out, F12);
  not not_352 (not_352_out, OP6);
  not not_353 (not_353_out, OP5);
  not not_354 (not_354_out, OP3);
  not not_355 (not_355_out, OP2);
  not not_356 (not_356_out, OP6);
  not not_357 (not_357_out, OP5);
  not not_358 (not_358_out, OP3);
  not not_359 (not_359_out, OP2);
  not not_360 (not_360_out, F12);
  not not_361 (not_361_out, OP6);
  not not_362 (not_362_out, OP5);
  not not_363 (not_363_out, OP3);
  not not_364 (not_364_out, OP2);
  not not_365 (not_365_out, F13);
  not not_366 (not_366_out, F12);
  not not_367 (not_367_out, OP6);
  not not_368 (not_368_out, OP5);
  not not_369 (not_369_out, OP3);
  not not_370 (not_370_out, OP2);
  not not_371 (not_371_out, F14);
  not not_372 (not_372_out, F12);
  not not_373 (not_373_out, OP6);
  not not_374 (not_374_out, OP5);
  not not_375 (not_375_out, OP3);
  not not_376 (not_376_out, OP2);
  not not_377 (not_377_out, F30);
  not not_378 (not_378_out, F25);
  not not_379 (not_379_out, F14);
  not not_380 (not_380_out, F13);
  not not_381 (not_381_out, OP6);
  not not_382 (not_382_out, OP5);
  not not_383 (not_383_out, OP3);
  not not_384 (not_384_out, OP2);
  not not_385 (not_385_out, F30);
  not not_386 (not_386_out, F25);
  not not_387 (not_387_out, F13);
  not not_388 (not_388_out, OP6);
  not not_389 (not_389_out, OP5);
  not not_390 (not_390_out, OP3);
  not not_391 (not_391_out, OP2);
  not not_392 (not_392_out, F25);
  not not_393 (not_393_out, F13);
  not not_394 (not_394_out, OP6);
  not not_395 (not_395_out, OP5);
  not not_396 (not_396_out, OP3);
  not not_397 (not_397_out, OP2);
  not not_398 (not_398_out, F14);
  not not_399 (not_399_out, F12);
  not not_400 (not_400_out, OP6);
  not not_401 (not_401_out, OP5);
  not not_402 (not_402_out, OP4);
  not not_403 (not_403_out, OP3);
  not not_404 (not_404_out, OP2);
  not not_405 (not_405_out, OP4);
  not not_406 (not_406_out, F14);
  not not_407 (not_407_out, F13);
  not not_408 (not_408_out, F12);
  not not_409 (not_409_out, OP4);
  not not_410 (not_410_out, OP3);
  not not_411 (not_411_out, F30);
  not not_412 (not_412_out, F25);
  not not_413 (not_413_out, F13);
  not not_414 (not_414_out, F12);
  not not_415 (not_415_out, OP6);
  not not_416 (not_416_out, OP3);
  not not_417 (not_417_out, OP2);
  not not_418 (not_418_out, OP6);
  not not_419 (not_419_out, OP3);
  not not_420 (not_420_out, F30);
  not not_421 (not_421_out, F25);
  not not_422 (not_422_out, F14);
  not not_423 (not_423_out, F13);
  not not_424 (not_424_out, F12);
  not not_425 (not_425_out, OP3);
  not not_426 (not_426_out, OP2);
  not not_427 (not_427_out, F14);
  not not_428 (not_428_out, F12);
  not not_429 (not_429_out, OP6);
  not not_430 (not_430_out, OP4);
  not not_431 (not_431_out, OP3);
  not not_432 (not_432_out, OP2);
  not not_433 (not_433_out, F14);
  not not_434 (not_434_out, F13);
  not not_435 (not_435_out, F12);
  not not_436 (not_436_out, OP6);
  not not_437 (not_437_out, OP4);
  not not_438 (not_438_out, OP3);
  not not_439 (not_439_out, OP2);
  not not_440 (not_440_out, F14);
  not not_441 (not_441_out, F13);
  not not_442 (not_442_out, F12);
  not not_443 (not_443_out, OP4);
  not not_444 (not_444_out, OP3);
  not not_445 (not_445_out, OP2);
  not not_446 (not_446_out, F14);
  not not_447 (not_447_out, F13);
  not not_448 (not_448_out, OP4);
  not not_449 (not_449_out, OP3);
  not not_450 (not_450_out, OP2);
  not not_451 (not_451_out, F14);
  not not_452 (not_452_out, F13);
  not not_453 (not_453_out, F12);
  not not_454 (not_454_out, OP4);
  not not_455 (not_455_out, OP3);
  not not_456 (not_456_out, OP4);
  not not_457 (not_457_out, OP6);
  not not_458 (not_458_out, OP3);
  not not_459 (not_459_out, F14);
  not not_460 (not_460_out, F13);
  not not_461 (not_461_out, F12);
  not not_462 (not_462_out, OP6);
  not not_463 (not_463_out, OP4);
  not not_464 (not_464_out, OP3);
  not not_465 (not_465_out, OP2);
  not not_466 (not_466_out, OP4);
  not not_467 (not_467_out, OP3);
  not not_468 (not_468_out, OP2);
  and and_1 (MemToReg, not_1_out, F13, not_2_out, not_3_out, not_4_out, not_5_out, not_6_out, not_7_out);
  and and_2 (and_2_out, not_8_out, F13, not_9_out, not_10_out, OP5, not_11_out, not_12_out, not_13_out);
  and and_3 (and_3_out, not_14_out, not_15_out, not_16_out, not_17_out, OP5, not_18_out, not_19_out, not_20_out);
  and and_4 (and_4_out, not_21_out, not_22_out, OP4, OP5, OP6, F13, F14);
  and and_5 (and_5_out, not_23_out, not_24_out, OP4, OP5, OP6, F12, not_25_out, not_26_out);
  and and_6 (and_6_out, not_27_out, not_28_out, not_29_out, not_30_out, not_31_out, not_32_out, OP5, OP4, not_33_out, not_34_out);
  and and_7 (and_7_out, F30, not_35_out, not_36_out, not_37_out, not_38_out, not_39_out, OP5, OP4, not_40_out, not_41_out);
  and and_8 (and_8_out, not_42_out, not_43_out, F14, F13, F12, not_44_out, OP5, OP4, not_45_out, not_46_out);
  and and_9 (and_9_out, not_47_out, not_48_out, F14, F13, not_49_out, not_50_out, OP5, OP4, not_51_out, not_52_out);
  and and_10 (and_10_out, not_53_out, not_54_out, not_55_out, F13, not_56_out, not_57_out, OP5, OP4, not_58_out, not_59_out);
  and and_11 (and_11_out, not_60_out, not_61_out, not_62_out, F13, F12, not_63_out, OP5, OP4, not_64_out, not_65_out);
  and and_12 (and_12_out, not_66_out, not_67_out, not_68_out, not_69_out, not_70_out, OP4, not_71_out, not_72_out);
  and and_13 (and_13_out, F14, F13, F12, not_73_out, not_74_out, OP4, not_75_out, not_76_out);
  and and_14 (and_14_out, F14, F13, not_77_out, not_78_out, not_79_out, OP4, not_80_out, not_81_out);
  and and_15 (and_15_out, F14, not_82_out, not_83_out, not_84_out, not_85_out, OP4, not_86_out, not_87_out);
  and and_16 (and_16_out, not_88_out, F13, not_89_out, not_90_out, not_91_out, OP4, not_92_out, not_93_out);
  and and_17 (and_17_out, not_94_out, not_95_out, not_96_out, not_97_out, F12, not_98_out, not_99_out, OP4, not_100_out, not_101_out);
  and and_18 (and_18_out, not_102_out, not_103_out, F14, not_104_out, F12, not_105_out, not_106_out, OP4, not_107_out, not_108_out);
  and and_19 (and_19_out, F30, not_109_out, F14, not_110_out, F12, not_111_out, not_112_out, OP4, not_113_out, not_114_out);
  and and_20 (and_20_out, not_115_out, F13, not_116_out, not_117_out, not_118_out, not_119_out, not_120_out, not_121_out);
  and and_21 (and_21_out, not_122_out, F13, not_123_out, not_124_out, OP5, not_125_out, not_126_out, not_127_out);
  and and_22 (and_22_out, not_128_out, not_129_out, not_130_out, OP6, OP5, not_131_out, not_132_out, not_133_out);
  and and_23 (and_23_out, not_134_out, not_135_out, F12, OP6, OP5, not_136_out, not_137_out, not_138_out);
  and and_24 (and_24_out, not_139_out, not_140_out, not_141_out, OP6, OP5, not_142_out, not_143_out, OP2);
  and and_25 (and_25_out, not_144_out, not_145_out, F14, not_146_out, not_147_out, not_148_out, OP5, OP4, not_149_out, not_150_out);
  and and_26 (and_26_out, not_151_out, OP5, OP4, not_152_out, OP2);
  and and_27 (and_27_out, not_153_out, not_154_out, not_155_out, not_156_out, OP5, not_157_out, not_158_out, not_159_out);
  and and_28 (and_28_out, F14, F13, F12, OP6, OP5, not_160_out, not_161_out, not_162_out);
  and and_29 (and_29_out, not_163_out, not_164_out, not_165_out, not_166_out, not_167_out, not_168_out, OP5, OP4, not_169_out, not_170_out);
  and and_30 (and_30_out, F30, not_171_out, not_172_out, not_173_out, not_174_out, not_175_out, OP5, OP4, not_176_out, not_177_out);
  and and_31 (and_31_out, not_178_out, not_179_out, F14, F13, F12, not_180_out, OP5, OP4, not_181_out, not_182_out);
  and and_32 (and_32_out, not_183_out, not_184_out, F14, F13, not_185_out, not_186_out, OP5, OP4, not_187_out, not_188_out);
  and and_33 (and_33_out, not_189_out, not_190_out, not_191_out, F13, not_192_out, not_193_out, OP5, OP4, not_194_out, not_195_out);
  and and_34 (and_34_out, not_196_out, not_197_out, not_198_out, F13, F12, not_199_out, OP5, OP4, not_200_out, not_201_out);
  and and_35 (and_35_out, not_202_out, F13, not_203_out, not_204_out, OP5, not_205_out, not_206_out, not_207_out);
  and and_36 (and_36_out, not_208_out, not_209_out, not_210_out, OP6, OP5, not_211_out, not_212_out, not_213_out);
  and and_37 (and_37_out, not_214_out, not_215_out, F12, OP6, OP5, not_216_out, not_217_out, not_218_out);
  and and_38 (and_38_out, not_219_out, not_220_out, F14, not_221_out, not_222_out, not_223_out, OP5, OP4, not_224_out, not_225_out);
  and and_39 (and_39_out, not_226_out, not_227_out, not_228_out, not_229_out, OP5, not_230_out, not_231_out, not_232_out);
  and and_40 (and_40_out, F14, F13, F12, OP6, OP5, not_233_out, not_234_out, not_235_out);
  and and_41 (and_41_out, not_236_out, not_237_out, not_238_out, not_239_out, not_240_out, OP4, not_241_out, not_242_out);
  and and_42 (and_42_out, F14, F13, F12, not_243_out, not_244_out, OP4, not_245_out, not_246_out);
  and and_43 (and_43_out, F14, F13, not_247_out, not_248_out, not_249_out, OP4, not_250_out, not_251_out);
  and and_44 (and_44_out, F14, not_252_out, not_253_out, not_254_out, not_255_out, OP4, not_256_out, not_257_out);
  and and_45 (and_45_out, not_258_out, F13, not_259_out, not_260_out, not_261_out, OP4, not_262_out, not_263_out);
  and and_46 (and_46_out, not_264_out, not_265_out, not_266_out, not_267_out, F12, not_268_out, not_269_out, OP4, not_270_out, not_271_out);
  and and_47 (and_47_out, not_272_out, not_273_out, F14, not_274_out, F12, not_275_out, not_276_out, OP4, not_277_out, not_278_out);
  and and_48 (and_48_out, F30, not_279_out, F14, not_280_out, F12, not_281_out, not_282_out, OP4, not_283_out, not_284_out);
  and and_49 (and_49_out, not_285_out, F13, not_286_out, not_287_out, not_288_out, not_289_out, not_290_out, not_291_out);
  and and_50 (and_50_out, not_292_out, F13, not_293_out, not_294_out, OP5, not_295_out, not_296_out, not_297_out);
  and and_51 (and_51_out, not_298_out, not_299_out, not_300_out, OP6, OP5, not_301_out, not_302_out, OP2);
  and and_52 (and_52_out, not_303_out, not_304_out, not_305_out, not_306_out, OP5, not_307_out, not_308_out, not_309_out);
  and and_53 (and_53_out, not_310_out, not_311_out, not_312_out, not_313_out, not_314_out, not_315_out, OP5, OP4, not_316_out, not_317_out);
  and and_54 (and_54_out, F30, not_318_out, not_319_out, not_320_out, not_321_out, not_322_out, OP5, OP4, not_323_out, not_324_out);
  and and_55 (and_55_out, not_325_out, not_326_out, F14, F13, F12, not_327_out, OP5, OP4, not_328_out, not_329_out);
  and and_56 (and_56_out, not_330_out, not_331_out, F14, F13, not_332_out, not_333_out, OP5, OP4, not_334_out, not_335_out);
  and and_57 (and_57_out, not_336_out, not_337_out, not_338_out, F13, not_339_out, not_340_out, OP5, OP4, not_341_out, not_342_out);
  and and_58 (and_58_out, not_343_out, not_344_out, not_345_out, F13, F12, not_346_out, OP5, OP4, not_347_out, not_348_out);
  and and_59 (and_59_out, not_349_out, not_350_out, not_351_out, not_352_out, not_353_out, OP4, not_354_out, not_355_out);
  and and_60 (and_60_out, F14, F13, F12, not_356_out, not_357_out, OP4, not_358_out, not_359_out);
  and and_61 (and_61_out, F14, F13, not_360_out, not_361_out, not_362_out, OP4, not_363_out, not_364_out);
  and and_62 (and_62_out, F14, not_365_out, not_366_out, not_367_out, not_368_out, OP4, not_369_out, not_370_out);
  and and_63 (and_63_out, not_371_out, F13, not_372_out, not_373_out, not_374_out, OP4, not_375_out, not_376_out);
  and and_64 (and_64_out, not_377_out, not_378_out, not_379_out, not_380_out, F12, not_381_out, not_382_out, OP4, not_383_out, not_384_out);
  and and_65 (and_65_out, not_385_out, not_386_out, F14, not_387_out, F12, not_388_out, not_389_out, OP4, not_390_out, not_391_out);
  and and_66 (and_66_out, F30, not_392_out, F14, not_393_out, F12, not_394_out, not_395_out, OP4, not_396_out, not_397_out);
  and and_67 (and_67_out, not_398_out, F13, not_399_out, not_400_out, not_401_out, not_402_out, not_403_out, not_404_out);
  and and_68 (and_68_out, OP6, OP5, not_405_out, OP3, OP2);
  and and_69 (and_69_out, not_406_out, not_407_out, not_408_out, OP6, OP5, not_409_out, not_410_out, OP2);
  and and_70 (and_70_out, not_411_out, not_412_out, F14, not_413_out, not_414_out, not_415_out, OP5, OP4, not_416_out, not_417_out);
  and and_71 (and_71_out, not_418_out, OP5, OP4, not_419_out, OP2);
  and and_72 (ecall, not_420_out, not_421_out, not_422_out, not_423_out, not_424_out, OP6, OP5, OP4, not_425_out, not_426_out);
  and and_73 (and_73_out, not_427_out, F13, not_428_out, not_429_out, OP5, not_430_out, not_431_out, not_432_out);
  and and_74 (and_74_out, not_433_out, not_434_out, not_435_out, not_436_out, OP5, not_437_out, not_438_out, not_439_out);
  and and_75 (BEQ, not_440_out, not_441_out, not_442_out, OP6, OP5, not_443_out, not_444_out, not_445_out);
  and and_76 (BNE, not_446_out, not_447_out, F12, OP6, OP5, not_448_out, not_449_out, not_450_out);
  and and_77 (JALR, not_451_out, not_452_out, not_453_out, OP6, OP5, not_454_out, not_455_out, OP2);
  and and_78 (JAL, OP6, OP5, not_456_out, OP3, OP2);
  and and_79 (LUI, not_457_out, OP5, OP4, not_458_out, OP2);
  and and_80 (SB, not_459_out, not_460_out, not_461_out, not_462_out, OP5, not_463_out, not_464_out, not_465_out);
  and and_81 (BEGU, F14, F13, F12, OP6, OP5, not_466_out, not_467_out, not_468_out);
  or or_1 (MemWrite, and_2_out, and_3_out);
  or or_2 (CSR, and_4_out, and_5_out);
  or or_3 (S_Type, and_73_out, and_74_out);
  or or_4 (rs2use, and_29_out, and_30_out, and_31_out, and_32_out, and_33_out, and_34_out, and_35_out, and_36_out, and_37_out, and_38_out, and_39_out, and_40_out);
  or or_5 (ALU_SRC, and_41_out, and_42_out, and_43_out, and_44_out, and_45_out, and_46_out, and_47_out, and_48_out, and_49_out, and_50_out, and_51_out, and_52_out);
  or or_6 (RegWrite, and_53_out, and_54_out, and_55_out, and_56_out, and_57_out, and_58_out, and_59_out, and_60_out, and_61_out, and_62_out, and_63_out, and_64_out, and_65_out, and_66_out, and_67_out, and_68_out, and_69_out, and_70_out, and_71_out);
  or or_7 (rs1use, and_6_out, and_7_out, and_8_out, and_9_out, and_10_out, and_11_out, and_12_out, and_13_out, and_14_out, and_15_out, and_16_out, and_17_out, and_18_out, and_19_out, and_20_out, and_21_out, and_22_out, and_23_out, and_24_out, and_25_out, and_26_out, and_27_out, and_28_out);
endmodule

// ALU
module ALU (
  input  [31:0] X,
  input  [31:0] Y,
  input  [3:0] AluOP,
  output out_4,
  output Equal,
  output out_6,
  output [31:0] Result,
  output [31:0] Result_2
);

  wire comparator_1_eq, comparator_1_gt, comparator_2_eq, comparator_2_gt, Great;
  wire [0:0] comparator_1_lt, comparator_2_lt;
  wire [31:0] adder_1_out, and_1_out, divider_1_out, divider_1_rem, multiplier_1_cout, multiplier_1_out,
       nor_1_out, or_1_out, shifter_1_out, shifter_2_out, shifter_3_out, subtractor_1_out, xor_1_out;

  Shifter #(.width(32), .shift("ll")) shifter_1 (.in(X), .\dist (Y[4:0]), .out(shifter_1_out));
  Shifter #(.width(32), .shift("ar")) shifter_2 (.in(X), .\dist (Y[4:0]), .out(shifter_2_out));
  Shifter #(.width(32), .shift("lr")) shifter_3 (.in(X), .\dist (Y[4:0]), .out(shifter_3_out));
  Multiplier #(.width(32)) multiplier_1 (.a(X), .b(Y), .out(multiplier_1_out), .cout(multiplier_1_cout));  // open: cin
  Divider #(.width(32)) divider_1 (.a(X), .b(Y), .out(divider_1_out), .rem(divider_1_rem));  // open: upper
  Adder #(.width(32)) adder_1 (.a(X), .b(Y), .out(adder_1_out));  // open: cin, cout
  Subtractor #(.width(32)) subtractor_1 (.a(X), .b(Y), .out(subtractor_1_out));  // open: bin, bout
  assign and_1_out = X & Y;  // AND_Gate and_1, 32 bits wide
  assign or_1_out = X | Y;  // OR_Gate or_1, 32 bits wide
  assign xor_1_out = X ^ Y;  // XOR_Gate xor_1, 32 bits wide
  assign nor_1_out = ~(X | Y);  // NOR_Gate nor_1, 32 bits wide
  Comparator #(.width(32), .mode("twosComplement")) comparator_1 (
    .a(X), .b(Y), .gt(comparator_1_gt), .eq(comparator_1_eq), .lt(comparator_1_lt[0]));
  Comparator #(.width(32), .mode("unsigned")) comparator_2 (
    .a(X), .b(Y), .gt(comparator_2_gt), .eq(comparator_2_eq), .lt(comparator_2_lt[0]));
  Multiplexer #(.select(1), .width(1), .disabled("Z"), .enable("false")) multiplexer_1 (
    .in0(comparator_2_gt), .in1(comparator_1_gt), .out(Great), .sel(AluOP[0]));
  Multiplexer #(.select(1), .width(1), .disabled("Z"), .enable("false")) multiplexer_2 (
    .in0(comparator_2_eq), .in1(comparator_1_eq), .out(Equal), .sel(AluOP[0]));
  Multiplexer #(.select(1), .width(1), .disabled("Z"), .enable("false")) multiplexer_3 (
    .in0(comparator_2_lt[0]), .in1(comparator_1_lt[0]), .out(out_6), .sel(AluOP[0]));
  Multiplexer #(.select(4), .width(32), .disabled("Z"), .enable("false")) multiplexer_4 (
    .in0(shifter_1_out), .in1(shifter_2_out), .in2(shifter_3_out), .in3(multiplier_1_out),
    .in4(divider_1_out), .in5(adder_1_out), .in6(subtractor_1_out), .in7(and_1_out), .in8(or_1_out),
    .in9(xor_1_out), .in10(nor_1_out), .in11({{31{1'b0}}, comparator_1_lt[0]}),
    .in12({{31{1'b0}}, comparator_2_lt[0]}), .in13({32{1'b0}}), .in14({32{1'b0}}), .in15({32{1'b0}}),
    .out(Result), .sel(AluOP));
  Multiplexer #(.select(1), .width(32), .disabled("Z"), .enable("false")) multiplexer_5 (
    .in0(divider_1_rem), .in1(multiplier_1_cout), .out(Result_2), .sel(AluOP[0]));
  or or_2 (out_4, Great, Equal);

  // Other names for the same wires on the sheet: Result2[31:0] = Result_2; S[3:0] = AluOP; tunnel = out_6

  // Notes on the sheet:
  //   不要改变此引脚区域内容，也不要改变ALU封装形式
  //   输入引脚
  //   输出引脚
endmodule

module Regifile (
  input  [31:0] Din,
  input  Clk,
  input  WE,
  input  [4:0] R1_num,
  input  [4:0] W_num,
  input  [4:0] R2_num,
  output [31:0] R1,
  output [31:0] R2
);

  // RegisterFile registerfile_1: pin names not known; wires that end beside it: Din, Clk, WE, W_num, R1_num, R2_num, R1, R2
endmodule

module \气泡流水线  (
  output RegWrite,
  output MemWrite,
  output [31:0] IF_PC,
  output [31:0] ID_PC,
  output [31:0] EX_PC,
  output [31:0] M_PC,
  output [31:0] WB_PC,
  output [31:0] RDin,
  output [31:0] MDin,
  output [31:0] LedData
);

  wire Alu_Src, and_1_out, and_2_out, and_3_out, and_4_out, and_5_out, and_6_out, and_7_out, and_8_out,
       and_9_out, and_10_out, and_15_out, and_16_out, and_17_out, and_18_out, and_19_out, Beq, BGEU, Bne,
       BranchSuc, CLK, clock_1_out, comparator_1_eq, comparator_1_lt, comparator_2_eq, d_ff_1_q, E, ecall,
       EX_MEM_halt_2, EX_MEM_jal_2, EX_MEM_jalr_2, EX_MEM_lui_2, EX_MEM_memtoreg_2, EX_MEM_sb_2, EXRegWrite,
       flush, G, Go, halt, id_ex_1_alusrcb_2, id_ex_1_beq_2, id_ex_1_bgeu_2, id_ex_1_bne_2, id_ex_1_ecall_2,
       id_ex_1_jal_2, id_ex_1_jalr_2, id_ex_1_lui_2, id_ex_1_memtoreg_2, id_ex_1_memwrite_2, id_ex_1_sb_2,
       IR1, IR2, IR3, JAL, JALR, LUI, MEM_WB_halt_2, MEM_WB_jal_2, MEM_WB_jalr_2, MEM_WB_lui_2,
       MEM_WB_memtoreg_2, MemRegWrite, MemToReg, nand_1_out, not_1_out, not_2_out, not_3_out, not_4_out,
       not_5_out, not_6_out, or_1_out, or_2_out, or_3_out, or_5_out, or_6_out, or_7_out, or_13_out,
       or_14_out, RST, S, S_type, sb, stall, URET, W1, W2, W3, \单周期硬布线控制器_1_memwrite ,
       \单周期硬布线控制器_1_regwrite , \单周期硬布线控制器_1_rs1 , \单周期硬布线控制器_1_rs2 , \无条件跳转 ;
  wire [1:0] priority_encoder_1_out, priority_encoder_2_out, priority_encoder_3_out;
  wire [3:0] ALUOP, id_ex_1_aluop_2;
  wire [4:0] EXrd, MEMrd, multiplexer_2_out, multiplexer_3_out, WBrd;
  wire [12:0] CNT_num;
  wire [15:0] \LoadUse次数 , \总周期数 , \插入气泡数 , \无条件分支数 , \条件分支成功数 ;
  wire [31:0] ALUResult, and_11_out, and_12_out, and_13_out, and_14_out, B, bit_extender_1_out,
       bit_extender_2_out, bit_extender_3_out, bit_extender_4_out, bit_extender_5_out, EX_IR, EX_MEM_pc_4_2,
       EX_MEM_result_2, EX_MEM_writedata_2, id_ex_1_imm_1_2, id_ex_1_imm_2_2, id_ex_1_pc_4_2, id_ex_1_r1_2,
       id_ex_1_r2_2, ID_IR, IF_ID_pc_4_2, IF_IR, J, MEM_IR, MEM_WB_aluresult_2, MEM_WB_pc_4_2,
       MEM_WB_readdata_2, multiplexer_1_out, multiplexer_4_out, multiplexer_5_out, multiplexer_6_out,
       multiplexer_8_out, or_9_out, or_10_out, or_11_out, or_12_out, PC_4, ram_1_data, regifile_1_r1,
       regifile_1_r2, shifter_1_out, shifter_2_out, shifter_3_out, shifter_4_out, shifter_5_out,
       shifter_6_out, U, WB_IR;

  Button \u_总复位  (.out(RST));
  Button _1 (.out(IR1));
  Button _2 (.out(IR2));
  Button _3 (.out(IR3));
  // Probe on \总周期数 
  // Probe on \总周期数 
  Button \u_继续运行  (.out(Go));
  LED #(.active("true")) led_1 (.in(W1));
  LED #(.active("true")) led_2 (.in(W2));
  LED #(.active("true")) led_3 (.in(W3));
  Hex_Digit_Display hex_digit_display_1 (.value(LedData[31:28]));  // open: dp
  // Probe on IF_PC[19:0]
  // RiscV_Probe riscv_probe_1: pin names not known; wires that end beside it: IF_IR
  Hex_Digit_Display hex_digit_display_2 (.value(LedData[27:24]));  // open: dp
  Hex_Digit_Display hex_digit_display_3 (.value(LedData[23:20]));  // open: dp
  // Probe on ID_PC[19:0]
  // RiscV_Probe riscv_probe_2: pin names not known; wires that end beside it: ID_IR
  Multiplexer #(.select(2), .width(32), .disabled("Z"), .enable("false")) multiplexer_1 (
    .in0(PC_4), .in1(ALUResult), .in2(B), .in3(J), .out(multiplexer_1_out), .sel(priority_encoder_1_out));
  and and_1 (and_1_out, not_1_out, or_1_out);
  or or_1 (or_1_out, not_2_out, Go);
  not not_1 (not_1_out, stall);
  not not_2 (not_2_out, halt);
  Hex_Digit_Display hex_digit_display_4 (.value(LedData[19:16]));  // open: dp
  Hex_Digit_Display hex_digit_display_5 (.value(LedData[15:12]));  // open: dp
  Register #(.width(32), .trigger("rising"), .Select("low")) PC (
    .D(multiplexer_1_out), .en(and_1_out), .Q(IF_PC), .clk(CLK), .clr(RST));
  Hex_Digit_Display hex_digit_display_6 (.value(LedData[7:4]));  // open: dp
  Hex_Digit_Display hex_digit_display_7 (.value(LedData[11:8]));  // open: dp
  // Probe on EX_PC[19:0]
  // RiscV_Probe riscv_probe_3: pin names not known; wires that end beside it: EX_IR
  Adder #(.width(32)) adder_1 (.a(IF_PC), .b(32'h4), .out(PC_4));  // open: cin, cout
  Hex_Digit_Display hex_digit_display_8 (.value(LedData[3:0]));  // open: dp
  // Probe on \总周期数 
  // Probe on M_PC[19:0]
  // RiscV_Probe riscv_probe_4: pin names not known; wires that end beside it: MEM_IR
  // RiscV_Probe riscv_probe_5: pin names not known; wires that end beside it: IF_IR
  ROM #(.addrWidth(10), .dataWidth(32), .Select("high")) rom_1 (.addr(IF_PC[11:2]), .data(IF_IR));
  and and_2 (and_2_out, ~stall, or_3_out);  // AND_Gate
  // Probe on \总周期数 
  // Probe on \无条件分支数 
  // Probe on \条件分支成功数 
  // Probe on \插入气泡数 
  // Probe on \LoadUse次数 
  or or_2 (or_2_out, priority_encoder_1_out[1], priority_encoder_1_out[0]);
  or or_3 (or_3_out, ~halt, Go);  // OR_Gate
  // Probe on IF_PC[11:0]
  // Probe on WB_PC[19:0]
  // RiscV_Probe riscv_probe_6: pin names not known; wires that end beside it: WB_IR
  IF_ID IF_ID (
    .IR(IF_IR), .PC(IF_PC), .PC_4(PC_4), .IR_2(ID_IR), .PC_2(ID_PC), .PC_4_2(IF_ID_pc_4_2),
    .branch(or_2_out), .CLK(CLK), .EN(and_2_out));  // open: IF_PredictJump, ID_PredictJump
  // Probe on EX_PC[11:0]
  // Probe on ID_PC[11:0]
  \气泡流水电路  \u_气泡流水  (
    .BranchTaken(or_2_out), .IR(ID_IR), .Ecall(ecall), .RS1_used(\单周期硬布线控制器_1_rs1 ),
    .EX_RegWrite(EXRegWrite), .EX_rd(EXrd), .RS2_used(\单周期硬布线控制器_1_rs2 ), .MEM_RegWrite(MemRegWrite),
    .MEM_rd(MEMrd), .stall(stall), .flush(flush));
  // Probe on M_PC[11:0]
  D_Flip_Flop #(.trigger("high"), .Pre_Clr_Positions("LEGACY"), .NegatePresetClear("false"), .enable("true"), .NewFFLayout("false")) d_ff_1 (.Q(d_ff_1_q));  // open: clk, D, Qn, preset, en, reset
  // Probe on 13'hc
  \单周期硬布线控制器  \u_单周期硬布线控制器_1  (
    .Funct({ID_IR[30], ID_IR[25], ID_IR[14:12]}), .OP(ID_IR[6:2]), .ALU_OP(ALUOP), .MemToReg(MemToReg),
    .MemWrite(\单周期硬布线控制器_1_memwrite ), .ALU_SRC(Alu_Src), .RegWrite(\单周期硬布线控制器_1_regwrite ), .ecall(ecall),
    .S_type(S_type), .Jalr(JALR), .Beq(Beq), .JAL(JAL), .Bne(Bne), .in_3(ID_IR[21]), .uret(URET), .LUI(LUI),
    .sb(sb), .BGEU(BGEU), .rs1(\单周期硬布线控制器_1_rs1 ), .rs2(\单周期硬布线控制器_1_rs2 ));  // open: CSR
  Multiplexer #(.select(1), .width(5), .disabled("Z"), .enable("false")) multiplexer_2 (
    .in0(ID_IR[19:15]), .in1(5'b10001), .out(multiplexer_2_out), .sel(ecall));
  Multiplexer #(.select(1), .width(5), .disabled("Z"), .enable("false")) multiplexer_3 (
    .in0(ID_IR[24:20]), .in1(5'b01010), .out(multiplexer_3_out), .sel(ecall));
  assign bit_extender_1_out = {{12{ID_IR[31]}}, ID_IR[31:12]};  // Bit_Extender bit_extender_1
  // Probe on WB_PC[11:0]
  Comparator #(.width(13), .mode("twosComplement")) comparator_1 (
    .a(CNT_num), .b(13'hc), .eq(comparator_1_eq), .lt(comparator_1_lt));  // open: gt
  Clock #(.highDuration(1), .lowDuration(1)) clock_1 (.out(clock_1_out));
  assign bit_extender_2_out = {{20{ID_IR[31]}}, ID_IR[31:20]};  // Bit_Extender bit_extender_2
  assign bit_extender_3_out = {{20{ID_IR[31]}}, {ID_IR[31:25], ID_IR[11:7]}};  // Bit_Extender bit_extender_3
  assign bit_extender_4_out = {{20{ID_IR[31]}}, {ID_IR[31], ID_IR[7], ID_IR[30:25], ID_IR[11:8]}};  // Bit_Extender bit_extender_4
  assign bit_extender_5_out = {{12{ID_IR[31]}}, {ID_IR[31], ID_IR[19:12], ID_IR[20], ID_IR[30:21]}};  // Bit_Extender bit_extender_5
  nand nand_1 (nand_1_out, d_ff_1_q, comparator_1_eq);
  Counter #(.width(13), .max('h1fff), .ongoal("stay"), .trigger("rising"), .behavior("old")) counter_1 (
    .count(comparator_1_lt), .Q(CNT_num), .clk(clock_1_out));  // open: load, D, carry, clr, preset
  not not_3 (not_3_out, CLK);
  Multiplexer #(.select(1), .width(32), .disabled("Z"), .enable("false")) multiplexer_4 (
    .in0(bit_extender_2_out), .in1(bit_extender_3_out), .out(multiplexer_4_out), .sel(S_type));
  assign CLK = nand_1_out ? clock_1_out : 1'bz;  // Controlled_Buffer controlled_buffer_1
  Priority_Encoder #(.select(2), .disabled("Z")) priority_encoder_1 (
    .in0(1'b1), .in1(id_ex_1_jalr_2), .in2(BranchSuc), .in3(id_ex_1_jal_2), .out(priority_encoder_1_out));  // open: gs, en_out, en_in
  Regifile regifile_1 (
    .Din(RDin), .Clk(not_3_out), .R1(regifile_1_r1), .R2(regifile_1_r2), .WE(RegWrite), .W_num(WBrd),
    .R1_num(multiplexer_2_out), .R2_num(multiplexer_3_out));
  Pull_Resistor #(.pull(1)) pull_resistor_1 (.node(CLK));
  or or_4 (BranchSuc, and_3_out, and_4_out, and_5_out);
  Multiplexer #(.select(2), .width(32), .disabled("Z"), .enable("false")) multiplexer_5 (
    .in0(bit_extender_4_out), .in1(bit_extender_4_out), .in2(bit_extender_5_out), .in3(bit_extender_1_out),
    .out(multiplexer_5_out), .sel(priority_encoder_2_out));
  Priority_Encoder #(.select(2), .disabled("Z")) priority_encoder_2 (
    .in0(1'b1), .in1(or_5_out), .in2(JAL), .in3(LUI), .out(priority_encoder_2_out));  // open: gs, en_out, en_in
  or or_5 (or_5_out, and_6_out, and_7_out, and_8_out);
  and and_3 (and_3_out, id_ex_1_bgeu_2, G);
  and and_4 (and_4_out, id_ex_1_beq_2, E);
  not not_4 (not_4_out, E);
  and and_5 (and_5_out, not_4_out, id_ex_1_bne_2);
  and and_6 (and_6_out, BGEU, G);
  and and_7 (and_7_out, Beq, E);
  and and_8 (and_8_out, not_5_out, Bne);
  ID_EX id_ex_1 (
    .Beq(Beq), .Beq_2(id_ex_1_beq_2), .Bne(Bne), .Bne_2(id_ex_1_bne_2), .MemToReg(MemToReg),
    .MemToReg_2(id_ex_1_memtoreg_2), .MemWrite(\单周期硬布线控制器_1_memwrite ), .MemWrite_2(id_ex_1_memwrite_2),
    .AluSrcB(Alu_Src), .AluSrcB_2(id_ex_1_alusrcb_2), .RegWrite(\单周期硬布线控制器_1_regwrite ),
    .RegWrite_2(EXRegWrite), .ecall(ecall), .ecall_2(id_ex_1_ecall_2), .Jal(JAL), .Jal_2(id_ex_1_jal_2),
    .Jalr(JALR), .Jalr_2(id_ex_1_jalr_2), .BGEU(BGEU), .BGEU_2(id_ex_1_bgeu_2), .Uret(URET), .AluOP(ALUOP),
    .AluOP_2(id_ex_1_aluop_2), .rd(ID_IR[11:7]), .rd_2(EXrd), .R1(regifile_1_r1), .R1_2(id_ex_1_r1_2),
    .R2(regifile_1_r2), .R2_2(id_ex_1_r2_2), .imm_1(multiplexer_4_out), .imm_1_2(id_ex_1_imm_1_2),
    .imm_2(multiplexer_5_out), .imm_2_2(id_ex_1_imm_2_2), .PC(ID_PC), .PC_2(EX_PC), .PC_4(IF_ID_pc_4_2),
    .PC_4_2(id_ex_1_pc_4_2), .IR(ID_IR), .IR_2(EX_IR), .en(or_6_out), .clk(CLK), .flush(flush), .sb(sb),
    .sb_2(id_ex_1_sb_2), .LUI(LUI), .LUI_2(id_ex_1_lui_2));  // open: Uret_2, RS1_Forward, RS1_Forward_2, RS2_Forward, RS2_Forward_2, ID_PredictJump, EX_PredictJump
  or or_6 (or_6_out, ~halt, Go);  // OR_Gate
  not not_5 (not_5_out, E);
  Comparator #(.width(32), .mode("twosComplement")) comparator_2 (
    .a(id_ex_1_r1_2), .b(32'h22), .eq(comparator_2_eq));  // open: gt, lt
  not not_6 (not_6_out, comparator_2_eq);
  and and_9 (and_9_out, id_ex_1_ecall_2, not_6_out);
  Multiplexer #(.select(1), .width(32), .disabled("Z"), .enable("false")) multiplexer_6 (
    .in0(id_ex_1_r2_2), .in1(id_ex_1_imm_1_2), .out(multiplexer_6_out), .sel(id_ex_1_alusrcb_2));
  Adder #(.width(32)) adder_2 (.a(EX_PC), .b(shifter_1_out), .out(B));  // open: cin, cout
  Shifter #(.width(32), .shift("ll")) shifter_1 (.in(id_ex_1_imm_2_2), .\dist (5'b00001), .out(shifter_1_out));
  Adder #(.width(32)) adder_3 (.a(EX_PC), .b(shifter_2_out), .out(J));  // open: cin, cout
  Shifter #(.width(32), .shift("ll")) shifter_2 (.in(id_ex_1_imm_2_2), .\dist (5'b00001), .out(shifter_2_out));
  Adder #(.width(32)) adder_4 (.a(EX_PC), .b(shifter_3_out), .out(U));  // open: cin, cout
  Shifter #(.width(32), .shift("ll")) shifter_3 (.in(id_ex_1_imm_2_2), .\dist (5'b01100), .out(shifter_3_out));
  and and_10 (and_10_out, comparator_2_eq, id_ex_1_ecall_2);
  ALU alu_1 (
    .X(id_ex_1_r1_2), .Y(multiplexer_6_out), .AluOP(id_ex_1_aluop_2), .Equal(E), .Result(ALUResult),
    .out_4(G), .out_6(S));  // open: Result_2
  Register #(.width(32), .trigger("rising"), .Select("low")) register_1 (
    .D(id_ex_1_r2_2), .en(and_10_out), .Q(LedData), .clk(CLK));  // open: clr
  or or_7 (or_7_out, ~halt, Go);  // OR_Gate
  EX_MEM EX_MEM (
    .LUI(id_ex_1_lui_2), .Jal(id_ex_1_jal_2), .Jalr(id_ex_1_jalr_2), .MemToReg(id_ex_1_memtoreg_2),
    .MemWrite(id_ex_1_memwrite_2), .sb(id_ex_1_sb_2), .RegWrite(EXRegWrite), .halt(and_9_out), .rd(EXrd),
    .Result(ALUResult), .WriteData(id_ex_1_r2_2), .IR(EX_IR), .PC(EX_PC), .PC_4(id_ex_1_pc_4_2),
    .LUI_2(EX_MEM_lui_2), .Jal_2(EX_MEM_jal_2), .Jalr_2(EX_MEM_jalr_2), .MemToReg_2(EX_MEM_memtoreg_2),
    .MemWrite_2(MemWrite), .sb_2(EX_MEM_sb_2), .RegWrite_2(MemRegWrite), .halt_2(EX_MEM_halt_2),
    .rd_2(MEMrd), .Result_2(EX_MEM_result_2), .WriteData_2(EX_MEM_writedata_2), .IR_2(MEM_IR), .PC_2(M_PC),
    .PC_4_2(EX_MEM_pc_4_2), .clk(CLK), .en(or_7_out));  // open: U, U_2
  or or_8 (\无条件跳转 , id_ex_1_jal_2, id_ex_1_jalr_2);
  Multiplexer #(.select(1), .width(32), .disabled("Z"), .enable("false")) multiplexer_7 (
    .in0(EX_MEM_writedata_2), .in1(multiplexer_8_out), .out(MDin), .sel(EX_MEM_sb_2));
  Multiplexer #(.select(2), .width(32), .disabled("Z"), .enable("false")) multiplexer_8 (
    .in0(or_10_out), .in1(or_11_out), .in2(or_12_out), .in3(or_9_out), .out(multiplexer_8_out),
    .sel(EX_MEM_result_2[1:0]));
  assign or_9_out = shifter_6_out | and_11_out;  // OR_Gate or_9, 32 bits wide
  assign or_10_out = and_14_out | EX_MEM_writedata_2;  // OR_Gate or_10, 32 bits wide
  assign or_11_out = and_13_out | shifter_4_out;  // OR_Gate or_11, 32 bits wide
  assign or_12_out = and_12_out | shifter_5_out;  // OR_Gate or_12, 32 bits wide
  RAM #(.addrWidth(10), .dataWidth(32), .bus("separate"), .Select("high")) ram_1 (
    .addr(EX_MEM_result_2[11:2]), .din(MDin), .data(ram_1_data), .str(MemWrite), .sel(1'b1), .clk(CLK),
    .ld(1'b1));  // open: clr
  assign and_11_out = ram_1_data & 32'hffffff;  // AND_Gate and_11, 32 bits wide
  assign and_12_out = ram_1_data & 32'hff00ffff;  // AND_Gate and_12, 32 bits wide
  assign and_13_out = ram_1_data & 32'hffff00ff;  // AND_Gate and_13, 32 bits wide
  assign and_14_out = ram_1_data & 32'hffffff00;  // AND_Gate and_14, 32 bits wide
  Counter #(.width(16), .max('hffff), .ongoal("wrap"), .trigger("rising"), .behavior("new")) counter_2 (
    .count(BranchSuc), .Q(\条件分支成功数 ), .clk(and_15_out));  // open: load, D, carry, clr, preset, down
  and and_15 (and_15_out, ~halt, CLK);  // AND_Gate
  Counter #(.width(16), .max('hffff), .ongoal("wrap"), .trigger("rising"), .behavior("new")) counter_3 (
    .count(flush), .Q(\插入气泡数 ), .clk(and_16_out));  // open: load, D, carry, clr, preset, down
  and and_16 (and_16_out, ~halt, CLK);  // AND_Gate
  Shifter #(.width(32), .shift("ll")) shifter_4 (.in(EX_MEM_writedata_2), .\dist (5'b01000), .out(shifter_4_out));
  Shifter #(.width(32), .shift("ll")) shifter_5 (.in(EX_MEM_writedata_2), .\dist (5'b10000), .out(shifter_5_out));
  Shifter #(.width(32), .shift("ll")) shifter_6 (.in(EX_MEM_writedata_2), .\dist (5'b11000), .out(shifter_6_out));
  or or_13 (or_13_out, ~halt, Go);  // OR_Gate
  Counter #(.width(16), .max('hffff), .ongoal("wrap"), .trigger("rising"), .behavior("new")) counter_4 (
    .count(\无条件跳转 ), .Q(\无条件分支数 ), .clk(and_17_out));  // open: load, D, carry, clr, preset, down
  and and_17 (and_17_out, ~halt, CLK);  // AND_Gate
  Counter #(.width(16), .max('hffff), .ongoal("wrap"), .trigger("rising"), .behavior("new")) counter_5 (
    .count(CLK), .Q(\总周期数 ), .clk(and_18_out));  // open: load, D, carry, clr, preset, down
  and and_18 (and_18_out, ~halt, CLK);  // AND_Gate
  MEM_WB MEM_WB (
    .LUI(EX_MEM_lui_2), .Jal(EX_MEM_jal_2), .Jalr(EX_MEM_jalr_2), .MemToReg(EX_MEM_memtoreg_2),
    .RegWrite(MemRegWrite), .halt(EX_MEM_halt_2), .rd(MEMrd), .ALUResult(EX_MEM_result_2),
    .ReadData(ram_1_data), .IR(MEM_IR), .PC(M_PC), .PC_4(EX_MEM_pc_4_2), .LUI_2(MEM_WB_lui_2),
    .Jal_2(MEM_WB_jal_2), .Jalr_2(MEM_WB_jalr_2), .MemToReg_2(MEM_WB_memtoreg_2), .RegWrite_2(RegWrite),
    .halt_2(MEM_WB_halt_2), .rd_2(WBrd), .ALUResult_2(MEM_WB_aluresult_2), .ReadData_2(MEM_WB_readdata_2),
    .IR_2(WB_IR), .PC_2(WB_PC), .PC_4_2(MEM_WB_pc_4_2), .clk(CLK), .en(or_13_out));  // open: U, U_2
  Counter #(.width(16), .max('hffff), .ongoal("wrap"), .trigger("rising"), .behavior("new")) counter_6 (
    .count(stall), .Q(\LoadUse次数 ), .clk(and_19_out));  // open: load, D, carry, clr, preset, down
  and and_19 (and_19_out, ~halt, CLK);  // AND_Gate
  Multiplexer #(.select(2), .width(32), .disabled("Z"), .enable("false")) multiplexer_9 (
    .in0(MEM_WB_aluresult_2), .in1(MEM_WB_readdata_2), .in2(MEM_WB_pc_4_2), .in3(U), .out(RDin),
    .sel(priority_encoder_3_out));
  Priority_Encoder #(.select(2), .disabled("Z")) priority_encoder_3 (
    .in0(1'b1), .in1(MEM_WB_memtoreg_2), .in2(or_14_out), .in3(MEM_WB_lui_2), .out(priority_encoder_3_out));  // open: gs, en_out, en_in
  or or_14 (or_14_out, MEM_WB_jalr_2, MEM_WB_jal_2);
  D_Flip_Flop #(.trigger("rising"), .Pre_Clr_Positions("ABOVE_BELOW"), .NegatePresetClear("false"), .enable("true"), .NewFFLayout("true")) d_ff_2 (
    .clk(MEM_WB_halt_2), .D(1'b1), .Q(halt), .en(1'b1), .reset(Go));  // open: Qn, preset

  // Other names for the same wires on the sheet: rd[4:0] = ID_IR[11:7]; IR[31:0] = IF_IR; MEM_PC[31:0] = M_PC;
  //   PC[31:0] = IF_PC

  // Notes on the sheet:
  //   中断源
  //   时空图监测，可删除
  //   中断等待指示
  //   数码管输出
  //   指令存储器
  //   指令探针
  //   contents of rom_1 (hex, n*v repeats v):
  //   100493 100006f 100493 200913 300993 100006f 100493 200913 300993 100006f 100493 200913 300993
  //   100006f 100493 200913 300993 29c000ef 100413 100493 1f49493 900533 2200893 73 24d493 48463 fedff06f
  //   900533 2200893 73 100493 249493 900533 2200893 73 48463 fedff06f 100493 1f49493 900533 2200893 73
  //   4034d493 900533 2200893 73 4044d493 900533 2200893 73 4044d493 900533 2200893 73 4044d493 900533
  //   2200893 73 4044d493 900533 2200893 73 4044d493 900533 2200893 73 4044d493 900533 2200893 73 4044d493
  //   900533 2200893 73 100413 1f41993 41f9d993 433 c00913 300b13 140413 f47413 800293 100313 499993
  //   89e9b3 1300533 2200893 73 406282b3 fe0294e3 140413 f00f93 1f47433 1c41413 800293 100313 49d993
  //   89e9b3 1300533 2200893 73 406282b3 fe0294e3 1c45413 406b0b33 b0463 f95ff06f 2b3 fff2c293 829293
  //   ff2e293 500533 2200893 73 fff00413 493 84a023 140413 448493 84a023 140413 448493 84a023 140413
  //   448493 84a023 140413 448493 84a023 140413 448493 84a023 140413 448493 84a023 140413 448493 84a023
  //   140413 448493 84a023 140413 448493 84a023 140413 448493 84a023 140413 448493 84a023 140413 448493
  //   84a023 140413 448493 84a023 140413 448493 84a023 140413 448493 84a023 140413 448493 140413 433
  //   3c00493 42983 4aa03 149a2b3 28663 134a023 1442023 ffc48493 fe9412e3 800533 2200893 73 440413 3c00493
  //   fc9416e3 a00893 73 413 140413 800533 2200893 73 240413 800533 2200893 73 340413 800533 2200893 73
  //   440413 800533 2200893 73 540413 800533 2200893 73 640413 800533 2200893 73 740413 800533 2200893 73
  //   840413 800533 2200893 2200893 73 8067
  //   指令字
  //   控制位
  //   流水调试日志用
  //   暂停节拍，不能为0
  //   戳工具置1进入计数暂停模式，ctrl+k时钟自动运行到对应节拍暂停
  //   ctrl+k关闭时钟连续运行，将控制位置零，进入单步调试模式调试
  //   可计数暂停的时钟源
  //   为方便自动评测，需要输出流水线各段保存的PC值，注意是PC不是PC+4，另外ID段寄存器写入信息，Mem段内存写入信息也要输出
  //   数据存储器
endmodule

module \理想流水线  (
  output RegWrite,
  output MemWrite,
  output [31:0] IF_PC,
  output [31:0] ID_PC,
  output [31:0] EX_PC,
  output [31:0] M_PC,
  output [31:0] WB_PC,
  output [31:0] RDin,
  output [31:0] MDin,
  output [31:0] LedData
);

  wire Alu_Src, and_1_out, and_2_out, and_3_out, and_4_out, and_5_out, and_6_out, and_7_out, and_8_out,
       AUIPC, Beq, BGEU, Bne, CLK, clock_1_out, comparator_1_eq, comparator_1_lt, comparator_2_eq, d_ff_1_q,
       E, ecall, EX_MEM_halt_2, EX_MEM_jal_2, EX_MEM_jalr_2, EX_MEM_lui_2, EX_MEM_memtoreg_2,
       EX_MEM_regwrite_2, EX_MEM_sb_2, G, Go, halt, id_ex_1_alusrcb_2, id_ex_1_beq_2, id_ex_1_bgeu_2,
       id_ex_1_bne_2, id_ex_1_ecall_2, id_ex_1_jal_2, id_ex_1_jalr_2, id_ex_1_lui_2, id_ex_1_memtoreg_2,
       id_ex_1_memwrite_2, id_ex_1_regwrite_2, id_ex_1_sb_2, IR1, IR2, IR3, JAL, JALR, MEM_WB_halt_2,
       MEM_WB_jal_2, MEM_WB_jalr_2, MEM_WB_lui_2, MEM_WB_memtoreg_2, MemToReg, nand_1_out, not_1_out,
       not_2_out, not_3_out, not_4_out, not_5_out, or_1_out, or_2_out, or_3_out, or_4_out, or_9_out, RST, S,
       S_type, sb, URET, W1, W2, W3, \单周期硬布线控制器_1_memwrite , \单周期硬布线控制器_1_regwrite ;
  wire [1:0] priority_encoder_1_out, priority_encoder_2_out, priority_encoder_3_out;
  wire [3:0] ALUOP, id_ex_1_aluop_2;
  wire [4:0] EX_MEM_rd_2, id_ex_1_rd_2, multiplexer_2_out, multiplexer_3_out, WBrd;
  wire [12:0] CNT_num;
  wire [15:0] \LoadUse次数 , \总周期数 , \插入气泡数 , \无条件分支数 , \条件分支成功数 ;
  wire [31:0] ALUResult, and_9_out, and_10_out, and_11_out, and_12_out, B, bit_extender_1_out,
       bit_extender_2_out, bit_extender_3_out, bit_extender_4_out, bit_extender_5_out, EX_IR, EX_MEM_pc_4_2,
       EX_MEM_result_2, EX_MEM_writedata_2, id_ex_1_imm_1_2, id_ex_1_imm_2_2, id_ex_1_pc_4_2, id_ex_1_r1_2,
       id_ex_1_r2_2, ID_IR, IF_ID_pc_4_2, IF_IR, J, MEM_IR, MEM_WB_aluresult_2, MEM_WB_pc_4_2,
       MEM_WB_readdata_2, multiplexer_1_out, multiplexer_4_out, multiplexer_5_out, multiplexer_6_out,
       multiplexer_8_out, or_5_out, or_6_out, or_7_out, or_8_out, PC_4, ram_1_data, regifile_1_r1,
       regifile_1_r2, shifter_1_out, shifter_2_out, shifter_3_out, shifter_4_out, shifter_5_out,
       shifter_6_out, U, WB_IR;

  Button \u_总复位  (.out(RST));
  Button _1 (.out(IR1));
  Button _2 (.out(IR2));
  Button _3 (.out(IR3));
  // Probe on \总周期数 
  // Probe on \总周期数 
  Button \u_继续运行  (.out(Go));
  LED #(.active("true")) led_1 (.in(W1));
  LED #(.active("true")) led_2 (.in(W2));
  LED #(.active("true")) led_3 (.in(W3));
  Multiplexer #(.select(2), .width(32), .disabled("Z"), .enable("false")) multiplexer_1 (
    .in0(PC_4), .in1(ALUResult), .in2(B), .in3(J), .out(multiplexer_1_out), .sel(priority_encoder_1_out));
  or or_1 (or_1_out, not_1_out, Go);
  not not_1 (not_1_out, halt);
  Hex_Digit_Display hex_digit_display_1 (.value(LedData[31:28]));  // open: dp
  // Probe on IF_PC[19:0]
  // RiscV_Probe riscv_probe_1: pin names not known; wires that end beside it: IF_IR
  Register #(.width(32), .trigger("rising"), .Select("low")) PC (
    .D(multiplexer_1_out), .en(or_1_out), .Q(IF_PC), .clk(CLK), .clr(RST));
  Hex_Digit_Display hex_digit_display_2 (.value(LedData[27:24]));  // open: dp
  Hex_Digit_Display hex_digit_display_3 (.value(LedData[23:20]));  // open: dp
  // Probe on ID_PC[19:0]
  // RiscV_Probe riscv_probe_2: pin names not known; wires that end beside it: ID_IR
  Adder #(.width(32)) adder_1 (.a(IF_PC), .b(32'h4), .out(PC_4));  // open: cin, cout
  Hex_Digit_Display hex_digit_display_4 (.value(LedData[15:12]));  // open: dp
  Hex_Digit_Display hex_digit_display_5 (.value(LedData[19:16]));  // open: dp
  Hex_Digit_Display hex_digit_display_6 (.value(LedData[11:8]));  // open: dp
  Hex_Digit_Display hex_digit_display_7 (.value(LedData[7:4]));  // open: dp
  // Probe on EX_PC[19:0]
  // RiscV_Probe riscv_probe_3: pin names not known; wires that end beside it: EX_IR
  // RiscV_Probe riscv_probe_4: pin names not known; wires that end beside it: IF_IR
  ROM #(.addrWidth(10), .dataWidth(32), .Select("high")) rom_1 (.addr(IF_PC[11:2]), .data(IF_IR));
  Hex_Digit_Display hex_digit_display_8 (.value(LedData[3:0]));  // open: dp
  or or_2 (or_2_out, priority_encoder_1_out[1], priority_encoder_1_out[0]);
  // Probe on \总周期数 
  // Probe on M_PC[19:0]
  // RiscV_Probe riscv_probe_5: pin names not known; wires that end beside it: MEM_IR
  IF_ID IF_ID (
    .IR(IF_IR), .PC(IF_PC), .PC_4(PC_4), .IR_2(ID_IR), .PC_2(ID_PC), .PC_4_2(IF_ID_pc_4_2),
    .branch(or_2_out), .CLK(CLK), .EN(1'b1));  // open: IF_PredictJump, ID_PredictJump
  // Probe on \总周期数 
  // Probe on \无条件分支数 
  // Probe on \条件分支成功数 
  // Probe on \插入气泡数 
  // Probe on \LoadUse次数 
  // Probe on IF_PC[11:0]
  // Probe on WB_PC[19:0]
  // RiscV_Probe riscv_probe_6: pin names not known; wires that end beside it: WB_IR
  Multiplexer #(.select(1), .width(5), .disabled("Z"), .enable("false")) multiplexer_2 (
    .in0(ID_IR[19:15]), .in1(5'b10001), .out(multiplexer_2_out), .sel(ecall));
  Multiplexer #(.select(1), .width(5), .disabled("Z"), .enable("false")) multiplexer_3 (
    .in0(ID_IR[24:20]), .in1(5'b01010), .out(multiplexer_3_out), .sel(ecall));
  assign bit_extender_1_out = {{12{ID_IR[31]}}, ID_IR[31:12]};  // Bit_Extender bit_extender_1
  // Probe on ID_PC[11:0]
  // Probe on EX_PC[11:0]
  \单周期硬布线控制器  \u_单周期硬布线控制器_1  (
    .Funct({ID_IR[30], ID_IR[25], ID_IR[14:12]}), .OP(ID_IR[6:2]), .ALU_OP(ALUOP), .MemToReg(MemToReg),
    .MemWrite(\单周期硬布线控制器_1_memwrite ), .ALU_SRC(Alu_Src), .RegWrite(\单周期硬布线控制器_1_regwrite ), .ecall(ecall),
    .S_type(S_type), .Jalr(JALR), .Beq(Beq), .JAL(JAL), .Bne(Bne), .in_3(ID_IR[21]), .uret(URET),
    .LUI(AUIPC), .sb(sb), .BGEU(BGEU));  // open: rs1, rs2, CSR
  assign bit_extender_2_out = {{20{ID_IR[31]}}, ID_IR[31:20]};  // Bit_Extender bit_extender_2
  assign bit_extender_3_out = {{20{ID_IR[31]}}, {ID_IR[31:25], ID_IR[11:7]}};  // Bit_Extender bit_extender_3
  assign bit_extender_4_out = {{20{ID_IR[31]}}, {ID_IR[31], ID_IR[7], ID_IR[30:25], ID_IR[11:8]}};  // Bit_Extender bit_extender_4
  assign bit_extender_5_out = {{12{ID_IR[31]}}, {ID_IR[31], ID_IR[19:12], ID_IR[20], ID_IR[30:21]}};  // Bit_Extender bit_extender_5
  // Probe on M_PC[11:0]
  D_Flip_Flop #(.trigger("high"), .Pre_Clr_Positions("LEGACY"), .NegatePresetClear("false"), .enable("true"), .NewFFLayout("false")) d_ff_1 (.Q(d_ff_1_q));  // open: clk, D, Qn, preset, en, reset
  // Probe on 13'h14
  Multiplexer #(.select(1), .width(32), .disabled("Z"), .enable("false")) multiplexer_4 (
    .in0(bit_extender_2_out), .in1(bit_extender_3_out), .out(multiplexer_4_out), .sel(S_type));
  Shifter #(.width(32), .shift("ll")) shifter_1 (.in(bit_extender_4_out), .\dist (5'b00001), .out(shifter_1_out));
  Shifter #(.width(32), .shift("ll")) shifter_2 (.in(bit_extender_5_out), .\dist (5'b00001), .out(shifter_2_out));
  Shifter #(.width(32), .shift("ll")) shifter_3 (.in(bit_extender_1_out), .\dist (5'b01100), .out(shifter_3_out));
  // Probe on WB_PC[11:0]
  Comparator #(.width(13), .mode("twosComplement")) comparator_1 (
    .a(CNT_num), .b(13'h14), .eq(comparator_1_eq), .lt(comparator_1_lt));  // open: gt
  Clock #(.highDuration(1), .lowDuration(1)) clock_1 (.out(clock_1_out));
  Priority_Encoder #(.select(2), .disabled("Z")) priority_encoder_1 (
    .in0(1'b1), .in1(id_ex_1_jalr_2), .in2(or_3_out), .in3(id_ex_1_jal_2), .out(priority_encoder_1_out));  // open: gs, en_out, en_in
  Regifile regifile_1 (
    .Din(RDin), .Clk(CLK), .R1(regifile_1_r1), .R2(regifile_1_r2), .WE(RegWrite), .W_num(WBrd),
    .R1_num(multiplexer_2_out), .R2_num(multiplexer_3_out));
  nand nand_1 (nand_1_out, d_ff_1_q, comparator_1_eq);
  Counter #(.width(13), .max('h1fff), .ongoal("stay"), .trigger("rising"), .behavior("old")) counter_1 (
    .count(comparator_1_lt), .Q(CNT_num), .clk(clock_1_out));  // open: load, D, carry, clr, preset
  or or_3 (or_3_out, and_1_out, and_2_out, and_3_out);
  Multiplexer #(.select(2), .width(32), .disabled("Z"), .enable("false")) multiplexer_5 (
    .in0(shifter_1_out), .in1(shifter_1_out), .in2(shifter_2_out), .in3(shifter_3_out),
    .out(multiplexer_5_out), .sel(priority_encoder_2_out));
  Priority_Encoder #(.select(2), .disabled("Z")) priority_encoder_2 (
    .in0(1'b1), .in1(or_4_out), .in2(JAL), .in3(AUIPC), .out(priority_encoder_2_out));  // open: gs, en_out, en_in
  assign CLK = nand_1_out ? clock_1_out : 1'bz;  // Controlled_Buffer controlled_buffer_1
  and and_1 (and_1_out, id_ex_1_bgeu_2, G);
  and and_2 (and_2_out, id_ex_1_beq_2, E);
  not not_2 (not_2_out, E);
  and and_3 (and_3_out, not_2_out, id_ex_1_bne_2);
  and and_4 (and_4_out, BGEU, G);
  and and_5 (and_5_out, Beq, E);
  or or_4 (or_4_out, and_4_out, and_5_out, and_6_out);
  and and_6 (and_6_out, not_3_out, Bne);
  Pull_Resistor #(.pull(1)) pull_resistor_1 (.node(CLK));
  ID_EX id_ex_1 (
    .Beq(Beq), .Beq_2(id_ex_1_beq_2), .Bne(Bne), .Bne_2(id_ex_1_bne_2), .MemToReg(MemToReg),
    .MemToReg_2(id_ex_1_memtoreg_2), .MemWrite(\单周期硬布线控制器_1_memwrite ), .MemWrite_2(id_ex_1_memwrite_2),
    .AluSrcB(Alu_Src), .AluSrcB_2(id_ex_1_alusrcb_2), .RegWrite(\单周期硬布线控制器_1_regwrite ),
    .RegWrite_2(id_ex_1_regwrite_2), .ecall(ecall), .ecall_2(id_ex_1_ecall_2), .Jal(JAL),
    .Jal_2(id_ex_1_jal_2), .Jalr(JALR), .Jalr_2(id_ex_1_jalr_2), .BGEU(BGEU), .BGEU_2(id_ex_1_bgeu_2),
    .Uret(URET), .AluOP(ALUOP), .AluOP_2(id_ex_1_aluop_2), .rd(ID_IR[11:7]), .rd_2(id_ex_1_rd_2),
    .R1(regifile_1_r1), .R1_2(id_ex_1_r1_2), .R2(regifile_1_r2), .R2_2(id_ex_1_r2_2),
    .imm_1(multiplexer_4_out), .imm_1_2(id_ex_1_imm_1_2), .imm_2(multiplexer_5_out),
    .imm_2_2(id_ex_1_imm_2_2), .PC(ID_PC), .PC_2(EX_PC), .PC_4(IF_ID_pc_4_2), .PC_4_2(id_ex_1_pc_4_2),
    .IR(ID_IR), .IR_2(EX_IR), .en(1'b1), .clk(CLK), .flush(1'b0), .sb(sb), .sb_2(id_ex_1_sb_2), .LUI(AUIPC),
    .LUI_2(id_ex_1_lui_2));  // open: Uret_2, RS1_Forward, RS1_Forward_2, RS2_Forward, RS2_Forward_2, ID_PredictJump, EX_PredictJump
  not not_3 (not_3_out, E);
  not not_4 (not_4_out, halt);
  Counter #(.width(16), .max('hffff), .ongoal("wrap"), .trigger("rising"), .behavior("new")) counter_2 (
    .count(not_4_out), .Q(\总周期数 ), .clk(CLK));  // open: load, D, carry, clr, preset, down
  Comparator #(.width(32), .mode("twosComplement")) comparator_2 (
    .a(id_ex_1_r1_2), .b(32'h22), .eq(comparator_2_eq));  // open: gt, lt
  not not_5 (not_5_out, comparator_2_eq);
  and and_7 (and_7_out, id_ex_1_ecall_2, not_5_out);
  Multiplexer #(.select(1), .width(32), .disabled("Z"), .enable("false")) multiplexer_6 (
    .in0(id_ex_1_r2_2), .in1(id_ex_1_imm_1_2), .out(multiplexer_6_out), .sel(id_ex_1_alusrcb_2));
  Adder #(.width(32)) adder_2 (.a(EX_PC), .b(id_ex_1_imm_2_2), .out(B));  // open: cin, cout
  Adder #(.width(32)) adder_3 (.a(id_ex_1_imm_2_2), .b(EX_PC), .out(J));  // open: cin, cout
  Adder #(.width(32)) adder_4 (.a(id_ex_1_imm_2_2), .b(EX_PC), .out(U));  // open: cin, cout
  and and_8 (and_8_out, comparator_2_eq, id_ex_1_ecall_2);
  ALU alu_1 (
    .X(id_ex_1_r1_2), .Y(multiplexer_6_out), .AluOP(id_ex_1_aluop_2), .Equal(E), .Result(ALUResult),
    .out_4(G), .out_6(S));  // open: Result_2
  Register #(.width(32), .trigger("rising"), .Select("low")) register_1 (
    .D(id_ex_1_r2_2), .en(and_8_out), .Q(LedData), .clk(CLK));  // open: clr
  EX_MEM EX_MEM (
    .LUI(id_ex_1_lui_2), .Jal(id_ex_1_jal_2), .Jalr(id_ex_1_jalr_2), .MemToReg(id_ex_1_memtoreg_2),
    .MemWrite(id_ex_1_memwrite_2), .sb(id_ex_1_sb_2), .RegWrite(id_ex_1_regwrite_2), .halt(and_7_out),
    .rd(id_ex_1_rd_2), .Result(ALUResult), .WriteData(id_ex_1_r2_2), .IR(EX_IR), .PC(EX_PC),
    .PC_4(id_ex_1_pc_4_2), .LUI_2(EX_MEM_lui_2), .Jal_2(EX_MEM_jal_2), .Jalr_2(EX_MEM_jalr_2),
    .MemToReg_2(EX_MEM_memtoreg_2), .MemWrite_2(MemWrite), .sb_2(EX_MEM_sb_2),
    .RegWrite_2(EX_MEM_regwrite_2), .halt_2(EX_MEM_halt_2), .rd_2(EX_MEM_rd_2), .Result_2(EX_MEM_result_2),
    .WriteData_2(EX_MEM_writedata_2), .IR_2(MEM_IR), .PC_2(M_PC), .PC_4_2(EX_MEM_pc_4_2), .clk(CLK));  // open: en, U, U_2
  Multiplexer #(.select(1), .width(32), .disabled("Z"), .enable("false")) multiplexer_7 (
    .in0(EX_MEM_writedata_2), .in1(multiplexer_8_out), .out(MDin), .sel(EX_MEM_sb_2));
  Multiplexer #(.select(2), .width(32), .disabled("Z"), .enable("false")) multiplexer_8 (
    .in0(or_6_out), .in1(or_7_out), .in2(or_8_out), .in3(or_5_out), .out(multiplexer_8_out),
    .sel(EX_MEM_result_2[1:0]));
  assign or_5_out = shifter_6_out | and_9_out;  // OR_Gate or_5, 32 bits wide
  assign or_6_out = and_12_out | EX_MEM_writedata_2;  // OR_Gate or_6, 32 bits wide
  assign or_7_out = and_11_out | shifter_4_out;  // OR_Gate or_7, 32 bits wide
  assign or_8_out = and_10_out | shifter_5_out;  // OR_Gate or_8, 32 bits wide
  RAM #(.addrWidth(10), .dataWidth(32), .bus("separate"), .Select("high")) ram_1 (
    .addr(EX_MEM_result_2[11:2]), .din(MDin), .data(ram_1_data), .str(MemWrite), .sel(1'b1), .clk(CLK),
    .ld(1'b1));  // open: clr
  assign and_9_out = ram_1_data & 32'hffffff;  // AND_Gate and_9, 32 bits wide
  assign and_10_out = ram_1_data & 32'hff00ffff;  // AND_Gate and_10, 32 bits wide
  assign and_11_out = ram_1_data & 32'hffff00ff;  // AND_Gate and_11, 32 bits wide
  assign and_12_out = ram_1_data & 32'hffffff00;  // AND_Gate and_12, 32 bits wide
  Shifter #(.width(32), .shift("ll")) shifter_4 (.in(EX_MEM_writedata_2), .\dist (5'b01000), .out(shifter_4_out));
  Shifter #(.width(32), .shift("ll")) shifter_5 (.in(EX_MEM_writedata_2), .\dist (5'b10000), .out(shifter_5_out));
  Shifter #(.width(32), .shift("ll")) shifter_6 (.in(EX_MEM_writedata_2), .\dist (5'b11000), .out(shifter_6_out));
  MEM_WB MEM_WB (
    .LUI(EX_MEM_lui_2), .Jal(EX_MEM_jal_2), .Jalr(EX_MEM_jalr_2), .MemToReg(EX_MEM_memtoreg_2),
    .RegWrite(EX_MEM_regwrite_2), .halt(EX_MEM_halt_2), .rd(EX_MEM_rd_2), .ALUResult(EX_MEM_result_2),
    .ReadData(ram_1_data), .IR(MEM_IR), .PC(M_PC), .PC_4(EX_MEM_pc_4_2), .LUI_2(MEM_WB_lui_2),
    .Jal_2(MEM_WB_jal_2), .Jalr_2(MEM_WB_jalr_2), .MemToReg_2(MEM_WB_memtoreg_2), .RegWrite_2(RegWrite),
    .halt_2(MEM_WB_halt_2), .rd_2(WBrd), .ALUResult_2(MEM_WB_aluresult_2), .ReadData_2(MEM_WB_readdata_2),
    .IR_2(WB_IR), .PC_2(WB_PC), .PC_4_2(MEM_WB_pc_4_2), .clk(CLK));  // open: en, U, U_2
  Multiplexer #(.select(2), .width(32), .disabled("Z"), .enable("false")) multiplexer_9 (
    .in0(MEM_WB_aluresult_2), .in1(MEM_WB_readdata_2), .in2(MEM_WB_pc_4_2), .in3(U), .out(RDin),
    .sel(priority_encoder_3_out));
  Priority_Encoder #(.select(2), .disabled("Z")) priority_encoder_3 (
    .in0(1'b1), .in1(MEM_WB_memtoreg_2), .in2(or_9_out), .in3(MEM_WB_lui_2), .out(priority_encoder_3_out));  // open: gs, en_out, en_in
  or or_9 (or_9_out, MEM_WB_jalr_2, MEM_WB_jal_2);
  D_Flip_Flop #(.trigger("rising"), .Pre_Clr_Positions("ABOVE_BELOW"), .NegatePresetClear("false"), .enable("true"), .NewFFLayout("true")) d_ff_2 (
    .clk(MEM_WB_halt_2), .D(1'b1), .Q(halt), .en(1'b1), .reset(Go));  // open: Qn, preset

  // Other names for the same wires on the sheet: rd[4:0] = ID_IR[11:7]; IR[31:0] = IF_IR; MEM_PC[31:0] = M_PC;
  //   PC[31:0] = IF_PC

  // Notes on the sheet:
  //   中断源
  //   时空图监测，可删除
  //   中断等待指示
  //   数码管输出
  //   指令存储器
  //   指令探针
  //   contents of rom_1 (hex, n*v repeats v):
  //   413 493 913 993 46413 14e493 296913 39e993 842023 942223 1242423 1342623 a00893 493 913 993 73
  //   指令字
  //   控制位
  //   流水调试日志用
  //   暂停节拍，不能为0
  //   戳工具置1进入计数暂停模式，ctrl+k时钟自动运行到对应节拍暂停
  //   ctrl+k关闭时钟连续运行，将控制位置零，进入单步调试模式调试
  //   可计数暂停的时钟源
  //   周期计数器
  //   为方便自动评测，需要输出流水线各段保存的PC值，注意是PC不是PC+4，另外ID段寄存器写入信息，Mem段内存写入信息也要输出
  //   数据存储器
endmodule

module \中断按键参考电路  (
  input  \同步清零信号 ,
  output \与中断屏蔽位与 
);

  wire \_1号中断_out , and_1_out, clock_1_out, d_ff_1_q, or_1_out, or_2_out;

  Clock #(.highDuration(1), .lowDuration(1)) clock_1 (.out(clock_1_out));
  Button \_1号中断  (.out(\_1号中断_out ));
  or or_1 (or_1_out, \与中断屏蔽位与 , d_ff_1_q);
  LED #(.active("true")) \_1号中断等待指示灯  (.in(or_1_out));
  D_Flip_Flop #(.trigger("rising"), .Pre_Clr_Positions("LEGACY"), .NegatePresetClear("false"), .enable("true"), .NewFFLayout("false")) d_ff_1 (
    .clk(\_1号中断_out ), .D(1'b1), .Q(d_ff_1_q), .reset(\与中断屏蔽位与 ));  // open: Qn, preset, en
  or or_2 (or_2_out, d_ff_1_q, \与中断屏蔽位与 );
  and and_1 (and_1_out, or_2_out, ~\同步清零信号 );  // AND_Gate
  D_Flip_Flop #(.trigger("rising"), .Pre_Clr_Positions("LEGACY"), .NegatePresetClear("false"), .enable("true"), .NewFFLayout("false")) IR1 (
    .clk(clock_1_out), .D(and_1_out), .Q(\与中断屏蔽位与 ));  // open: Qn, preset, en, reset

  // Notes on the sheet:
  //   中断信号采样参考电路
  //   Reset 
endmodule
module \重定向流水线  (
  output RegWrite,
  output MemWrite,
  output [31:0] IF_PC,
  output [31:0] ID_PC,
  output [31:0] EX_PC,
  output [31:0] M_PC,
  output [31:0] WB_PC,
  output [31:0] RDin,
  output [31:0] MDin,
  output [31:0] LedData
);

  wire Alu_Src, and_1_out, and_2_out, and_3_out, and_4_out, and_5_out, and_6_out, and_7_out, and_8_out,
       and_9_out, and_10_out, and_15_out, and_16_out, and_17_out, and_18_out, and_19_out, Beq, BGEU, Bne,
       BranchSuc, CLK, clock_1_out, comparator_1_eq, comparator_1_lt, comparator_2_eq, d_ff_1_q, E, ecall,
       EX_LUI, EX_MEM_halt_2, EX_MEM_jal_2, EX_MEM_jalr_2, EX_MEM_memtoreg_2, EX_MEM_sb_2, EXRegWrite, flush,
       G, Go, halt, id_ex_1_alusrcb_2, id_ex_1_beq_2, id_ex_1_bgeu_2, id_ex_1_bne_2, id_ex_1_ecall_2,
       id_ex_1_jal_2, id_ex_1_jalr_2, id_ex_1_memtoreg_2, id_ex_1_memwrite_2, id_ex_1_sb_2, IR1, IR2, IR3,
       JAL, JALR, LUI, MEM_LUI, MEM_WB_halt_2, MEM_WB_jal_2, MEM_WB_jalr_2, MEM_WB_lui_2, MEM_WB_memtoreg_2,
       MemRegWrite, MemToReg, nand_1_out, not_1_out, not_2_out, not_3_out, not_4_out, not_5_out, not_6_out,
       or_1_out, or_2_out, or_3_out, or_5_out, or_6_out, or_7_out, or_13_out, or_14_out, RST, S, S_type, sb,
       stall, URET, W1, W2, W3, \单周期硬布线控制器_1_memwrite , \单周期硬布线控制器_1_regwrite , \单周期硬布线控制器_1_rs1 ,
       \单周期硬布线控制器_1_rs2 , \无条件跳转 ;
  wire [1:0] priority_encoder_1_out, priority_encoder_2_out, priority_encoder_3_out, RSFL, RSFR, RTFL, RTFR;
  wire [3:0] ALUOP, id_ex_1_aluop_2;
  wire [4:0] EXrd, MEMrd, multiplexer_2_out, multiplexer_3_out, WBrd;
  wire [12:0] CNT_num;
  wire [15:0] \LoadUse次数 , \总周期数 , \插入气泡数 , \无条件分支数 , \条件分支成功数 ;
  wire [31:0] ALUResult, and_11_out, and_12_out, and_13_out, and_14_out, B, bit_extender_1_out,
       bit_extender_2_out, bit_extender_3_out, bit_extender_4_out, bit_extender_5_out, EX_IR, EX_MEM_pc_4_2,
       EX_MEM_writedata_2, id_ex_1_imm_1_2, id_ex_1_imm_2_2, id_ex_1_pc_4_2, id_ex_1_r1_2, id_ex_1_r2_2,
       ID_IR, IF_ID_pc_4_2, IF_IR, J, MEM_IR, MEM_WB_aluresult_2, MEM_WB_pc_4_2, MEM_WB_readdata_2,
       MEM_WB_u_2, MEMAL, MU, multiplexer_1_out, multiplexer_4_out, multiplexer_5_out, multiplexer_6_out,
       multiplexer_7_out, multiplexer_8_out, multiplexer_10_out, or_9_out, or_10_out, or_11_out, or_12_out,
       PC_4, ram_1_data, regifile_1_r1, regifile_1_r2, shifter_1_out, shifter_2_out, shifter_4_out,
       shifter_5_out, shifter_6_out, U, WB_IR;

  Button \u_总复位  (.out(RST));
  Button _1 (.out(IR1));
  Button _2 (.out(IR2));
  Button _3 (.out(IR3));
  // Probe on \总周期数 
  // Probe on \总周期数 
  Button \u_继续运行  (.out(Go));
  LED #(.active("true")) led_1 (.in(W1));
  LED #(.active("true")) led_2 (.in(W2));
  LED #(.active("true")) led_3 (.in(W3));
  Hex_Digit_Display hex_digit_display_1 (.value(LedData[31:28]));  // open: dp
  // Probe on IF_PC[19:0]
  // RiscV_Probe riscv_probe_1: pin names not known; wires that end beside it: IF_IR
  Hex_Digit_Display hex_digit_display_2 (.value(LedData[27:24]));  // open: dp
  Hex_Digit_Display hex_digit_display_3 (.value(LedData[23:20]));  // open: dp
  // Probe on ID_PC[19:0]
  // RiscV_Probe riscv_probe_2: pin names not known; wires that end beside it: ID_IR
  Multiplexer #(.select(2), .width(32), .disabled("Z"), .enable("false")) multiplexer_1 (
    .in0(PC_4), .in1(ALUResult), .in2(B), .in3(J), .out(multiplexer_1_out), .sel(priority_encoder_1_out));
  and and_1 (and_1_out, not_1_out, or_1_out);
  or or_1 (or_1_out, not_2_out, Go);
  not not_1 (not_1_out, stall);
  not not_2 (not_2_out, halt);
  Hex_Digit_Display hex_digit_display_4 (.value(LedData[19:16]));  // open: dp
  Hex_Digit_Display hex_digit_display_5 (.value(LedData[15:12]));  // open: dp
  Register #(.width(32), .trigger("rising"), .Select("low")) PC (
    .D(multiplexer_1_out), .en(and_1_out), .Q(IF_PC), .clk(CLK), .clr(RST));
  Hex_Digit_Display hex_digit_display_6 (.value(LedData[7:4]));  // open: dp
  Hex_Digit_Display hex_digit_display_7 (.value(LedData[11:8]));  // open: dp
  // Probe on EX_PC[19:0]
  // RiscV_Probe riscv_probe_3: pin names not known; wires that end beside it: EX_IR
  Adder #(.width(32)) adder_1 (.a(IF_PC), .b(32'h4), .out(PC_4));  // open: cin, cout
  Hex_Digit_Display hex_digit_display_8 (.value(LedData[3:0]));  // open: dp
  // Probe on \总周期数 
  // Probe on M_PC[19:0]
  // RiscV_Probe riscv_probe_4: pin names not known; wires that end beside it: MEM_IR
  // RiscV_Probe riscv_probe_5: pin names not known; wires that end beside it: IF_IR
  ROM #(.addrWidth(10), .dataWidth(32), .Select("high")) rom_1 (.addr(IF_PC[11:2]), .data(IF_IR));
  and and_2 (and_2_out, ~stall, or_3_out);  // AND_Gate
  // Probe on \总周期数 
  // Probe on \无条件分支数 
  // Probe on \条件分支成功数 
  // Probe on \插入气泡数 
  // Probe on \LoadUse次数 
  or or_2 (or_2_out, priority_encoder_1_out[1], priority_encoder_1_out[0]);
  or or_3 (or_3_out, ~halt, Go);  // OR_Gate
  // Probe on IF_PC[11:0]
  // Probe on WB_PC[19:0]
  // RiscV_Probe riscv_probe_6: pin names not known; wires that end beside it: WB_IR
  IF_ID IF_ID (
    .IR(IF_IR), .PC(IF_PC), .PC_4(PC_4), .IR_2(ID_IR), .PC_2(ID_PC), .PC_4_2(IF_ID_pc_4_2),
    .branch(or_2_out), .CLK(CLK), .EN(and_2_out));  // open: IF_PredictJump, ID_PredictJump
  // Probe on ID_PC[11:0]
  // Probe on EX_PC[11:0]
  \重定向电路  \u_重定向电路  (
    .RS1_used(\单周期硬布线控制器_1_rs1 ), .EX_RegWrite(EXRegWrite), .EX_MemToReg(id_ex_1_memtoreg_2), .IR(ID_IR),
    .RS2_used(\单周期硬布线控制器_1_rs2 ), .MEM_RegWrite(MemRegWrite), .EX_rd(EXrd), .Ecall(ecall),
    .BranchTaken(or_2_out), .MEM_rd(MEMrd), .Stall(stall), .Flush(flush), .RS1_Forward(RSFL),
    .RS2_Forward(RTFL), .EX_LUI(EX_LUI), .MEM_LUI(MEM_LUI));
  // Probe on M_PC[11:0]
  D_Flip_Flop #(.trigger("high"), .Pre_Clr_Positions("LEGACY"), .NegatePresetClear("false"), .enable("true"), .NewFFLayout("false")) d_ff_1 (.Q(d_ff_1_q));  // open: clk, D, Qn, preset, en, reset
  // Probe on 13'hc
  \单周期硬布线控制器  \u_单周期硬布线控制器_1  (
    .Funct({ID_IR[30], ID_IR[25], ID_IR[14:12]}), .OP(ID_IR[6:2]), .ALU_OP(ALUOP), .MemToReg(MemToReg),
    .MemWrite(\单周期硬布线控制器_1_memwrite ), .ALU_SRC(Alu_Src), .RegWrite(\单周期硬布线控制器_1_regwrite ), .ecall(ecall),
    .S_type(S_type), .Jalr(JALR), .Beq(Beq), .JAL(JAL), .Bne(Bne), .in_3(ID_IR[21]), .uret(URET), .LUI(LUI),
    .sb(sb), .BGEU(BGEU), .rs1(\单周期硬布线控制器_1_rs1 ), .rs2(\单周期硬布线控制器_1_rs2 ));  // open: CSR
  Multiplexer #(.select(1), .width(5), .disabled("Z"), .enable("false")) multiplexer_2 (
    .in0(ID_IR[19:15]), .in1(5'b10001), .out(multiplexer_2_out), .sel(ecall));
  Multiplexer #(.select(1), .width(5), .disabled("Z"), .enable("false")) multiplexer_3 (
    .in0(ID_IR[24:20]), .in1(5'b01010), .out(multiplexer_3_out), .sel(ecall));
  assign bit_extender_1_out = {{12{ID_IR[31]}}, ID_IR[31:12]};  // Bit_Extender bit_extender_1
  // Probe on WB_PC[11:0]
  Comparator #(.width(13), .mode("twosComplement")) comparator_1 (
    .a(CNT_num), .b(13'hc), .eq(comparator_1_eq), .lt(comparator_1_lt));  // open: gt
  Clock #(.highDuration(1), .lowDuration(1)) clock_1 (.out(clock_1_out));
  assign bit_extender_2_out = {{20{ID_IR[31]}}, ID_IR[31:20]};  // Bit_Extender bit_extender_2
  assign bit_extender_3_out = {{20{ID_IR[31]}}, {ID_IR[31:25], ID_IR[11:7]}};  // Bit_Extender bit_extender_3
  assign bit_extender_4_out = {{20{ID_IR[31]}}, {ID_IR[31], ID_IR[7], ID_IR[30:25], ID_IR[11:8]}};  // Bit_Extender bit_extender_4
  assign bit_extender_5_out = {{12{ID_IR[31]}}, {ID_IR[31], ID_IR[19:12], ID_IR[20], ID_IR[30:21]}};  // Bit_Extender bit_extender_5
  nand nand_1 (nand_1_out, d_ff_1_q, comparator_1_eq);
  Counter #(.width(13), .max('h1fff), .ongoal("stay"), .trigger("rising"), .behavior("old")) counter_1 (
    .count(comparator_1_lt), .Q(CNT_num), .clk(clock_1_out));  // open: load, D, carry, clr, preset
  not not_3 (not_3_out, CLK);
  Multiplexer #(.select(1), .width(32), .disabled("Z"), .enable("false")) multiplexer_4 (
    .in0(bit_extender_2_out), .in1(bit_extender_3_out), .out(multiplexer_4_out), .sel(S_type));
  assign CLK = nand_1_out ? clock_1_out : 1'bz;  // Controlled_Buffer controlled_buffer_1
  Priority_Encoder #(.select(2), .disabled("Z")) priority_encoder_1 (
    .in0(1'b1), .in1(id_ex_1_jalr_2), .in2(BranchSuc), .in3(id_ex_1_jal_2), .out(priority_encoder_1_out));  // open: gs, en_out, en_in
  Regifile regifile_1 (
    .Din(RDin), .Clk(not_3_out), .R1(regifile_1_r1), .R2(regifile_1_r2), .WE(RegWrite), .W_num(WBrd),
    .R1_num(multiplexer_2_out), .R2_num(multiplexer_3_out));
  // RiscV_Probe riscv_probe_7: pin names not known; wires that end beside it: ID_IR
  Pull_Resistor #(.pull(1)) pull_resistor_1 (.node(CLK));
  or or_4 (BranchSuc, and_3_out, and_4_out, and_5_out);
  Multiplexer #(.select(2), .width(32), .disabled("Z"), .enable("false")) multiplexer_5 (
    .in0(bit_extender_4_out), .in1(bit_extender_4_out), .in2(bit_extender_5_out), .in3(bit_extender_1_out),
    .out(multiplexer_5_out), .sel(priority_encoder_2_out));
  Priority_Encoder #(.select(2), .disabled("Z")) priority_encoder_2 (
    .in0(1'b1), .in1(or_5_out), .in2(JAL), .in3(LUI), .out(priority_encoder_2_out));  // open: gs, en_out, en_in
  or or_5 (or_5_out, and_6_out, and_7_out, and_8_out);
  and and_3 (and_3_out, id_ex_1_bgeu_2, G);
  and and_4 (and_4_out, id_ex_1_beq_2, E);
  not not_4 (not_4_out, E);
  and and_5 (and_5_out, not_4_out, id_ex_1_bne_2);
  and and_6 (and_6_out, BGEU, G);
  and and_7 (and_7_out, Beq, E);
  and and_8 (and_8_out, not_5_out, Bne);
  ID_EX id_ex_1 (
    .Beq(Beq), .Beq_2(id_ex_1_beq_2), .Bne(Bne), .Bne_2(id_ex_1_bne_2), .MemToReg(MemToReg),
    .MemToReg_2(id_ex_1_memtoreg_2), .MemWrite(\单周期硬布线控制器_1_memwrite ), .MemWrite_2(id_ex_1_memwrite_2),
    .AluSrcB(Alu_Src), .AluSrcB_2(id_ex_1_alusrcb_2), .RegWrite(\单周期硬布线控制器_1_regwrite ),
    .RegWrite_2(EXRegWrite), .ecall(ecall), .ecall_2(id_ex_1_ecall_2), .Jal(JAL), .Jal_2(id_ex_1_jal_2),
    .Jalr(JALR), .Jalr_2(id_ex_1_jalr_2), .BGEU(BGEU), .BGEU_2(id_ex_1_bgeu_2), .Uret(URET), .AluOP(ALUOP),
    .AluOP_2(id_ex_1_aluop_2), .rd(ID_IR[11:7]), .rd_2(EXrd), .R1(regifile_1_r1), .R1_2(id_ex_1_r1_2),
    .R2(regifile_1_r2), .R2_2(id_ex_1_r2_2), .imm_1(multiplexer_4_out), .imm_1_2(id_ex_1_imm_1_2),
    .imm_2(multiplexer_5_out), .imm_2_2(id_ex_1_imm_2_2), .PC(ID_PC), .PC_2(EX_PC), .PC_4(IF_ID_pc_4_2),
    .PC_4_2(id_ex_1_pc_4_2), .IR(ID_IR), .IR_2(EX_IR), .RS1_Forward(RSFL), .RS1_Forward_2(RSFR),
    .RS2_Forward(RTFL), .RS2_Forward_2(RTFR), .en(or_6_out), .clk(CLK), .flush(flush), .sb(sb),
    .sb_2(id_ex_1_sb_2), .LUI(LUI), .LUI_2(EX_LUI));  // open: Uret_2, ID_PredictJump, EX_PredictJump
  or or_6 (or_6_out, ~halt, Go);  // OR_Gate
  not not_5 (not_5_out, E);
  Multiplexer #(.select(2), .width(32), .disabled("Z"), .enable("false")) multiplexer_6 (
    .in0(id_ex_1_r1_2), .in1(RDin), .in2(MEMAL), .out(multiplexer_6_out), .sel(RSFR));  // open: in3
  Multiplexer #(.select(2), .width(32), .disabled("Z"), .enable("false")) multiplexer_7 (
    .in0(id_ex_1_r2_2), .in1(RDin), .in2(MEMAL), .out(multiplexer_7_out), .sel(RTFR));  // open: in3
  Comparator #(.width(32), .mode("twosComplement")) comparator_2 (
    .a(multiplexer_6_out), .b(32'h22), .eq(comparator_2_eq));  // open: gt, lt
  not not_6 (not_6_out, comparator_2_eq);
  and and_9 (and_9_out, id_ex_1_ecall_2, not_6_out);
  Multiplexer #(.select(1), .width(32), .disabled("Z"), .enable("false")) multiplexer_8 (
    .in0(multiplexer_7_out), .in1(id_ex_1_imm_1_2), .out(multiplexer_8_out), .sel(id_ex_1_alusrcb_2));
  // RiscV_Probe riscv_probe_8: pin names not known; wires that end beside it: EX_IR
  Adder #(.width(32)) adder_2 (.a(EX_PC), .b(shifter_1_out), .out(B));  // open: cin, cout
  Shifter #(.width(32), .shift("ll")) shifter_1 (.in(id_ex_1_imm_2_2), .\dist (5'b00001), .out(shifter_1_out));
  Adder #(.width(32)) adder_3 (.a(EX_PC), .b(shifter_2_out), .out(J));  // open: cin, cout
  Shifter #(.width(32), .shift("ll")) shifter_2 (.in(id_ex_1_imm_2_2), .\dist (5'b00001), .out(shifter_2_out));
  Shifter #(.width(32), .shift("ll")) shifter_3 (.in(id_ex_1_imm_2_2), .\dist (5'b01100), .out(U));
  and and_10 (and_10_out, comparator_2_eq, id_ex_1_ecall_2);
  ALU alu_1 (
    .X(multiplexer_6_out), .Y(multiplexer_8_out), .AluOP(id_ex_1_aluop_2), .Equal(E), .Result(ALUResult),
    .out_4(G), .out_6(S));  // open: Result_2
  Register #(.width(32), .trigger("rising"), .Select("low")) register_1 (
    .D(multiplexer_7_out), .en(and_10_out), .Q(LedData), .clk(CLK));  // open: clr
  or or_7 (or_7_out, ~halt, Go);  // OR_Gate
  EX_MEM EX_MEM (
    .LUI(EX_LUI), .Jal(id_ex_1_jal_2), .Jalr(id_ex_1_jalr_2), .MemToReg(id_ex_1_memtoreg_2),
    .MemWrite(id_ex_1_memwrite_2), .sb(id_ex_1_sb_2), .RegWrite(EXRegWrite), .halt(and_9_out), .rd(EXrd),
    .Result(ALUResult), .WriteData(multiplexer_7_out), .IR(EX_IR), .PC(EX_PC), .PC_4(id_ex_1_pc_4_2),
    .LUI_2(MEM_LUI), .Jal_2(EX_MEM_jal_2), .Jalr_2(EX_MEM_jalr_2), .MemToReg_2(EX_MEM_memtoreg_2),
    .MemWrite_2(MemWrite), .sb_2(EX_MEM_sb_2), .RegWrite_2(MemRegWrite), .halt_2(EX_MEM_halt_2),
    .rd_2(MEMrd), .Result_2(MEMAL), .WriteData_2(EX_MEM_writedata_2), .IR_2(MEM_IR), .PC_2(M_PC),
    .PC_4_2(EX_MEM_pc_4_2), .clk(CLK), .en(or_7_out), .U(U), .U_2(MU));
  or or_8 (\无条件跳转 , id_ex_1_jal_2, id_ex_1_jalr_2);
  Multiplexer #(.select(1), .width(32), .disabled("Z"), .enable("false")) multiplexer_9 (
    .in0(EX_MEM_writedata_2), .in1(multiplexer_10_out), .out(MDin), .sel(EX_MEM_sb_2));
  Multiplexer #(.select(2), .width(32), .disabled("Z"), .enable("false")) multiplexer_10 (
    .in0(or_10_out), .in1(or_11_out), .in2(or_12_out), .in3(or_9_out), .out(multiplexer_10_out),
    .sel(MEMAL[1:0]));
  assign or_9_out = shifter_6_out | and_11_out;  // OR_Gate or_9, 32 bits wide
  // RiscV_Probe riscv_probe_9: pin names not known; wires that end beside it: MEM_IR
  assign or_10_out = and_14_out | EX_MEM_writedata_2;  // OR_Gate or_10, 32 bits wide
  assign or_11_out = and_13_out | shifter_4_out;  // OR_Gate or_11, 32 bits wide
  assign or_12_out = and_12_out | shifter_5_out;  // OR_Gate or_12, 32 bits wide
  RAM #(.addrWidth(10), .dataWidth(32), .bus("separate"), .Select("high")) ram_1 (
    .addr(MEMAL[11:2]), .din(MDin), .data(ram_1_data), .str(MemWrite), .sel(1'b1), .clk(CLK), .ld(1'b1));  // open: clr
  assign and_11_out = ram_1_data & 32'hffffff;  // AND_Gate and_11, 32 bits wide
  assign and_12_out = ram_1_data & 32'hff00ffff;  // AND_Gate and_12, 32 bits wide
  assign and_13_out = ram_1_data & 32'hffff00ff;  // AND_Gate and_13, 32 bits wide
  assign and_14_out = ram_1_data & 32'hffffff00;  // AND_Gate and_14, 32 bits wide
  Counter #(.width(16), .max('hffff), .ongoal("wrap"), .trigger("rising"), .behavior("new")) counter_2 (
    .count(BranchSuc), .Q(\条件分支成功数 ), .clk(and_15_out));  // open: load, D, carry, clr, preset, down
  and and_15 (and_15_out, ~halt, CLK);  // AND_Gate
  Counter #(.width(16), .max('hffff), .ongoal("wrap"), .trigger("rising"), .behavior("new")) counter_3 (
    .count(flush), .Q(\插入气泡数 ), .clk(and_16_out));  // open: load, D, carry, clr, preset, down
  and and_16 (and_16_out, ~halt, CLK);  // AND_Gate
  Shifter #(.width(32), .shift("ll")) shifter_4 (.in(EX_MEM_writedata_2), .\dist (5'b01000), .out(shifter_4_out));
  Shifter #(.width(32), .shift("ll")) shifter_5 (.in(EX_MEM_writedata_2), .\dist (5'b10000), .out(shifter_5_out));
  Shifter #(.width(32), .shift("ll")) shifter_6 (.in(EX_MEM_writedata_2), .\dist (5'b11000), .out(shifter_6_out));
  or or_13 (or_13_out, ~halt, Go);  // OR_Gate
  Counter #(.width(16), .max('hffff), .ongoal("wrap"), .trigger("rising"), .behavior("new")) counter_4 (
    .count(\无条件跳转 ), .Q(\无条件分支数 ), .clk(and_17_out));  // open: load, D, carry, clr, preset, down
  and and_17 (and_17_out, ~halt, CLK);  // AND_Gate
  Counter #(.width(16), .max('hffff), .ongoal("wrap"), .trigger("rising"), .behavior("new")) counter_5 (
    .count(CLK), .Q(\总周期数 ), .clk(and_18_out));  // open: load, D, carry, clr, preset, down
  and and_18 (and_18_out, ~halt, CLK);  // AND_Gate
  MEM_WB MEM_WB (
    .LUI(MEM_LUI), .Jal(EX_MEM_jal_2), .Jalr(EX_MEM_jalr_2), .MemToReg(EX_MEM_memtoreg_2),
    .RegWrite(MemRegWrite), .halt(EX_MEM_halt_2), .rd(MEMrd), .ALUResult(MEMAL), .ReadData(ram_1_data),
    .IR(MEM_IR), .PC(M_PC), .PC_4(EX_MEM_pc_4_2), .LUI_2(MEM_WB_lui_2), .Jal_2(MEM_WB_jal_2),
    .Jalr_2(MEM_WB_jalr_2), .MemToReg_2(MEM_WB_memtoreg_2), .RegWrite_2(RegWrite), .halt_2(MEM_WB_halt_2),
    .rd_2(WBrd), .ALUResult_2(MEM_WB_aluresult_2), .ReadData_2(MEM_WB_readdata_2), .IR_2(WB_IR),
    .PC_2(WB_PC), .PC_4_2(MEM_WB_pc_4_2), .clk(CLK), .en(or_13_out), .U(MU), .U_2(MEM_WB_u_2));
  Counter #(.width(16), .max('hffff), .ongoal("wrap"), .trigger("rising"), .behavior("new")) counter_6 (
    .count(stall), .Q(\LoadUse次数 ), .clk(and_19_out));  // open: load, D, carry, clr, preset, down
  and and_19 (and_19_out, ~halt, CLK);  // AND_Gate
  Multiplexer #(.select(2), .width(32), .disabled("Z"), .enable("false")) multiplexer_11 (
    .in0(MEM_WB_aluresult_2), .in1(MEM_WB_readdata_2), .in2(MEM_WB_pc_4_2), .in3(MEM_WB_u_2), .out(RDin),
    .sel(priority_encoder_3_out));
  Priority_Encoder #(.select(2), .disabled("Z")) priority_encoder_3 (
    .in0(1'b1), .in1(MEM_WB_memtoreg_2), .in2(or_14_out), .in3(MEM_WB_lui_2), .out(priority_encoder_3_out));  // open: gs, en_out, en_in
  // RiscV_Probe riscv_probe_10: pin names not known; wires that end beside it: WB_IR
  or or_14 (or_14_out, MEM_WB_jalr_2, MEM_WB_jal_2);
  D_Flip_Flop #(.trigger("rising"), .Pre_Clr_Positions("ABOVE_BELOW"), .NegatePresetClear("false"), .enable("true"), .NewFFLayout("true")) d_ff_2 (
    .clk(MEM_WB_halt_2), .D(1'b1), .Q(halt), .en(1'b1), .reset(Go));  // open: Qn, preset

  // Other names for the same wires on the sheet: rd[4:0] = ID_IR[11:7]; IR[31:0] = IF_IR; MEM_PC[31:0] = M_PC;
  //   PC[31:0] = IF_PC

  // Notes on the sheet:
  //   中断源
  //   时空图监测，可删除
  //   中断等待指示
  //   数码管输出
  //   指令存储器
  //   指令探针
  //   contents of rom_1 (hex, n*v repeats v):
  //   100493 100006f 100493 200913 300993 100006f 100493 200913 300993 100006f 100493 200913 300993
  //   100006f 100493 200913 300993 3b4000ef 100413 100493 1f49493 900533 2200893 73 24d493 48463 fedff06f
  //   900533 2200893 73 100493 249493 900533 2200893 73 48463 fedff06f 100493 1f49493 900533 2200893 73
  //   4034d493 900533 2200893 73 4044d493 900533 2200893 73 4044d493 900533 2200893 73 4044d493 900533
  //   2200893 73 4044d493 900533 2200893 73 4044d493 900533 2200893 73 4044d493 900533 2200893 73 4044d493
  //   900533 2200893 73 100413 1f41993 41f9d993 433 c00913 300b13 140413 f47413 800293 100313 499993
  //   89e9b3 1300533 2200893 73 406282b3 fe0294e3 140413 f00f93 1f47433 1c41413 800293 100313 49d993
  //   89e9b3 1300533 2200893 73 406282b3 fe0294e3 1c45413 406b0b33 b0463 f95ff06f 2b3 fff2c293 829293
  //   ff2e293 500533 2200893 73 fff00413 493 84a023 140413 448493 84a023 140413 448493 84a023 140413
  //   448493 84a023 140413 448493 84a023 140413 448493 84a023 140413 448493 84a023 140413 448493 84a023
  //   140413 448493 84a023 140413 448493 84a023 140413 448493 84a023 140413 448493 84a023 140413 448493
  //   84a023 140413 448493 84a023 140413 448493 84a023 140413 448493 84a023 140413 448493 140413 433
  //   3c00493 42983 4aa03 149a2b3 28663 134a023 1442023 ffc48493 fe9412e3 800533 2200893 73 440413 3c00493
  //   fc9416e3 a00893 73 fff00293 7700493 849493 7748493 900533 2200893 73 1000e13 54c4b3 900533 2200893
  //   73 fffe0e13 fe0e16e3 a00893 73 800e13 fedc04b7 fff00413 1045413 84e4b3 900533 2200893 73 ba984b7
  //   900533 73 76544b7 900533 73 32104b7 900533 73 fffe0e13 fa0e1ee3 a00893 73 313 2000e13 493 100913
  //   930023 900533 2200893 73 12484b3 130313 fffe0e13 fe0e12e3 800e13 313 32483 900533 2200893 73 430313
  //   fffe0e13 fe0e14e3 a00893 73 f00493 100913 409909b3 900533 2200893 73 fff48493 ff29f6e3 a00893 73 413
  //   140413 800533 2200893 73 240413 800533 2200893 73 340413 800533 2200893 73 440413 800533 2200893 73
  //   540413 800533 2200893 73 640413 800533 2200893 73 740413 800533 2200893 73 840413 800533 2200893
  //   2200893 73 8067
  //   指令字
  //   控制位
  //   流水调试日志用
  //   暂停节拍，不能为0
  //   戳工具置1进入计数暂停模式，ctrl+k时钟自动运行到对应节拍暂停
  //   ctrl+k关闭时钟连续运行，将控制位置零，进入单步调试模式调试
  //   可计数暂停的时钟源
  //   为方便自动评测，需要输出流水线各段保存的PC值，注意是PC不是PC+4，另外ID段寄存器写入信息，Mem段内存写入信息也要输出
  //   指令探针
  //   数据存储器
  //   指令探针
  //   指令探针
endmodule

module \单周期_单级中断  (
  input  IR1,
  input  IR2,
  input  IR3,
  output RegWrite,
  output MemWrite,
  output [31:0] PC,
  output [31:0] IR,
  output [31:0] RDin,
  output [31:0] MDin,
  output [31:0] LedData
);

  wire Alu_Src, and_1_out, and_2_out, and_3_out, and_4_out, and_5_out, and_6_out, and_9_out, AUIPC, Beq,
       BGEU, Bne, CLK, clock_1_out, comparator_1_eq, comparator_2_eq, comparator_3_eq, comparator_4_eq,
       comparator_5_eq, comparator_6_eq, comparator_7_eq, comparator_7_lt, d_ff_1_q, d_ff_2_q, d_ff_3_q,
       d_ff_4_q, E, ecall, G, Go, halt, IE, Interrupt, IR1_Reset, IR1_t, IR2_2_q, IR2_q, IR2_Reset, IR2_t,
       IR3_q, IR3_Reset, IR3_t, IRA, IRB, IRC, JAL, JALR, MemToReg, nand_1_out, not_1_out, not_2_out,
       not_3_out, not_4_out, not_5_out, or_4_out, or_5_out, or_6_out, or_7_out, or_8_out, or_13_out,
       or_17_out, priority_encoder_2_gs, RST, S, S_type, sb, URET, W1, W2, W3;
  wire [1:0] IR_id, priority_encoder_1_out, priority_encoder_3_out, register_2_q;
  wire [3:0] \单周期硬布线控制器_1_alu_op ;
  wire [4:0] multiplexer_3_out, multiplexer_4_out;
  wire [12:0] CNT_num;
  wire [15:0] \总周期数 ;
  wire [31:0] ALUResult, and_10_out, and_11_out, and_12_out, and_13_out, B, bit_extender_1_out,
       bit_extender_2_out, bit_extender_3_out, bit_extender_4_out, bit_extender_5_out, EPC, J,
       multiplexer_2_out, multiplexer_5_out, multiplexer_7_out, multiplexer_8_out, multiplexer_9_out,
       multiplexer_10_out, or_12_out, or_14_out, or_15_out, or_16_out, PC_4, PC_Next, PC_Ori, ram_1_data,
       regifile_1_r1, shifter_1_out, shifter_2_out, shifter_3_out, shifter_4_out, shifter_5_out,
       shifter_6_out, U;

  Button \u_继续运行  (.out(Go));
  Button _1 ();  // open: out
  Button _2 ();  // open: out
  Button _3 ();  // open: out
  LED #(.active("true")) led_1 (.in(W1));
  LED #(.active("true")) led_2 (.in(W2));
  LED #(.active("true")) led_3 (.in(W3));
  LED #(.active("true")) \_1号中断等待指示灯  (.in(W1));
  LED #(.active("true")) \_2号中断等待指示灯  (.in(W2));
  LED #(.active("true")) \_3号中断等待指示灯  (.in(W3));
  Hex_Digit_Display hex_digit_display_1 (.value(LedData[31:28]));  // open: dp
  Comparator #(.width(16), .mode("twosComplement")) comparator_1 (
    .a(16'h23b), .b(\总周期数 ), .eq(comparator_1_eq));  // open: gt, lt
  Comparator #(.width(16), .mode("twosComplement")) comparator_2 (
    .a(\总周期数 ), .b(16'h1), .eq(comparator_2_eq));  // open: gt, lt
  Comparator #(.width(16), .mode("twosComplement")) comparator_3 (
    .a(\总周期数 ), .b(16'h4), .eq(comparator_3_eq));  // open: gt, lt
  Comparator #(.width(16), .mode("twosComplement")) comparator_4 (
    .a(\总周期数 ), .b(16'h7), .eq(comparator_4_eq));  // open: gt, lt
  or or_1 (W1, IR2_q, d_ff_1_q);
  or or_2 (W2, IR2_2_q, d_ff_2_q);
  or or_3 (W3, IR3_q, d_ff_3_q);
  Hex_Digit_Display hex_digit_display_2 (.value(LedData[27:24]));  // open: dp
  Hex_Digit_Display hex_digit_display_3 (.value(LedData[23:20]));  // open: dp
  or or_4 (or_4_out, comparator_1_eq, comparator_2_eq);
  assign IRA = or_4_out ? ~CLK : 1'bz;  // Controlled_Inverter controlled_inverter_1
  assign IRB = comparator_3_eq ? ~CLK : 1'bz;  // Controlled_Inverter controlled_inverter_2
  assign IRC = comparator_4_eq ? ~CLK : 1'bz;  // Controlled_Inverter controlled_inverter_3
  D_Flip_Flop #(.trigger("rising"), .Pre_Clr_Positions("LEGACY"), .NegatePresetClear("false"), .enable("true"), .NewFFLayout("false")) d_ff_1 (
    .clk(IR1_t), .D(1'b1), .Q(d_ff_1_q), .reset(IR2_q));  // open: Qn, preset, en
  D_Flip_Flop #(.trigger("rising"), .Pre_Clr_Positions("LEGACY"), .NegatePresetClear("false"), .enable("true"), .NewFFLayout("false")) d_ff_2 (
    .clk(IR2_t), .D(1'b1), .Q(d_ff_2_q), .reset(IR2_2_q));  // open: Qn, preset, en
  D_Flip_Flop #(.trigger("rising"), .Pre_Clr_Positions("LEGACY"), .NegatePresetClear("false"), .enable("true"), .NewFFLayout("false")) d_ff_3 (
    .clk(IR3_t), .D(1'b1), .Q(d_ff_3_q), .reset(IR3_q));  // open: Qn, preset, en
  Hex_Digit_Display hex_digit_display_4 (.value(LedData[19:16]));  // open: dp
  Hex_Digit_Display hex_digit_display_5 (.value(LedData[15:12]));  // open: dp
  Pull_Resistor #(.pull(0)) pull_resistor_1 (.node(IRA));
  Pull_Resistor #(.pull(0)) pull_resistor_2 (.node(IRB));
  Pull_Resistor #(.pull(0)) pull_resistor_3 (.node(IRC));
  or or_5 (or_5_out, d_ff_1_q, IR2_q);
  or or_6 (or_6_out, d_ff_2_q, IR2_2_q);
  or or_7 (or_7_out, d_ff_3_q, IR3_q);
  Hex_Digit_Display hex_digit_display_6 (.value(LedData[7:4]));  // open: dp
  Hex_Digit_Display hex_digit_display_7 (.value(LedData[11:8]));  // open: dp
  // Probe on \总周期数 
  Priority_Encoder #(.select(2), .disabled("Z")) priority_encoder_1 (
    .in0(1'b1), .in1(JALR), .in2(or_8_out), .in3(JAL), .out(priority_encoder_1_out));  // open: gs, en_out, en_in
  Multiplexer #(.select(2), .width(32), .disabled("Z"), .enable("false")) multiplexer_1 (
    .in0(PC_4), .in1(ALUResult), .in2(B), .in3(J), .out(PC_Ori), .sel(priority_encoder_1_out));
  not not_1 (not_1_out, halt);
  and and_1 (and_1_out, or_5_out, ~IR1_Reset);  // AND_Gate
  and and_2 (and_2_out, or_6_out, ~IR2_Reset);  // AND_Gate
  and and_3 (and_3_out, or_7_out, ~IR3_Reset);  // AND_Gate
  Hex_Digit_Display hex_digit_display_8 (.value(LedData[3:0]));  // open: dp
  or or_8 (or_8_out, and_4_out, and_5_out, and_6_out);
  Register #(.width(32), .trigger("rising"), .Select("low")) u_PC (
    .D(PC_Next), .en(not_1_out), .Q(PC), .clk(CLK), .clr(RST));
  D_Flip_Flop #(.trigger("rising"), .Pre_Clr_Positions("LEGACY"), .NegatePresetClear("false"), .enable("true"), .NewFFLayout("false")) u_IR2 (
    .clk(CLK), .D(and_1_out), .Q(IR2_q), .reset(RST));  // open: Qn, preset, en
  D_Flip_Flop #(.trigger("rising"), .Pre_Clr_Positions("LEGACY"), .NegatePresetClear("false"), .enable("true"), .NewFFLayout("false")) IR2_2 (
    .clk(CLK), .D(and_2_out), .Q(IR2_2_q), .reset(RST));  // open: Qn, preset, en
  D_Flip_Flop #(.trigger("rising"), .Pre_Clr_Positions("LEGACY"), .NegatePresetClear("false"), .enable("true"), .NewFFLayout("false")) u_IR3 (
    .clk(CLK), .D(and_3_out), .Q(IR3_q), .reset(RST));  // open: Qn, preset, en
  and and_4 (and_4_out, BGEU, G);
  and and_5 (and_5_out, Beq, E);
  not not_2 (not_2_out, E);
  and and_6 (and_6_out, not_2_out, Bne);
  Adder #(.width(32)) adder_1 (.a(PC), .b(32'h4), .out(PC_4));  // open: cin, cout
  not not_3 (not_3_out, halt);
  Counter #(.width(16), .max('hffff), .ongoal("wrap"), .trigger("rising"), .behavior("new")) counter_1 (
    .count(not_3_out), .Q(\总周期数 ), .clk(CLK));  // open: load, D, carry, clr, preset, down
  Priority_Encoder #(.select(2), .disabled("Z")) priority_encoder_2 (
    .in1(IR2_q), .in2(IR2_2_q), .in3(IR3_q), .out(IR_id), .gs(priority_encoder_2_gs));  // open: in0, en_out, en_in
  or or_9 (IR1_t, IR1, IRA);
  // RiscV_Probe riscv_probe_1: pin names not known; wires that end beside it: IR
  and and_7 (Interrupt, priority_encoder_2_gs, IE);
  or or_10 (IR2_t, IR2, IRB);
  ROM #(.addrWidth(10), .dataWidth(32), .Select("high")) rom_1 (.addr(PC[11:2]), .data(IR));
  Multiplexer #(.select(2), .width(32), .disabled("Z"), .enable("false")) multiplexer_2 (
    .in1(32'h30ac), .in2(32'h3150), .in3(32'h31f4), .out(multiplexer_2_out), .sel(IR_id));  // open: in0
  Button button_1 (.out(RST));
  Multiplexer #(.select(1), .width(5), .disabled("Z"), .enable("false")) multiplexer_3 (
    .in0(IR[19:15]), .in1(5'b10001), .out(multiplexer_3_out), .sel(ecall));
  Multiplexer #(.select(1), .width(5), .disabled("Z"), .enable("false")) multiplexer_4 (
    .in0(IR[24:20]), .in1(5'b01010), .out(multiplexer_4_out), .sel(ecall));
  Multiplexer #(.select(1), .width(32), .disabled("Z"), .enable("false")) multiplexer_5 (
    .in0(PC_Ori), .in1(multiplexer_2_out), .out(multiplexer_5_out), .sel(Interrupt));
  or or_11 (IR3_t, IR3, IRC);
  \单周期硬布线控制器  \u_单周期硬布线控制器_1  (
    .Funct({IR[30], IR[25], IR[14:12]}), .OP(IR[6:2]), .ALU_OP(\单周期硬布线控制器_1_alu_op ), .MemToReg(MemToReg),
    .MemWrite(MemWrite), .ALU_SRC(Alu_Src), .RegWrite(RegWrite), .ecall(ecall), .S_type(S_type), .Jalr(JALR),
    .Beq(Beq), .JAL(JAL), .Bne(Bne), .in_3(IR[21]), .uret(URET), .LUI(AUIPC), .sb(sb), .BGEU(BGEU));  // open: rs1, rs2, CSR
  assign bit_extender_1_out = {{20{IR[31]}}, IR[31:20]};  // Bit_Extender bit_extender_1
  assign bit_extender_2_out = {{20{IR[31]}}, {IR[31], IR[7], IR[30:25], IR[11:8]}};  // Bit_Extender bit_extender_2
  assign bit_extender_3_out = {{12{IR[31]}}, {IR[31], IR[19:12], IR[20], IR[30:21]}};  // Bit_Extender bit_extender_3
  assign bit_extender_4_out = {{12{IR[31]}}, IR[31:12]};  // Bit_Extender bit_extender_4
  Multiplexer #(.select(1), .width(32), .disabled("Z"), .enable("false")) multiplexer_6 (
    .in0(multiplexer_5_out), .in1(EPC), .out(PC_Next), .sel(URET));
  assign bit_extender_5_out = {{20{IR[31]}}, {IR[31:25], IR[11:7]}};  // Bit_Extender bit_extender_5
  Shifter #(.width(32), .shift("ll")) shifter_1 (.in(bit_extender_2_out), .\dist (5'b00001), .out(shifter_1_out));
  Shifter #(.width(32), .shift("ll")) shifter_2 (.in(bit_extender_3_out), .\dist (5'b00001), .out(shifter_2_out));
  Shifter #(.width(32), .shift("ll")) shifter_3 (.in(bit_extender_4_out), .\dist (5'b01100), .out(shifter_3_out));
  Regifile regifile_1 (
    .Din(RDin), .Clk(CLK), .R1(regifile_1_r1), .R2(MDin), .WE(RegWrite), .W_num(IR[11:7]),
    .R1_num(multiplexer_3_out), .R2_num(multiplexer_4_out));
  Multiplexer #(.select(1), .width(32), .disabled("Z"), .enable("false")) multiplexer_7 (
    .in0(bit_extender_1_out), .in1(bit_extender_5_out), .out(multiplexer_7_out), .sel(S_type));
  Adder #(.width(32)) adder_2 (.a(shifter_1_out), .b(PC), .out(B));  // open: cin, cout
  Adder #(.width(32)) adder_3 (.a(PC), .b(shifter_2_out), .out(J));  // open: cin, cout
  Adder #(.width(32)) adder_4 (.a(PC), .b(shifter_3_out), .out(U));  // open: cin, cout
  Multiplexer #(.select(1), .width(32), .disabled("Z"), .enable("false")) multiplexer_8 (
    .in0(MDin), .in1(multiplexer_7_out), .out(multiplexer_8_out), .sel(Alu_Src));
  Register #(.width(32), .trigger("rising"), .Select("low")) u_EPC (
    .D(PC_Ori), .en(Interrupt), .Q(EPC), .clk(CLK), .clr(RST));
  ALU alu_1 (
    .X(regifile_1_r1), .Y(multiplexer_8_out), .AluOP(\单周期硬布线控制器_1_alu_op ), .Equal(E), .Result(ALUResult),
    .out_4(G), .out_6(S));  // open: Result_2
  Comparator #(.width(32), .mode("twosComplement")) comparator_5 (
    .a(regifile_1_r1), .b(32'h22), .eq(comparator_5_eq));  // open: gt, lt
  not not_4 (not_4_out, comparator_5_eq);
  and and_8 (halt, ecall, not_4_out);
  Comparator #(.width(16), .mode("twosComplement")) comparator_6 (
    .a(\总周期数 ), .b({16{1'b0}}), .eq(comparator_6_eq));  // open: gt, lt
  and and_9 (and_9_out, comparator_5_eq, ecall);
  Multiplexer #(.select(1), .width(32), .disabled("Z"), .enable("false")) multiplexer_9 (
    .in0(MDin), .in1(multiplexer_10_out), .out(multiplexer_9_out), .sel(sb));
  assign or_12_out = shifter_6_out | and_10_out;  // OR_Gate or_12, 32 bits wide
  not not_5 (not_5_out, Interrupt);
  or or_13 (or_13_out, Interrupt, URET, comparator_6_eq);
  D_Flip_Flop #(.trigger("high"), .Pre_Clr_Positions("LEGACY"), .NegatePresetClear("false"), .enable("true"), .NewFFLayout("false")) d_ff_4 (.Q(d_ff_4_q));  // open: clk, D, Qn, preset, en, reset
  // Probe on 13'hc
  Multiplexer #(.select(2), .width(32), .disabled("Z"), .enable("false")) multiplexer_10 (
    .in0(or_16_out), .in1(or_14_out), .in2(or_15_out), .in3(or_12_out), .out(multiplexer_10_out),
    .sel(ALUResult[1:0]));
  assign or_14_out = and_12_out | shifter_4_out;  // OR_Gate or_14, 32 bits wide
  assign or_15_out = and_11_out | shifter_5_out;  // OR_Gate or_15, 32 bits wide
  Register #(.width(1), .trigger("rising"), .Select("low")) u_IE (
    .D(not_5_out), .en(or_13_out), .Q(IE), .clk(CLK), .clr(RST));
  Comparator #(.width(13), .mode("twosComplement")) comparator_7 (
    .a(CNT_num), .b(13'hc), .eq(comparator_7_eq), .lt(comparator_7_lt));  // open: gt
  Clock #(.highDuration(1), .lowDuration(1)) clock_1 (.out(clock_1_out));
  Register #(.width(32), .trigger("rising"), .Select("low")) register_1 (
    .D(MDin), .en(and_9_out), .Q(LedData), .clk(CLK));  // open: clr
  assign and_10_out = ram_1_data & 32'hffffff;  // AND_Gate and_10, 32 bits wide
  assign and_11_out = ram_1_data & 32'hff00ffff;  // AND_Gate and_11, 32 bits wide
  assign and_12_out = ram_1_data & 32'hffff00ff;  // AND_Gate and_12, 32 bits wide
  assign and_13_out = ram_1_data & 32'hffffff00;  // AND_Gate and_13, 32 bits wide
  assign or_16_out = and_13_out | MDin;  // OR_Gate or_16, 32 bits wide
  Counter #(.width(13), .max('h1fff), .ongoal("stay"), .trigger("rising"), .behavior("old")) counter_2 (
    .count(comparator_7_lt), .Q(CNT_num), .clk(clock_1_out));  // open: load, D, carry, clr, preset
  RAM #(.addrWidth(10), .dataWidth(32), .bus("separate"), .Select("high")) ram_1 (
    .addr(ALUResult[11:2]), .din(multiplexer_9_out), .data(ram_1_data), .str(MemWrite), .sel(1'b1),
    .clk(CLK), .ld(1'b1), .clr(RST));
  Shifter #(.width(32), .shift("ll")) shifter_4 (.in(MDin), .\dist (5'b01000), .out(shifter_4_out));
  Shifter #(.width(32), .shift("ll")) shifter_5 (.in(MDin), .\dist (5'b10000), .out(shifter_5_out));
  Shifter #(.width(32), .shift("ll")) shifter_6 (.in(MDin), .\dist (5'b11000), .out(shifter_6_out));
  Register #(.width(2), .trigger("rising"), .Select("low")) register_2 (
    .D(IR_id), .en(Interrupt), .Q(register_2_q), .clk(CLK), .clr(RST));
  Demultiplexer #(.select(2), .width(1), .tristate("false"), .disabled("Z"), .enable("false")) demultiplexer_1 (
    .out1(IR1_Reset), .out2(IR2_Reset), .out3(IR3_Reset), .in(URET), .sel(register_2_q));  // open: out0
  nand nand_1 (nand_1_out, d_ff_4_q, comparator_7_eq);
  assign CLK = nand_1_out ? clock_1_out : 1'bz;  // Controlled_Buffer controlled_buffer_1
  Pull_Resistor #(.pull(1)) pull_resistor_4 (.node(CLK));
  Multiplexer #(.select(2), .width(32), .disabled("Z"), .enable("false")) multiplexer_11 (
    .in0(ALUResult), .in1(ram_1_data), .in2(PC_4), .in3(U), .out(RDin), .sel(priority_encoder_3_out));
  Priority_Encoder #(.select(2), .disabled("Z")) priority_encoder_3 (
    .in0(1'b1), .in1(MemToReg), .in2(or_17_out), .in3(AUIPC), .out(priority_encoder_3_out));  // open: gs, en_out, en_in
  or or_17 (or_17_out, JALR, JAL);
  \单周期_多级中断  \u_单周期_多级中断_1  ();  // open: IR1, IR2, IR3, RegWrite, MemWrite, PC, IR, RDin, MDin, LedData

  // Notes on the sheet:
  //   中断源
  //   中断等待指示
  //   总复位信号应将除ROM以外所有存储组件全部清零
  //   单级中断测试信号模拟器
  //   数码管输出
  //   数码管输出应该用寄存器锁存，否则显示数据只能一闪而过
  //   Reset 
  //   Reset 
  //   Reset 
  //   指令探针
  //   指令存储器
  //   周期计数器
  //   指令字
  //   contents of rom_1 (hex, n*v repeats v):
  //   7d000113 100413 1f41993 41f9d993 433 c00913 800b13 140413 f47413 800293 100313 499993 89e9b3 1300533
  //   2200893 73 406282b3 fe0294e3 140413 f00f93 1f47433 1c41413 800293 100313 49d993 89e9b3 1300533
  //   2200893 73 406282b3 fe0294e3 1c45413 406b0b33 b0463 f95ff06f 2b3 fff2c293 1029293 fff2e293 500533
  //   2200893 73 f5dff06f 1112023 410113 a12023 410113 812023 410113 1312023 410113 1412023 410113 1512023
  //   410113 1612023 410113 100b13 300a13 100a93 1600433 441413 14469b3 1300533 2200893 73 fe0416e3
  //   415a0a33 fe0a10e3 ffc10113 12b03 ffc10113 12a83 ffc10113 12a03 ffc10113 12983 ffc10113 12403
  //   ffc10113 12503 ffc10113 12883 200073 1112023 410113 a12023 410113 812023 410113 1312023 410113
  //   1412023 410113 1512023 410113 1612023 410113 200b13 300a13 100a93 1600433 441413 14469b3 1300533
  //   2200893 73 fe0416e3 415a0a33 fe0a10e3 ffc10113 12b03 ffc10113 12a83 ffc10113 12a03 ffc10113 12983
  //   ffc10113 12403 ffc10113 12503 ffc10113 12883 200073 1112023 410113 a12023 410113 812023 410113
  //   1312023 410113 1412023 410113 1512023 410113 1612023 410113 300b13 300a13 100a93 1600433 441413
  //   14469b3 1300533 2200893 73 fe0416e3 415a0a33 fe0a10e3 ffc10113 12b03 ffc10113 12a83 ffc10113 12a03
  //   ffc10113 12983 ffc10113 12403 ffc10113 12503 ffc10113 12883 200073
  //   清零按钮
  //   为方便自动评测，需要输出PC，IR，寄存器堆写如数据RDin
  //   RAM写使能MemWrite、RAM写入数据MDin等信号
  //   控制位
  //   暂停节拍，不能为0
  //   戳工具置1进入计数暂停模式，ctrl+k时钟自动运行到对应节拍暂停
  //   ctrl+k关闭时钟连续运行，将控制位置零，进入单步调试模式调试
  //   数据存储器
  //   可计数暂停的时钟源
endmodule

module \单周期_多级中断  (
  input  IR1,
  input  IR2,
  input  IR3,
  output RegWrite,
  output MemWrite,
  output [31:0] PC,
  output [31:0] IR,
  output [31:0] RDin,
  output [31:0] MDin,
  output [31:0] LedData
);

  wire Alu_Src, and_1_out, and_2_out, and_3_out, and_4_out, and_5_out, and_6_out, and_8_out, and_10_out,
       and_11_out, and_12_out, and_13_out, and_14_out, and_15_out, AUIPC, Beq, BGEU, Bne, CLK, clock_1_out,
       comparator_1_eq, comparator_2_eq, comparator_3_eq, comparator_4_eq, comparator_5_eq, comparator_6_eq,
       comparator_6_lt, comparator_7_eq, comparator_8_eq, comparator_9_eq, comparator_10_eq,
       controlled_inverter_1_out, controlled_inverter_2_out, controlled_inverter_3_out, CSR, CSRRCI, CSRRSI,
       d_ff_1_q, d_ff_2_q, d_ff_3_q, d_ff_4_q, decoder_1_out2, decoder_1_out3, decoder_2_out0,
       decoder_2_out1, decoder_2_out2, E, ecall, G, Go, halt, IE, Interrupt, IR1_q, IR1_Reset, IR1_t, IR2_q,
       IR2_Reset, IR2_t, IR3_q, IR3_Reset, IR3_t, IRA, IRB, IRC, JAL, JALR, MemToReg, nand_1_out, not_1_out,
       not_2_out, not_3_out, not_4_out, or_1_out, or_2_out, or_9_out, or_10_out, or_11_out, or_12_out,
       or_13_out, or_18_out, or_19_out, or_20_out, Priority, priority_encoder_2_gs, pull_resistor_7_node,
       RST, S, S_type, sb, URET, W1, W2, W3;
  wire [1:0] adder_5_out, exist, IR_id, IR_id_CUR, IRNum1_q, IRNum2_q, IRNum3_q, multiplexer_6_out,
       priority_encoder_1_out, priority_encoder_3_out;
  wire [3:0] \单周期硬布线控制器_1_alu_op ;
  wire [4:0] multiplexer_2_out, multiplexer_3_out;
  wire [12:0] CNT_num;
  wire [15:0] \总周期数 ;
  wire [31:0] ALUResult, and_18_out, and_19_out, and_20_out, and_21_out, B, bit_extender_1_out,
       bit_extender_2_out, bit_extender_3_out, bit_extender_4_out, bit_extender_5_out, EPC, EPC1_q, EPC2_q,
       EPC3_q, J, multiplexer_4_out, multiplexer_5_out, multiplexer_7_out, multiplexer_8_out,
       multiplexer_10_out, multiplexer_11_out, or_14_out, or_15_out, or_16_out, or_17_out, PC_4, PC_Next,
       PC_Ori, ram_1_data, regifile_1_r1, shifter_1_out, shifter_2_out, shifter_3_out, shifter_4_out,
       shifter_5_out, shifter_6_out, U;

  Button \u_继续运行  (.out(Go));
  Button _1 (.out(IRA));
  Button _2 (.out(IRB));
  Button _3 (.out(IRC));
  LED #(.active("true")) led_1 (.in(W1));
  LED #(.active("true")) led_2 (.in(W2));
  LED #(.active("true")) led_3 (.in(W3));
  Hex_Digit_Display hex_digit_display_1 (.value(LedData[31:28]));  // open: dp
  Comparator #(.width(16), .mode("twosComplement")) comparator_1 (
    .a(\总周期数 ), .b(16'h7), .eq(comparator_1_eq));  // open: gt, lt
  Comparator #(.width(16), .mode("twosComplement")) comparator_2 (
    .a(\总周期数 ), .b(16'h241), .eq(comparator_2_eq));  // open: gt, lt
  Hex_Digit_Display hex_digit_display_2 (.value(LedData[27:24]));  // open: dp
  Hex_Digit_Display hex_digit_display_3 (.value(LedData[23:20]));  // open: dp
  Comparator #(.width(16), .mode("twosComplement")) comparator_3 (
    .a(16'h258), .b(\总周期数 ), .eq(comparator_3_eq));  // open: gt, lt
  or or_1 (or_1_out, comparator_3_eq, comparator_4_eq);
  Comparator #(.width(16), .mode("twosComplement")) comparator_4 (
    .a(\总周期数 ), .b(16'h1), .eq(comparator_4_eq));  // open: gt, lt
  Comparator #(.width(16), .mode("twosComplement")) comparator_5 (
    .a(\总周期数 ), .b(16'h4), .eq(comparator_5_eq));  // open: gt, lt
  or or_2 (or_2_out, comparator_1_eq, comparator_2_eq);
  Hex_Digit_Display hex_digit_display_4 (.value(LedData[19:16]));  // open: dp
  Hex_Digit_Display hex_digit_display_5 (.value(LedData[15:12]));  // open: dp
  Pull_Resistor #(.pull(0)) pull_resistor_1 ();  // open: node
  assign controlled_inverter_1_out = or_1_out ? ~CLK : 1'bz;  // Controlled_Inverter controlled_inverter_1
  Pull_Resistor #(.pull(0)) pull_resistor_2 ();  // open: node
  assign controlled_inverter_2_out = comparator_5_eq ? ~CLK : 1'bz;  // Controlled_Inverter controlled_inverter_2
  Pull_Resistor #(.pull(0)) pull_resistor_3 ();  // open: node
  assign controlled_inverter_3_out = or_2_out ? ~CLK : 1'bz;  // Controlled_Inverter controlled_inverter_3
  Hex_Digit_Display hex_digit_display_6 (.value(LedData[11:8]));  // open: dp
  Hex_Digit_Display hex_digit_display_7 (.value(LedData[7:4]));  // open: dp
  // Probe on \总周期数 
  Hex_Digit_Display hex_digit_display_8 (.value(LedData[3:0]));  // open: dp
  or or_3 (IR1_t, IR1, IRA);
  or or_4 (IR2_t, IR2, IRB);
  Priority_Encoder #(.select(2), .disabled("Z")) priority_encoder_1 (
    .in0(1'b1), .in1(JALR), .in2(or_9_out), .in3(JAL), .out(priority_encoder_1_out));  // open: gs, en_out, en_in
  Multiplexer #(.select(2), .width(32), .disabled("Z"), .enable("false")) multiplexer_1 (
    .in0(PC_4), .in1(ALUResult), .in2(B), .in3(J), .out(PC_Ori), .sel(priority_encoder_1_out));
  not not_1 (not_1_out, halt);
  LED #(.active("true")) \_1号中断等待指示灯  (.in(W1));
  LED #(.active("true")) \_2号中断等待指示灯  (.in(W2));
  LED #(.active("true")) \_3号中断等待指示灯  (.in(W3));
  Register #(.width(32), .trigger("rising"), .Select("low")) u_PC (
    .D(PC_Next), .en(not_1_out), .Q(PC), .clk(CLK), .clr(RST));
  or or_5 (W1, IR1_q, d_ff_1_q);
  or or_6 (W2, IR2_q, d_ff_2_q);
  or or_7 (W3, IR3_q, d_ff_3_q);
  or or_8 (IR3_t, IR3, IRC);
  and and_1 (and_1_out, BGEU, G);
  or or_9 (or_9_out, and_1_out, and_2_out, and_3_out);
  and and_2 (and_2_out, Beq, E);
  and and_3 (and_3_out, not_3_out, Bne);
  not not_2 (not_2_out, halt);
  D_Flip_Flop #(.trigger("rising"), .Pre_Clr_Positions("LEGACY"), .NegatePresetClear("false"), .enable("true"), .NewFFLayout("false")) d_ff_1 (
    .clk(IR1_t), .D(1'b1), .Q(d_ff_1_q), .reset(IR1_q));  // open: Qn, preset, en
  D_Flip_Flop #(.trigger("rising"), .Pre_Clr_Positions("LEGACY"), .NegatePresetClear("false"), .enable("true"), .NewFFLayout("false")) d_ff_2 (
    .clk(IR2_t), .D(1'b1), .Q(d_ff_2_q), .reset(IR2_q));  // open: Qn, preset, en
  D_Flip_Flop #(.trigger("rising"), .Pre_Clr_Positions("LEGACY"), .NegatePresetClear("false"), .enable("true"), .NewFFLayout("false")) d_ff_3 (
    .clk(IR3_t), .D(1'b1), .Q(d_ff_3_q), .reset(IR3_q));  // open: Qn, preset, en
  not not_3 (not_3_out, E);
  // RiscV_Probe riscv_probe_1: pin names not known; wires that end beside it: IR
  Adder #(.width(32)) adder_1 (.a(PC), .b(32'h4), .out(PC_4));  // open: cin, cout
  Counter #(.width(16), .max('hffff), .ongoal("wrap"), .trigger("rising"), .behavior("new")) counter_1 (
    .count(not_2_out), .Q(\总周期数 ), .clk(CLK));  // open: load, D, carry, clr, preset, down
  or or_10 (or_10_out, d_ff_1_q, IR1_q);
  and and_4 (and_4_out, or_10_out, ~IR1_Reset);  // AND_Gate
  or or_11 (or_11_out, d_ff_2_q, IR2_q);
  and and_5 (and_5_out, or_11_out, ~IR2_Reset);  // AND_Gate
  or or_12 (or_12_out, d_ff_3_q, IR3_q);
  and and_6 (and_6_out, or_12_out, ~IR3_Reset);  // AND_Gate
  ROM #(.addrWidth(10), .dataWidth(32), .Select("high")) rom_1 (.addr(PC[11:2]), .data(IR));
  D_Flip_Flop #(.trigger("rising"), .Pre_Clr_Positions("LEGACY"), .NegatePresetClear("false"), .enable("true"), .NewFFLayout("false")) u_IR1 (
    .clk(CLK), .D(and_4_out), .Q(IR1_q), .reset(RST));  // open: Qn, preset, en
  D_Flip_Flop #(.trigger("rising"), .Pre_Clr_Positions("LEGACY"), .NegatePresetClear("false"), .enable("true"), .NewFFLayout("false")) u_IR2 (
    .clk(CLK), .D(and_5_out), .Q(IR2_q), .reset(RST));  // open: Qn, preset, en
  D_Flip_Flop #(.trigger("rising"), .Pre_Clr_Positions("LEGACY"), .NegatePresetClear("false"), .enable("true"), .NewFFLayout("false")) u_IR3 (
    .clk(CLK), .D(and_6_out), .Q(IR3_q), .reset(RST));  // open: Qn, preset, en
  Button button_1 (.out(RST));
  \单周期硬布线控制器  \u_单周期硬布线控制器_1  (
    .Funct({IR[30], IR[25], IR[14:12]}), .OP(IR[6:2]), .ALU_OP(\单周期硬布线控制器_1_alu_op ), .MemToReg(MemToReg),
    .MemWrite(MemWrite), .ALU_SRC(Alu_Src), .RegWrite(RegWrite), .ecall(ecall), .S_type(S_type), .Jalr(JALR),
    .Beq(Beq), .JAL(JAL), .Bne(Bne), .in_3(IR[21]), .uret(URET), .LUI(AUIPC), .sb(sb), .BGEU(BGEU), .CSR(CSR));  // open: rs1, rs2
  Multiplexer #(.select(1), .width(5), .disabled("Z"), .enable("false")) multiplexer_2 (
    .in0(IR[19:15]), .in1(5'b10001), .out(multiplexer_2_out), .sel(ecall));
  Multiplexer #(.select(1), .width(5), .disabled("Z"), .enable("false")) multiplexer_3 (
    .in0(IR[24:20]), .in1(5'b01010), .out(multiplexer_3_out), .sel(ecall));
  assign bit_extender_1_out = {{20{IR[31]}}, IR[31:20]};  // Bit_Extender bit_extender_1
  assign bit_extender_2_out = {{12{IR[31]}}, IR[31:12]};  // Bit_Extender bit_extender_2
  Priority_Encoder #(.select(2), .disabled("Z")) priority_encoder_2 (
    .in1(IR1_q), .in2(IR2_q), .in3(IR3_q), .out(IR_id), .gs(priority_encoder_2_gs));  // open: in0, en_out, en_in
  assign bit_extender_3_out = {{20{IR[31]}}, {IR[31:25], IR[11:7]}};  // Bit_Extender bit_extender_3
  assign bit_extender_4_out = {{20{IR[31]}}, {IR[31], IR[7], IR[30:25], IR[11:8]}};  // Bit_Extender bit_extender_4
  assign bit_extender_5_out = {{12{IR[31]}}, {IR[31], IR[19:12], IR[20], IR[30:21]}};  // Bit_Extender bit_extender_5
  Multiplexer #(.select(2), .width(32), .disabled("Z"), .enable("false")) multiplexer_4 (
    .in1(32'h30ac), .in2(32'h3158), .in3(32'h3204), .out(multiplexer_4_out), .sel(IR_id));  // open: in0
  and and_7 (Interrupt, priority_encoder_2_gs, Priority, IE);
  Demultiplexer #(.select(2), .width(1), .tristate("false"), .disabled("Z"), .enable("false")) demultiplexer_1 (
    .out1(IR1_Reset), .out2(IR2_Reset), .out3(IR3_Reset), .in(URET), .sel(IR_id));  // open: out0
  Pull_Resistor #(.pull(0)) pull_resistor_4 (.node(IR2_Reset));
  Regifile regifile_1 (
    .Din(RDin), .Clk(CLK), .R1(regifile_1_r1), .R2(MDin), .WE(RegWrite), .W_num(IR[11:7]),
    .R1_num(multiplexer_2_out), .R2_num(multiplexer_3_out));
  Multiplexer #(.select(1), .width(32), .disabled("Z"), .enable("false")) multiplexer_5 (
    .in0(bit_extender_1_out), .in1(bit_extender_3_out), .out(multiplexer_5_out), .sel(S_type));
  Shifter #(.width(32), .shift("ll")) shifter_1 (.in(bit_extender_4_out), .\dist (5'b00001), .out(shifter_1_out));
  Shifter #(.width(32), .shift("ll")) shifter_2 (.in(bit_extender_5_out), .\dist (5'b00001), .out(shifter_2_out));
  Shifter #(.width(32), .shift("ll")) shifter_3 (.in(bit_extender_2_out), .\dist (5'b01100), .out(shifter_3_out));
  Pull_Resistor #(.pull(0)) pull_resistor_5 (.node(IR1_Reset));
  Pull_Resistor #(.pull(0)) pull_resistor_6 (.node(IR3_Reset));
  Multiplexer #(.select(1), .width(2), .disabled("Z"), .enable("false")) multiplexer_6 (
    .in0(2'b11), .in1(2'b01), .out(multiplexer_6_out), .sel(Interrupt));
  D_Flip_Flop #(.trigger("high"), .Pre_Clr_Positions("LEGACY"), .NegatePresetClear("false"), .enable("true"), .NewFFLayout("false")) d_ff_4 (.Q(d_ff_4_q));  // open: clk, D, Qn, preset, en, reset
  // Probe on 13'hc
  Adder #(.width(32)) adder_2 (.a(shifter_1_out), .b(PC), .out(B));  // open: cin, cout
  Adder #(.width(32)) adder_3 (.a(PC), .b(shifter_2_out), .out(J));  // open: cin, cout
  Adder #(.width(32)) adder_4 (.a(PC), .b(shifter_3_out), .out(U));  // open: cin, cout
  Multiplexer #(.select(1), .width(32), .disabled("Z"), .enable("false")) multiplexer_7 (
    .in0(PC_Ori), .in1(multiplexer_4_out), .out(multiplexer_7_out), .sel(Interrupt));
  Adder #(.width(2)) adder_5 (.a(exist), .b(multiplexer_6_out), .out(adder_5_out));  // open: cin, cout
  Register #(.width(2), .trigger("rising"), .Select("low")) register_1 (
    .D(adder_5_out), .en(or_13_out), .Q(exist), .clk(CLK), .clr(RST));
  or or_13 (or_13_out, Interrupt, URET);
  Comparator #(.width(13), .mode("twosComplement")) comparator_6 (
    .a(CNT_num), .b(13'hc), .eq(comparator_6_eq), .lt(comparator_6_lt));  // open: gt
  Clock #(.highDuration(1), .lowDuration(1)) clock_1 (.out(clock_1_out));
  Multiplexer #(.select(1), .width(32), .disabled("Z"), .enable("false")) multiplexer_8 (
    .in0(MDin), .in1(multiplexer_5_out), .out(multiplexer_8_out), .sel(Alu_Src));
  Multiplexer #(.select(1), .width(32), .disabled("Z"), .enable("false")) multiplexer_9 (
    .in0(multiplexer_7_out), .in1(EPC), .out(PC_Next), .sel(URET));
  Pull_Resistor #(.pull(0)) pull_resistor_7 (.node(pull_resistor_7_node));
  Decoder #(.select(2), .tristate("false"), .disabled("Z"), .enable("false")) decoder_1 (
    .out1(pull_resistor_7_node), .out2(decoder_1_out2), .out3(decoder_1_out3), .sel(IR_id));  // open: out0
  Pull_Resistor #(.pull(0)) pull_resistor_8 (.node(decoder_1_out3));
  Decoder #(.select(2), .tristate("false"), .disabled("Z"), .enable("false")) decoder_2 (
    .out0(decoder_2_out0), .out1(decoder_2_out1), .out2(decoder_2_out2), .sel(exist));  // open: out3
  Counter #(.width(13), .max('h1fff), .ongoal("stay"), .trigger("rising"), .behavior("old")) counter_2 (
    .count(comparator_6_lt), .Q(CNT_num), .clk(clock_1_out));  // open: load, D, carry, clr, preset
  Comparator #(.width(32), .mode("twosComplement")) comparator_7 (
    .a(regifile_1_r1), .b(32'h22), .eq(comparator_7_eq));  // open: gt, lt
  ALU alu_1 (
    .X(regifile_1_r1), .Y(multiplexer_8_out), .AluOP(\单周期硬布线控制器_1_alu_op ), .Equal(E), .Result(ALUResult),
    .out_4(G), .out_6(S));  // open: Result_2
  Pull_Resistor #(.pull(0)) pull_resistor_9 (.node(decoder_1_out2));
  nand nand_1 (nand_1_out, d_ff_4_q, comparator_6_eq);
  and and_8 (and_8_out, comparator_7_eq, ecall);
  not not_4 (not_4_out, comparator_7_eq);
  and and_9 (halt, ecall, not_4_out);
  and and_10 (and_10_out, pull_resistor_7_node, Interrupt);
  and and_11 (and_11_out, decoder_1_out2, Interrupt);
  and and_12 (and_12_out, decoder_1_out3, Interrupt);
  and and_13 (and_13_out, decoder_2_out0, Interrupt);
  and and_14 (and_14_out, decoder_2_out1, Interrupt);
  and and_15 (and_15_out, decoder_2_out2, Interrupt);
  assign CLK = nand_1_out ? clock_1_out : 1'bz;  // Controlled_Buffer controlled_buffer_1
  Pull_Resistor #(.pull(1)) pull_resistor_10 (.node(CLK));
  Multiplexer #(.select(1), .width(32), .disabled("Z"), .enable("false")) multiplexer_10 (
    .in0(MDin), .in1(multiplexer_11_out), .out(multiplexer_10_out), .sel(sb));
  Multiplexer #(.select(2), .width(32), .disabled("Z"), .enable("false")) multiplexer_11 (
    .in0(or_16_out), .in1(or_17_out), .in2(or_14_out), .in3(or_15_out), .out(multiplexer_11_out),
    .sel(ALUResult[1:0]));
  assign or_14_out = and_19_out | shifter_5_out;  // OR_Gate or_14, 32 bits wide
  assign or_15_out = shifter_6_out | and_18_out;  // OR_Gate or_15, 32 bits wide
  Comparator #(.width(3), .mode("twosComplement")) comparator_8 (
    .a(3'b111), .b(IR[14:12]), .eq(comparator_8_eq));  // open: gt, lt
  Comparator #(.width(3), .mode("twosComplement")) comparator_9 (
    .a(IR[14:12]), .b(3'b110), .eq(comparator_9_eq));  // open: gt, lt
  Register #(.width(32), .trigger("rising"), .Select("low")) EPC1 (
    .D(PC_Ori), .en(and_10_out), .Q(EPC1_q), .clk(CLK), .clr(RST));
  Register #(.width(32), .trigger("rising"), .Select("low")) EPC2 (
    .D(PC_Ori), .en(and_11_out), .Q(EPC2_q), .clk(CLK), .clr(RST));
  Register #(.width(32), .trigger("rising"), .Select("low")) EPC3 (
    .D(PC_Ori), .en(and_12_out), .Q(EPC3_q), .clk(CLK), .clr(RST));
  Register #(.width(2), .trigger("rising"), .Select("low")) IRNum1 (
    .D(IR_id), .en(and_13_out), .Q(IRNum1_q), .clk(CLK), .clr(RST));
  Register #(.width(2), .trigger("rising"), .Select("low")) IRNum2 (
    .D(IR_id), .en(and_14_out), .Q(IRNum2_q), .clk(CLK), .clr(RST));
  Register #(.width(2), .trigger("rising"), .Select("low")) IRNum3 (
    .D(IR_id), .en(and_15_out), .Q(IRNum3_q), .clk(CLK), .clr(RST));
  Register #(.width(32), .trigger("rising"), .Select("low")) register_2 (
    .D(MDin), .en(and_8_out), .Q(LedData), .clk(CLK));  // open: clr
  assign or_16_out = and_21_out | MDin;  // OR_Gate or_16, 32 bits wide
  assign or_17_out = and_20_out | shifter_4_out;  // OR_Gate or_17, 32 bits wide
  and and_16 (CSRRCI, comparator_8_eq, CSR);
  and and_17 (CSRRSI, CSR, comparator_9_eq);
  Multiplexer #(.select(2), .width(32), .disabled("Z"), .enable("false")) multiplexer_12 (
    .in1(EPC1_q), .in2(EPC2_q), .in3(EPC3_q), .out(EPC), .sel(IR_id_CUR));  // open: in0
  Multiplexer #(.select(2), .width(2), .disabled("Z"), .enable("false")) multiplexer_13 (
    .in1(IRNum1_q), .in2(IRNum2_q), .in3(IRNum3_q), .out(IR_id_CUR), .sel(exist));  // open: in0
  RAM #(.addrWidth(10), .dataWidth(32), .bus("separate"), .Select("high")) ram_1 (
    .addr(ALUResult[11:2]), .din(multiplexer_10_out), .data(ram_1_data), .str(MemWrite), .sel(1'b1),
    .clk(CLK), .ld(1'b1), .clr(RST));
  assign and_18_out = ram_1_data & 32'hffffff;  // AND_Gate and_18, 32 bits wide
  assign and_19_out = ram_1_data & 32'hff00ffff;  // AND_Gate and_19, 32 bits wide
  assign and_20_out = ram_1_data & 32'hffff00ff;  // AND_Gate and_20, 32 bits wide
  assign and_21_out = ram_1_data & 32'hffffff00;  // AND_Gate and_21, 32 bits wide
  Shifter #(.width(32), .shift("ll")) shifter_4 (.in(MDin), .\dist (5'b01000), .out(shifter_4_out));
  Shifter #(.width(32), .shift("ll")) shifter_5 (.in(MDin), .\dist (5'b10000), .out(shifter_5_out));
  Shifter #(.width(32), .shift("ll")) shifter_6 (.in(MDin), .\dist (5'b11000), .out(shifter_6_out));
  Comparator #(.width(16), .mode("twosComplement")) comparator_10 (
    .a(\总周期数 ), .b({16{1'b0}}), .eq(comparator_10_eq));  // open: gt, lt
  Comparator #(.width(2), .mode("unsigned")) comparator_11 (.a(IR_id_CUR), .b(IR_id), .lt(Priority));  // open: gt, eq
  Pull_Resistor #(.pull(1)) pull_resistor_11 (.node(Priority));
  Priority_Encoder #(.select(2), .disabled("Z")) priority_encoder_3 (
    .in0(1'b1), .in1(MemToReg), .in2(or_20_out), .in3(AUIPC), .out(priority_encoder_3_out));  // open: gs, en_out, en_in
  or or_18 (or_18_out, CSRRSI, ~Interrupt);  // OR_Gate
  or or_19 (or_19_out, Interrupt, URET, comparator_10_eq, CSRRCI, CSRRSI);
  Multiplexer #(.select(2), .width(32), .disabled("Z"), .enable("false")) multiplexer_14 (
    .in0(ALUResult), .in1(ram_1_data), .in2(PC_4), .in3(U), .out(RDin), .sel(priority_encoder_3_out));
  or or_20 (or_20_out, JALR, JAL);
  Register #(.width(1), .trigger("rising"), .Select("low")) u_IE (
    .D(or_18_out), .en(or_19_out), .Q(IE), .clk(CLK), .clr(RST));

  // Other names for the same wires on the sheet: Funt3[2:0] = IR[14:12]

  // Notes on the sheet:
  //   中断源
  //   中断等待指示
  //   总复位信号应将除ROM以外所有存储组件全部清零
  //   多级中断测试信号模拟器
  //   数码管输出
  //   数码管输出应该用寄存器锁存，否则显示数据只能一闪而过
  //   指令探针
  //   指令存储器
  //   周期计数器
  //   指令字
  //   contents of rom_1 (hex, n*v repeats v):
  //   7d000113 100413 1f41993 41f9d993 433 c00913 800b13 140413 f47413 800293 100313 499993 89e9b3 1300533
  //   2200893 73 406282b3 fe0294e3 140413 f00f93 1f47433 1c41413 800293 100313 49d993 89e9b3 1300533
  //   2200893 73 406282b3 fe0294e3 1c45413 406b0b33 b0463 f95ff06f 2b3 fff2c293 1029293 fff2e293 500533
  //   2200893 73 f5dff06f 1112023 410113 a12023 410113 812023 410113 1312023 410113 1412023 410113 1512023
  //   410113 1612023 410113 40e073 100b13 300a13 100a93 1600433 441413 14469b3 1300533 2200893 73 fe0416e3
  //   415a0a33 fe0a10e3 40f073 ffc10113 12b03 ffc10113 12a83 ffc10113 12a03 ffc10113 12983 ffc10113 12403
  //   ffc10113 12503 ffc10113 12883 200073 1112023 410113 a12023 410113 812023 410113 1312023 410113
  //   1412023 410113 1512023 410113 1612023 410113 40e073 200b13 300a13 100a93 1600433 441413 14469b3
  //   1300533 2200893 73 fe0416e3 415a0a33 fe0a10e3 40f073 ffc10113 12b03 ffc10113 12a83 ffc10113 12a03
  //   ffc10113 12983 ffc10113 12403 ffc10113 12503 ffc10113 12883 200073 1112023 410113 a12023 410113
  //   812023 410113 1312023 410113 1412023 410113 1512023 410113 1612023 410113 40e073 300b13 300a13
  //   100a93 1600433 441413 14469b3 1300533 2200893 73 fe0416e3 415a0a33 fe0a10e3 40f073 ffc10113 12b03
  //   ffc10113 12a83 ffc10113 12a03 ffc10113 12983 ffc10113 12403 ffc10113 12503 ffc10113 12883 200073
  //   Reset 
  //   Reset 
  //   Reset 
  //   为方便自动评测，需要输出PC，IR，寄存器堆写如数据RDin
  //   清零按钮
  //   RAM写使能MemWrite、RAM写入数据MDin等信号
  //   控制位
  //   暂停节拍，不能为0
  //   戳工具置1进入计数暂停模式，ctrl+k时钟自动运行到对应节拍暂停
  //   ctrl+k关闭时钟连续运行，将控制位置零，进入单步调试模式调试
  //   可计数暂停的时钟源
  //   数据存储器
endmodule

module \封装正确性测试  (
);

  wire IR1, IR2, IR3, MemW, RegW;
  wire [31:0] EX_PC, ID_PC, IF_PC, IR, LED, MDin, MDinr, MEM_PC, PC, RDin, RDinr, WB_PC;

  \单周期RISC_V  \u_单周期risc_v_1  (
    .IR1(IR1), .IR2(IR2), .IR3(IR3), .RegWrite(RegW), .MemWrite(MemW), .PC(PC), .IR(IR), .RDin(RDin),
    .MDin(MDin), .LedData(LED));
  \气泡流水线  \u_气泡流水线_1  (
    .RegWrite(RegW), .MemWrite(MemW), .IF_PC(IF_PC), .ID_PC(ID_PC), .EX_PC(EX_PC), .M_PC(MEM_PC),
    .WB_PC(WB_PC), .RDin(RDinr), .MDin(MDinr), .LedData(LED));
  \单周期_单级中断  \u_单周期_单级中断_1  (
    .IR1(IR1), .IR2(IR2), .IR3(IR3), .RegWrite(RegW), .MemWrite(MemW), .PC(PC), .IR(IR), .RDin(RDin),
    .MDin(MDin), .LedData(LED));
  \理想流水线  \u_理想流水线_1  (
    .RegWrite(RegW), .MemWrite(MemW), .IF_PC(IF_PC), .ID_PC(ID_PC), .EX_PC(EX_PC), .M_PC(MEM_PC),
    .WB_PC(WB_PC), .RDin(RDinr), .MDin(MDinr), .LedData(LED));
  \重定向流水线  \u_重定向流水线_1  (
    .RegWrite(RegW), .MemWrite(MemW), .IF_PC(IF_PC), .ID_PC(ID_PC), .EX_PC(EX_PC), .M_PC(MEM_PC),
    .WB_PC(WB_PC), .RDin(RDinr), .MDin(MDinr), .LedData(LED));
  \单周期_多级中断  \u_单周期_多级中断_1  (
    .IR1(IR1), .IR2(IR2), .IR3(IR3), .RegWrite(RegW), .MemWrite(MemW), .PC(PC), .IR(IR), .RDin(RDin),
    .MDin(MDin), .LedData(LED));

  // Notes on the sheet:
  //   单周期封装测试
  //   气泡流水封装测试
  //   单周期+单级中断封装测试
  //   请检查上面封装有无位宽不匹配，引脚标签是否和连接的标签相对应，否则无法在educoder平台上正确测试
  //   理想流水封装测试
  //   重定向流水封装测试
  //   单周期+多级中断封装测试
endmodule

module IF_ID (
  input  [31:0] IR,
  input  [31:0] PC,
  input  [31:0] PC_4,
  input  IF_PredictJump,
  input  branch,
  input  EN,
  input  CLK,
  output [31:0] IR_2,
  output [31:0] PC_2,
  output [31:0] PC_4_2,
  output ID_PredictJump
);

  wire multiplexer_4_out;
  wire [31:0] multiplexer_1_out, multiplexer_2_out, multiplexer_3_out;

  Multiplexer #(.select(1), .width(32), .disabled("Z"), .enable("false")) multiplexer_1 (
    .in0(IR), .in1({32{1'b0}}), .out(multiplexer_1_out), .sel(branch));
  Multiplexer #(.select(1), .width(32), .disabled("Z"), .enable("false")) multiplexer_2 (
    .in0(PC), .in1({32{1'b0}}), .out(multiplexer_2_out), .sel(branch));
  Multiplexer #(.select(1), .width(32), .disabled("Z"), .enable("false")) multiplexer_3 (
    .in0(PC_4), .in1({32{1'b0}}), .out(multiplexer_3_out), .sel(branch));
  Multiplexer #(.select(1), .width(1), .disabled("Z"), .enable("false")) multiplexer_4 (
    .in0(IF_PredictJump), .in1(1'b0), .out(multiplexer_4_out), .sel(branch));
  Register #(.width(32), .trigger("rising"), .Select("low")) register_1 (
    .D(multiplexer_1_out), .en(EN), .Q(IR_2), .clk(CLK));  // open: clr
  Register #(.width(32), .trigger("rising"), .Select("low")) register_2 (
    .D(multiplexer_2_out), .en(EN), .Q(PC_2), .clk(CLK));  // open: clr
  Register #(.width(32), .trigger("rising"), .Select("low")) register_3 (
    .D(multiplexer_3_out), .en(EN), .Q(PC_4_2), .clk(CLK));  // open: clr
  Register #(.width(1), .trigger("rising"), .Select("low")) register_4 (
    .D(multiplexer_4_out), .en(EN), .Q(ID_PredictJump), .clk(CLK));  // open: clr
endmodule

module ID_EX (
  input  sb,
  input  LUI,
  input  Beq,
  input  Bne,
  input  MemToReg,
  input  MemWrite,
  input  AluSrcB,
  input  RegWrite,
  input  ecall,
  input  Jal,
  input  Jalr,
  input  BGEU,
  input  Uret,
  input  [3:0] AluOP,
  input  [4:0] rd,
  input  [31:0] R1,
  input  [31:0] R2,
  input  [31:0] imm_1,
  input  [31:0] imm_2,
  input  [31:0] PC,
  input  [31:0] PC_4,
  input  [31:0] IR,
  input  [1:0] RS1_Forward,
  input  [1:0] RS2_Forward,
  input  ID_PredictJump,
  input  flush,
  input  en,
  input  clk,
  output sb_2,
  output LUI_2,
  output Beq_2,
  output Bne_2,
  output MemToReg_2,
  output MemWrite_2,
  output AluSrcB_2,
  output RegWrite_2,
  output ecall_2,
  output Jal_2,
  output Jalr_2,
  output BGEU_2,
  output Uret_2,
  output [3:0] AluOP_2,
  output [4:0] rd_2,
  output [31:0] R1_2,
  output [31:0] R2_2,
  output [31:0] imm_1_2,
  output [31:0] imm_2_2,
  output [31:0] PC_2,
  output [31:0] PC_4_2,
  output [31:0] IR_2,
  output [1:0] RS1_Forward_2,
  output [1:0] RS2_Forward_2,
  output EX_PredictJump
);

  wire multiplexer_1_out, multiplexer_2_out, multiplexer_3_out, multiplexer_4_out, multiplexer_5_out,
       multiplexer_6_out, multiplexer_7_out, multiplexer_8_out, multiplexer_9_out, multiplexer_10_out,
       multiplexer_11_out, multiplexer_12_out, multiplexer_13_out, multiplexer_25_out;
  wire [1:0] multiplexer_23_out, multiplexer_24_out;
  wire [3:0] multiplexer_14_out;
  wire [4:0] multiplexer_15_out;
  wire [31:0] multiplexer_16_out, multiplexer_17_out, multiplexer_18_out, multiplexer_19_out,
       multiplexer_20_out, multiplexer_21_out, multiplexer_22_out;

  Multiplexer #(.select(1), .width(1), .disabled("Z"), .enable("false")) multiplexer_1 (
    .in0(sb), .in1(1'b0), .out(multiplexer_1_out), .sel(flush));
  Multiplexer #(.select(1), .width(1), .disabled("Z"), .enable("false")) multiplexer_2 (
    .in0(LUI), .in1(1'b0), .out(multiplexer_2_out), .sel(flush));
  Multiplexer #(.select(1), .width(1), .disabled("Z"), .enable("false")) multiplexer_3 (
    .in0(Beq), .in1(1'b0), .out(multiplexer_3_out), .sel(flush));
  Multiplexer #(.select(1), .width(1), .disabled("Z"), .enable("false")) multiplexer_4 (
    .in0(Bne), .in1(1'b0), .out(multiplexer_4_out), .sel(flush));
  Multiplexer #(.select(1), .width(1), .disabled("Z"), .enable("false")) multiplexer_5 (
    .in0(MemToReg), .in1(1'b0), .out(multiplexer_5_out), .sel(flush));
  Multiplexer #(.select(1), .width(1), .disabled("Z"), .enable("false")) multiplexer_6 (
    .in0(MemWrite), .in1(1'b0), .out(multiplexer_6_out), .sel(flush));
  Multiplexer #(.select(1), .width(1), .disabled("Z"), .enable("false")) multiplexer_7 (
    .in0(AluSrcB), .in1(1'b0), .out(multiplexer_7_out), .sel(flush));
  Multiplexer #(.select(1), .width(1), .disabled("Z"), .enable("false")) multiplexer_8 (
    .in0(RegWrite), .in1(1'b0), .out(multiplexer_8_out), .sel(flush));
  Multiplexer #(.select(1), .width(1), .disabled("Z"), .enable("false")) multiplexer_9 (
    .in0(ecall), .in1(1'b0), .out(multiplexer_9_out), .sel(flush));
  Multiplexer #(.select(1), .width(1), .disabled("Z"), .enable("false")) multiplexer_10 (
    .in0(Jal), .in1(1'b0), .out(multiplexer_10_out), .sel(flush));
  Multiplexer #(.select(1), .width(1), .disabled("Z"), .enable("false")) multiplexer_11 (
    .in0(Jalr), .in1(1'b0), .out(multiplexer_11_out), .sel(flush));
  Multiplexer #(.select(1), .width(1), .disabled("Z"), .enable("false")) multiplexer_12 (
    .in0(BGEU), .in1(1'b0), .out(multiplexer_12_out), .sel(flush));
  Multiplexer #(.select(1), .width(1), .disabled("Z"), .enable("false")) multiplexer_13 (
    .in0(Uret), .in1(1'b0), .out(multiplexer_13_out), .sel(flush));
  Multiplexer #(.select(1), .width(4), .disabled("Z"), .enable("false")) multiplexer_14 (
    .in0(AluOP), .in1(4'b0000), .out(multiplexer_14_out), .sel(flush));
  Multiplexer #(.select(1), .width(5), .disabled("Z"), .enable("false")) multiplexer_15 (
    .in0(rd), .in1({5{1'b0}}), .out(multiplexer_15_out), .sel(flush));
  Multiplexer #(.select(1), .width(32), .disabled("Z"), .enable("false")) multiplexer_16 (
    .in0(R1), .in1({32{1'b0}}), .out(multiplexer_16_out), .sel(flush));
  Multiplexer #(.select(1), .width(32), .disabled("Z"), .enable("false")) multiplexer_17 (
    .in0(R2), .in1({32{1'b0}}), .out(multiplexer_17_out), .sel(flush));
  Multiplexer #(.select(1), .width(32), .disabled("Z"), .enable("false")) multiplexer_18 (
    .in0(imm_1), .in1({32{1'b0}}), .out(multiplexer_18_out), .sel(flush));
  Multiplexer #(.select(1), .width(32), .disabled("Z"), .enable("false")) multiplexer_19 (
    .in0(imm_2), .in1({32{1'b0}}), .out(multiplexer_19_out), .sel(flush));
  Multiplexer #(.select(1), .width(32), .disabled("Z"), .enable("false")) multiplexer_20 (
    .in0(PC), .in1({32{1'b0}}), .out(multiplexer_20_out), .sel(flush));
  Multiplexer #(.select(1), .width(32), .disabled("Z"), .enable("false")) multiplexer_21 (
    .in0(PC_4), .in1({32{1'b0}}), .out(multiplexer_21_out), .sel(flush));
  Multiplexer #(.select(1), .width(32), .disabled("Z"), .enable("false")) multiplexer_22 (
    .in0(IR), .in1({32{1'b0}}), .out(multiplexer_22_out), .sel(flush));
  Multiplexer #(.select(1), .width(2), .disabled("Z"), .enable("false")) multiplexer_23 (
    .in0(RS1_Forward), .in1(2'b00), .out(multiplexer_23_out), .sel(flush));
  Multiplexer #(.select(1), .width(2), .disabled("Z"), .enable("false")) multiplexer_24 (
    .in0(RS2_Forward), .in1(2'b00), .out(multiplexer_24_out), .sel(flush));
  Multiplexer #(.select(1), .width(1), .disabled("Z"), .enable("false")) multiplexer_25 (
    .in0(ID_PredictJump), .in1(1'b0), .out(multiplexer_25_out), .sel(flush));
  Register #(.width(1), .trigger("rising"), .Select("low")) register_1 (
    .D(multiplexer_1_out), .en(en), .Q(sb_2), .clk(clk));  // open: clr
  Register #(.width(1), .trigger("rising"), .Select("low")) register_2 (
    .D(multiplexer_2_out), .en(en), .Q(LUI_2), .clk(clk));  // open: clr
  Register #(.width(1), .trigger("rising"), .Select("low")) register_3 (
    .D(multiplexer_3_out), .en(en), .Q(Beq_2), .clk(clk));  // open: clr
  Register #(.width(1), .trigger("rising"), .Select("low")) register_4 (
    .D(multiplexer_4_out), .en(en), .Q(Bne_2), .clk(clk));  // open: clr
  Register #(.width(1), .trigger("rising"), .Select("low")) register_5 (
    .D(multiplexer_5_out), .en(en), .Q(MemToReg_2), .clk(clk));  // open: clr
  Register #(.width(1), .trigger("rising"), .Select("low")) register_6 (
    .D(multiplexer_6_out), .en(en), .Q(MemWrite_2), .clk(clk));  // open: clr
  Register #(.width(1), .trigger("rising"), .Select("low")) register_7 (
    .D(multiplexer_7_out), .en(en), .Q(AluSrcB_2), .clk(clk));  // open: clr
  Register #(.width(1), .trigger("rising"), .Select("low")) register_8 (
    .D(multiplexer_8_out), .en(en), .Q(RegWrite_2), .clk(clk));  // open: clr
  Register #(.width(1), .trigger("rising"), .Select("low")) register_9 (
    .D(multiplexer_9_out), .en(en), .Q(ecall_2), .clk(clk));  // open: clr
  Register #(.width(1), .trigger("rising"), .Select("low")) register_10 (
    .D(multiplexer_10_out), .en(en), .Q(Jal_2), .clk(clk));  // open: clr
  Register #(.width(1), .trigger("rising"), .Select("low")) register_11 (
    .D(multiplexer_11_out), .en(en), .Q(Jalr_2), .clk(clk));  // open: clr
  Register #(.width(1), .trigger("rising"), .Select("low")) register_12 (
    .D(multiplexer_12_out), .en(en), .Q(BGEU_2), .clk(clk));  // open: clr
  Register #(.width(1), .trigger("rising"), .Select("low")) register_13 (
    .D(multiplexer_13_out), .Q(Uret_2), .clk(clk));  // open: en, clr
  Register #(.width(4), .trigger("rising"), .Select("low")) register_14 (
    .D(multiplexer_14_out), .en(en), .Q(AluOP_2), .clk(clk));  // open: clr
  Register #(.width(5), .trigger("rising"), .Select("low")) register_15 (
    .D(multiplexer_15_out), .en(en), .Q(rd_2), .clk(clk));  // open: clr
  Register #(.width(32), .trigger("rising"), .Select("low")) register_16 (
    .D(multiplexer_16_out), .en(en), .Q(R1_2), .clk(clk));  // open: clr
  Register #(.width(32), .trigger("rising"), .Select("low")) register_17 (
    .D(multiplexer_17_out), .en(en), .Q(R2_2), .clk(clk));  // open: clr
  Register #(.width(32), .trigger("rising"), .Select("low")) register_18 (
    .D(multiplexer_18_out), .en(en), .Q(imm_1_2), .clk(clk));  // open: clr
  Register #(.width(32), .trigger("rising"), .Select("low")) register_19 (
    .D(multiplexer_19_out), .en(en), .Q(imm_2_2), .clk(clk));  // open: clr
  Register #(.width(32), .trigger("rising"), .Select("low")) register_20 (
    .D(multiplexer_20_out), .en(en), .Q(PC_2), .clk(clk));  // open: clr
  Register #(.width(32), .trigger("rising"), .Select("low")) register_21 (
    .D(multiplexer_21_out), .en(en), .Q(PC_4_2), .clk(clk));  // open: clr
  Register #(.width(32), .trigger("rising"), .Select("low")) register_22 (
    .D(multiplexer_22_out), .en(en), .Q(IR_2), .clk(clk));  // open: clr
  Register #(.width(2), .trigger("rising"), .Select("low")) register_23 (
    .D(multiplexer_23_out), .en(en), .Q(RS1_Forward_2), .clk(clk));  // open: clr
  Register #(.width(2), .trigger("rising"), .Select("low")) register_24 (
    .D(multiplexer_24_out), .en(en), .Q(RS2_Forward_2), .clk(clk));  // open: clr
  Register #(.width(1), .trigger("rising"), .Select("low")) register_25 (
    .D(multiplexer_25_out), .en(en), .Q(EX_PredictJump), .clk(clk));  // open: clr
endmodule

module EX_MEM (
  input  LUI,
  input  Jal,
  input  Jalr,
  input  MemToReg,
  input  MemWrite,
  input  sb,
  input  RegWrite,
  input  halt,
  input  [4:0] rd,
  input  [31:0] Result,
  input  [31:0] WriteData,
  input  [31:0] IR,
  input  [31:0] PC,
  input  [31:0] PC_4,
  input  [31:0] U,
  input  en,
  input  clk,
  output LUI_2,
  output Jal_2,
  output Jalr_2,
  output MemToReg_2,
  output MemWrite_2,
  output sb_2,
  output RegWrite_2,
  output halt_2,
  output [4:0] rd_2,
  output [31:0] Result_2,
  output [31:0] WriteData_2,
  output [31:0] IR_2,
  output [31:0] PC_2,
  output [31:0] PC_4_2,
  output [31:0] U_2
);

  Register #(.width(1), .trigger("rising"), .Select("low")) register_1 (
    .D(LUI), .en(en), .Q(LUI_2), .clk(clk));  // open: clr
  Register #(.width(1), .trigger("rising"), .Select("low")) register_2 (
    .D(Jal), .en(en), .Q(Jal_2), .clk(clk));  // open: clr
  Register #(.width(1), .trigger("rising"), .Select("low")) register_3 (
    .D(Jalr), .en(en), .Q(Jalr_2), .clk(clk));  // open: clr
  Register #(.width(1), .trigger("rising"), .Select("low")) register_4 (
    .D(MemToReg), .en(en), .Q(MemToReg_2), .clk(clk));  // open: clr
  Register #(.width(1), .trigger("rising"), .Select("low")) register_5 (
    .D(MemWrite), .en(en), .Q(MemWrite_2), .clk(clk));  // open: clr
  Register #(.width(1), .trigger("rising"), .Select("low")) register_6 (
    .D(sb), .en(en), .Q(sb_2), .clk(clk));  // open: clr
  Register #(.width(1), .trigger("rising"), .Select("low")) register_7 (
    .D(RegWrite), .en(en), .Q(RegWrite_2), .clk(clk));  // open: clr
  Register #(.width(1), .trigger("rising"), .Select("low")) register_8 (
    .D(halt), .en(en), .Q(halt_2), .clk(clk));  // open: clr
  Register #(.width(5), .trigger("rising"), .Select("low")) register_9 (
    .D(rd), .en(en), .Q(rd_2), .clk(clk));  // open: clr
  Register #(.width(32), .trigger("rising"), .Select("low")) register_10 (
    .D(Result), .en(en), .Q(Result_2), .clk(clk));  // open: clr
  Register #(.width(32), .trigger("rising"), .Select("low")) register_11 (
    .D(WriteData), .en(en), .Q(WriteData_2), .clk(clk));  // open: clr
  Register #(.width(32), .trigger("rising"), .Select("low")) register_12 (
    .D(IR), .en(en), .Q(IR_2), .clk(clk));  // open: clr
  Register #(.width(32), .trigger("rising"), .Select("low")) register_13 (
    .D(PC), .en(en), .Q(PC_2), .clk(clk));  // open: clr
  Register #(.width(32), .trigger("rising"), .Select("low")) register_14 (
    .D(PC_4), .en(en), .Q(PC_4_2), .clk(clk));  // open: clr
  Register #(.width(32), .trigger("rising"), .Select("low")) register_15 (
    .D(U), .en(en), .Q(U_2), .clk(clk));  // open: clr
endmodule

module MEM_WB (
  input  LUI,
  input  Jal,
  input  Jalr,
  input  MemToReg,
  input  RegWrite,
  input  halt,
  input  [4:0] rd,
  input  [31:0] ALUResult,
  input  [31:0] ReadData,
  input  [31:0] IR,
  input  [31:0] PC,
  input  [31:0] PC_4,
  input  [31:0] U,
  input  en,
  input  clk,
  output LUI_2,
  output Jal_2,
  output Jalr_2,
  output MemToReg_2,
  output RegWrite_2,
  output halt_2,
  output [4:0] rd_2,
  output [31:0] ALUResult_2,
  output [31:0] ReadData_2,
  output [31:0] IR_2,
  output [31:0] PC_2,
  output [31:0] PC_4_2,
  output [31:0] U_2
);

  Register #(.width(1), .trigger("rising"), .Select("low")) register_1 (
    .D(LUI), .en(en), .Q(LUI_2), .clk(clk));  // open: clr
  Register #(.width(1), .trigger("rising"), .Select("low")) register_2 (
    .D(Jal), .en(en), .Q(Jal_2), .clk(clk));  // open: clr
  Register #(.width(1), .trigger("rising"), .Select("low")) register_3 (
    .D(Jalr), .en(en), .Q(Jalr_2), .clk(clk));  // open: clr
  Register #(.width(1), .trigger("rising"), .Select("low")) register_4 (
    .D(MemToReg), .en(en), .Q(MemToReg_2), .clk(clk));  // open: clr
  Register #(.width(1), .trigger("rising"), .Select("low")) register_5 (
    .D(RegWrite), .en(en), .Q(RegWrite_2), .clk(clk));  // open: clr
  Register #(.width(1), .trigger("rising"), .Select("low")) register_6 (
    .D(halt), .en(en), .Q(halt_2), .clk(clk));  // open: clr
  Register #(.width(5), .trigger("rising"), .Select("low")) register_7 (.D(rd), .Q(rd_2), .clk(clk));  // open: en, clr
  Register #(.width(32), .trigger("rising"), .Select("low")) register_8 (
    .D(ALUResult), .en(en), .Q(ALUResult_2), .clk(clk));  // open: clr
  Register #(.width(32), .trigger("rising"), .Select("low")) register_9 (
    .D(ReadData), .en(en), .Q(ReadData_2), .clk(clk));  // open: clr
  Register #(.width(32), .trigger("rising"), .Select("low")) register_10 (
    .D(IR), .en(en), .Q(IR_2), .clk(clk));  // open: clr
  Register #(.width(32), .trigger("rising"), .Select("low")) register_11 (
    .D(PC), .en(en), .Q(PC_2), .clk(clk));  // open: clr
  Register #(.width(32), .trigger("rising"), .Select("low")) register_12 (
    .D(PC_4), .en(en), .Q(PC_4_2), .clk(clk));  // open: clr
  Register #(.width(32), .trigger("rising"), .Select("low")) register_13 (
    .D(U), .en(en), .Q(U_2), .clk(clk));  // open: clr
endmodule

module \气泡流水电路  (
  input  BranchTaken,
  input  [31:0] IR,
  input  Ecall,
  input  RS1_used,
  input  EX_RegWrite,
  input  [4:0] EX_rd,
  input  RS2_used,
  input  MEM_RegWrite,
  input  [4:0] MEM_rd,
  output stall,
  output flush
);

  wire and_1_out, and_2_out, and_3_out, and_4_out, and_5_out, and_6_out, comparator_1_eq, comparator_2_eq,
       comparator_3_eq, comparator_4_eq, comparator_5_eq, comparator_6_eq, comparator_7_eq, comparator_8_eq,
       comparator_9_eq, comparator_10_eq, comparator_11_eq, comparator_12_eq, or_1_out, or_2_out;

  Comparator #(.width(5), .mode("twosComplement")) comparator_1 (
    .a({5{1'b0}}), .b(IR[19:15]), .eq(comparator_1_eq));  // open: gt, lt
  Comparator #(.width(5), .mode("twosComplement")) comparator_2 (
    .a(IR[19:15]), .b(EX_rd), .eq(comparator_2_eq));  // open: gt, lt
  Comparator #(.width(5), .mode("twosComplement")) comparator_3 (
    .a({5{1'b0}}), .b(IR[19:15]), .eq(comparator_3_eq));  // open: gt, lt
  Comparator #(.width(5), .mode("twosComplement")) comparator_4 (
    .a(IR[19:15]), .b(MEM_rd), .eq(comparator_4_eq));  // open: gt, lt
  Comparator #(.width(5), .mode("twosComplement")) comparator_5 (
    .a({5{1'b0}}), .b(IR[24:20]), .eq(comparator_5_eq));  // open: gt, lt
  Comparator #(.width(5), .mode("twosComplement")) comparator_6 (
    .a(IR[24:20]), .b(EX_rd), .eq(comparator_6_eq));  // open: gt, lt
  Comparator #(.width(5), .mode("twosComplement")) comparator_7 (
    .a({5{1'b0}}), .b(IR[24:20]), .eq(comparator_7_eq));  // open: gt, lt
  Comparator #(.width(5), .mode("twosComplement")) comparator_8 (
    .a(IR[24:20]), .b(MEM_rd), .eq(comparator_8_eq));  // open: gt, lt
  Comparator #(.width(5), .mode("twosComplement")) comparator_9 (
    .a(5'b10001), .b(EX_rd), .eq(comparator_9_eq));  // open: gt, lt
  or or_1 (or_1_out, comparator_9_eq, comparator_10_eq);
  Comparator #(.width(5), .mode("twosComplement")) comparator_10 (
    .a(EX_rd), .b(5'b01010), .eq(comparator_10_eq));  // open: gt, lt
  Comparator #(.width(5), .mode("twosComplement")) comparator_11 (
    .a(5'b10001), .b(MEM_rd), .eq(comparator_11_eq));  // open: gt, lt
  or or_2 (or_2_out, comparator_11_eq, comparator_12_eq);
  Comparator #(.width(5), .mode("twosComplement")) comparator_12 (
    .a(MEM_rd), .b(5'b01010), .eq(comparator_12_eq));  // open: gt, lt
  and and_1 (and_1_out, RS1_used, ~comparator_1_eq, comparator_2_eq, EX_RegWrite);  // AND_Gate
  and and_2 (and_2_out, RS1_used, ~comparator_3_eq, comparator_4_eq, MEM_RegWrite);  // AND_Gate
  and and_3 (and_3_out, RS2_used, ~comparator_5_eq, comparator_6_eq, EX_RegWrite);  // AND_Gate
  and and_4 (and_4_out, RS2_used, ~comparator_7_eq, comparator_8_eq, MEM_RegWrite);  // AND_Gate
  and and_5 (and_5_out, or_1_out, Ecall);
  and and_6 (and_6_out, Ecall, or_2_out);
  or or_3 (stall, and_1_out, and_2_out, and_3_out, and_4_out, and_5_out, and_6_out);
  or or_4 (flush, stall, BranchTaken);

  // Other names for the same wires on the sheet: DataHazzard = stall; RS1[4:0] = IR[19:15]; RS2[4:0] = IR[24:20]

  // Notes on the sheet:
  //   气泡处理逻辑输入
  //   气泡处理逻辑输出
endmodule

module \重定向电路  (
  input  RS1_used,
  input  EX_RegWrite,
  input  EX_MemToReg,
  input  [31:0] IR,
  input  RS2_used,
  input  MEM_RegWrite,
  input  [4:0] EX_rd,
  input  Ecall,
  input  BranchTaken,
  input  [4:0] MEM_rd,
  input  MEM_LUI,
  input  EX_LUI,
  output [1:0] RS1_Forward,
  output [1:0] RS2_Forward,
  output Stall,
  output Flush
);

  wire and_1_out, and_2_out, and_3_out, and_4_out, and_5_out, and_6_out, and_7_out, and_8_out, and_9_out,
       and_10_out, and_11_out, and_12_out, and_13_out, and_14_out, and_15_out, and_16_out, and_17_out,
       and_18_out, and_23_out, and_24_out, comparator_1_eq, comparator_2_eq, comparator_3_eq,
       comparator_4_eq, comparator_5_eq, comparator_6_eq, comparator_7_eq, comparator_8_eq, comparator_9_eq,
       comparator_10_eq, comparator_11_eq, comparator_12_eq, comparator_13_eq, comparator_14_eq,
       comparator_15_eq, comparator_16_eq, Ecall1, Ecall2, Ecall3, Ecall4, LoadUse, or_3_out, or_5_out;

  Comparator #(.width(5), .mode("twosComplement")) comparator_1 (
    .a(EX_rd), .b(IR[19:15]), .eq(comparator_1_eq));  // open: gt, lt
  Comparator #(.width(5), .mode("twosComplement")) comparator_2 (
    .a(IR[19:15]), .b({5{1'b0}}), .eq(comparator_2_eq));  // open: gt, lt
  Comparator #(.width(5), .mode("twosComplement")) comparator_3 (
    .a({5{1'b0}}), .b(IR[24:20]), .eq(comparator_3_eq));  // open: gt, lt
  Comparator #(.width(5), .mode("twosComplement")) comparator_4 (
    .a(IR[24:20]), .b(EX_rd), .eq(comparator_4_eq));  // open: gt, lt
  Comparator #(.width(5), .mode("twosComplement")) comparator_5 (
    .a(EX_rd), .b(IR[19:15]), .eq(comparator_5_eq));  // open: gt, lt
  Comparator #(.width(5), .mode("twosComplement")) comparator_6 (
    .a(IR[19:15]), .b({5{1'b0}}), .eq(comparator_6_eq));  // open: gt, lt
  Comparator #(.width(5), .mode("twosComplement")) comparator_7 (
    .a({5{1'b0}}), .b(IR[19:15]), .eq(comparator_7_eq));  // open: gt, lt
  Comparator #(.width(5), .mode("twosComplement")) comparator_8 (
    .a(IR[19:15]), .b(MEM_rd), .eq(comparator_8_eq));  // open: gt, lt
  Comparator #(.width(5), .mode("twosComplement")) comparator_9 (
    .a(EX_rd), .b(IR[24:20]), .eq(comparator_9_eq));  // open: gt, lt
  Comparator #(.width(5), .mode("twosComplement")) comparator_10 (
    .a(IR[24:20]), .b({5{1'b0}}), .eq(comparator_10_eq));  // open: gt, lt
  Comparator #(.width(5), .mode("twosComplement")) comparator_11 (
    .a({5{1'b0}}), .b(IR[24:20]), .eq(comparator_11_eq));  // open: gt, lt
  Comparator #(.width(5), .mode("twosComplement")) comparator_12 (
    .a(IR[24:20]), .b(MEM_rd), .eq(comparator_12_eq));  // open: gt, lt
  and and_1 (and_1_out, Ecall, EX_RegWrite);
  and and_2 (and_2_out, Ecall, MEM_RegWrite);
  and and_3 (and_3_out, Ecall, EX_RegWrite);
  and and_4 (and_4_out, Ecall, MEM_RegWrite);
  and and_5 (and_5_out, RS1_used, ~comparator_2_eq);  // AND_Gate
  and and_6 (and_6_out, ~comparator_3_eq, RS2_used);  // AND_Gate
  and and_7 (and_7_out, comparator_5_eq, ~comparator_6_eq);  // AND_Gate
  and and_8 (and_8_out, ~comparator_7_eq, comparator_8_eq);  // AND_Gate
  and and_9 (and_9_out, comparator_9_eq, ~comparator_10_eq);  // AND_Gate
  and and_10 (and_10_out, ~comparator_11_eq, comparator_12_eq);  // AND_Gate
  Comparator #(.width(5), .mode("twosComplement")) comparator_13 (
    .a(EX_rd), .b(5'b10001), .eq(comparator_13_eq));  // open: gt, lt
  Comparator #(.width(5), .mode("twosComplement")) comparator_14 (
    .a(MEM_rd), .b(5'b10001), .eq(comparator_14_eq));  // open: gt, lt
  Comparator #(.width(5), .mode("twosComplement")) comparator_15 (
    .a(EX_rd), .b(5'b01010), .eq(comparator_15_eq));  // open: gt, lt
  Comparator #(.width(5), .mode("twosComplement")) comparator_16 (
    .a(MEM_rd), .b(5'b01010), .eq(comparator_16_eq));  // open: gt, lt
  and and_11 (and_11_out, comparator_1_eq, and_5_out, EX_MemToReg);
  and and_12 (and_12_out, EX_MemToReg, and_6_out, comparator_4_eq);
  and and_13 (and_13_out, and_7_out, and_14_out);
  and and_14 (and_14_out, EX_RegWrite, RS1_used);
  and and_15 (and_15_out, RS1_used, MEM_RegWrite);
  and and_16 (and_16_out, and_15_out, and_8_out);
  and and_17 (and_17_out, EX_RegWrite, RS2_used);
  and and_18 (and_18_out, RS2_used, MEM_RegWrite);
  and and_19 (Ecall1, comparator_13_eq, and_1_out);
  and and_20 (Ecall2, and_2_out, comparator_14_eq);
  and and_21 (Ecall3, comparator_15_eq, and_3_out);
  and and_22 (Ecall4, and_4_out, comparator_16_eq);
  or or_1 (LoadUse, and_11_out, and_12_out);
  or or_2 (RS1_Forward[1], Ecall1, and_13_out);
  or or_3 (or_3_out, and_16_out, Ecall2);
  or or_4 (RS2_Forward[1], Ecall3, and_23_out);
  and and_23 (and_23_out, and_9_out, and_17_out);
  and and_24 (and_24_out, and_18_out, and_10_out);
  or or_5 (or_5_out, and_24_out, Ecall4);
  and and_25 (RS1_Forward[0], ~RS1_Forward[1], or_3_out);  // AND_Gate
  and and_26 (RS2_Forward[0], ~RS2_Forward[1], or_5_out);  // AND_Gate
  or or_6 (Stall, MEM_LUI, LoadUse, EX_LUI);
  or or_7 (Flush, Stall, BranchTaken);

  // Other names for the same wires on the sheet: RS1[4:0] = IR[19:15]; RS2[4:0] = IR[24:20]

  // Notes on the sheet:
  //   LoadUse处理逻辑
  //   寄存器处理逻辑
  //   重定向处理输入
  //   重定向处理输出
endmodule
module \流水线中断  (
  output RegWrite,
  output MemWrite,
  output [31:0] IF_PC,
  output [31:0] ID_PC,
  output [31:0] EX_PC,
  output [31:0] M_PC,
  output [31:0] WB_PC,
  output [31:0] RDin,
  output [31:0] MDin,
  output [31:0] LedData
);

  wire Alu_Src, and_1_out, and_2_out, and_3_out, and_4_out, and_5_out, and_7_out, and_8_out, and_9_out,
       and_10_out, and_11_out, and_12_out, and_13_out, and_14_out, and_15_out, and_20_out, and_21_out,
       and_22_out, and_23_out, and_24_out, AUIPC, Beq, BGEU, Bne, BranchSuc, BranchTaken, CLK, clock_1_out,
       comparator_1_eq, comparator_2_eq, comparator_3_eq, comparator_4_eq, comparator_5_eq, comparator_5_lt,
       comparator_7_eq, counter_2_q, d_ff_1_q, d_ff_2_q, d_ff_3_q, d_ff_4_q, E, ecall, EX_MEM_halt_2,
       EX_MEM_jal_2, EX_MEM_jalr_2, EX_MEM_lui_2, EX_MEM_memtoreg_2, EX_MEM_sb_2, EX_URET, EXRegWrite, flush,
       G, Go, halt, id_ex_1_alusrcb_2, id_ex_1_beq_2, id_ex_1_bgeu_2, id_ex_1_bne_2, id_ex_1_ecall_2,
       id_ex_1_jal_2, id_ex_1_jalr_2, id_ex_1_lui_2, id_ex_1_memtoreg_2, id_ex_1_memwrite_2, id_ex_1_sb_2,
       IE, IF_URET, INT, Interrupt, IR1, IR1_q, IR1_Reset, IR2, IR2_q, IR2_Reset, IR3, IR3_q, IR3_Reset, IRA,
       IRB, IRC, JAL, JALR, MEM_WB_halt_2, MEM_WB_jal_2, MEM_WB_jalr_2, MEM_WB_lui_2, MEM_WB_memtoreg_2,
       MemRegWrite, MemToReg, multiplexer_3_out, nand_1_out, not_1_out, not_2_out, not_3_out, not_4_out,
       not_6_out, not_7_out, not_8_out, or_1_out, or_5_out, or_6_out, or_7_out, or_8_out, or_9_out,
       or_10_out, or_11_out, or_12_out, or_14_out, or_15_out, or_16_out, or_22_out, or_23_out,
       priority_encoder_1_gs, register_1_q, RST, S, S_type, sb, stall, URET, W1, W2, W3,
       \单周期硬布线控制器_1_memwrite , \单周期硬布线控制器_1_regwrite , \单周期硬布线控制器_1_rs1 , \单周期硬布线控制器_1_rs2 , \无条件跳转 ;
  wire [1:0] IR_id, priority_encoder_2_out, priority_encoder_3_out, priority_encoder_4_out, register_5_q,
       RSFL, RSFR, RTFL, RTFR;
  wire [2:0] register_2_q;
  wire [3:0] ALUOP, id_ex_1_aluop_2;
  wire [4:0] EXrd, MEMrd, multiplexer_4_out, multiplexer_5_out, WBrd;
  wire [12:0] CNT_num;
  wire [15:0] \LoadUse次数 , \总周期数 , \插入气泡数 , \无条件分支数 , \条件分支成功数 ;
  wire [31:0] ALUResult, and_16_out, and_17_out, and_18_out, and_19_out, B, bit_extender_1_out,
       bit_extender_2_out, bit_extender_3_out, bit_extender_4_out, bit_extender_5_out, EPC, EX_IR,
       EX_MEM_pc_4_2, EX_MEM_writedata_2, id_ex_1_imm_1_2, id_ex_1_imm_2_2, id_ex_1_pc_4_2, id_ex_1_r1_2,
       id_ex_1_r2_2, ID_IR, IF_ID_pc_4_2, IF_IR, INT_addr, J, MEM_IR, MEM_WB_aluresult_2, MEM_WB_pc_4_2,
       MEM_WB_readdata_2, MEMAL, multiplexer_1_out, multiplexer_6_out, multiplexer_7_out, multiplexer_8_out,
       multiplexer_9_out, multiplexer_10_out, multiplexer_11_out, multiplexer_13_out, or_18_out, or_19_out,
       or_20_out, or_21_out, PC_4, ram_1_data, regifile_1_r1, regifile_1_r2, shifter_1_out, shifter_2_out,
       shifter_3_out, shifter_4_out, shifter_5_out, shifter_6_out, U, WB_IR;

  Button \u_总复位  (.out(RST));
  Button _1 (.out(IR1));
  Button _2 (.out(IR2));
  Button _3 (.out(IR3));
  // Probe on \总周期数 
  // Probe on \总周期数 
  Button \u_继续运行  (.out(Go));
  LED #(.active("true")) led_1 (.in(W1));
  LED #(.active("true")) led_2 (.in(W2));
  LED #(.active("true")) led_3 (.in(W3));
  Hex_Digit_Display hex_digit_display_1 (.value(LedData[31:28]));  // open: dp
  // Probe on IF_PC[19:0]
  // RiscV_Probe riscv_probe_1: pin names not known; wires that end beside it: IF_IR
  Hex_Digit_Display hex_digit_display_2 (.value(LedData[27:24]));  // open: dp
  Hex_Digit_Display hex_digit_display_3 (.value(LedData[23:20]));  // open: dp
  // Probe on ID_PC[19:0]
  // RiscV_Probe riscv_probe_2: pin names not known; wires that end beside it: ID_IR
  Multiplexer #(.select(2), .width(32), .disabled("Z"), .enable("false")) multiplexer_1 (
    .in0(PC_4), .in1(ALUResult), .in2(B), .in3(J), .out(multiplexer_1_out), .sel(priority_encoder_2_out));
  and and_1 (and_1_out, not_2_out, or_1_out);
  or or_1 (or_1_out, not_1_out, Go);
  not not_1 (not_1_out, halt);
  not not_2 (not_2_out, stall);
  LED #(.active("true")) \_1号中断等待指示灯  (.in(W1));
  LED #(.active("true")) \_2号中断等待指示灯  (.in(W2));
  LED #(.active("true")) \_3号中断等待指示灯  (.in(W3));
  Hex_Digit_Display hex_digit_display_4 (.value(LedData[15:12]));  // open: dp
  Hex_Digit_Display hex_digit_display_5 (.value(LedData[19:16]));  // open: dp
  Register #(.width(32), .trigger("rising"), .Select("low")) PC (
    .D(multiplexer_1_out), .en(and_1_out), .Q(IF_PC), .clk(CLK), .clr(RST));
  D_Flip_Flop #(.trigger("rising"), .Pre_Clr_Positions("LEGACY"), .NegatePresetClear("false"), .enable("true"), .NewFFLayout("false")) d_ff_1 (
    .clk(IR1), .D(1'b1), .Q(d_ff_1_q), .reset(IR1_q));  // open: Qn, preset, en
  or or_2 (W1, IR1_q, d_ff_1_q);
  D_Flip_Flop #(.trigger("rising"), .Pre_Clr_Positions("LEGACY"), .NegatePresetClear("false"), .enable("true"), .NewFFLayout("false")) d_ff_2 (
    .clk(IR2), .D(1'b1), .Q(d_ff_2_q), .reset(IR2_q));  // open: Qn, preset, en
  or or_3 (W2, IR2_q, d_ff_2_q);
  D_Flip_Flop #(.trigger("rising"), .Pre_Clr_Positions("LEGACY"), .NegatePresetClear("false"), .enable("true"), .NewFFLayout("false")) d_ff_3 (
    .clk(IR3), .D(1'b1), .Q(d_ff_3_q), .reset(IR3_q));  // open: Qn, preset, en
  or or_4 (W3, IR3_q, d_ff_3_q);
  Comparator #(.width(16), .mode("twosComplement")) comparator_1 (
    .a(16'h23b), .b(\总周期数 ), .eq(comparator_1_eq));  // open: gt, lt
  Comparator #(.width(16), .mode("twosComplement")) comparator_2 (
    .a(\总周期数 ), .b(16'h1), .eq(comparator_2_eq));  // open: gt, lt
  Comparator #(.width(16), .mode("twosComplement")) comparator_3 (
    .a(\总周期数 ), .b(16'h4), .eq(comparator_3_eq));  // open: gt, lt
  Comparator #(.width(16), .mode("twosComplement")) comparator_4 (
    .a(\总周期数 ), .b(16'h7), .eq(comparator_4_eq));  // open: gt, lt
  Hex_Digit_Display hex_digit_display_6 (.value(LedData[11:8]));  // open: dp
  Hex_Digit_Display hex_digit_display_7 (.value(LedData[7:4]));  // open: dp
  // Probe on EX_PC[19:0]
  // RiscV_Probe riscv_probe_3: pin names not known; wires that end beside it: EX_IR
  Adder #(.width(32)) adder_1 (.a(IF_PC), .b(32'h4), .out(PC_4));  // open: cin, cout
  or or_5 (or_5_out, d_ff_1_q, IR1_q);
  or or_6 (or_6_out, d_ff_2_q, IR2_q);
  or or_7 (or_7_out, d_ff_3_q, IR3_q);
  or or_8 (or_8_out, comparator_1_eq, comparator_2_eq);
  Pull_Resistor #(.pull(0)) pull_resistor_1 (.node(IRA));
  assign IRA = or_8_out ? ~CLK : 1'bz;  // Controlled_Inverter controlled_inverter_1
  Pull_Resistor #(.pull(0)) pull_resistor_2 (.node(IRB));
  assign IRB = comparator_3_eq ? ~CLK : 1'bz;  // Controlled_Inverter controlled_inverter_2
  Pull_Resistor #(.pull(0)) pull_resistor_3 (.node(IRC));
  assign IRC = comparator_4_eq ? ~CLK : 1'bz;  // Controlled_Inverter controlled_inverter_3
  Hex_Digit_Display hex_digit_display_8 (.value(LedData[3:0]));  // open: dp
  and and_2 (and_2_out, or_5_out, ~IR1_Reset);  // AND_Gate
  and and_3 (and_3_out, or_6_out, ~IR2_Reset);  // AND_Gate
  and and_4 (and_4_out, or_7_out, ~IR3_Reset);  // AND_Gate
  // Probe on \总周期数 
  // Probe on M_PC[19:0]
  // RiscV_Probe riscv_probe_4: pin names not known; wires that end beside it: MEM_IR
  // RiscV_Probe riscv_probe_5: pin names not known; wires that end beside it: IF_IR
  ROM #(.addrWidth(10), .dataWidth(32), .Select("high")) rom_1 (.addr(IF_PC[11:2]), .data(IF_IR));
  and and_5 (and_5_out, ~stall, or_10_out);  // AND_Gate
  D_Flip_Flop #(.trigger("rising"), .Pre_Clr_Positions("LEGACY"), .NegatePresetClear("false"), .enable("true"), .NewFFLayout("false")) u_IR1 (
    .clk(CLK), .D(and_2_out), .Q(IR1_q), .reset(RST));  // open: Qn, preset, en
  D_Flip_Flop #(.trigger("rising"), .Pre_Clr_Positions("LEGACY"), .NegatePresetClear("false"), .enable("true"), .NewFFLayout("false")) u_IR2 (
    .clk(CLK), .D(and_3_out), .Q(IR2_q), .reset(RST));  // open: Qn, preset, en
  D_Flip_Flop #(.trigger("rising"), .Pre_Clr_Positions("LEGACY"), .NegatePresetClear("false"), .enable("true"), .NewFFLayout("false")) u_IR3 (
    .clk(CLK), .D(and_4_out), .Q(IR3_q), .reset(RST));  // open: Qn, preset, en
  // Probe on \总周期数 
  // Probe on \无条件分支数 
  // Probe on \条件分支成功数 
  // Probe on \插入气泡数 
  // Probe on \LoadUse次数 
  or or_9 (or_9_out, priority_encoder_2_out[1], priority_encoder_2_out[0]);
  or or_10 (or_10_out, ~halt, Go);  // OR_Gate
  // Probe on IF_PC[11:0]
  // Probe on WB_PC[19:0]
  // RiscV_Probe riscv_probe_6: pin names not known; wires that end beside it: WB_IR
  IF_ID IF_ID (
    .IR(IF_IR), .PC(IF_PC), .PC_4(PC_4), .IR_2(ID_IR), .PC_2(ID_PC), .PC_4_2(IF_ID_pc_4_2),
    .branch(or_9_out), .CLK(CLK), .EN(and_5_out));  // open: IF_PredictJump, ID_PredictJump
  Priority_Encoder #(.select(2), .disabled("Z")) priority_encoder_1 (
    .in1(IR1_q), .in2(IR2_q), .in3(IR3_q), .out(IR_id), .gs(priority_encoder_1_gs));  // open: in0, en_out, en_in
  // Probe on EX_PC[11:0]
  // Probe on ID_PC[11:0]
  \重定向电路  \u_重定向电路  (
    .RS1_used(\单周期硬布线控制器_1_rs1 ), .EX_RegWrite(EXRegWrite), .EX_MemToReg(EX_MEM_memtoreg_2), .IR(ID_IR),
    .RS2_used(\单周期硬布线控制器_1_rs2 ), .MEM_RegWrite(MemRegWrite), .EX_rd(EXrd), .Ecall(ecall),
    .BranchTaken(or_9_out), .MEM_rd(MEMrd), .Stall(stall), .Flush(flush), .RS1_Forward(RSFL),
    .RS2_Forward(RTFL), .EX_LUI(1'b0), .MEM_LUI(1'b0));
  Multiplexer #(.select(2), .width(32), .disabled("Z"), .enable("false")) multiplexer_2 (
    .in1(32'h30ac), .in2(32'h3150), .in3(32'h31f4), .out(INT_addr), .sel(IR_id));  // open: in0
  and and_6 (Interrupt, priority_encoder_1_gs, IE);
  Multiplexer #(.select(1), .width(1), .disabled("Z"), .enable("false")) multiplexer_3 (
    .in0(1'b1), .in1(CLK), .out(multiplexer_3_out), .sel(INT));
  // Probe on M_PC[11:0]
  D_Flip_Flop #(.trigger("high"), .Pre_Clr_Positions("LEGACY"), .NegatePresetClear("false"), .enable("true"), .NewFFLayout("false")) d_ff_4 (.Q(d_ff_4_q));  // open: clk, D, Qn, preset, en, reset
  // Probe on 13'hc
  \单周期硬布线控制器  \u_单周期硬布线控制器_1  (
    .Funct({ID_IR[30], ID_IR[25], ID_IR[14:12]}), .OP(ID_IR[6:2]), .ALU_OP(ALUOP), .MemToReg(MemToReg),
    .MemWrite(\单周期硬布线控制器_1_memwrite ), .ALU_SRC(Alu_Src), .RegWrite(\单周期硬布线控制器_1_regwrite ), .ecall(ecall),
    .S_type(S_type), .Jalr(JALR), .Beq(Beq), .JAL(JAL), .Bne(Bne), .in_3(ID_IR[21]), .uret(URET),
    .LUI(AUIPC), .sb(sb), .BGEU(BGEU), .rs1(\单周期硬布线控制器_1_rs1 ), .rs2(\单周期硬布线控制器_1_rs2 ));  // open: CSR
  Multiplexer #(.select(1), .width(5), .disabled("Z"), .enable("false")) multiplexer_4 (
    .in0(ID_IR[19:15]), .in1(5'b10001), .out(multiplexer_4_out), .sel(ecall));
  Multiplexer #(.select(1), .width(5), .disabled("Z"), .enable("false")) multiplexer_5 (
    .in0(ID_IR[24:20]), .in1(5'b01010), .out(multiplexer_5_out), .sel(ecall));
  assign bit_extender_1_out = {{12{ID_IR[31]}}, ID_IR[31:12]};  // Bit_Extender bit_extender_1
  Counter #(.width(1), .max('h1), .ongoal("wrap"), .trigger("rising"), .behavior("new")) counter_1 (
    .D(1'b1), .Q(INT), .clk(Interrupt), .clr(or_11_out));  // open: load, count, carry, preset, down
  or or_11 (or_11_out, RST, counter_2_q);
  Counter #(.width(1), .max('h1), .ongoal("wrap"), .trigger("rising"), .behavior("new")) counter_2 (
    .D(1'b1), .Q(counter_2_q), .clk(multiplexer_3_out), .clr(or_12_out));  // open: load, count, carry, preset, down
  or or_12 (or_12_out, counter_2_q, RST);
  // Probe on WB_PC[11:0]
  Comparator #(.width(13), .mode("twosComplement")) comparator_5 (
    .a(CNT_num), .b(13'hc), .eq(comparator_5_eq), .lt(comparator_5_lt));  // open: gt
  Clock #(.highDuration(1), .lowDuration(1)) clock_1 (.out(clock_1_out));
  assign bit_extender_2_out = {{20{ID_IR[31]}}, ID_IR[31:20]};  // Bit_Extender bit_extender_2
  assign bit_extender_3_out = {{20{ID_IR[31]}}, {ID_IR[31:25], ID_IR[11:7]}};  // Bit_Extender bit_extender_3
  assign bit_extender_4_out = {{20{ID_IR[31]}}, {ID_IR[31], ID_IR[7], ID_IR[30:25], ID_IR[11:8]}};  // Bit_Extender bit_extender_4
  assign bit_extender_5_out = {{12{ID_IR[31]}}, {ID_IR[31], ID_IR[19:12], ID_IR[20], ID_IR[30:21]}};  // Bit_Extender bit_extender_5
  Comparator #(.width(32), .mode("twosComplement")) comparator_6 (
    .a(IF_IR), .b(32'h200073), .eq(IF_URET));  // open: gt, lt
  nand nand_1 (nand_1_out, d_ff_4_q, comparator_5_eq);
  Counter #(.width(13), .max('h1fff), .ongoal("stay"), .trigger("rising"), .behavior("old")) counter_3 (
    .count(comparator_5_lt), .Q(CNT_num), .clk(clock_1_out));  // open: load, D, carry, clr, preset
  not not_3 (not_3_out, CLK);
  Multiplexer #(.select(1), .width(32), .disabled("Z"), .enable("false")) multiplexer_6 (
    .in0(bit_extender_2_out), .in1(bit_extender_3_out), .out(multiplexer_6_out), .sel(S_type));
  assign CLK = nand_1_out ? clock_1_out : 1'bz;  // Controlled_Buffer controlled_buffer_1
  Priority_Encoder #(.select(2), .disabled("Z")) priority_encoder_2 (
    .in0(1'b1), .in1(id_ex_1_jalr_2), .in2(BranchSuc), .in3(id_ex_1_jal_2), .out(priority_encoder_2_out));  // open: gs, en_out, en_in
  Regifile regifile_1 (
    .Din(RDin), .Clk(not_3_out), .R1(regifile_1_r1), .R2(regifile_1_r2), .WE(RegWrite), .W_num(WBrd),
    .R1_num(multiplexer_4_out), .R2_num(multiplexer_5_out));
  Register #(.width(1), .trigger("rising"), .Select("low")) register_1 (
    .D(1'b0), .Q(register_1_q), .clk(not_4_out), .clr(RST), .preset(Interrupt));  // open: en, cs
  not not_4 (not_4_out, IF_URET);
  Register #(.width(1), .trigger("rising"), .Select("low")) register_2 (
    .D(BranchTaken), .Q(register_2_q[0]), .clk(CLK), .clr(RST));  // open: en
  Pull_Resistor #(.pull(1)) pull_resistor_4 (.node(CLK));
  or or_13 (BranchSuc, and_7_out, and_8_out, and_9_out);
  Multiplexer #(.select(2), .width(32), .disabled("Z"), .enable("false")) multiplexer_7 (
    .in0(bit_extender_4_out), .in1(bit_extender_4_out), .in2(bit_extender_5_out), .in3(bit_extender_1_out),
    .out(multiplexer_7_out), .sel(priority_encoder_3_out));
  Priority_Encoder #(.select(2), .disabled("Z")) priority_encoder_3 (
    .in0(1'b1), .in1(or_14_out), .in2(JAL), .in3(AUIPC), .out(priority_encoder_3_out));  // open: gs, en_out, en_in
  or or_14 (or_14_out, and_10_out, and_11_out, and_12_out);
  not not_5 (IE, register_1_q);
  Register #(.width(1), .trigger("rising"), .Select("low")) register_3 (
    .D(stall), .Q(register_2_q[2]), .clk(CLK), .clr(RST));  // open: en
  and and_7 (and_7_out, id_ex_1_bgeu_2, G);
  and and_8 (and_8_out, id_ex_1_beq_2, E);
  not not_6 (not_6_out, E);
  and and_9 (and_9_out, not_6_out, id_ex_1_bne_2);
  and and_10 (and_10_out, BGEU, G);
  and and_11 (and_11_out, Beq, E);
  and and_12 (and_12_out, not_7_out, Bne);
  Register #(.width(1), .trigger("rising"), .Select("low")) register_4 (
    .D(register_2_q[0]), .Q(register_2_q[1]), .clk(CLK), .clr(RST));  // open: en
  ID_EX id_ex_1 (
    .Beq(Beq), .Beq_2(id_ex_1_beq_2), .Bne(Bne), .Bne_2(id_ex_1_bne_2), .MemToReg(MemToReg),
    .MemToReg_2(id_ex_1_memtoreg_2), .MemWrite(\单周期硬布线控制器_1_memwrite ), .MemWrite_2(id_ex_1_memwrite_2),
    .AluSrcB(Alu_Src), .AluSrcB_2(id_ex_1_alusrcb_2), .RegWrite(\单周期硬布线控制器_1_regwrite ),
    .RegWrite_2(EXRegWrite), .ecall(ecall), .ecall_2(id_ex_1_ecall_2), .Jal(JAL), .Jal_2(id_ex_1_jal_2),
    .Jalr(JALR), .Jalr_2(id_ex_1_jalr_2), .BGEU(BGEU), .BGEU_2(id_ex_1_bgeu_2), .Uret(URET),
    .Uret_2(EX_URET), .AluOP(ALUOP), .AluOP_2(id_ex_1_aluop_2), .rd(ID_IR[11:7]), .rd_2(EXrd),
    .R1(regifile_1_r1), .R1_2(id_ex_1_r1_2), .R2(regifile_1_r2), .R2_2(id_ex_1_r2_2),
    .imm_1(multiplexer_6_out), .imm_1_2(id_ex_1_imm_1_2), .imm_2(multiplexer_7_out),
    .imm_2_2(id_ex_1_imm_2_2), .PC(ID_PC), .PC_2(EX_PC), .PC_4(IF_ID_pc_4_2), .PC_4_2(id_ex_1_pc_4_2),
    .IR(ID_IR), .IR_2(EX_IR), .RS1_Forward(RSFL), .RS1_Forward_2(RSFR), .RS2_Forward(RTFL),
    .RS2_Forward_2(RTFR), .en(or_15_out), .clk(CLK), .flush(flush), .sb(sb), .sb_2(id_ex_1_sb_2),
    .LUI(AUIPC), .LUI_2(id_ex_1_lui_2));  // open: ID_PredictJump, EX_PredictJump
  or or_15 (or_15_out, ~halt, Go);  // OR_Gate
  not not_7 (not_7_out, E);
  Register #(.width(2), .trigger("rising"), .Select("low")) register_5 (
    .D(IR_id), .Q(register_5_q), .clk(Interrupt), .clr(RST));  // open: en
  Demultiplexer #(.select(2), .width(1), .tristate("false"), .disabled("Z"), .enable("false")) demultiplexer_1 (
    .out1(IR1_Reset), .out2(IR2_Reset), .out3(IR3_Reset), .in(IF_URET), .sel(register_5_q));  // open: out0
  Multiplexer #(.select(2), .width(32), .disabled("Z"), .enable("false")) multiplexer_8 (
    .in0(id_ex_1_r1_2), .in1(RDin), .in2(MEMAL), .out(multiplexer_8_out), .sel(RSFR));  // open: in3
  Multiplexer #(.select(2), .width(32), .disabled("Z"), .enable("false")) multiplexer_9 (
    .in0(id_ex_1_r2_2), .in1(RDin), .in2(MEMAL), .out(multiplexer_9_out), .sel(RTFR));  // open: in3
  Multiplexer #(.select(3), .width(32), .disabled("Z"), .enable("false")) multiplexer_10 (
    .in0(EX_PC), .in1(IF_PC), .in2(ID_PC), .in4(ID_PC), .out(multiplexer_10_out), .sel(register_2_q));  // open: in3, in5, in6, in7
  and and_13 (and_13_out, ~URET, ~EX_URET);  // AND_Gate
  Register #(.width(32), .trigger("rising"), .Select("low")) u_EPC (
    .D(multiplexer_10_out), .en(and_13_out), .Q(EPC), .clk(Interrupt), .clr(RST));
  Comparator #(.width(32), .mode("twosComplement")) comparator_7 (
    .a(multiplexer_8_out), .b(32'h22), .eq(comparator_7_eq));  // open: gt, lt
  not not_8 (not_8_out, comparator_7_eq);
  and and_14 (and_14_out, id_ex_1_ecall_2, not_8_out);
  Multiplexer #(.select(1), .width(32), .disabled("Z"), .enable("false")) multiplexer_11 (
    .in0(multiplexer_9_out), .in1(id_ex_1_imm_1_2), .out(multiplexer_11_out), .sel(id_ex_1_alusrcb_2));
  Adder #(.width(32)) adder_2 (.a(EX_PC), .b(shifter_1_out), .out(B));  // open: cin, cout
  Shifter #(.width(32), .shift("ll")) shifter_1 (.in(id_ex_1_imm_2_2), .\dist (5'b00001), .out(shifter_1_out));
  Adder #(.width(32)) adder_3 (.a(EX_PC), .b(shifter_2_out), .out(J));  // open: cin, cout
  Shifter #(.width(32), .shift("ll")) shifter_2 (.in(id_ex_1_imm_2_2), .\dist (5'b00001), .out(shifter_2_out));
  Adder #(.width(32)) adder_4 (.a(EX_PC), .b(shifter_3_out), .out(U));  // open: cin, cout
  Shifter #(.width(32), .shift("ll")) shifter_3 (.in(id_ex_1_imm_2_2), .\dist (5'b01100), .out(shifter_3_out));
  and and_15 (and_15_out, comparator_7_eq, id_ex_1_ecall_2);
  ALU alu_1 (
    .X(multiplexer_8_out), .Y(multiplexer_11_out), .AluOP(id_ex_1_aluop_2), .Equal(E), .Result(ALUResult),
    .out_4(G), .out_6(S));  // open: Result_2
  Register #(.width(32), .trigger("rising"), .Select("low")) register_6 (
    .D(multiplexer_9_out), .en(and_15_out), .Q(LedData), .clk(CLK));  // open: clr
  or or_16 (or_16_out, ~halt, Go);  // OR_Gate
  EX_MEM EX_MEM (
    .LUI(id_ex_1_lui_2), .Jal(id_ex_1_jal_2), .Jalr(id_ex_1_jalr_2), .MemToReg(id_ex_1_memtoreg_2),
    .MemWrite(id_ex_1_memwrite_2), .sb(id_ex_1_sb_2), .RegWrite(EXRegWrite), .halt(and_14_out), .rd(EXrd),
    .Result(ALUResult), .WriteData(multiplexer_9_out), .IR(EX_IR), .PC(EX_PC), .PC_4(id_ex_1_pc_4_2),
    .LUI_2(EX_MEM_lui_2), .Jal_2(EX_MEM_jal_2), .Jalr_2(EX_MEM_jalr_2), .MemToReg_2(EX_MEM_memtoreg_2),
    .MemWrite_2(MemWrite), .sb_2(EX_MEM_sb_2), .RegWrite_2(MemRegWrite), .halt_2(EX_MEM_halt_2),
    .rd_2(MEMrd), .Result_2(MEMAL), .WriteData_2(EX_MEM_writedata_2), .IR_2(MEM_IR), .PC_2(M_PC),
    .PC_4_2(EX_MEM_pc_4_2), .clk(CLK), .en(or_16_out));  // open: U, U_2
  or or_17 (\无条件跳转 , id_ex_1_jal_2, id_ex_1_jalr_2);
  Multiplexer #(.select(1), .width(32), .disabled("Z"), .enable("false")) multiplexer_12 (
    .in0(EX_MEM_writedata_2), .in1(multiplexer_13_out), .out(MDin), .sel(EX_MEM_sb_2));
  Multiplexer #(.select(2), .width(32), .disabled("Z"), .enable("false")) multiplexer_13 (
    .in0(or_19_out), .in1(or_20_out), .in2(or_21_out), .in3(or_18_out), .out(multiplexer_13_out),
    .sel(MEMAL[1:0]));
  assign or_18_out = shifter_6_out | and_16_out;  // OR_Gate or_18, 32 bits wide
  assign or_19_out = and_19_out | EX_MEM_writedata_2;  // OR_Gate or_19, 32 bits wide
  assign or_20_out = and_18_out | shifter_4_out;  // OR_Gate or_20, 32 bits wide
  assign or_21_out = and_17_out | shifter_5_out;  // OR_Gate or_21, 32 bits wide
  RAM #(.addrWidth(10), .dataWidth(32), .bus("separate"), .Select("high")) ram_1 (
    .addr(MEMAL[11:2]), .din(MDin), .data(ram_1_data), .str(MemWrite), .sel(1'b1), .clk(CLK), .ld(1'b1));  // open: clr
  assign and_16_out = ram_1_data & 32'hffffff;  // AND_Gate and_16, 32 bits wide
  assign and_17_out = ram_1_data & 32'hff00ffff;  // AND_Gate and_17, 32 bits wide
  assign and_18_out = ram_1_data & 32'hffff00ff;  // AND_Gate and_18, 32 bits wide
  assign and_19_out = ram_1_data & 32'hffffff00;  // AND_Gate and_19, 32 bits wide
  Counter #(.width(16), .max('hffff), .ongoal("wrap"), .trigger("rising"), .behavior("new")) counter_4 (
    .count(BranchSuc), .Q(\条件分支成功数 ), .clk(and_20_out));  // open: load, D, carry, clr, preset, down
  and and_20 (and_20_out, ~halt, CLK);  // AND_Gate
  Counter #(.width(16), .max('hffff), .ongoal("wrap"), .trigger("rising"), .behavior("new")) counter_5 (
    .count(flush), .Q(\插入气泡数 ), .clk(and_21_out));  // open: load, D, carry, clr, preset, down
  and and_21 (and_21_out, ~halt, CLK);  // AND_Gate
  Shifter #(.width(32), .shift("ll")) shifter_4 (.in(EX_MEM_writedata_2), .\dist (5'b01000), .out(shifter_4_out));
  Shifter #(.width(32), .shift("ll")) shifter_5 (.in(EX_MEM_writedata_2), .\dist (5'b10000), .out(shifter_5_out));
  Shifter #(.width(32), .shift("ll")) shifter_6 (.in(EX_MEM_writedata_2), .\dist (5'b11000), .out(shifter_6_out));
  or or_22 (or_22_out, ~halt, Go);  // OR_Gate
  Counter #(.width(16), .max('hffff), .ongoal("wrap"), .trigger("rising"), .behavior("new")) counter_6 (
    .count(\无条件跳转 ), .Q(\无条件分支数 ), .clk(and_22_out));  // open: load, D, carry, clr, preset, down
  and and_22 (and_22_out, ~halt, CLK);  // AND_Gate
  Counter #(.width(16), .max('hffff), .ongoal("wrap"), .trigger("rising"), .behavior("new")) counter_7 (
    .count(CLK), .Q(\总周期数 ), .clk(and_23_out));  // open: load, D, carry, clr, preset, down
  and and_23 (and_23_out, ~halt, CLK);  // AND_Gate
  MEM_WB MEM_WB (
    .LUI(EX_MEM_lui_2), .Jal(EX_MEM_jal_2), .Jalr(EX_MEM_jalr_2), .MemToReg(EX_MEM_memtoreg_2),
    .RegWrite(MemRegWrite), .halt(EX_MEM_halt_2), .rd(MEMrd), .ALUResult(MEMAL), .ReadData(ram_1_data),
    .IR(MEM_IR), .PC(M_PC), .PC_4(EX_MEM_pc_4_2), .LUI_2(MEM_WB_lui_2), .Jal_2(MEM_WB_jal_2),
    .Jalr_2(MEM_WB_jalr_2), .MemToReg_2(MEM_WB_memtoreg_2), .RegWrite_2(RegWrite), .halt_2(MEM_WB_halt_2),
    .rd_2(WBrd), .ALUResult_2(MEM_WB_aluresult_2), .ReadData_2(MEM_WB_readdata_2), .IR_2(WB_IR),
    .PC_2(WB_PC), .PC_4_2(MEM_WB_pc_4_2), .clk(CLK), .en(or_22_out));  // open: U, U_2
  Counter #(.width(16), .max('hffff), .ongoal("wrap"), .trigger("rising"), .behavior("new")) counter_8 (
    .count(stall), .Q(\LoadUse次数 ), .clk(and_24_out));  // open: load, D, carry, clr, preset, down
  and and_24 (and_24_out, ~halt, CLK);  // AND_Gate
  Multiplexer #(.select(2), .width(32), .disabled("Z"), .enable("false")) multiplexer_14 (
    .in0(MEM_WB_aluresult_2), .in1(MEM_WB_readdata_2), .in2(MEM_WB_pc_4_2), .in3(U), .out(RDin),
    .sel(priority_encoder_4_out));
  Priority_Encoder #(.select(2), .disabled("Z")) priority_encoder_4 (
    .in0(1'b1), .in1(MEM_WB_memtoreg_2), .in2(or_23_out), .in3(MEM_WB_lui_2), .out(priority_encoder_4_out));  // open: gs, en_out, en_in
  or or_23 (or_23_out, MEM_WB_jalr_2, MEM_WB_jal_2);
  D_Flip_Flop #(.trigger("rising"), .Pre_Clr_Positions("ABOVE_BELOW"), .NegatePresetClear("false"), .enable("true"), .NewFFLayout("true")) d_ff_5 (
    .clk(MEM_WB_halt_2), .D(1'b1), .Q(halt), .en(1'b1), .reset(Go));  // open: Qn, preset
  // also tied to VCC on the sheet: id_ex_1_jalr_2

  // Other names for the same wires on the sheet: rd[4:0] = ID_IR[11:7]; IR[31:0] = IF_IR; MEM_PC[31:0] = M_PC;
  //   PC[31:0] = IF_PC

  // Notes on the sheet:
  //   中断源
  //   时空图监测，可删除
  //   中断等待指示
  //   单级中断测试信号模拟器
  //   数码管输出
  //   指令存储器
  //   指令探针
  //   contents of rom_1 (hex, n*v repeats v):
  //   7d000113 100413 1f41993 41f9d993 433 c00913 800b13 140413 f47413 800293 100313 499993 89e9b3 1300533
  //   2200893 73 406282b3 fe0294e3 140413 f00f93 1f47433 1c41413 800293 100313 49d993 89e9b3 1300533
  //   2200893 73 406282b3 fe0294e3 1c45413 406b0b33 b0463 f95ff06f 2b3 fff2c293 1029293 fff2e293 500533
  //   2200893 73 f5dff06f 1112023 410113 a12023 410113 812023 410113 1312023 410113 1412023 410113 1512023
  //   410113 1612023 410113 100b13 300a13 100a93 1600433 441413 14469b3 1300533 2200893 73 fe0416e3
  //   415a0a33 fe0a10e3 ffc10113 12b03 ffc10113 12a83 ffc10113 12a03 ffc10113 12983 ffc10113 12403
  //   ffc10113 12503 ffc10113 12883 200073 1112023 410113 a12023 410113 812023 410113 1312023 410113
  //   1412023 410113 1512023 410113 1612023 410113 200b13 300a13 100a93 1600433 441413 14469b3 1300533
  //   2200893 73 fe0416e3 415a0a33 fe0a10e3 ffc10113 12b03 ffc10113 12a83 ffc10113 12a03 ffc10113 12983
  //   ffc10113 12403 ffc10113 12503 ffc10113 12883 200073 1112023 410113 a12023 410113 812023 410113
  //   1312023 410113 1412023 410113 1512023 410113 1612023 410113 300b13 300a13 100a93 1600433 441413
  //   14469b3 1300533 2200893 73 fe0416e3 415a0a33 fe0a10e3 ffc10113 12b03 ffc10113 12a83 ffc10113 12a03
  //   ffc10113 12983 ffc10113 12403 ffc10113 12503 ffc10113 12883 200073
  //   Reset 
  //   Reset 
  //   Reset 
  //   指令字
  //   控制位
  //   流水调试日志用
  //   暂停节拍，不能为0
  //   戳工具置1进入计数暂停模式，ctrl+k时钟自动运行到对应节拍暂停
  //   ctrl+k关闭时钟连续运行，将控制位置零，进入单步调试模式调试
  //   可计数暂停的时钟源
  //   为方便自动评测，需要输出流水线各段保存的PC值，注意是PC不是PC+4，另外ID段寄存器写入信息，Mem段内存写入信息也要输出
  //   数据存储器
endmodule

module \动态分支预测  (
  output RegWrite,
  output MemWrite,
  output [31:0] IF_PC,
  output [31:0] ID_PC,
  output [31:0] EX_PC,
  output [31:0] M_PC,
  output [31:0] WB_PC,
  output [31:0] RDin,
  output [31:0] MDin,
  output [31:0] LedData
);

  wire Alu_Src, and_1_out, and_2_out, and_3_out, and_4_out, and_5_out, and_6_out, and_7_out, and_8_out,
       and_9_out, and_10_out, and_15_out, and_16_out, and_17_out, and_18_out, and_19_out, AUIPC, Beq, BGEU,
       Bne, Branch, BranchSuc, BranchTaken, CLK, clock_1_out, comparator_1_eq, comparator_1_lt,
       comparator_2_eq, d_ff_1_q, E, ecall, EX_Branch, EX_JAL, EX_JALR, EX_MEM_halt_2, EX_MEM_jal_2,
       EX_MEM_jalr_2, EX_MEM_memtoreg_2, EX_MEM_sb_2, EX_PredictJump, EXRegWrite, flush, G, Go, halt,
       id_ex_1_alusrcb_2, id_ex_1_beq_2, id_ex_1_bgeu_2, id_ex_1_bne_2, id_ex_1_ecall_2, id_ex_1_lui_2,
       id_ex_1_memtoreg_2, id_ex_1_memwrite_2, id_ex_1_sb_2, IF_ID_id_predictjump, IF_PredictJump, IR1, IR2,
       IR3, JAL, JALR, MAU, MEM_WB_halt_2, MEM_WB_jal_2, MEM_WB_jalr_2, MEM_WB_lui_2, MEM_WB_memtoreg_2,
       MemRegWrite, MemToReg, nand_1_out, not_1_out, not_2_out, not_3_out, not_4_out, not_5_out, not_6_out,
       or_1_out, or_3_out, or_5_out, or_6_out, or_7_out, or_9_out, or_16_out, or_17_out, PredictError, RST,
       S, S_type, sb, stall, URET, W1, W2, W3, \单周期硬布线控制器_1_memwrite , \单周期硬布线控制器_1_regwrite ,
       \单周期硬布线控制器_1_rs1 , \单周期硬布线控制器_1_rs2 , \无条件跳转 ;
  wire [1:0] priority_encoder_1_out, priority_encoder_2_out, priority_encoder_3_out, RSFL, RSFR, RTFL, RTFR;
  wire [3:0] ALUOP, id_ex_1_aluop_2;
  wire [4:0] EXrd, MEMrd, multiplexer_5_out, multiplexer_6_out, WBrd;
  wire [12:0] CNT_num;
  wire [15:0] \LoadUse次数 , \总周期数 , \插入气泡数 , \无条件分支数 , \条件分支成功数 ;
  wire [31:0] adder_1_out, ALU_addr, ALUResult, and_11_out, and_12_out, and_13_out, and_14_out, B,
       bhb_1_predictaddr, bit_extender_1_out, bit_extender_2_out, bit_extender_3_out, bit_extender_4_out,
       bit_extender_5_out, EX_IR, EX_MEM_pc_4_2, EX_MEM_writedata_2, id_ex_1_imm_1_2, id_ex_1_imm_2_2,
       id_ex_1_pc_4_2, id_ex_1_r1_2, id_ex_1_r2_2, ID_IR, IF_ID_pc_4_2, IF_IR, J, MEM_IR, MEM_WB_aluresult_2,
       MEM_WB_pc_4_2, MEM_WB_readdata_2, MEM_WB_u_2, MEMAL, MU, multiplexer_1_out, multiplexer_2_out,
       multiplexer_3_out, multiplexer_4_out, multiplexer_8_out, multiplexer_9_out, multiplexer_10_out,
       multiplexer_11_out, multiplexer_12_out, multiplexer_13_out, multiplexer_15_out, or_12_out, or_13_out,
       or_14_out, or_15_out, PC_4, PredictAddr, ram_1_data, regifile_1_r1, regifile_1_r2, shifter_1_out,
       shifter_2_out, shifter_3_out, shifter_4_out, shifter_5_out, shifter_6_out, U, WB_IR;

  Button \u_总复位  (.out(RST));
  Button _1 (.out(IR1));
  Button _2 (.out(IR2));
  Button _3 (.out(IR3));
  // Probe on \总周期数 
  // Probe on \总周期数 
  Button \u_继续运行  (.out(Go));
  LED #(.active("true")) led_1 (.in(W1));
  LED #(.active("true")) led_2 (.in(W2));
  LED #(.active("true")) led_3 (.in(W3));
  Hex_Digit_Display hex_digit_display_1 (.value(LedData[31:28]));  // open: dp
  // Probe on IF_PC[19:0]
  // RiscV_Probe riscv_probe_1: pin names not known; wires that end beside it: IF_IR
  Adder #(.width(32)) adder_1 (.a(EX_PC), .b(32'h4), .out(adder_1_out));  // open: cin, cout
  Hex_Digit_Display hex_digit_display_2 (.value(LedData[23:20]));  // open: dp
  Hex_Digit_Display hex_digit_display_3 (.value(LedData[27:24]));  // open: dp
  // Probe on ID_PC[19:0]
  // RiscV_Probe riscv_probe_2: pin names not known; wires that end beside it: ID_IR
  Multiplexer #(.select(2), .width(32), .disabled("Z"), .enable("false")) multiplexer_1 (
    .in0(adder_1_out), .in1(ALUResult), .in2(B), .in3(J), .out(multiplexer_1_out),
    .sel(priority_encoder_1_out));
  and and_1 (and_1_out, not_2_out, or_1_out);
  or or_1 (or_1_out, not_1_out, Go);
  not not_1 (not_1_out, halt);
  not not_2 (not_2_out, stall);
  Hex_Digit_Display hex_digit_display_4 (.value(LedData[19:16]));  // open: dp
  Hex_Digit_Display hex_digit_display_5 (.value(LedData[15:12]));  // open: dp
  // Probe on PredictAddr
  Register #(.width(32), .trigger("rising"), .Select("low")) PC (
    .D(multiplexer_2_out), .en(and_1_out), .Q(IF_PC), .clk(CLK), .clr(RST));
  Hex_Digit_Display hex_digit_display_6 (.value(LedData[7:4]));  // open: dp
  Hex_Digit_Display hex_digit_display_7 (.value(LedData[11:8]));  // open: dp
  // Probe on EX_PC[19:0]
  // RiscV_Probe riscv_probe_3: pin names not known; wires that end beside it: EX_IR
  Multiplexer #(.select(1), .width(32), .disabled("Z"), .enable("false")) multiplexer_2 (
    .in0(PredictAddr), .in1(multiplexer_1_out), .out(multiplexer_2_out), .sel(PredictError));
  Adder #(.width(32)) adder_2 (.a(IF_PC), .b(32'h4), .out(PC_4));  // open: cin, cout
  Hex_Digit_Display hex_digit_display_8 (.value(LedData[3:0]));  // open: dp
  // Probe on \总周期数 
  // Probe on M_PC[19:0]
  // RiscV_Probe riscv_probe_4: pin names not known; wires that end beside it: MEM_IR
  // RiscV_Probe riscv_probe_5: pin names not known; wires that end beside it: IF_IR
  ROM #(.addrWidth(10), .dataWidth(32), .Select("high")) rom_1 (.addr(IF_PC[11:2]), .data(IF_IR));
  and and_2 (and_2_out, ~stall, or_3_out);  // AND_Gate
  // Probe on \总周期数 
  // Probe on \无条件分支数 
  // Probe on \条件分支成功数 
  // Probe on \插入气泡数 
  // Probe on \LoadUse次数 
  or or_2 (BranchTaken, priority_encoder_1_out[1], priority_encoder_1_out[0]);
  or or_3 (or_3_out, ~halt, Go);  // OR_Gate
  Multiplexer #(.select(2), .width(32), .disabled("Z"), .enable("false")) multiplexer_3 (
    .in0(IF_PC), .in1(ALU_addr), .in2(J), .out(multiplexer_3_out), .sel({EX_JAL, EX_JALR}));  // open: in3
  // Probe on IF_PC[11:0]
  // Probe on WB_PC[19:0]
  // RiscV_Probe riscv_probe_6: pin names not known; wires that end beside it: WB_IR
  IF_ID IF_ID (
    .IR(IF_IR), .PC(IF_PC), .PC_4(PC_4), .IR_2(ID_IR), .PC_2(ID_PC), .PC_4_2(IF_ID_pc_4_2),
    .branch(PredictError), .CLK(CLK), .EN(and_2_out), .IF_PredictJump(IF_PredictJump),
    .ID_PredictJump(IF_ID_id_predictjump));
  Multiplexer #(.select(1), .width(32), .disabled("Z"), .enable("false")) multiplexer_4 (
    .in0(multiplexer_3_out), .in1(J), .out(multiplexer_4_out), .sel(Branch));
  // Probe on EX_PC[11:0]
  // Probe on ID_PC[11:0]
  \重定向电路  \u_重定向电路  (
    .RS1_used(\单周期硬布线控制器_1_rs1 ), .EX_RegWrite(EXRegWrite), .EX_MemToReg(EX_MEM_memtoreg_2), .IR(ID_IR),
    .RS2_used(\单周期硬布线控制器_1_rs2 ), .MEM_RegWrite(MemRegWrite), .EX_rd(EXrd), .Ecall(ecall),
    .BranchTaken(BranchTaken), .MEM_rd(MEMrd), .Stall(stall), .Flush(flush), .RS1_Forward(RSFL),
    .RS2_Forward(RTFL), .EX_LUI(1'b0), .MEM_LUI(1'b0));
  // Probe on M_PC[11:0]
  D_Flip_Flop #(.trigger("high"), .Pre_Clr_Positions("LEGACY"), .NegatePresetClear("false"), .enable("true"), .NewFFLayout("false")) d_ff_1 (.Q(d_ff_1_q));  // open: clk, D, Qn, preset, en, reset
  // Probe on 13'hc
  \单周期硬布线控制器  \u_单周期硬布线控制器_1  (
    .Funct({ID_IR[30], ID_IR[25], ID_IR[14:12]}), .OP(ID_IR[6:2]), .ALU_OP(ALUOP), .MemToReg(MemToReg),
    .MemWrite(\单周期硬布线控制器_1_memwrite ), .ALU_SRC(Alu_Src), .RegWrite(\单周期硬布线控制器_1_regwrite ), .ecall(ecall),
    .S_type(S_type), .Jalr(JALR), .Beq(Beq), .JAL(JAL), .Bne(Bne), .in_3(ID_IR[21]), .uret(URET),
    .LUI(AUIPC), .sb(sb), .BGEU(BGEU), .rs1(\单周期硬布线控制器_1_rs1 ), .rs2(\单周期硬布线控制器_1_rs2 ));  // open: CSR
  Multiplexer #(.select(1), .width(5), .disabled("Z"), .enable("false")) multiplexer_5 (
    .in0(ID_IR[19:15]), .in1(5'b10001), .out(multiplexer_5_out), .sel(ecall));
  Multiplexer #(.select(1), .width(5), .disabled("Z"), .enable("false")) multiplexer_6 (
    .in0(ID_IR[24:20]), .in1(5'b01010), .out(multiplexer_6_out), .sel(ecall));
  assign bit_extender_1_out = {{12{ID_IR[31]}}, ID_IR[31:12]};  // Bit_Extender bit_extender_1
  BHB bhb_1 (
    .IF_PC(IF_PC), .EX_PC(EX_PC), .EX_BranchAddr(multiplexer_4_out), .BranchTaken(BranchTaken),
    .EX_Branch(EX_Branch), .clk(CLK), .PredictAddr(bhb_1_predictaddr), .ID_PredictJump(IF_PredictJump));
  // Probe on WB_PC[11:0]
  Comparator #(.width(13), .mode("twosComplement")) comparator_1 (
    .a(CNT_num), .b(13'hc), .eq(comparator_1_eq), .lt(comparator_1_lt));  // open: gt
  Clock #(.highDuration(1), .lowDuration(1)) clock_1 (.out(clock_1_out));
  assign bit_extender_2_out = {{20{ID_IR[31]}}, ID_IR[31:20]};  // Bit_Extender bit_extender_2
  assign bit_extender_3_out = {{20{ID_IR[31]}}, {ID_IR[31:25], ID_IR[11:7]}};  // Bit_Extender bit_extender_3
  assign bit_extender_4_out = {{20{ID_IR[31]}}, {ID_IR[31], ID_IR[7], ID_IR[30:25], ID_IR[11:8]}};  // Bit_Extender bit_extender_4
  assign bit_extender_5_out = {{12{ID_IR[31]}}, {ID_IR[31], ID_IR[19:12], ID_IR[20], ID_IR[30:21]}};  // Bit_Extender bit_extender_5
  Multiplexer #(.select(1), .width(32), .disabled("Z"), .enable("false")) multiplexer_7 (
    .in0(PC_4), .in1(bhb_1_predictaddr), .out(PredictAddr), .sel(IF_PredictJump));
  nand nand_1 (nand_1_out, d_ff_1_q, comparator_1_eq);
  Counter #(.width(13), .max('h1fff), .ongoal("stay"), .trigger("rising"), .behavior("old")) counter_1 (
    .count(comparator_1_lt), .Q(CNT_num), .clk(clock_1_out));  // open: load, D, carry, clr, preset
  not not_3 (not_3_out, CLK);
  Multiplexer #(.select(1), .width(32), .disabled("Z"), .enable("false")) multiplexer_8 (
    .in0(bit_extender_2_out), .in1(bit_extender_3_out), .out(multiplexer_8_out), .sel(S_type));
  assign CLK = nand_1_out ? clock_1_out : 1'bz;  // Controlled_Buffer controlled_buffer_1
  Priority_Encoder #(.select(2), .disabled("Z")) priority_encoder_1 (
    .in0(1'b1), .in1(EX_JALR), .in2(BranchSuc), .in3(EX_JAL), .out(priority_encoder_1_out));  // open: gs, en_out, en_in
  Regifile regifile_1 (
    .Din(RDin), .Clk(not_3_out), .R1(regifile_1_r1), .R2(regifile_1_r2), .WE(RegWrite), .W_num(WBrd),
    .R1_num(multiplexer_5_out), .R2_num(multiplexer_6_out));
  // RiscV_Probe riscv_probe_7: pin names not known; wires that end beside it: ID_IR
  Pull_Resistor #(.pull(1)) pull_resistor_1 (.node(CLK));
  or or_4 (BranchSuc, and_3_out, and_4_out, and_5_out);
  or or_5 (or_5_out, stall, PredictError);
  Multiplexer #(.select(2), .width(32), .disabled("Z"), .enable("false")) multiplexer_9 (
    .in0(bit_extender_4_out), .in1(bit_extender_4_out), .in2(bit_extender_5_out), .in3(bit_extender_1_out),
    .out(multiplexer_9_out), .sel(priority_encoder_2_out));
  Priority_Encoder #(.select(2), .disabled("Z")) priority_encoder_2 (
    .in0(1'b1), .in1(or_6_out), .in2(JAL), .in3(AUIPC), .out(priority_encoder_2_out));  // open: gs, en_out, en_in
  or or_6 (or_6_out, and_6_out, and_7_out, and_8_out);
  and and_3 (and_3_out, id_ex_1_bgeu_2, G);
  and and_4 (and_4_out, id_ex_1_beq_2, E);
  not not_4 (not_4_out, E);
  and and_5 (and_5_out, not_4_out, id_ex_1_bne_2);
  and and_6 (and_6_out, BGEU, G);
  and and_7 (and_7_out, Beq, E);
  and and_8 (and_8_out, not_5_out, Bne);
  ID_EX id_ex_1 (
    .Beq(Beq), .Beq_2(id_ex_1_beq_2), .Bne(Bne), .Bne_2(id_ex_1_bne_2), .MemToReg(MemToReg),
    .MemToReg_2(id_ex_1_memtoreg_2), .MemWrite(\单周期硬布线控制器_1_memwrite ), .MemWrite_2(id_ex_1_memwrite_2),
    .AluSrcB(Alu_Src), .AluSrcB_2(id_ex_1_alusrcb_2), .RegWrite(\单周期硬布线控制器_1_regwrite ),
    .RegWrite_2(EXRegWrite), .ecall(ecall), .ecall_2(id_ex_1_ecall_2), .Jal(JAL), .Jal_2(EX_JAL),
    .Jalr(JALR), .Jalr_2(EX_JALR), .BGEU(BGEU), .BGEU_2(id_ex_1_bgeu_2), .Uret(URET), .AluOP(ALUOP),
    .AluOP_2(id_ex_1_aluop_2), .rd(ID_IR[11:7]), .rd_2(EXrd), .R1(regifile_1_r1), .R1_2(id_ex_1_r1_2),
    .R2(regifile_1_r2), .R2_2(id_ex_1_r2_2), .imm_1(multiplexer_8_out), .imm_1_2(id_ex_1_imm_1_2),
    .imm_2(multiplexer_9_out), .imm_2_2(id_ex_1_imm_2_2), .PC(ID_PC), .PC_2(EX_PC), .PC_4(IF_ID_pc_4_2),
    .PC_4_2(id_ex_1_pc_4_2), .IR(ID_IR), .IR_2(EX_IR), .RS1_Forward(RSFL), .RS1_Forward_2(RSFR),
    .RS2_Forward(RTFL), .RS2_Forward_2(RTFR), .ID_PredictJump(IF_ID_id_predictjump),
    .EX_PredictJump(EX_PredictJump), .en(or_7_out), .clk(CLK), .flush(or_5_out), .sb(sb),
    .sb_2(id_ex_1_sb_2), .LUI(AUIPC), .LUI_2(id_ex_1_lui_2));  // open: Uret_2
  or or_7 (or_7_out, ~halt, Go);  // OR_Gate
  not not_5 (not_5_out, E);
  Multiplexer #(.select(2), .width(32), .disabled("Z"), .enable("false")) multiplexer_10 (
    .in0(id_ex_1_r1_2), .in1(RDin), .in2(multiplexer_12_out), .out(multiplexer_10_out), .sel(RSFR));  // open: in3
  Multiplexer #(.select(2), .width(32), .disabled("Z"), .enable("false")) multiplexer_11 (
    .in0(id_ex_1_r2_2), .in1(RDin), .in2(multiplexer_12_out), .out(multiplexer_11_out), .sel(RTFR));  // open: in3
  Multiplexer #(.select(1), .width(32), .disabled("Z"), .enable("false")) multiplexer_12 (
    .in0(MEMAL), .in1(MU), .out(multiplexer_12_out), .sel(MAU));
  xor xor_1 (PredictError, BranchTaken, EX_PredictJump);
  or or_8 (Branch, id_ex_1_bgeu_2, id_ex_1_beq_2, id_ex_1_bne_2);
  Comparator #(.width(32), .mode("twosComplement")) comparator_2 (
    .a(multiplexer_10_out), .b(32'h22), .eq(comparator_2_eq));  // open: gt, lt
  not not_6 (not_6_out, comparator_2_eq);
  and and_9 (and_9_out, id_ex_1_ecall_2, not_6_out);
  Multiplexer #(.select(1), .width(32), .disabled("Z"), .enable("false")) multiplexer_13 (
    .in0(multiplexer_11_out), .in1(id_ex_1_imm_1_2), .out(multiplexer_13_out), .sel(id_ex_1_alusrcb_2));
  // RiscV_Probe riscv_probe_8: pin names not known; wires that end beside it: EX_IR
  Adder #(.width(32)) adder_3 (.a(EX_PC), .b(shifter_1_out), .out(B));  // open: cin, cout
  Shifter #(.width(32), .shift("ll")) shifter_1 (.in(id_ex_1_imm_2_2), .\dist (5'b00001), .out(shifter_1_out));
  Adder #(.width(32)) adder_4 (.a(EX_PC), .b(shifter_2_out), .out(J));  // open: cin, cout
  Shifter #(.width(32), .shift("ll")) shifter_2 (.in(id_ex_1_imm_2_2), .\dist (5'b00001), .out(shifter_2_out));
  Adder #(.width(32)) adder_5 (.a(EX_PC), .b(shifter_3_out), .out(U));  // open: cin, cout
  Shifter #(.width(32), .shift("ll")) shifter_3 (.in(id_ex_1_imm_2_2), .\dist (5'b01100), .out(shifter_3_out));
  and and_10 (and_10_out, comparator_2_eq, id_ex_1_ecall_2);
  ALU alu_1 (
    .X(multiplexer_10_out), .Y(multiplexer_13_out), .AluOP(id_ex_1_aluop_2), .Equal(E), .Result(ALUResult),
    .out_4(G), .out_6(S));  // open: Result_2
  Register #(.width(32), .trigger("rising"), .Select("low")) register_1 (
    .D(multiplexer_11_out), .en(and_10_out), .Q(LedData), .clk(CLK));  // open: clr
  or or_9 (or_9_out, ~halt, Go);  // OR_Gate
  or or_10 (EX_Branch, EX_JAL, EX_JALR, Branch);
  EX_MEM EX_MEM (
    .LUI(id_ex_1_lui_2), .Jal(EX_JAL), .Jalr(EX_JALR), .MemToReg(id_ex_1_memtoreg_2),
    .MemWrite(id_ex_1_memwrite_2), .sb(id_ex_1_sb_2), .RegWrite(EXRegWrite), .halt(and_9_out), .rd(EXrd),
    .Result(ALUResult), .WriteData(multiplexer_11_out), .IR(EX_IR), .PC(EX_PC), .PC_4(id_ex_1_pc_4_2),
    .LUI_2(MAU), .Jal_2(EX_MEM_jal_2), .Jalr_2(EX_MEM_jalr_2), .MemToReg_2(EX_MEM_memtoreg_2),
    .MemWrite_2(MemWrite), .sb_2(EX_MEM_sb_2), .RegWrite_2(MemRegWrite), .halt_2(EX_MEM_halt_2),
    .rd_2(MEMrd), .Result_2(MEMAL), .WriteData_2(EX_MEM_writedata_2), .IR_2(MEM_IR), .PC_2(M_PC),
    .PC_4_2(EX_MEM_pc_4_2), .clk(CLK), .en(or_9_out), .U(U), .U_2(MU));
  or or_11 (\无条件跳转 , EX_JAL, EX_JALR);
  Multiplexer #(.select(1), .width(32), .disabled("Z"), .enable("false")) multiplexer_14 (
    .in0(EX_MEM_writedata_2), .in1(multiplexer_15_out), .out(MDin), .sel(EX_MEM_sb_2));
  Multiplexer #(.select(2), .width(32), .disabled("Z"), .enable("false")) multiplexer_15 (
    .in0(or_13_out), .in1(or_14_out), .in2(or_15_out), .in3(or_12_out), .out(multiplexer_15_out),
    .sel(MEMAL[1:0]));
  assign or_12_out = shifter_6_out | and_11_out;  // OR_Gate or_12, 32 bits wide
  // RiscV_Probe riscv_probe_9: pin names not known; wires that end beside it: MEM_IR
  assign or_13_out = and_14_out | EX_MEM_writedata_2;  // OR_Gate or_13, 32 bits wide
  assign or_14_out = and_13_out | shifter_4_out;  // OR_Gate or_14, 32 bits wide
  assign or_15_out = and_12_out | shifter_5_out;  // OR_Gate or_15, 32 bits wide
  RAM #(.addrWidth(10), .dataWidth(32), .bus("separate"), .Select("high")) ram_1 (
    .addr(MEMAL[11:2]), .din(MDin), .data(ram_1_data), .str(MemWrite), .sel(1'b1), .clk(CLK), .ld(1'b1));  // open: clr
  assign and_11_out = ram_1_data & 32'hffffff;  // AND_Gate and_11, 32 bits wide
  assign and_12_out = ram_1_data & 32'hff00ffff;  // AND_Gate and_12, 32 bits wide
  assign and_13_out = ram_1_data & 32'hffff00ff;  // AND_Gate and_13, 32 bits wide
  assign and_14_out = ram_1_data & 32'hffffff00;  // AND_Gate and_14, 32 bits wide
  Counter #(.width(16), .max('hffff), .ongoal("wrap"), .trigger("rising"), .behavior("new")) counter_2 (
    .count(BranchSuc), .Q(\条件分支成功数 ), .clk(and_15_out));  // open: load, D, carry, clr, preset, down
  and and_15 (and_15_out, ~halt, CLK);  // AND_Gate
  Counter #(.width(16), .max('hffff), .ongoal("wrap"), .trigger("rising"), .behavior("new")) counter_3 (
    .count(flush), .Q(\插入气泡数 ), .clk(and_16_out));  // open: load, D, carry, clr, preset, down
  and and_16 (and_16_out, ~halt, CLK);  // AND_Gate
  Shifter #(.width(32), .shift("ll")) shifter_4 (.in(EX_MEM_writedata_2), .\dist (5'b01000), .out(shifter_4_out));
  Shifter #(.width(32), .shift("ll")) shifter_5 (.in(EX_MEM_writedata_2), .\dist (5'b10000), .out(shifter_5_out));
  Shifter #(.width(32), .shift("ll")) shifter_6 (.in(EX_MEM_writedata_2), .\dist (5'b11000), .out(shifter_6_out));
  or or_16 (or_16_out, ~halt, Go);  // OR_Gate
  Counter #(.width(16), .max('hffff), .ongoal("wrap"), .trigger("rising"), .behavior("new")) counter_4 (
    .count(\无条件跳转 ), .Q(\无条件分支数 ), .clk(and_17_out));  // open: load, D, carry, clr, preset, down
  and and_17 (and_17_out, ~halt, CLK);  // AND_Gate
  Counter #(.width(16), .max('hffff), .ongoal("wrap"), .trigger("rising"), .behavior("new")) counter_5 (
    .count(CLK), .Q(\总周期数 ), .clk(and_18_out));  // open: load, D, carry, clr, preset, down
  and and_18 (and_18_out, ~halt, CLK);  // AND_Gate
  MEM_WB MEM_WB (
    .LUI(MAU), .Jal(EX_MEM_jal_2), .Jalr(EX_MEM_jalr_2), .MemToReg(EX_MEM_memtoreg_2),
    .RegWrite(MemRegWrite), .halt(EX_MEM_halt_2), .rd(MEMrd), .ALUResult(MEMAL), .ReadData(ram_1_data),
    .IR(MEM_IR), .PC(M_PC), .PC_4(EX_MEM_pc_4_2), .LUI_2(MEM_WB_lui_2), .Jal_2(MEM_WB_jal_2),
    .Jalr_2(MEM_WB_jalr_2), .MemToReg_2(MEM_WB_memtoreg_2), .RegWrite_2(RegWrite), .halt_2(MEM_WB_halt_2),
    .rd_2(WBrd), .ALUResult_2(MEM_WB_aluresult_2), .ReadData_2(MEM_WB_readdata_2), .IR_2(WB_IR),
    .PC_2(WB_PC), .PC_4_2(MEM_WB_pc_4_2), .clk(CLK), .en(or_16_out), .U(MU), .U_2(MEM_WB_u_2));
  Counter #(.width(16), .max('hffff), .ongoal("wrap"), .trigger("rising"), .behavior("new")) counter_6 (
    .count(stall), .Q(\LoadUse次数 ), .clk(and_19_out));  // open: load, D, carry, clr, preset, down
  and and_19 (and_19_out, ~halt, CLK);  // AND_Gate
  Multiplexer #(.select(2), .width(32), .disabled("Z"), .enable("false")) multiplexer_16 (
    .in0(MEM_WB_aluresult_2), .in1(MEM_WB_readdata_2), .in2(MEM_WB_pc_4_2), .in3(MEM_WB_u_2), .out(RDin),
    .sel(priority_encoder_3_out));
  Priority_Encoder #(.select(2), .disabled("Z")) priority_encoder_3 (
    .in0(1'b1), .in1(MEM_WB_memtoreg_2), .in2(or_17_out), .in3(MEM_WB_lui_2), .out(priority_encoder_3_out));  // open: gs, en_out, en_in
  // RiscV_Probe riscv_probe_10: pin names not known; wires that end beside it: WB_IR
  or or_17 (or_17_out, MEM_WB_jalr_2, MEM_WB_jal_2);
  D_Flip_Flop #(.trigger("rising"), .Pre_Clr_Positions("ABOVE_BELOW"), .NegatePresetClear("false"), .enable("true"), .NewFFLayout("true")) d_ff_2 (
    .clk(MEM_WB_halt_2), .D(1'b1), .Q(halt), .en(1'b1), .reset(Go));  // open: Qn, preset

  // Other names for the same wires on the sheet: rd[4:0] = ID_IR[11:7]; IR[31:0] = IF_IR; MEM_PC[31:0] = M_PC;
  //   PC[31:0] = IF_PC

  // Notes on the sheet:
  //   中断源
  //   时空图监测，可删除
  //   中断等待指示
  //   数码管输出
  //   指令存储器
  //   指令探针
  //   contents of rom_1 (hex, n*v repeats v):
  //   100493 100006f 100493 200913 300993 100006f 100493 200913 300993 100006f 100493 200913 300993
  //   100006f 100493 200913 300993 3b4000ef 100413 100493 1f49493 900533 2200893 73 24d493 48463 fedff06f
  //   900533 2200893 73 100493 249493 900533 2200893 73 48463 fedff06f 100493 1f49493 900533 2200893 73
  //   4034d493 900533 2200893 73 4044d493 900533 2200893 73 4044d493 900533 2200893 73 4044d493 900533
  //   2200893 73 4044d493 900533 2200893 73 4044d493 900533 2200893 73 4044d493 900533 2200893 73 4044d493
  //   900533 2200893 73 100413 1f41993 41f9d993 433 c00913 300b13 140413 f47413 800293 100313 499993
  //   89e9b3 1300533 2200893 73 406282b3 fe0294e3 140413 f00f93 1f47433 1c41413 800293 100313 49d993
  //   89e9b3 1300533 2200893 73 406282b3 fe0294e3 1c45413 406b0b33 b0463 f95ff06f 2b3 fff2c293 829293
  //   ff2e293 500533 2200893 73 fff00413 493 84a023 140413 448493 84a023 140413 448493 84a023 140413
  //   448493 84a023 140413 448493 84a023 140413 448493 84a023 140413 448493 84a023 140413 448493 84a023
  //   140413 448493 84a023 140413 448493 84a023 140413 448493 84a023 140413 448493 84a023 140413 448493
  //   84a023 140413 448493 84a023 140413 448493 84a023 140413 448493 84a023 140413 448493 140413 433
  //   3c00493 42983 4aa03 149a2b3 28663 134a023 1442023 ffc48493 fe9412e3 800533 2200893 73 440413 3c00493
  //   fc9416e3 a00893 73 fff00293 7700493 849493 7748493 900533 2200893 73 1000e13 54c4b3 900533 2200893
  //   73 fffe0e13 fe0e16e3 a00893 73 800e13 fedc04b7 fff00413 1045413 84e4b3 900533 2200893 73 ba984b7
  //   900533 73 76544b7 900533 73 32104b7 900533 73 fffe0e13 fa0e1ee3 a00893 73 313 2000e13 493 100913
  //   930023 900533 2200893 73 12484b3 130313 fffe0e13 fe0e12e3 800e13 313 32483 900533 2200893 73 430313
  //   fffe0e13 fe0e14e3 a00893 73 f00493 100913 409909b3 900533 2200893 73 fff48493 ff29f6e3 a00893 73 413
  //   140413 800533 2200893 73 240413 800533 2200893 73 340413 800533 2200893 73 440413 800533 2200893 73
  //   540413 800533 2200893 73 640413 800533 2200893 73 740413 800533 2200893 73 840413 800533 2200893
  //   2200893 73 8067
  //   指令字
  //   控制位
  //   流水调试日志用
  //   暂停节拍，不能为0
  //   戳工具置1进入计数暂停模式，ctrl+k时钟自动运行到对应节拍暂停
  //   ctrl+k关闭时钟连续运行，将控制位置零，进入单步调试模式调试
  //   可计数暂停的时钟源
  //   为方便自动评测，需要输出流水线各段保存的PC值，注意是PC不是PC+4，另外ID段寄存器写入信息，Mem段内存写入信息也要输出
  //   指令探针
  //   数据存储器
  //   指令探针
  //   指令探针
endmodule

module BHB (
  input  [31:0] IF_PC,
  input  [31:0] EX_PC,
  input  [31:0] EX_BranchAddr,
  input  BranchTaken,
  input  EX_Branch,
  input  clk,
  output [31:0] PredictAddr,
  output ID_PredictJump
);

  wire and_17_out, and_18_out, and_19_out, and_28_out, and_29_out, and_30_out, and_31_out, and_32_out,
       and_33_out, and_34_out, and_35_out, comparator_1_eq, comparator_2_eq, comparator_3_eq,
       comparator_4_eq, comparator_5_eq, comparator_6_eq, comparator_7_eq, comparator_8_eq, comparator_9_eq,
       comparator_10_eq, comparator_11_eq, comparator_12_eq, comparator_13_eq, comparator_14_eq,
       comparator_15_eq, comparator_16_eq, d_ff_1_q, d_ff_2_q, d_ff_3_q, d_ff_4_q, d_ff_5_q, d_ff_6_q,
       d_ff_7_q, d_ff_8_q, decoder_1_out0, decoder_1_out1, decoder_1_out2, decoder_1_out3, decoder_1_out4,
       decoder_1_out5, decoder_1_out6, decoder_1_out7, demultiplexer_1_out0, demultiplexer_1_out1,
       demultiplexer_1_out2, demultiplexer_1_out3, demultiplexer_1_out4, demultiplexer_1_out5,
       demultiplexer_1_out6, demultiplexer_1_out7, EX_Hit, EX_Miss, L0, L1, L2, L3, L4, L5, L6, L7, M0, M1,
       M2, M3, M4, M5, M6, M7, not_1_out, not_2_out, not_3_out, not_4_out, not_5_out, not_6_out, not_7_out,
       not_8_out, or_1_out, or_2_out, or_3_out, or_4_out, or_5_out, or_6_out, or_7_out, or_8_out, or_9_out,
       or_10_out, or_12_out, or_13_out, or_14_out, or_15_out, or_16_out, or_17_out, or_18_out, or_19_out,
       priority_encoder_1_gs, v0, v1, v2, v3, v4, v5, v6, v7, Write0, Write1, Write2, Write3, Write4, Write5,
       Write6, Write7;
  wire [0:0] controlled_buffer_9_out, controlled_buffer_10_out, controlled_buffer_11_out,
       controlled_buffer_12_out, controlled_buffer_13_out, controlled_buffer_14_out,
       controlled_buffer_15_out, controlled_buffer_16_out;
  wire [1:0] fsm_1_nextlow, fsm_2_nextlow, fsm_3_nextlow, fsm_4_nextlow, fsm_5_nextlow, fsm_6_nextlow,
       fsm_7_nextlow, fsm_8_nextlow, Predict0, Predict1, Predict2, Predict3, Predict4, Predict5, Predict6,
       Predict7;
  wire [2:0] max_1_maxid, max_2_maxid, max_3_maxid, max_4_maxid, max_5_maxid, max_6_maxid, max_7_maxid,
       priority_encoder_1_out;
  wire [15:0] C0, C1, C2, C3, C4, C5, C6, C7, max_1_max, max_2_max, max_3_max, max_4_max, max_5_max,
       max_6_max;
  wire [31:0] register_17_q, register_18_q, register_19_q, register_20_q, register_21_q, register_22_q,
       register_23_q, register_24_q, Tag0, Tag1, Tag2, Tag3, Tag4, Tag5, Tag6, Tag7;

  Register #(.width(1), .trigger("rising"), .Select("low")) register_1 (
    .D(1'b1), .en(Write5), .Q(v5), .clk(clk));  // open: clr
  Register #(.width(1), .trigger("rising"), .Select("low")) register_2 (
    .D(1'b1), .en(Write6), .Q(v6), .clk(clk));  // open: clr
  Register #(.width(1), .trigger("rising"), .Select("low")) register_3 (
    .D(1'b1), .en(Write7), .Q(v7), .clk(clk));  // open: clr
  Register #(.width(1), .trigger("rising"), .Select("low")) register_4 (
    .D(1'b1), .en(Write0), .Q(v0), .clk(clk));  // open: clr
  Register #(.width(1), .trigger("rising"), .Select("low")) register_5 (
    .D(1'b1), .en(Write1), .Q(v1), .clk(clk));  // open: clr
  Register #(.width(1), .trigger("rising"), .Select("low")) register_6 (
    .D(1'b1), .en(Write2), .Q(v2), .clk(clk));  // open: clr
  Register #(.width(1), .trigger("rising"), .Select("low")) register_7 (
    .D(1'b1), .en(Write3), .Q(v3), .clk(clk));  // open: clr
  Register #(.width(1), .trigger("rising"), .Select("low")) register_8 (
    .D(1'b1), .en(Write4), .Q(v4), .clk(clk));  // open: clr
  Register #(.width(32), .trigger("rising"), .Select("low")) register_9 (
    .D(EX_PC), .en(Write0), .Q(Tag0), .clk(clk));  // open: clr
  Register #(.width(32), .trigger("rising"), .Select("low")) register_10 (
    .D(EX_PC), .en(Write1), .Q(Tag1), .clk(clk));  // open: clr
  Register #(.width(32), .trigger("rising"), .Select("low")) register_11 (
    .D(EX_PC), .en(Write2), .Q(Tag2), .clk(clk));  // open: clr
  Register #(.width(32), .trigger("rising"), .Select("low")) register_12 (
    .D(EX_PC), .en(Write3), .Q(Tag3), .clk(clk));  // open: clr
  Register #(.width(32), .trigger("rising"), .Select("low")) register_13 (
    .D(EX_PC), .en(Write4), .Q(Tag4), .clk(clk));  // open: clr
  Register #(.width(32), .trigger("rising"), .Select("low")) register_14 (
    .D(EX_PC), .en(Write5), .Q(Tag5), .clk(clk));  // open: clr
  Register #(.width(32), .trigger("rising"), .Select("low")) register_15 (
    .D(EX_PC), .en(Write6), .Q(Tag6), .clk(clk));  // open: clr
  Register #(.width(32), .trigger("rising"), .Select("low")) register_16 (
    .D(EX_PC), .en(Write7), .Q(Tag7), .clk(clk));  // open: clr
  or or_1 (or_1_out, Write5, L5);
  or or_2 (or_2_out, Write6, L6);
  or or_3 (or_3_out, Write7, L7);
  Counter #(.width(16), .max('hffff), .ongoal("wrap"), .trigger("rising"), .behavior("new")) counter_1 (
    .Q(C0), .clk(clk), .clr(d_ff_1_q));  // open: load, D, count, carry, preset, down
  D_Flip_Flop #(.trigger("rising"), .Pre_Clr_Positions("ABOVE_BELOW"), .NegatePresetClear("false"), .enable("false"), .NewFFLayout("false")) d_ff_1 (
    .clk(clk), .D(or_4_out), .Q(d_ff_1_q));  // open: Qn, preset, reset
  or or_4 (or_4_out, Write0, L0);
  Counter #(.width(16), .max('hffff), .ongoal("wrap"), .trigger("rising"), .behavior("new")) counter_2 (
    .Q(C1), .clk(clk), .clr(d_ff_2_q));  // open: load, D, count, carry, preset, down
  D_Flip_Flop #(.trigger("rising"), .Pre_Clr_Positions("ABOVE_BELOW"), .NegatePresetClear("false"), .enable("false"), .NewFFLayout("false")) d_ff_2 (
    .clk(clk), .D(or_5_out), .Q(d_ff_2_q));  // open: Qn, preset, reset
  or or_5 (or_5_out, Write1, L1);
  Counter #(.width(16), .max('hffff), .ongoal("wrap"), .trigger("rising"), .behavior("new")) counter_3 (
    .Q(C2), .clk(clk), .clr(d_ff_3_q));  // open: load, D, count, carry, preset, down
  D_Flip_Flop #(.trigger("rising"), .Pre_Clr_Positions("ABOVE_BELOW"), .NegatePresetClear("false"), .enable("false"), .NewFFLayout("false")) d_ff_3 (
    .clk(clk), .D(or_6_out), .Q(d_ff_3_q));  // open: Qn, preset, reset
  or or_6 (or_6_out, Write2, L2);
  Counter #(.width(16), .max('hffff), .ongoal("wrap"), .trigger("rising"), .behavior("new")) counter_4 (
    .Q(C3), .clk(clk), .clr(d_ff_4_q));  // open: load, D, count, carry, preset, down
  D_Flip_Flop #(.trigger("rising"), .Pre_Clr_Positions("ABOVE_BELOW"), .NegatePresetClear("false"), .enable("false"), .NewFFLayout("false")) d_ff_4 (
    .clk(clk), .D(or_7_out), .Q(d_ff_4_q));  // open: Qn, preset, reset
  or or_7 (or_7_out, Write3, L3);
  Counter #(.width(16), .max('hffff), .ongoal("wrap"), .trigger("rising"), .behavior("new")) counter_5 (
    .Q(C4), .clk(clk), .clr(d_ff_5_q));  // open: load, D, count, carry, preset, down
  D_Flip_Flop #(.trigger("rising"), .Pre_Clr_Positions("ABOVE_BELOW"), .NegatePresetClear("false"), .enable("false"), .NewFFLayout("false")) d_ff_5 (
    .clk(clk), .D(or_8_out), .Q(d_ff_5_q));  // open: Qn, preset, reset
  or or_8 (or_8_out, Write4, L4);
  Counter #(.width(16), .max('hffff), .ongoal("wrap"), .trigger("rising"), .behavior("new")) counter_6 (
    .Q(C5), .clk(clk), .clr(d_ff_6_q));  // open: load, D, count, carry, preset, down
  D_Flip_Flop #(.trigger("rising"), .Pre_Clr_Positions("ABOVE_BELOW"), .NegatePresetClear("false"), .enable("false"), .NewFFLayout("false")) d_ff_6 (
    .clk(clk), .D(or_1_out), .Q(d_ff_6_q));  // open: Qn, preset, reset
  Counter #(.width(16), .max('hffff), .ongoal("wrap"), .trigger("rising"), .behavior("new")) counter_7 (
    .Q(C6), .clk(clk), .clr(d_ff_7_q));  // open: load, D, count, carry, preset, down
  D_Flip_Flop #(.trigger("rising"), .Pre_Clr_Positions("ABOVE_BELOW"), .NegatePresetClear("false"), .enable("false"), .NewFFLayout("false")) d_ff_7 (
    .clk(clk), .D(or_2_out), .Q(d_ff_7_q));  // open: Qn, preset, reset
  Counter #(.width(16), .max('hffff), .ongoal("wrap"), .trigger("rising"), .behavior("new")) counter_8 (
    .Q(C7), .clk(clk), .clr(d_ff_8_q));  // open: load, D, count, carry, preset, down
  D_Flip_Flop #(.trigger("rising"), .Pre_Clr_Positions("ABOVE_BELOW"), .NegatePresetClear("false"), .enable("false"), .NewFFLayout("false")) d_ff_8 (
    .clk(clk), .D(or_3_out), .Q(d_ff_8_q));  // open: Qn, preset, reset
  Register #(.width(32), .trigger("rising"), .Select("low")) register_17 (
    .D(EX_BranchAddr), .en(Write0), .Q(register_17_q), .clk(clk));  // open: clr
  assign PredictAddr = L0 ? register_17_q : 32'bz;  // Controlled_Buffer controlled_buffer_1
  assign PredictAddr = L1 ? register_18_q : 32'bz;  // Controlled_Buffer controlled_buffer_2
  Register #(.width(32), .trigger("rising"), .Select("low")) register_18 (
    .D(EX_BranchAddr), .en(Write1), .Q(register_18_q), .clk(clk));  // open: clr
  assign PredictAddr = L2 ? register_19_q : 32'bz;  // Controlled_Buffer controlled_buffer_3
  Register #(.width(32), .trigger("rising"), .Select("low")) register_19 (
    .D(EX_BranchAddr), .en(Write2), .Q(register_19_q), .clk(clk));  // open: clr
  assign PredictAddr = L3 ? register_20_q : 32'bz;  // Controlled_Buffer controlled_buffer_4
  Register #(.width(32), .trigger("rising"), .Select("low")) register_20 (
    .D(EX_BranchAddr), .en(Write3), .Q(register_20_q), .clk(clk));  // open: clr
  Register #(.width(32), .trigger("rising"), .Select("low")) register_21 (
    .D(EX_BranchAddr), .en(Write4), .Q(register_21_q), .clk(clk));  // open: clr
  assign PredictAddr = L4 ? register_21_q : 32'bz;  // Controlled_Buffer controlled_buffer_5
  assign PredictAddr = L5 ? register_22_q : 32'bz;  // Controlled_Buffer controlled_buffer_6
  Register #(.width(32), .trigger("rising"), .Select("low")) register_22 (
    .D(EX_BranchAddr), .en(Write5), .Q(register_22_q), .clk(clk));  // open: clr
  Register #(.width(32), .trigger("rising"), .Select("low")) register_23 (
    .D(EX_BranchAddr), .en(Write6), .Q(register_23_q), .clk(clk));  // open: clr
  assign PredictAddr = L6 ? register_23_q : 32'bz;  // Controlled_Buffer controlled_buffer_7
  assign PredictAddr = L7 ? register_24_q : 32'bz;  // Controlled_Buffer controlled_buffer_8
  Register #(.width(32), .trigger("rising"), .Select("low")) register_24 (
    .D(EX_BranchAddr), .en(Write7), .Q(register_24_q), .clk(clk));  // open: clr
  Comparator #(.width(32), .mode("twosComplement")) comparator_1 (
    .a(EX_PC), .b(Tag0), .eq(comparator_1_eq));  // open: gt, lt
  Comparator #(.width(32), .mode("twosComplement")) comparator_2 (
    .a(Tag0), .b(IF_PC), .eq(comparator_2_eq));  // open: gt, lt
  Comparator #(.width(32), .mode("twosComplement")) comparator_3 (
    .a(EX_PC), .b(Tag1), .eq(comparator_3_eq));  // open: gt, lt
  Comparator #(.width(32), .mode("twosComplement")) comparator_4 (
    .a(Tag1), .b(IF_PC), .eq(comparator_4_eq));  // open: gt, lt
  Comparator #(.width(32), .mode("twosComplement")) comparator_5 (
    .a(EX_PC), .b(Tag2), .eq(comparator_5_eq));  // open: gt, lt
  Comparator #(.width(32), .mode("twosComplement")) comparator_6 (
    .a(Tag2), .b(IF_PC), .eq(comparator_6_eq));  // open: gt, lt
  Comparator #(.width(32), .mode("twosComplement")) comparator_7 (
    .a(EX_PC), .b(Tag3), .eq(comparator_7_eq));  // open: gt, lt
  Comparator #(.width(32), .mode("twosComplement")) comparator_8 (
    .a(Tag3), .b(IF_PC), .eq(comparator_8_eq));  // open: gt, lt
  Comparator #(.width(32), .mode("twosComplement")) comparator_9 (
    .a(EX_PC), .b(Tag4), .eq(comparator_9_eq));  // open: gt, lt
  Comparator #(.width(32), .mode("twosComplement")) comparator_10 (
    .a(Tag4), .b(IF_PC), .eq(comparator_10_eq));  // open: gt, lt
  Comparator #(.width(32), .mode("twosComplement")) comparator_11 (
    .a(EX_PC), .b(Tag5), .eq(comparator_11_eq));  // open: gt, lt
  Comparator #(.width(32), .mode("twosComplement")) comparator_12 (
    .a(Tag5), .b(IF_PC), .eq(comparator_12_eq));  // open: gt, lt
  Comparator #(.width(32), .mode("twosComplement")) comparator_13 (
    .a(EX_PC), .b(Tag6), .eq(comparator_13_eq));  // open: gt, lt
  Comparator #(.width(32), .mode("twosComplement")) comparator_14 (
    .a(Tag6), .b(IF_PC), .eq(comparator_14_eq));  // open: gt, lt
  Comparator #(.width(32), .mode("twosComplement")) comparator_15 (
    .a(EX_PC), .b(Tag7), .eq(comparator_15_eq));  // open: gt, lt
  Comparator #(.width(32), .mode("twosComplement")) comparator_16 (
    .a(Tag7), .b(IF_PC), .eq(comparator_16_eq));  // open: gt, lt
  and and_1 (M0, comparator_1_eq, v0);
  and and_2 (L0, v0, comparator_2_eq);
  and and_3 (M1, comparator_3_eq, v1);
  and and_4 (L1, v1, comparator_4_eq);
  and and_5 (M2, comparator_5_eq, v2);
  and and_6 (L2, v2, comparator_6_eq);
  and and_7 (M3, comparator_7_eq, v3);
  and and_8 (L3, v3, comparator_8_eq);
  and and_9 (M4, comparator_9_eq, v4);
  and and_10 (L4, v4, comparator_10_eq);
  and and_11 (M5, comparator_11_eq, v5);
  and and_12 (L5, v5, comparator_12_eq);
  and and_13 (M6, comparator_13_eq, v6);
  and and_14 (L6, v6, comparator_14_eq);
  and and_15 (M7, comparator_15_eq, v7);
  and and_16 (L7, v7, comparator_16_eq);
  not not_1 (not_1_out, v0);
  not not_2 (not_2_out, v1);
  not not_3 (not_3_out, v2);
  not not_4 (not_4_out, v3);
  not not_5 (not_5_out, v4);
  not not_6 (not_6_out, v5);
  not not_7 (not_7_out, v6);
  not not_8 (not_8_out, v7);
  or or_9 (or_9_out, M0, M1, M2, M3);
  or or_10 (or_10_out, M4, M5, M6, M7);
  Priority_Encoder #(.select(3), .disabled(0)) priority_encoder_1 (
    .in0(not_1_out), .in1(not_2_out), .in2(not_3_out), .in3(not_4_out), .in4(not_5_out), .in5(not_6_out),
    .in6(not_7_out), .in7(not_8_out), .out(priority_encoder_1_out), .gs(priority_encoder_1_gs));  // open: en_out, en_in
  and and_17 (and_17_out, v0, v1, v2, v3);
  and and_18 (and_18_out, v4, v5, v6, v7);
  MAX max_1 (.X(C0), .Y(C1), .Xid(3'b000), .Yid(3'b001), .MAX(max_1_max), .MAXID(max_1_maxid));
  MAX max_2 (.X(C2), .Y(C3), .Xid(3'b010), .Yid(3'b011), .MAX(max_2_max), .MAXID(max_2_maxid));
  MAX max_3 (.X(C4), .Y(C5), .Xid(3'b100), .Yid(3'b101), .MAX(max_3_max), .MAXID(max_3_maxid));
  MAX max_4 (.X(C6), .Y(C7), .Xid(3'b110), .Yid(3'b111), .MAX(max_4_max), .MAXID(max_4_maxid));
  or or_11 (EX_Hit, or_9_out, or_10_out);
  and and_19 (and_19_out, and_17_out, and_18_out);
  MAX max_5 (.X(max_1_max), .Y(max_2_max), .Xid(max_1_maxid), .Yid(max_2_maxid), .MAX(max_5_max), .MAXID(max_5_maxid));
  MAX max_6 (.X(max_3_max), .Y(max_4_max), .Xid(max_3_maxid), .Yid(max_4_maxid), .MAX(max_6_max), .MAXID(max_6_maxid));
  not not_9 (EX_Miss, EX_Hit);
  Decoder #(.select(3), .tristate("false"), .disabled(0), .enable("true")) decoder_1 (
    .out0(decoder_1_out0), .out1(decoder_1_out1), .out2(decoder_1_out2), .out3(decoder_1_out3),
    .out4(decoder_1_out4), .out5(decoder_1_out5), .out6(decoder_1_out6), .out7(decoder_1_out7),
    .sel(priority_encoder_1_out), .en(priority_encoder_1_gs));
  Demultiplexer #(.select(3), .width(1), .tristate("false"), .disabled(0), .enable("false")) demultiplexer_1 (
    .out0(demultiplexer_1_out0), .out1(demultiplexer_1_out1), .out2(demultiplexer_1_out2),
    .out3(demultiplexer_1_out3), .out4(demultiplexer_1_out4), .out5(demultiplexer_1_out5),
    .out6(demultiplexer_1_out6), .out7(demultiplexer_1_out7), .in(and_19_out), .sel(max_7_maxid));
  MAX max_7 (.X(max_5_max), .Y(max_6_max), .Xid(max_5_maxid), .Yid(max_6_maxid), .MAXID(max_7_maxid));  // open: MAX
  or or_12 (or_12_out, decoder_1_out0, demultiplexer_1_out0);
  or or_13 (or_13_out, decoder_1_out1, demultiplexer_1_out1);
  or or_14 (or_14_out, decoder_1_out2, demultiplexer_1_out2);
  or or_15 (or_15_out, decoder_1_out3, demultiplexer_1_out3);
  or or_16 (or_16_out, decoder_1_out4, demultiplexer_1_out4);
  or or_17 (or_17_out, decoder_1_out5, demultiplexer_1_out5);
  or or_18 (or_18_out, decoder_1_out6, demultiplexer_1_out6);
  or or_19 (or_19_out, decoder_1_out7, demultiplexer_1_out7);
  and and_20 (Write0, or_12_out, EX_Miss, EX_Branch);
  and and_21 (Write1, or_13_out, EX_Miss, EX_Branch);
  and and_22 (Write2, or_14_out, EX_Miss, EX_Branch);
  and and_23 (Write3, or_15_out, EX_Miss, EX_Branch);
  and and_24 (Write4, or_16_out, EX_Miss, EX_Branch);
  and and_25 (Write5, or_17_out, EX_Miss, EX_Branch);
  and and_26 (Write6, or_18_out, EX_Miss, EX_Branch);
  and and_27 (Write7, or_19_out, EX_Miss, EX_Branch);
  assign {ID_PredictJump, controlled_buffer_9_out[0]} = L0 ? Predict0 : 2'bz;  // Controlled_Buffer controlled_buffer_9
  assign {ID_PredictJump, controlled_buffer_10_out[0]} = L1 ? Predict1 : 2'bz;  // Controlled_Buffer controlled_buffer_10
  assign {ID_PredictJump, controlled_buffer_11_out[0]} = L2 ? Predict2 : 2'bz;  // Controlled_Buffer controlled_buffer_11
  assign {ID_PredictJump, controlled_buffer_12_out[0]} = L3 ? Predict3 : 2'bz;  // Controlled_Buffer controlled_buffer_12
  assign {ID_PredictJump, controlled_buffer_13_out[0]} = L4 ? Predict4 : 2'bz;  // Controlled_Buffer controlled_buffer_13
  assign {ID_PredictJump, controlled_buffer_14_out[0]} = L5 ? Predict5 : 2'bz;  // Controlled_Buffer controlled_buffer_14
  assign {ID_PredictJump, controlled_buffer_15_out[0]} = L6 ? Predict6 : 2'bz;  // Controlled_Buffer controlled_buffer_15
  assign {ID_PredictJump, controlled_buffer_16_out[0]} = L7 ? Predict7 : 2'bz;  // Controlled_Buffer controlled_buffer_16
  Pull_Resistor #(.pull(0)) pull_resistor_1 (.node(ID_PredictJump));
  FSM fsm_1 (
    .High(Predict0[1]), .Low(Predict0[0]), .Jump(BranchTaken), .NextHigh(fsm_1_nextlow[1]),
    .NextLow(fsm_1_nextlow[0]));
  FSM fsm_2 (
    .High(Predict1[1]), .Low(Predict1[0]), .Jump(BranchTaken), .NextHigh(fsm_2_nextlow[1]),
    .NextLow(fsm_2_nextlow[0]));
  FSM fsm_3 (
    .High(Predict2[1]), .Low(Predict2[0]), .Jump(BranchTaken), .NextHigh(fsm_3_nextlow[1]),
    .NextLow(fsm_3_nextlow[0]));
  FSM fsm_4 (
    .High(Predict3[1]), .Low(Predict3[0]), .Jump(BranchTaken), .NextHigh(fsm_4_nextlow[1]),
    .NextLow(fsm_4_nextlow[0]));
  FSM fsm_5 (
    .High(Predict4[1]), .Low(Predict4[0]), .Jump(BranchTaken), .NextHigh(fsm_5_nextlow[1]),
    .NextLow(fsm_5_nextlow[0]));
  FSM fsm_6 (
    .High(Predict5[1]), .Low(Predict5[0]), .Jump(BranchTaken), .NextHigh(fsm_6_nextlow[1]),
    .NextLow(fsm_6_nextlow[0]));
  FSM fsm_7 (
    .High(Predict6[1]), .Low(Predict6[0]), .Jump(BranchTaken), .NextHigh(fsm_7_nextlow[1]),
    .NextLow(fsm_7_nextlow[0]));
  FSM fsm_8 (
    .High(Predict7[1]), .Low(Predict7[0]), .Jump(BranchTaken), .NextHigh(fsm_8_nextlow[1]),
    .NextLow(fsm_8_nextlow[0]));
  and and_28 (and_28_out, EX_Branch, M0);
  and and_29 (and_29_out, EX_Branch, M1);
  and and_30 (and_30_out, EX_Branch, M2);
  and and_31 (and_31_out, EX_Branch, M3);
  and and_32 (and_32_out, EX_Branch, M4);
  and and_33 (and_33_out, EX_Branch, M5);
  and and_34 (and_34_out, EX_Branch, M6);
  and and_35 (and_35_out, EX_Branch, M7);
  Register #(.width(2), .trigger("rising"), .Select("low")) register_25 (
    .D(fsm_1_nextlow), .en(and_28_out), .Q(Predict0), .clk(clk));  // open: clr
  Register #(.width(2), .trigger("rising"), .Select("low")) register_26 (
    .D(fsm_2_nextlow), .en(and_29_out), .Q(Predict1), .clk(clk));  // open: clr
  Register #(.width(2), .trigger("rising"), .Select("low")) register_27 (
    .D(fsm_3_nextlow), .en(and_30_out), .Q(Predict2), .clk(clk));  // open: clr
  Register #(.width(2), .trigger("rising"), .Select("low")) register_28 (
    .D(fsm_4_nextlow), .en(and_31_out), .Q(Predict3), .clk(clk));  // open: clr
  Register #(.width(2), .trigger("rising"), .Select("low")) register_29 (
    .D(fsm_5_nextlow), .en(and_32_out), .Q(Predict4), .clk(clk));  // open: clr
  Register #(.width(2), .trigger("rising"), .Select("low")) register_30 (
    .D(fsm_6_nextlow), .en(and_33_out), .Q(Predict5), .clk(clk));  // open: clr
  Register #(.width(2), .trigger("rising"), .Select("low")) register_31 (
    .D(fsm_7_nextlow), .en(and_34_out), .Q(Predict6), .clk(clk));  // open: clr
  Register #(.width(2), .trigger("rising"), .Select("low")) register_32 (
    .D(fsm_8_nextlow), .en(and_35_out), .Q(Predict7), .clk(clk));  // open: clr

  // Other names for the same wires on the sheet: JumpAddr[31:0] = PredictAddr; Tag[31:0] = EX_PC
endmodule

module MAX (
  input  [15:0] X,
  input  [15:0] Y,
  input  [2:0] Xid,
  input  [2:0] Yid,
  output [15:0] MAX,
  output [2:0] MAXID
);

  wire comparator_1_eq, comparator_1_lt, or_1_out;

  Comparator #(.width(16), .mode("unsigned")) comparator_1 (
    .a(X), .b(Y), .eq(comparator_1_eq), .lt(comparator_1_lt));  // open: gt
  or or_1 (or_1_out, comparator_1_eq, comparator_1_lt);
  Multiplexer #(.select(1), .width(16), .disabled("Z"), .enable("false")) multiplexer_1 (
    .in0(X), .in1(Y), .out(MAX), .sel(or_1_out));
  Multiplexer #(.select(1), .width(3), .disabled("Z"), .enable("false")) multiplexer_2 (
    .in0(Xid), .in1(Yid), .out(MAXID), .sel(or_1_out));
endmodule

module FSM (
  input  High,
  input  Low,
  input  Jump,
  output NextHigh,
  output NextLow
);

  wire and_1_out, and_2_out, and_3_out, and_4_out, not_1_out, not_2_out, not_3_out, not_4_out, not_5_out;

  not not_1 (not_1_out, Low);
  not not_2 (not_2_out, High);
  not not_3 (not_3_out, Low);
  not not_4 (not_4_out, Low);
  not not_5 (not_5_out, Jump);
  and and_1 (and_1_out, Low, Jump);
  and and_2 (and_2_out, High, not_1_out);
  and and_3 (and_3_out, not_2_out, not_3_out, Jump);
  and and_4 (and_4_out, High, not_4_out, not_5_out);
  or or_1 (NextHigh, and_1_out, and_2_out);
  or or_2 (NextLow, and_3_out, and_4_out);
endmodule
